// Logisim project 实验1-CS1806-U201814655-杨雨鑫.circ as structural Verilog: 5 circuits, main circuit 半加器
module \先行进位的四位二进制并行加法器测试电路  (
  input  in_1,
  input  in_2,
  input  in_3,
  input  in_4,
  input  in_5,
  input  in_6,
  input  in_7,
  input  in_8,
  input  in_9,
  output out_10,
  output out_11,
  output out_12,
  output out_13,
  output out_14
);

  \先行进位的四位二进制并行加法器  \u_先行进位的四位二进制并行加法器_1  (
    .C0(in_1), .A0(in_3), .B0(in_5), .A1(in_7), .B1(in_9), .A2(in_2), .B2(in_4), .A3(in_6), .B3(in_8),
    .S0(out_13), .S1(out_12), .S2(out_11), .S3(out_10), .C4(out_14));
endmodule

module \半加器  (
  input  A,
  input  B,
  output S,
  output C
);

  wire and_1_out, and_2_out, not_1_out, not_2_out;

  not not_1 (not_1_out, A);
  not not_2 (not_2_out, B);
  and and_1 (and_1_out, not_1_out, B);
  and and_2 (and_2_out, A, not_2_out);
  and and_3 (C, A, B);
  or or_1 (S, and_1_out, and_2_out);
endmodule

module \全加器  (
  input  A,
  input  Ci,
  input  B,
  output S,
  output Co
);

  wire nand_1_out, nand_2_out, xor_1_out;

  xor xor_1 (xor_1_out, A, B);
  nand nand_1 (nand_1_out, B, A);
  nand nand_2 (nand_2_out, Ci, xor_1_out);
  xor xor_2 (S, xor_1_out, Ci);
  nand nand_3 (Co, nand_2_out, nand_1_out);
endmodule

module \串行进位的四位二进制并行加法器  (
  input  C0,
  input  A0,
  input  B0,
  input  A1,
  input  B1,
  input  A2,
  input  B2,
  input  A3,
  input  B3,
  output S0,
  output S1,
  output S2,
  output S3,
  output C4
);

  wire \全加器_1_co , \全加器_2_co , \全加器_3_co ;

  \全加器  \u_全加器_1  (.A(A0), .Ci(B0), .B(C0), .S(S0), .Co(\全加器_1_co ));
  \全加器  \u_全加器_2  (.A(A1), .Ci(B1), .B(\全加器_1_co ), .S(S1), .Co(\全加器_2_co ));
  \全加器  \u_全加器_3  (.A(A2), .Ci(B2), .B(\全加器_2_co ), .S(S2), .Co(\全加器_3_co ));
  \全加器  \u_全加器_4  (.A(A3), .Ci(B3), .B(\全加器_3_co ), .S(S3), .Co(C4));
endmodule

module \先行进位的四位二进制并行加法器  (
  input  C0,
  input  A0,
  input  B0,
  input  A1,
  input  B1,
  input  A2,
  input  B2,
  input  A3,
  input  B3,
  output S0,
  output S1,
  output S2,
  output S3,
  output C4
);

  wire C1_out, C2_out, C3_out, G0_out, G1_out, G2_out, G4_out, P0_out, P0C0_out, P0P1C0_out, P1_out,
       P1G0_out, P2_out, P2G1_out, P2P1G0_out, P2P1P0C0_out, P3_out, P3G2_out, P3P2G1_out, P3P2P1G0_out,
       P3P2P1P0C0_out, xor_1_out, xor_2_out, xor_3_out, xor_4_out;

  xor P0 (P0_out, A0, B0);
  and G0 (G0_out, A0, B0);
  xor P1 (P1_out, A1, B1);
  and G1 (G1_out, A1, B1);
  xor P2 (P2_out, A2, B2);
  and G2 (G2_out, A2, B2);
  xor P3 (P3_out, A3, B3);
  and G4 (G4_out, A3, B3);
  and P0C0 (P0C0_out, C0, P0_out);
  and P0P1C0 (P0P1C0_out, P0_out, C0, P1_out);
  and P1G0 (P1G0_out, G0_out, P1_out);
  and P2P1P0C0 (P2P1P0C0_out, C0, P0_out, P1_out, P2_out);
  and P2P1G0 (P2P1G0_out, G0_out, P1_out, P2_out);
  and P3P2P1P0C0 (P3P2P1P0C0_out, C0, P0_out, P1_out, P2_out, P3_out);
  and P3P2P1G0 (P3P2P1G0_out, P3_out, P2_out, P1_out, G0_out);
  and P3P2G1 (P3P2G1_out, P3_out, P2_out, G1_out);
  and P3G2 (P3G2_out, P3_out, G2_out);
  or C1 (C1_out, P0C0_out, G0_out);
  and P2G1 (P2G1_out, P2_out, G1_out);
  or C2 (C2_out, P0P1C0_out, P1G0_out, G1_out);
  or C3 (C3_out, P2P1P0C0_out, P2P1G0_out, P2G1_out, G2_out);
  or u_C4 (C4, P3P2P1P0C0_out, P3P2P1G0_out, P3P2G1_out, P3G2_out, G4_out);
  xor xor_1 (xor_1_out, A0, B0);
  xor xor_2 (xor_2_out, C1_out, A1);
  xor xor_3 (xor_3_out, C2_out, A2);
  xor xor_4 (xor_4_out, C3_out, A3);
  xor xor_5 (S0, C0, xor_1_out);
  xor xor_6 (S1, xor_2_out, B1);
  xor xor_7 (S2, xor_3_out, B2);
  xor xor_8 (S3, xor_4_out, B3);
endmodule
