// Logisim project 实验2-CS1806-U201814655-杨雨鑫.circ as structural Verilog: 10 circuits, main circuit 四位二进制可逆计数器
module \四位二进制可逆计数器  (
  input  CLR,
  input  CPu,
  input  CPd,
  input  A,
  input  B,
  input  C,
  input  D,
  input  \LD非 ,
  output Q0,
  output Q1,
  output Q2,
  output Q3
);

  wire A_q, A_qn, and_1_out, and_2_out, and_3_out, and_4_out, and_5_out, and_6_out, and_7_out, and_8_out,
       and_9_out, and_10_out, B_q, B_qn, C0_out, C1_out, C2_out, C3_out, C_q, C_qn, d_ff_1_q, d_ff_1_qn,
       not_1_out, or_1_out, or_2_out, or_3_out, or_4_out, or_5_out;

  and and_1 (and_1_out, CPu, A_q);
  and and_2 (and_2_out, CPd, A_qn);
  and and_3 (and_3_out, CPu, B_q, A_q);
  and and_4 (and_4_out, A_qn, CPd, B_qn);
  and and_5 (and_5_out, A_q, B_q, CPu, C_q);
  and and_6 (and_6_out, A_qn, B_qn, CPd, C_qn);
  not not_1 (not_1_out, \LD非 );
  or C0 (C0_out, CPu, CPd);
  or C1 (C1_out, and_1_out, and_2_out);
  or C2 (C2_out, and_3_out, and_4_out);
  or C3 (C3_out, and_5_out, and_6_out);
  and and_7 (and_7_out, A, not_1_out);
  and and_8 (and_8_out, B, not_1_out);
  and and_9 (and_9_out, C, not_1_out);
  or or_1 (or_1_out, CLR, not_1_out);
  and and_10 (and_10_out, D, not_1_out);
  or or_2 (or_2_out, C0_out, and_7_out);
  or or_3 (or_3_out, C1_out, and_8_out);
  or or_4 (or_4_out, C2_out, and_9_out);
  or or_5 (or_5_out, C3_out, and_10_out);
  D_Flip_Flop #(.trigger("falling"), .Pre_Clr_Positions("ABOVE_BELOW"), .NegatePresetClear("false"), .enable("false"), .NewFFLayout("true")) u_A (
    .clk(or_2_out), .D(A_qn), .Q(A_q), .Qn(A_qn), .reset(or_1_out));  // open: preset
  D_Flip_Flop #(.trigger("falling"), .Pre_Clr_Positions("ABOVE_BELOW"), .NegatePresetClear("false"), .enable("false"), .NewFFLayout("true")) u_B (
    .clk(or_3_out), .D(B_qn), .Q(B_q), .Qn(B_qn), .reset(or_1_out));  // open: preset
  D_Flip_Flop #(.trigger("falling"), .Pre_Clr_Positions("ABOVE_BELOW"), .NegatePresetClear("false"), .enable("false"), .NewFFLayout("true")) u_C (
    .clk(or_4_out), .D(C_qn), .Q(C_q), .Qn(C_qn), .reset(or_1_out));  // open: preset
  D_Flip_Flop #(.trigger("falling"), .Pre_Clr_Positions("ABOVE_BELOW"), .NegatePresetClear("false"), .enable("false"), .NewFFLayout("true")) d_ff_1 (
    .clk(or_5_out), .D(d_ff_1_qn), .Q(d_ff_1_q), .Qn(d_ff_1_qn), .reset(or_1_out));  // open: preset
  or or_6 (Q0, A_q, and_7_out);
  or or_7 (Q1, B_q, and_8_out);
  or or_8 (Q2, C_q, and_9_out);
  or or_9 (Q3, d_ff_1_q, and_10_out);
endmodule

module \四位二进制可逆计数器测试电路  (
  input  in_1,
  input  in_2,
  input  in_3,
  input  in_4,
  input  in_5,
  input  in_6,
  input  in_7,
  input  in_8,
  output out_9,
  output out_10,
  output out_11,
  output out_12
);

  \四位二进制可逆计数器  \u_四位二进制可逆计数器_1  (
    .CLR(in_1), .CPu(in_2), .CPd(in_3), .Q0(out_12), .Q1(out_11), .Q2(out_10), .Q3(out_9), .\LD非 (in_4),
    .A(in_8), .B(in_7), .C(in_6), .D(in_5));
endmodule

module \二进制转8421码电路  (
  input  in_1,
  input  in_2,
  input  in_3,
  input  in_4,
  output out_5,
  output out_6,
  output out_7,
  output out_8,
  output out_9,
  output out_10,
  output out_11,
  output out_12
);

  wire and_1_out, or_1_out;

  or or_1 (or_1_out, in_3, in_2);
  \先行进位并行加法器  \u_先行进位并行加法器_1  (
    .C0(1'b0), .A0(in_4), .B0(1'b0), .A1(in_3), .B1(and_1_out), .A2(in_2), .B2(and_1_out), .A3(in_1),
    .B3(1'b0), .S0(out_8), .S1(out_7), .S2(out_6), .S3(out_5), .C4(out_9));
  and and_1 (and_1_out, or_1_out, in_1);

  assign out_10 = 1'b0;
  assign out_11 = 1'b0;
  assign out_12 = 1'b0;
endmodule

module \二进制转8421码测试电路  (
  input  in_1,
  input  in_2,
  input  in_3,
  input  in_4,
  output out_5,
  output out_6,
  output out_7,
  output out_8,
  output out_9,
  output out_10,
  output out_11,
  output out_12
);

  \二进制转8421码电路  \u_二进制转8421码电路_1  (
    .out_10(out_7), .out_11(out_6), .out_12(out_5), .out_9(out_8), .out_5(out_9), .out_6(out_10),
    .out_7(out_11), .out_8(out_12), .in_1(in_1), .in_2(in_2), .in_3(in_3), .in_4(in_4));
endmodule

module \显示电路  (
  input  A0,
  input  A1,
  input  A2,
  input  A3,
  output a,
  output b,
  output c,
  output d,
  output e,
  output f,
  output g
);

  wire and_1_out, and_2_out, and_3_out, and_4_out, and_5_out, and_6_out, and_7_out, and_8_out, and_9_out,
       and_10_out, and_11_out, and_12_out, and_13_out, and_14_out, and_15_out, and_16_out, and_17_out,
       not_1_out, not_2_out, not_3_out, not_4_out, not_5_out, not_6_out, not_7_out, not_8_out, not_9_out,
       not_10_out, not_11_out, not_12_out, not_13_out, not_14_out, not_15_out, not_16_out, not_17_out,
       not_18_out, not_19_out, not_20_out, not_21_out, not_22_out;

  not not_1 (not_1_out, A1);
  and and_1 (and_1_out, not_1_out, not_2_out);
  not not_2 (not_2_out, A3);
  not not_3 (not_3_out, A1);
  and and_2 (and_2_out, not_3_out, A2);
  and and_3 (and_3_out, A1, A3);
  not not_4 (not_4_out, A1);
  not not_5 (not_5_out, A2);
  and and_4 (and_4_out, not_5_out, not_6_out);
  not not_6 (not_6_out, A3);
  and and_5 (and_5_out, A2, A3);
  not not_7 (not_7_out, A2);
  or or_1 (c, not_7_out, A3, A1);
  not not_8 (not_8_out, A1);
  and and_6 (and_6_out, not_8_out, not_9_out);
  not not_9 (not_9_out, A3);
  not not_10 (not_10_out, A1);
  and and_7 (and_7_out, not_10_out, A2);
  and and_8 (and_8_out, A2, not_11_out);
  not not_11 (not_11_out, A3);
  and and_9 (and_9_out, A1, not_12_out, A3);
  not not_12 (not_12_out, A2);
  not not_13 (not_13_out, A1);
  and and_10 (and_10_out, not_13_out, not_14_out);
  not not_14 (not_14_out, A3);
  and and_11 (and_11_out, A2, not_15_out);
  not not_15 (not_15_out, A3);
  not not_16 (not_16_out, A2);
  and and_12 (and_12_out, not_16_out, not_17_out);
  not not_17 (not_17_out, A3);
  and and_13 (and_13_out, A1, not_18_out);
  not not_18 (not_18_out, A2);
  and and_14 (and_14_out, A1, not_19_out);
  not not_19 (not_19_out, A3);
  not not_20 (not_20_out, A1);
  and and_15 (and_15_out, not_20_out, A2);
  and and_16 (and_16_out, A1, not_21_out);
  not not_21 (not_21_out, A2);
  and and_17 (and_17_out, A1, not_22_out);
  not not_22 (not_22_out, A3);
  or or_2 (a, and_1_out, and_2_out, and_3_out, A0);
  or or_3 (b, not_4_out, and_4_out, and_5_out);
  or or_4 (d, and_6_out, and_7_out, and_8_out, and_9_out);
  or or_5 (e, and_10_out, and_11_out);
  or or_6 (f, and_12_out, and_13_out, and_14_out, A0);
  or or_7 (g, and_15_out, and_16_out, and_17_out, A0);
endmodule

module \显示电路测试电路  (
  input  in_1,
  input  in_2,
  input  in_3,
  input  in_4
);

  wire \显示电路_1_a , \显示电路_1_b , \显示电路_1_c , \显示电路_1_d , \显示电路_1_e , \显示电路_1_f , \显示电路_1_g ;

  _7_Segment_Display #(.active("true")) u_7_segment_display_1 (
    .g(\显示电路_1_g ), .f(\显示电路_1_f ), .a(\显示电路_1_a ), .b(\显示电路_1_b ), .e(\显示电路_1_e ), .d(\显示电路_1_d ),
    .c(\显示电路_1_c ), .dp(1'b0));
  \显示电路  \u_显示电路_1  (
    .A0(in_1), .A1(in_2), .A2(in_3), .A3(in_4), .a(\显示电路_1_a ), .b(\显示电路_1_b ), .c(\显示电路_1_c ),
    .d(\显示电路_1_d ), .e(\显示电路_1_e ), .f(\显示电路_1_f ), .g(\显示电路_1_g ));
endmodule

module \报警电路  (
  input  in_1,
  input  in_2,
  input  in_3,
  output out_4,
  output out_5,
  output out_6,
  output out_7,
  output \报警 
);

  wire and_1_out, and_2_out, not_1_out, \满了_out , \空了_out ;

  not not_1 (not_1_out, \满了_out );
  or \u_空了  (\空了_out , out_7, out_6, out_5, out_4);
  and and_1 (and_1_out, \空了_out , in_2);
  and and_2 (and_2_out, not_1_out, in_1);
  and and_3 (\报警 , \满了_out , in_1);
  and \u_满了  (\满了_out , out_4, out_5, out_6, out_7);
  \四位二进制可逆计数器  \u_四位二进制可逆计数器_1  (
    .CLR(in_3), .CPu(and_2_out), .CPd(and_1_out), .Q0(out_7), .Q1(out_6), .Q2(out_5), .Q3(out_4), .A(1'b0),
    .B(1'b0), .C(1'b0), .D(1'b0));  // open: LD非
endmodule

module \小型实验室门禁系统  (
  input  in_1,
  input  in_2,
  input  in_3,
  output out_4,
  output out_5,
  output out_6,
  output out_7,
  output out_8,
  output out_9,
  output out_10,
  output out_11,
  output out_12,
  output out_13,
  output out_14,
  output out_15,
  output out_16,
  output out_17,
  output out_18
);

  wire \二进制转8421码电路_1_out_5 , \二进制转8421码电路_1_out_6 , \二进制转8421码电路_1_out_7 , \二进制转8421码电路_1_out_8 ,
       \二进制转8421码电路_1_out_9 , \二进制转8421码电路_1_out_10 , \二进制转8421码电路_1_out_11 , \二进制转8421码电路_1_out_12 ,
       \报警电路_1_out_4 , \报警电路_1_out_5 , \报警电路_1_out_6 , \报警电路_1_out_7 ;

  \二进制转8421码电路  \u_二进制转8421码电路_1  (
    .out_10(\二进制转8421码电路_1_out_10 ), .out_11(\二进制转8421码电路_1_out_11 ), .out_12(\二进制转8421码电路_1_out_12 ),
    .out_9(\二进制转8421码电路_1_out_9 ), .out_5(\二进制转8421码电路_1_out_5 ), .out_6(\二进制转8421码电路_1_out_6 ),
    .out_7(\二进制转8421码电路_1_out_7 ), .out_8(\二进制转8421码电路_1_out_8 ), .in_1(\报警电路_1_out_4 ),
    .in_2(\报警电路_1_out_5 ), .in_3(\报警电路_1_out_6 ), .in_4(\报警电路_1_out_7 ));
  \报警电路  \u_报警电路_1  (
    .\报警 (out_18), .in_1(in_1), .in_2(in_3), .in_3(in_2), .out_4(\报警电路_1_out_4 ), .out_5(\报警电路_1_out_5 ),
    .out_6(\报警电路_1_out_6 ), .out_7(\报警电路_1_out_7 ));
  \显示电路  \u_显示电路_1  (
    .A0(\二进制转8421码电路_1_out_12 ), .A1(\二进制转8421码电路_1_out_11 ), .A2(\二进制转8421码电路_1_out_10 ),
    .A3(\二进制转8421码电路_1_out_9 ), .a(out_4), .b(out_5), .c(out_6), .d(out_7), .e(out_8), .f(out_9), .g(out_10));
  \显示电路  \u_显示电路_2  (
    .A0(\二进制转8421码电路_1_out_5 ), .A1(\二进制转8421码电路_1_out_6 ), .A2(\二进制转8421码电路_1_out_7 ),
    .A3(\二进制转8421码电路_1_out_8 ), .a(out_11), .b(out_12), .c(out_13), .d(out_14), .e(out_15), .f(out_16),
    .g(out_17));
endmodule

module \小型门禁系统测试电路  (
  input  in_1,
  input  in_2,
  input  in_3,
  output out_4
);

  wire \小型实验室门禁系统_1_out_4 , \小型实验室门禁系统_1_out_5 , \小型实验室门禁系统_1_out_6 , \小型实验室门禁系统_1_out_7 ,
       \小型实验室门禁系统_1_out_8 , \小型实验室门禁系统_1_out_9 , \小型实验室门禁系统_1_out_10 , \小型实验室门禁系统_1_out_11 ,
       \小型实验室门禁系统_1_out_12 , \小型实验室门禁系统_1_out_13 , \小型实验室门禁系统_1_out_14 , \小型实验室门禁系统_1_out_15 ,
       \小型实验室门禁系统_1_out_16 , \小型实验室门禁系统_1_out_17 ;

  _7_Segment_Display #(.active("true")) u_7_segment_display_1 (
    .g(\小型实验室门禁系统_1_out_10 ), .f(\小型实验室门禁系统_1_out_9 ), .a(\小型实验室门禁系统_1_out_4 ), .b(\小型实验室门禁系统_1_out_5 ),
    .e(\小型实验室门禁系统_1_out_8 ), .d(\小型实验室门禁系统_1_out_7 ), .c(\小型实验室门禁系统_1_out_6 ), .dp(1'b0));
  _7_Segment_Display #(.active("true")) u_7_segment_display_2 (
    .g(\小型实验室门禁系统_1_out_17 ), .f(\小型实验室门禁系统_1_out_16 ), .a(\小型实验室门禁系统_1_out_11 ), .b(\小型实验室门禁系统_1_out_12 ),
    .e(\小型实验室门禁系统_1_out_15 ), .d(\小型实验室门禁系统_1_out_14 ), .c(\小型实验室门禁系统_1_out_13 ), .dp(1'b0));
  \小型实验室门禁系统  \u_小型实验室门禁系统_1  (
    .in_1(in_1), .in_2(in_2), .in_3(in_3), .out_4(\小型实验室门禁系统_1_out_4 ), .out_5(\小型实验室门禁系统_1_out_5 ),
    .out_6(\小型实验室门禁系统_1_out_6 ), .out_7(\小型实验室门禁系统_1_out_7 ), .out_8(\小型实验室门禁系统_1_out_8 ),
    .out_9(\小型实验室门禁系统_1_out_9 ), .out_10(\小型实验室门禁系统_1_out_10 ), .out_11(\小型实验室门禁系统_1_out_11 ),
    .out_12(\小型实验室门禁系统_1_out_12 ), .out_13(\小型实验室门禁系统_1_out_13 ), .out_14(\小型实验室门禁系统_1_out_14 ),
    .out_15(\小型实验室门禁系统_1_out_15 ), .out_16(\小型实验室门禁系统_1_out_16 ), .out_17(\小型实验室门禁系统_1_out_17 ),
    .out_18(out_4));
endmodule

module \先行进位并行加法器  (
  input  C0,
  input  A0,
  input  B0,
  input  A1,
  input  B1,
  input  A2,
  input  B2,
  input  A3,
  input  B3,
  output S0,
  output S1,
  output S2,
  output S3,
  output C4
);

  wire C1_out, C2_out, C3_out, G0_out, G1_out, G2_out, G4_out, P0_out, P0C0_out, P0P1C0_out, P1_out,
       P1G0_out, P2_out, P2G1_out, P2P1G0_out, P2P1P0C0_out, P3_out, P3G2_out, P3P2G1_out, P3P2P1G0_out,
       P3P2P1P0C0_out, xor_1_out, xor_2_out, xor_3_out, xor_4_out;

  xor P0 (P0_out, A0, B0);
  and G0 (G0_out, A0, B0);
  xor P1 (P1_out, A1, B1);
  and G1 (G1_out, A1, B1);
  xor P2 (P2_out, A2, B2);
  and G2 (G2_out, A2, B2);
  xor P3 (P3_out, A3, B3);
  and G4 (G4_out, A3, B3);
  and P0C0 (P0C0_out, C0, P0_out);
  and P0P1C0 (P0P1C0_out, P0_out, C0, P1_out);
  and P1G0 (P1G0_out, G0_out, P1_out);
  and P2P1P0C0 (P2P1P0C0_out, C0, P0_out, P1_out, P2_out);
  and P2P1G0 (P2P1G0_out, G0_out, P1_out, P2_out);
  and P3P2P1P0C0 (P3P2P1P0C0_out, C0, P0_out, P1_out, P2_out, P3_out);
  and P3P2P1G0 (P3P2P1G0_out, P3_out, P2_out, P1_out, G0_out);
  and P3P2G1 (P3P2G1_out, P3_out, P2_out, G1_out);
  and P3G2 (P3G2_out, P3_out, G2_out);
  or C1 (C1_out, P0C0_out, G0_out);
  and P2G1 (P2G1_out, P2_out, G1_out);
  or C2 (C2_out, P0P1C0_out, P1G0_out, G1_out);
  or C3 (C3_out, P2P1P0C0_out, P2P1G0_out, P2G1_out, G2_out);
  or u_C4 (C4, P3P2P1P0C0_out, P3P2P1G0_out, P3P2G1_out, P3G2_out, G4_out);
  xor xor_1 (xor_1_out, A0, B0);
  xor xor_2 (xor_2_out, C1_out, A1);
  xor xor_3 (xor_3_out, C2_out, A2);
  xor xor_4 (xor_4_out, C3_out, A3);
  xor xor_5 (S0, C0, xor_1_out);
  xor xor_6 (S1, xor_2_out, B1);
  xor xor_7 (S2, xor_3_out, B2);
  xor xor_8 (S3, xor_4_out, B3);
endmodule
