// Logisim project 实验3-CS1806-U201814655-杨雨鑫.circ as structural Verilog: 6 circuits, main circuit 四位乘法器
module \四位乘法器  (
  input  [3:0] b,
  input  [3:0] a,
  output [7:0] out_3
);

  wire adder_1_cout;
  wire [7:0] adder_1_out, adder_2_out, bit_extender_1_out, multiplexer_1_out, multiplexer_2_out,
       multiplexer_3_out, multiplexer_4_out, shifter_1_out, shifter_2_out, shifter_3_out;

  assign bit_extender_1_out = {{4{1'b0}}, a};  // Bit_Extender bit_extender_1
  Multiplexer #(.select(1), .width(8), .disabled("Z"), .enable("false")) multiplexer_1 (
    .in0({8{1'b0}}), .in1(bit_extender_1_out), .out(multiplexer_1_out), .sel(b[0]));
  Shifter #(.width(8), .shift("ll")) shifter_1 (.in(bit_extender_1_out), .\dist (3'b001), .out(shifter_1_out));
  Multiplexer #(.select(1), .width(8), .disabled("Z"), .enable("false")) multiplexer_2 (
    .in0({8{1'b0}}), .in1(shifter_1_out), .out(multiplexer_2_out), .sel(b[1]));
  Shifter #(.width(8), .shift("ll")) shifter_2 (.in(shifter_1_out), .\dist (3'b001), .out(shifter_2_out));
  Shifter #(.width(8), .shift("ll")) shifter_3 (.in(shifter_2_out), .\dist (3'b001), .out(shifter_3_out));
  Multiplexer #(.select(1), .width(8), .disabled("Z"), .enable("false")) multiplexer_3 (
    .in0({8{1'b0}}), .in1(shifter_2_out), .out(multiplexer_3_out), .sel(b[2]));
  Multiplexer #(.select(1), .width(8), .disabled("Z"), .enable("false")) multiplexer_4 (
    .in0({8{1'b0}}), .in1(shifter_3_out), .out(multiplexer_4_out), .sel(b[3]));
  Adder #(.width(8)) adder_1 (
    .a(multiplexer_1_out), .b(multiplexer_2_out), .out(adder_1_out), .cout(adder_1_cout));  // open: cin
  Adder #(.width(8)) adder_2 (
    .a(multiplexer_3_out), .b(multiplexer_4_out), .out(adder_2_out), .cin(adder_1_cout));  // open: cout
  Adder #(.width(8)) adder_3 (.a(adder_1_out), .b(adder_2_out), .out(out_3));  // open: cin, cout
endmodule

module \四位乘法器测试电路  (
  input  [3:0] in_1,
  input  [3:0] in_2,
  output [7:0] out_3
);

  \四位乘法器  \u_四位乘法器_1  (.b(in_1), .a(in_2), .out_3(out_3));
endmodule

module \_32X4乘法器  (
  input  [3:0] in_1,
  input  [31:0] in_2,
  output [31:0] out_3,
  output [31:0] out_4
);

  wire adder_7_cout;
  wire [3:0] adder_8_out;
  wire [7:0] \四位乘法器_1_out_3 , \四位乘法器_2_out_3 , \四位乘法器_3_out_3 , \四位乘法器_4_out_3 , \四位乘法器_5_out_3 ,
       \四位乘法器_6_out_3 , \四位乘法器_7_out_3 , \四位乘法器_8_out_3 ;
  wire [31:0] adder_1_out, adder_2_out, adder_3_out, adder_4_out, adder_5_out, adder_6_out,
       bit_extender_1_out, bit_extender_2_out, bit_extender_3_out, bit_extender_4_out, bit_extender_5_out,
       bit_extender_6_out, bit_extender_7_out, bit_extender_8_out, shifter_1_out, shifter_2_out,
       shifter_3_out, shifter_4_out, shifter_5_out, shifter_6_out, shifter_7_out;

  \四位乘法器  \u_四位乘法器_1  (.b(in_2[3:0]), .a(in_1), .out_3(\四位乘法器_1_out_3 ));
  \四位乘法器  \u_四位乘法器_2  (.b(in_2[7:4]), .a(in_1), .out_3(\四位乘法器_2_out_3 ));
  \四位乘法器  \u_四位乘法器_3  (.b(in_2[11:8]), .a(in_1), .out_3(\四位乘法器_3_out_3 ));
  \四位乘法器  \u_四位乘法器_4  (.b(in_2[15:12]), .a(in_1), .out_3(\四位乘法器_4_out_3 ));
  \四位乘法器  \u_四位乘法器_5  (.b(in_2[19:16]), .a(in_1), .out_3(\四位乘法器_5_out_3 ));
  \四位乘法器  \u_四位乘法器_6  (.b(in_2[23:20]), .a(in_1), .out_3(\四位乘法器_6_out_3 ));
  \四位乘法器  \u_四位乘法器_7  (.b(in_2[27:24]), .a(in_1), .out_3(\四位乘法器_7_out_3 ));
  \四位乘法器  \u_四位乘法器_8  (.b(in_2[31:28]), .a(in_1), .out_3(\四位乘法器_8_out_3 ));
  assign bit_extender_1_out = {{24{1'b0}}, \四位乘法器_1_out_3 };  // Bit_Extender bit_extender_1
  assign bit_extender_2_out = {{24{1'b0}}, \四位乘法器_2_out_3 };  // Bit_Extender bit_extender_2
  assign bit_extender_3_out = {{24{1'b0}}, \四位乘法器_3_out_3 };  // Bit_Extender bit_extender_3
  assign bit_extender_4_out = {{24{1'b0}}, \四位乘法器_4_out_3 };  // Bit_Extender bit_extender_4
  assign bit_extender_5_out = {{24{1'b0}}, \四位乘法器_5_out_3 };  // Bit_Extender bit_extender_5
  assign bit_extender_6_out = {{24{1'b0}}, \四位乘法器_6_out_3 };  // Bit_Extender bit_extender_6
  assign bit_extender_7_out = {{24{1'b0}}, \四位乘法器_7_out_3 };  // Bit_Extender bit_extender_7
  assign bit_extender_8_out = {{28{1'b0}}, \四位乘法器_8_out_3 [3:0]};  // Bit_Extender bit_extender_8
  Shifter #(.width(32), .shift("ll")) shifter_1 (.in(bit_extender_2_out), .\dist (5'b00100), .out(shifter_1_out));
  Shifter #(.width(32), .shift("ll")) shifter_2 (.in(bit_extender_3_out), .\dist (5'b01000), .out(shifter_2_out));
  Shifter #(.width(32), .shift("ll")) shifter_3 (.in(bit_extender_4_out), .\dist (5'b01100), .out(shifter_3_out));
  Shifter #(.width(32), .shift("ll")) shifter_4 (.in(bit_extender_5_out), .\dist (5'b10000), .out(shifter_4_out));
  Shifter #(.width(32), .shift("ll")) shifter_5 (.in(bit_extender_6_out), .\dist (5'b10100), .out(shifter_5_out));
  Shifter #(.width(32), .shift("ll")) shifter_6 (.in(bit_extender_7_out), .\dist (5'b11000), .out(shifter_6_out));
  Shifter #(.width(32), .shift("ll")) shifter_7 (.in(bit_extender_8_out), .\dist (5'b11100), .out(shifter_7_out));
  Adder #(.width(32)) adder_1 (.a(bit_extender_1_out), .b(shifter_1_out), .out(adder_1_out), .cin(1'b0));  // open: cout
  Adder #(.width(32)) adder_2 (.a(adder_1_out), .b(shifter_2_out), .out(adder_2_out), .cin(1'b0));  // open: cout
  Adder #(.width(32)) adder_3 (.a(adder_2_out), .b(shifter_3_out), .out(adder_3_out), .cin(1'b0));  // open: cout
  Adder #(.width(32)) adder_4 (.a(adder_3_out), .b(shifter_4_out), .out(adder_4_out), .cin(1'b0));  // open: cout
  Adder #(.width(32)) adder_5 (.a(adder_4_out), .b(shifter_5_out), .out(adder_5_out), .cin(1'b0));  // open: cout
  Adder #(.width(32)) adder_6 (.a(adder_5_out), .b(shifter_6_out), .out(adder_6_out), .cin(1'b0));  // open: cout
  Adder #(.width(32)) adder_7 (.a(adder_6_out), .b(shifter_7_out), .out(out_3), .cin(1'b0), .cout(adder_7_cout));
  Adder #(.width(4)) adder_8 (
    .a(4'b0000), .b(\四位乘法器_8_out_3 [7:4]), .out(adder_8_out), .cin(adder_7_cout));  // open: cout
  assign out_4 = {{28{1'b0}}, adder_8_out};  // Bit_Extender bit_extender_9
endmodule

module \_32X32乘法器  (
  input  [31:0] in_1,
  input  [31:0] in_2,
  output [31:0] out_3,
  output [31:0] out_4
);

  wire adder_8_cout, adder_9_cout, adder_10_cout, adder_11_cout, adder_12_cout, adder_13_cout, adder_14_cout;
  wire [31:0] adder_1_out, adder_2_out, adder_3_out, adder_4_out, adder_5_out, adder_6_out, adder_7_out,
       adder_8_out, adder_9_out, adder_10_out, adder_11_out, adder_12_out, adder_13_out, adder_15_out,
       adder_16_out, adder_17_out, adder_18_out, adder_19_out, adder_20_out, adder_21_out,
       bit_extender_1_out, bit_extender_2_out, bit_extender_3_out, bit_extender_4_out, bit_extender_5_out,
       bit_extender_6_out, bit_extender_7_out, \n32x4乘法器_1_out_3 , \n32x4乘法器_1_out_4 , \n32x4乘法器_2_out_3 ,
       \n32x4乘法器_2_out_4 , \n32x4乘法器_3_out_3 , \n32x4乘法器_3_out_4 , \n32x4乘法器_4_out_3 , \n32x4乘法器_4_out_4 ,
       \n32x4乘法器_5_out_3 , \n32x4乘法器_5_out_4 , \n32x4乘法器_6_out_3 , \n32x4乘法器_6_out_4 , \n32x4乘法器_7_out_3 ,
       \n32x4乘法器_7_out_4 , \n32x4乘法器_8_out_3 , \n32x4乘法器_8_out_4 , shifter_1_out, shifter_2_out,
       shifter_3_out, shifter_4_out, shifter_5_out, shifter_6_out, shifter_7_out, shifter_8_out,
       shifter_9_out, shifter_10_out, shifter_11_out, shifter_12_out, shifter_13_out, shifter_14_out;

  \_32X4乘法器  \u_32x4乘法器_1  (.in_1(in_1[3:0]), .in_2(in_2), .out_3(\n32x4乘法器_1_out_3 ), .out_4(\n32x4乘法器_1_out_4 ));
  \_32X4乘法器  \u_32x4乘法器_2  (.in_1(in_1[7:4]), .in_2(in_2), .out_3(\n32x4乘法器_2_out_3 ), .out_4(\n32x4乘法器_2_out_4 ));
  \_32X4乘法器  \u_32x4乘法器_3  (.in_1(in_1[11:8]), .in_2(in_2), .out_3(\n32x4乘法器_3_out_3 ), .out_4(\n32x4乘法器_3_out_4 ));
  \_32X4乘法器  \u_32x4乘法器_4  (.in_1(in_1[15:12]), .in_2(in_2), .out_3(\n32x4乘法器_4_out_3 ), .out_4(\n32x4乘法器_4_out_4 ));
  \_32X4乘法器  \u_32x4乘法器_5  (.in_1(in_1[19:16]), .in_2(in_2), .out_3(\n32x4乘法器_5_out_3 ), .out_4(\n32x4乘法器_5_out_4 ));
  \_32X4乘法器  \u_32x4乘法器_6  (.in_1(in_1[23:20]), .in_2(in_2), .out_3(\n32x4乘法器_6_out_3 ), .out_4(\n32x4乘法器_6_out_4 ));
  \_32X4乘法器  \u_32x4乘法器_7  (.in_1(in_1[27:24]), .in_2(in_2), .out_3(\n32x4乘法器_7_out_3 ), .out_4(\n32x4乘法器_7_out_4 ));
  \_32X4乘法器  \u_32x4乘法器_8  (.in_1(in_1[31:28]), .in_2(in_2), .out_3(\n32x4乘法器_8_out_3 ), .out_4(\n32x4乘法器_8_out_4 ));
  Shifter #(.width(32), .shift("ll")) shifter_1 (.in(\n32x4乘法器_2_out_3 ), .\dist (5'b00100), .out(shifter_1_out));
  Shifter #(.width(32), .shift("ll")) shifter_2 (.in(\n32x4乘法器_2_out_4 ), .\dist (5'b00100), .out(shifter_2_out));
  Shifter #(.width(32), .shift("ll")) shifter_3 (.in(\n32x4乘法器_3_out_3 ), .\dist (5'b01000), .out(shifter_3_out));
  Shifter #(.width(32), .shift("ll")) shifter_4 (.in(\n32x4乘法器_3_out_4 ), .\dist (5'b01000), .out(shifter_4_out));
  Shifter #(.width(32), .shift("ll")) shifter_5 (.in(\n32x4乘法器_4_out_3 ), .\dist (5'b01100), .out(shifter_5_out));
  Shifter #(.width(32), .shift("ll")) shifter_6 (.in(\n32x4乘法器_4_out_4 ), .\dist (5'b01100), .out(shifter_6_out));
  Shifter #(.width(32), .shift("ll")) shifter_7 (.in(\n32x4乘法器_5_out_3 ), .\dist (5'b10000), .out(shifter_7_out));
  Shifter #(.width(32), .shift("ll")) shifter_8 (.in(\n32x4乘法器_5_out_4 ), .\dist (5'b10000), .out(shifter_8_out));
  Shifter #(.width(32), .shift("ll")) shifter_9 (.in(\n32x4乘法器_6_out_3 ), .\dist (5'b10100), .out(shifter_9_out));
  Shifter #(.width(32), .shift("ll")) shifter_10 (.in(\n32x4乘法器_6_out_4 ), .\dist (5'b10100), .out(shifter_10_out));
  Shifter #(.width(32), .shift("ll")) shifter_11 (.in(\n32x4乘法器_7_out_3 ), .\dist (5'b11000), .out(shifter_11_out));
  Shifter #(.width(32), .shift("ll")) shifter_12 (.in(\n32x4乘法器_7_out_4 ), .\dist (5'b11000), .out(shifter_12_out));
  Shifter #(.width(32), .shift("ll")) shifter_13 (.in(\n32x4乘法器_8_out_3 ), .\dist (5'b11100), .out(shifter_13_out));
  Shifter #(.width(32), .shift("ll")) shifter_14 (.in(\n32x4乘法器_8_out_4 ), .\dist (5'b11100), .out(shifter_14_out));
  assign bit_extender_1_out = {{28{1'b0}}, \n32x4乘法器_2_out_3 [31:28]};  // Bit_Extender bit_extender_1
  assign bit_extender_2_out = {{24{1'b0}}, \n32x4乘法器_3_out_3 [31:24]};  // Bit_Extender bit_extender_2
  assign bit_extender_3_out = {{20{1'b0}}, \n32x4乘法器_4_out_3 [31:20]};  // Bit_Extender bit_extender_3
  assign bit_extender_4_out = {{16{1'b0}}, \n32x4乘法器_5_out_3 [31:16]};  // Bit_Extender bit_extender_4
  assign bit_extender_5_out = {{12{1'b0}}, \n32x4乘法器_6_out_3 [31:12]};  // Bit_Extender bit_extender_5
  assign bit_extender_6_out = {{8{1'b0}}, \n32x4乘法器_7_out_3 [31:8]};  // Bit_Extender bit_extender_6
  assign bit_extender_7_out = {{4{1'b0}}, \n32x4乘法器_8_out_3 [31:4]};  // Bit_Extender bit_extender_7
  Adder #(.width(32)) adder_1 (.a(bit_extender_1_out), .b(shifter_2_out), .out(adder_1_out));  // open: cin, cout
  Adder #(.width(32)) adder_2 (.a(bit_extender_2_out), .b(shifter_4_out), .out(adder_2_out));  // open: cin, cout
  Adder #(.width(32)) adder_3 (.a(bit_extender_3_out), .b(shifter_6_out), .out(adder_3_out));  // open: cin, cout
  Adder #(.width(32)) adder_4 (.a(bit_extender_4_out), .b(shifter_8_out), .out(adder_4_out));  // open: cin, cout
  Adder #(.width(32)) adder_5 (.a(bit_extender_5_out), .b(shifter_10_out), .out(adder_5_out));  // open: cin, cout
  Adder #(.width(32)) adder_6 (.a(bit_extender_6_out), .b(shifter_12_out), .out(adder_6_out));  // open: cin, cout
  Adder #(.width(32)) adder_7 (.a(bit_extender_7_out), .b(shifter_14_out), .out(adder_7_out));  // open: cin, cout
  Adder #(.width(32)) adder_8 (
    .a(\n32x4乘法器_1_out_3 ), .b(shifter_1_out), .out(adder_8_out), .cout(adder_8_cout));  // open: cin
  Adder #(.width(32)) adder_9 (
    .a(adder_8_out), .b(shifter_3_out), .out(adder_9_out), .cout(adder_9_cout));  // open: cin
  Adder #(.width(32)) adder_10 (
    .a(adder_9_out), .b(shifter_5_out), .out(adder_10_out), .cout(adder_10_cout));  // open: cin
  Adder #(.width(32)) adder_11 (
    .a(adder_10_out), .b(shifter_7_out), .out(adder_11_out), .cout(adder_11_cout));  // open: cin
  Adder #(.width(32)) adder_12 (
    .a(adder_11_out), .b(shifter_9_out), .out(adder_12_out), .cout(adder_12_cout));  // open: cin
  Adder #(.width(32)) adder_13 (
    .a(adder_12_out), .b(shifter_11_out), .out(adder_13_out), .cout(adder_13_cout));  // open: cin
  Adder #(.width(32)) adder_14 (.a(adder_13_out), .b(shifter_13_out), .out(out_3), .cout(adder_14_cout));  // open: cin
  Adder #(.width(32)) adder_15 (
    .a({32{1'b0}}), .b(\n32x4乘法器_1_out_4 ), .out(adder_15_out), .cin(adder_14_cout));  // open: cout
  Adder #(.width(32)) adder_16 (
    .a(adder_15_out), .b(adder_1_out), .out(adder_16_out), .cin(adder_8_cout));  // open: cout
  Adder #(.width(32)) adder_17 (
    .a(adder_16_out), .b(adder_2_out), .out(adder_17_out), .cin(adder_9_cout));  // open: cout
  Adder #(.width(32)) adder_18 (
    .a(adder_17_out), .b(adder_3_out), .out(adder_18_out), .cin(adder_10_cout));  // open: cout
  Adder #(.width(32)) adder_19 (
    .a(adder_18_out), .b(adder_4_out), .out(adder_19_out), .cin(adder_11_cout));  // open: cout
  Adder #(.width(32)) adder_20 (
    .a(adder_19_out), .b(adder_5_out), .out(adder_20_out), .cin(adder_12_cout));  // open: cout
  Adder #(.width(32)) adder_21 (
    .a(adder_20_out), .b(adder_6_out), .out(adder_21_out), .cin(adder_13_cout));  // open: cout
  Adder #(.width(32)) adder_22 (.a(adder_21_out), .b(adder_7_out), .out(out_4));  // open: cin, cout
endmodule

module \_32X4乘法器测试电路  (
  input  [3:0] in_1,
  input  [31:0] in_2,
  output [31:0] out_3,
  output [31:0] out_4
);

  \_32X4乘法器  \u_32x4乘法器_1  (.in_1(in_1), .in_2(in_2), .out_3(out_3), .out_4(out_4));
endmodule

module \_32X32乘法器测试电路  (
  input  [31:0] in_1,
  input  [31:0] in_2,
  output [31:0] out_3,
  output [31:0] out_4,
  output [31:0] out_5,
  output [31:0] out_6
);

  Multiplier #(.width(32)) multiplier_1 (.a(in_1), .b(in_2), .out(out_5), .cout(out_6));  // open: cin
  \_32X32乘法器  \u_32x32乘法器_1  (.in_1(in_1), .in_2(in_2), .out_3(out_3), .out_4(out_4));
endmodule
