// Logisim project 实验4-CS1806-U201814655-杨雨鑫.circ as structural Verilog: 6 circuits, main circuit 四位除法器
module \四位除法器  (
  input  [3:0] in_1,
  input  [3:0] in_2,
  output [3:0] out_3,
  output [3:0] out_4
);

  wire comparator_1_eq, comparator_2_eq, nor_1_out;
  wire [3:0] \四位除法器模块_4_out_3 ;
  wire [7:0] bit_extender_1_out, \四位除法器模块_1_out_3 , \四位除法器模块_2_out_3 , \四位除法器模块_3_out_3 ;

  assign bit_extender_1_out = {{4{1'b0}}, in_1};  // Bit_Extender bit_extender_1
  Comparator #(.width(4), .mode("twosComplement")) comparator_1 (
    .a(4'b0000), .b(in_1), .eq(comparator_1_eq));  // open: gt, lt
  Comparator #(.width(4), .mode("twosComplement")) comparator_2 (
    .a(in_2), .b(4'b0000), .eq(comparator_2_eq));  // open: gt, lt
  \四位除法器模块  \u_四位除法器模块_1  (.in_1(bit_extender_1_out), .in_2(in_2), .out_3(\四位除法器模块_1_out_3 ));
  nor nor_1 (nor_1_out, comparator_1_eq, comparator_2_eq);
  \四位除法器模块  \u_四位除法器模块_2  (.in_1(\四位除法器模块_1_out_3 ), .in_2(in_2), .out_3(\四位除法器模块_2_out_3 ));
  \四位除法器模块  \u_四位除法器模块_3  (.in_1(\四位除法器模块_2_out_3 ), .in_2(in_2), .out_3(\四位除法器模块_3_out_3 ));
  \四位除法器模块  \u_四位除法器模块_4  (.in_1(\四位除法器模块_3_out_3 ), .in_2(in_2), .out_3({out_4, \四位除法器模块_4_out_3 }));
  Multiplexer #(.select(1), .width(4), .disabled("Z"), .enable("false")) multiplexer_1 (
    .in0(4'b0000), .in1(\四位除法器模块_4_out_3 ), .out(out_3), .sel(nor_1_out));
endmodule

module \四位除法器测试电路  (
  input  [3:0] in_1,
  input  [3:0] in_2,
  output [3:0] out_3,
  output [3:0] out_4,
  output [3:0] out_5,
  output [3:0] out_6
);

  Divider #(.width(4)) divider_1 (.a(in_1), .b(in_2), .out(out_5), .rem(out_6));  // open: upper
  \四位除法器  \u_四位除法器_1  (.in_1(in_1), .in_2(in_2), .out_3(out_3), .out_4(out_4));
endmodule

module \_32位除法器  (
  input  [31:0] in_1,
  input  [31:0] in_2,
  output [31:0] out_3,
  output [31:0] out_4
);

  wire comparator_1_eq, comparator_2_eq, or_1_out;
  wire [31:0] \n32位除法器模块_1_next_quot , \n32位除法器模块_1_next_rem , \n32位除法器模块_2_next_quot ,
       \n32位除法器模块_2_next_rem , \n32位除法器模块_3_next_quot , \n32位除法器模块_3_next_rem , \n32位除法器模块_4_next_quot ,
       \n32位除法器模块_4_next_rem , \n32位除法器模块_5_next_quot , \n32位除法器模块_5_next_rem , \n32位除法器模块_6_next_quot ,
       \n32位除法器模块_6_next_rem , \n32位除法器模块_7_next_quot , \n32位除法器模块_7_next_rem , \n32位除法器模块_8_next_quot ,
       \n32位除法器模块_8_next_rem , \n32位除法器模块_9_next_quot , \n32位除法器模块_9_next_rem , \n32位除法器模块_10_next_quot ,
       \n32位除法器模块_10_next_rem , \n32位除法器模块_11_next_quot , \n32位除法器模块_11_next_rem , \n32位除法器模块_12_next_quot ,
       \n32位除法器模块_12_next_rem , \n32位除法器模块_13_next_quot , \n32位除法器模块_13_next_rem , \n32位除法器模块_14_next_quot ,
       \n32位除法器模块_14_next_rem , \n32位除法器模块_15_next_quot , \n32位除法器模块_15_next_rem , \n32位除法器模块_16_next_quot ,
       \n32位除法器模块_16_next_rem , \n32位除法器模块_17_next_quot , \n32位除法器模块_17_next_rem , \n32位除法器模块_18_next_quot ,
       \n32位除法器模块_18_next_rem , \n32位除法器模块_19_next_quot , \n32位除法器模块_19_next_rem , \n32位除法器模块_20_next_quot ,
       \n32位除法器模块_20_next_rem , \n32位除法器模块_21_next_quot , \n32位除法器模块_21_next_rem , \n32位除法器模块_22_next_quot ,
       \n32位除法器模块_22_next_rem , \n32位除法器模块_23_next_quot , \n32位除法器模块_23_next_rem , \n32位除法器模块_24_next_quot ,
       \n32位除法器模块_24_next_rem , \n32位除法器模块_25_next_quot , \n32位除法器模块_25_next_rem , \n32位除法器模块_26_next_quot ,
       \n32位除法器模块_26_next_rem , \n32位除法器模块_27_next_quot , \n32位除法器模块_27_next_rem , \n32位除法器模块_28_next_quot ,
       \n32位除法器模块_28_next_rem , \n32位除法器模块_29_next_quot , \n32位除法器模块_29_next_rem , \n32位除法器模块_30_next_quot ,
       \n32位除法器模块_30_next_rem , \n32位除法器模块_31_next_quot , \n32位除法器模块_31_next_rem , \n32位除法器模块_32_next_quot ;

  \_32位除法器模块  \u_32位除法器模块_1  (
    .cur_rem({32{1'b0}}), .cur_quot(in_1), .d(in_2), .next_rem(\n32位除法器模块_1_next_rem ),
    .next_quot(\n32位除法器模块_1_next_quot ));
  \_32位除法器模块  \u_32位除法器模块_2  (
    .cur_rem(\n32位除法器模块_29_next_rem ), .cur_quot(\n32位除法器模块_29_next_quot ), .d(in_2),
    .next_rem(\n32位除法器模块_2_next_rem ), .next_quot(\n32位除法器模块_2_next_quot ));
  \_32位除法器模块  \u_32位除法器模块_3  (
    .cur_rem(\n32位除法器模块_30_next_rem ), .cur_quot(\n32位除法器模块_30_next_quot ), .d(in_2),
    .next_rem(\n32位除法器模块_3_next_rem ), .next_quot(\n32位除法器模块_3_next_quot ));
  \_32位除法器模块  \u_32位除法器模块_4  (
    .cur_rem(\n32位除法器模块_31_next_rem ), .cur_quot(\n32位除法器模块_31_next_quot ), .d(in_2),
    .next_rem(\n32位除法器模块_4_next_rem ), .next_quot(\n32位除法器模块_4_next_quot ));
  Comparator #(.width(32), .mode("twosComplement")) comparator_1 (
    .a(in_1), .b({32{1'b0}}), .eq(comparator_1_eq));  // open: gt, lt
  Comparator #(.width(32), .mode("twosComplement")) comparator_2 (
    .a({32{1'b0}}), .b(in_2), .eq(comparator_2_eq));  // open: gt, lt
  \_32位除法器模块  \u_32位除法器模块_5  (
    .cur_rem(\n32位除法器模块_1_next_rem ), .cur_quot(\n32位除法器模块_1_next_quot ), .d(in_2),
    .next_rem(\n32位除法器模块_5_next_rem ), .next_quot(\n32位除法器模块_5_next_quot ));
  \_32位除法器模块  \u_32位除法器模块_6  (
    .cur_rem(\n32位除法器模块_2_next_rem ), .cur_quot(\n32位除法器模块_2_next_quot ), .d(in_2),
    .next_rem(\n32位除法器模块_6_next_rem ), .next_quot(\n32位除法器模块_6_next_quot ));
  \_32位除法器模块  \u_32位除法器模块_7  (
    .cur_rem(\n32位除法器模块_3_next_rem ), .cur_quot(\n32位除法器模块_3_next_quot ), .d(in_2),
    .next_rem(\n32位除法器模块_7_next_rem ), .next_quot(\n32位除法器模块_7_next_quot ));
  \_32位除法器模块  \u_32位除法器模块_8  (
    .cur_rem(\n32位除法器模块_4_next_rem ), .cur_quot(\n32位除法器模块_4_next_quot ), .d(in_2),
    .next_rem(\n32位除法器模块_8_next_rem ), .next_quot(\n32位除法器模块_8_next_quot ));
  \_32位除法器模块  \u_32位除法器模块_9  (
    .cur_rem(\n32位除法器模块_5_next_rem ), .cur_quot(\n32位除法器模块_5_next_quot ), .d(in_2),
    .next_rem(\n32位除法器模块_9_next_rem ), .next_quot(\n32位除法器模块_9_next_quot ));
  \_32位除法器模块  \u_32位除法器模块_10  (
    .cur_rem(\n32位除法器模块_6_next_rem ), .cur_quot(\n32位除法器模块_6_next_quot ), .d(in_2),
    .next_rem(\n32位除法器模块_10_next_rem ), .next_quot(\n32位除法器模块_10_next_quot ));
  \_32位除法器模块  \u_32位除法器模块_11  (
    .cur_rem(\n32位除法器模块_7_next_rem ), .cur_quot(\n32位除法器模块_7_next_quot ), .d(in_2),
    .next_rem(\n32位除法器模块_11_next_rem ), .next_quot(\n32位除法器模块_11_next_quot ));
  \_32位除法器模块  \u_32位除法器模块_12  (
    .cur_rem(\n32位除法器模块_8_next_rem ), .cur_quot(\n32位除法器模块_8_next_quot ), .d(in_2),
    .next_rem(\n32位除法器模块_12_next_rem ), .next_quot(\n32位除法器模块_12_next_quot ));
  or or_1 (or_1_out, comparator_1_eq, comparator_2_eq);
  \_32位除法器模块  \u_32位除法器模块_13  (
    .cur_rem(\n32位除法器模块_9_next_rem ), .cur_quot(\n32位除法器模块_9_next_quot ), .d(in_2),
    .next_rem(\n32位除法器模块_13_next_rem ), .next_quot(\n32位除法器模块_13_next_quot ));
  \_32位除法器模块  \u_32位除法器模块_14  (
    .cur_rem(\n32位除法器模块_10_next_rem ), .cur_quot(\n32位除法器模块_10_next_quot ), .d(in_2),
    .next_rem(\n32位除法器模块_14_next_rem ), .next_quot(\n32位除法器模块_14_next_quot ));
  \_32位除法器模块  \u_32位除法器模块_15  (
    .cur_rem(\n32位除法器模块_11_next_rem ), .cur_quot(\n32位除法器模块_11_next_quot ), .d(in_2),
    .next_rem(\n32位除法器模块_15_next_rem ), .next_quot(\n32位除法器模块_15_next_quot ));
  \_32位除法器模块  \u_32位除法器模块_16  (
    .cur_rem(\n32位除法器模块_12_next_rem ), .cur_quot(\n32位除法器模块_12_next_quot ), .d(in_2),
    .next_rem(\n32位除法器模块_16_next_rem ), .next_quot(\n32位除法器模块_16_next_quot ));
  \_32位除法器模块  \u_32位除法器模块_17  (
    .cur_rem(\n32位除法器模块_13_next_rem ), .cur_quot(\n32位除法器模块_13_next_quot ), .d(in_2),
    .next_rem(\n32位除法器模块_17_next_rem ), .next_quot(\n32位除法器模块_17_next_quot ));
  \_32位除法器模块  \u_32位除法器模块_18  (
    .cur_rem(\n32位除法器模块_14_next_rem ), .cur_quot(\n32位除法器模块_14_next_quot ), .d(in_2),
    .next_rem(\n32位除法器模块_18_next_rem ), .next_quot(\n32位除法器模块_18_next_quot ));
  \_32位除法器模块  \u_32位除法器模块_19  (
    .cur_rem(\n32位除法器模块_15_next_rem ), .cur_quot(\n32位除法器模块_15_next_quot ), .d(in_2),
    .next_rem(\n32位除法器模块_19_next_rem ), .next_quot(\n32位除法器模块_19_next_quot ));
  \_32位除法器模块  \u_32位除法器模块_20  (
    .cur_rem(\n32位除法器模块_16_next_rem ), .cur_quot(\n32位除法器模块_16_next_quot ), .d(in_2),
    .next_rem(\n32位除法器模块_20_next_rem ), .next_quot(\n32位除法器模块_20_next_quot ));
  \_32位除法器模块  \u_32位除法器模块_21  (
    .cur_rem(\n32位除法器模块_17_next_rem ), .cur_quot(\n32位除法器模块_17_next_quot ), .d(in_2),
    .next_rem(\n32位除法器模块_21_next_rem ), .next_quot(\n32位除法器模块_21_next_quot ));
  \_32位除法器模块  \u_32位除法器模块_22  (
    .cur_rem(\n32位除法器模块_18_next_rem ), .cur_quot(\n32位除法器模块_18_next_quot ), .d(in_2),
    .next_rem(\n32位除法器模块_22_next_rem ), .next_quot(\n32位除法器模块_22_next_quot ));
  \_32位除法器模块  \u_32位除法器模块_23  (
    .cur_rem(\n32位除法器模块_19_next_rem ), .cur_quot(\n32位除法器模块_19_next_quot ), .d(in_2),
    .next_rem(\n32位除法器模块_23_next_rem ), .next_quot(\n32位除法器模块_23_next_quot ));
  \_32位除法器模块  \u_32位除法器模块_24  (
    .cur_rem(\n32位除法器模块_20_next_rem ), .cur_quot(\n32位除法器模块_20_next_quot ), .d(in_2),
    .next_rem(\n32位除法器模块_24_next_rem ), .next_quot(\n32位除法器模块_24_next_quot ));
  \_32位除法器模块  \u_32位除法器模块_25  (
    .cur_rem(\n32位除法器模块_21_next_rem ), .cur_quot(\n32位除法器模块_21_next_quot ), .d(in_2),
    .next_rem(\n32位除法器模块_25_next_rem ), .next_quot(\n32位除法器模块_25_next_quot ));
  \_32位除法器模块  \u_32位除法器模块_26  (
    .cur_rem(\n32位除法器模块_22_next_rem ), .cur_quot(\n32位除法器模块_22_next_quot ), .d(in_2),
    .next_rem(\n32位除法器模块_26_next_rem ), .next_quot(\n32位除法器模块_26_next_quot ));
  \_32位除法器模块  \u_32位除法器模块_27  (
    .cur_rem(\n32位除法器模块_23_next_rem ), .cur_quot(\n32位除法器模块_23_next_quot ), .d(in_2),
    .next_rem(\n32位除法器模块_27_next_rem ), .next_quot(\n32位除法器模块_27_next_quot ));
  \_32位除法器模块  \u_32位除法器模块_28  (
    .cur_rem(\n32位除法器模块_24_next_rem ), .cur_quot(\n32位除法器模块_24_next_quot ), .d(in_2),
    .next_rem(\n32位除法器模块_28_next_rem ), .next_quot(\n32位除法器模块_28_next_quot ));
  \_32位除法器模块  \u_32位除法器模块_29  (
    .cur_rem(\n32位除法器模块_25_next_rem ), .cur_quot(\n32位除法器模块_25_next_quot ), .d(in_2),
    .next_rem(\n32位除法器模块_29_next_rem ), .next_quot(\n32位除法器模块_29_next_quot ));
  \_32位除法器模块  \u_32位除法器模块_30  (
    .cur_rem(\n32位除法器模块_26_next_rem ), .cur_quot(\n32位除法器模块_26_next_quot ), .d(in_2),
    .next_rem(\n32位除法器模块_30_next_rem ), .next_quot(\n32位除法器模块_30_next_quot ));
  \_32位除法器模块  \u_32位除法器模块_31  (
    .cur_rem(\n32位除法器模块_27_next_rem ), .cur_quot(\n32位除法器模块_27_next_quot ), .d(in_2),
    .next_rem(\n32位除法器模块_31_next_rem ), .next_quot(\n32位除法器模块_31_next_quot ));
  \_32位除法器模块  \u_32位除法器模块_32  (
    .cur_rem(\n32位除法器模块_28_next_rem ), .cur_quot(\n32位除法器模块_28_next_quot ), .d(in_2), .next_rem(out_3),
    .next_quot(\n32位除法器模块_32_next_quot ));
  Multiplexer #(.select(1), .width(32), .disabled("Z"), .enable("false")) multiplexer_1 (
    .in0(\n32位除法器模块_32_next_quot ), .in1({32{1'b0}}), .out(out_4), .sel(or_1_out));
endmodule

module \_32位除法器测试电路  (
  input  [31:0] in_1,
  input  [31:0] in_2,
  output [31:0] out_3,
  output [31:0] out_4,
  output [31:0] out_5,
  output [31:0] out_6
);

  Divider #(.width(32)) divider_1 (.a(in_1), .b(in_2), .out(out_5), .rem(out_6));  // open: upper
  \_32位除法器  \u_32位除法器_1  (.in_1(in_1), .in_2(in_2), .out_3(out_4), .out_4(out_3));
endmodule

module \四位除法器模块  (
  input  [7:0] in_1,
  input  [3:0] in_2,
  output [7:0] out_3
);

  wire comparator_1_eq, comparator_1_gt, or_1_out;
  wire [3:0] multiplexer_1_out, subtractor_1_out;
  wire [7:0] shifter_1_out;

  Shifter #(.width(8), .shift("ll")) shifter_1 (.in(in_1), .\dist (3'b001), .out(shifter_1_out));
  Subtractor #(.width(4)) subtractor_1 (.a(shifter_1_out[7:4]), .b(in_2), .out(subtractor_1_out));  // open: bin, bout
  Comparator #(.width(4), .mode("unsigned")) comparator_1 (
    .a(shifter_1_out[7:4]), .b(in_2), .gt(comparator_1_gt), .eq(comparator_1_eq));  // open: lt
  or or_1 (or_1_out, comparator_1_gt, comparator_1_eq);
  Multiplexer #(.select(1), .width(4), .disabled("Z"), .enable("false")) multiplexer_1 (
    .in0(shifter_1_out[7:4]), .in1(subtractor_1_out), .out(multiplexer_1_out), .sel(or_1_out));
  Adder #(.width(8)) adder_1 (
    .a({8{1'b0}}), .b({multiplexer_1_out, shifter_1_out[3:0]}), .out(out_3), .cin(or_1_out));  // open: cout
endmodule

module \_32位除法器模块  (
  input  [31:0] cur_rem,
  input  [31:0] cur_quot,
  input  [31:0] d,
  output [31:0] next_rem,
  output [31:0] next_quot
);

  wire comparator_1_gt;
  wire [31:0] or_1_out, or_2_out, shifter_1_out, shifter_2_out, shifter_3_out, subtractor_1_out;

  Shifter #(.width(32), .shift("ll")) shifter_1 (.in(cur_rem), .\dist (5'b00001), .out(shifter_1_out));
  Shifter #(.width(32), .shift("lr")) shifter_2 (.in(cur_quot), .\dist ({5{1'b1}}), .out(shifter_2_out));
  Shifter #(.width(32), .shift("ll")) shifter_3 (.in(cur_quot), .\dist (5'b00001), .out(shifter_3_out));
  assign or_1_out = 32'h1 | shifter_3_out;  // OR_Gate or_1, 32 bits wide
  assign or_2_out = shifter_1_out | shifter_2_out;  // OR_Gate or_2, 32 bits wide
  Comparator #(.width(32), .mode("unsigned")) comparator_1 (.a(d), .b(or_2_out), .gt(comparator_1_gt));  // open: eq, lt
  Subtractor #(.width(32)) subtractor_1 (.a(or_2_out), .b(d), .out(subtractor_1_out));  // open: bin, bout
  Multiplexer #(.select(1), .width(32), .disabled("Z"), .enable("false")) multiplexer_1 (
    .in0(or_1_out), .in1(shifter_3_out), .out(next_quot), .sel(comparator_1_gt));
  Multiplexer #(.select(1), .width(32), .disabled("Z"), .enable("false")) multiplexer_2 (
    .in0(subtractor_1_out), .in1(or_2_out), .out(next_rem), .sel(comparator_1_gt));
endmodule
