// Logisim project 实验5-CS1806-U201814655-杨雨鑫.circ as structural Verilog
module \四位二进制可逆计数器  (
  input  CLR,
  input  CPu,
  input  CPd,
  input  A,
  input  B,
  input  C,
  input  D,
  input  \LD非 ,
  output Q0,
  output Q1,
  output Q2,
  output Q3
);

  wire A_q, A_qn, and_1_out, and_2_out, and_3_out, and_4_out, and_5_out, and_6_out, and_7_out, and_8_out,
       and_9_out, and_10_out, B_q, B_qn, C0_out, C1_out, C2_out, C3_out, C_q, C_qn, d_ff_1_q, d_ff_1_qn,
       not_1_out, or_1_out, or_2_out, or_3_out, or_4_out, or_5_out;

  and and_1 (and_1_out, CPu, A_q);
  and and_2 (and_2_out, CPd, A_qn);
  and and_3 (and_3_out, CPu, B_q, A_q);
  and and_4 (and_4_out, A_qn, CPd, B_qn);
  and and_5 (and_5_out, A_q, B_q, CPu, C_q);
  and and_6 (and_6_out, A_qn, B_qn, CPd, C_qn);
  not not_1 (not_1_out, \LD非 );
  or C0 (C0_out, CPu, CPd);
  or C1 (C1_out, and_1_out, and_2_out);
  or C2 (C2_out, and_3_out, and_4_out);
  or C3 (C3_out, and_5_out, and_6_out);
  and and_7 (and_7_out, A, not_1_out);
  and and_8 (and_8_out, B, not_1_out);
  and and_9 (and_9_out, C, not_1_out);
  or or_1 (or_1_out, CLR, not_1_out);
  and and_10 (and_10_out, D, not_1_out);
  or or_2 (or_2_out, C0_out, and_7_out);
  or or_3 (or_3_out, C1_out, and_8_out);
  or or_4 (or_4_out, C2_out, and_9_out);
  or or_5 (or_5_out, C3_out, and_10_out);
  D_Flip_Flop #(.trigger("falling"), .Pre_Clr_Positions("ABOVE_BELOW"), .NegatePresetClear("false"), .enable("false"), .NewFFLayout("true")) u_A (
    .clk(or_2_out), .D(A_qn), .Q(A_q), .Qn(A_qn), .reset(or_1_out));  // open: preset
  D_Flip_Flop #(.trigger("falling"), .Pre_Clr_Positions("ABOVE_BELOW"), .NegatePresetClear("false"), .enable("false"), .NewFFLayout("true")) u_B (
    .clk(or_3_out), .D(B_qn), .Q(B_q), .Qn(B_qn), .reset(or_1_out));  // open: preset
  D_Flip_Flop #(.trigger("falling"), .Pre_Clr_Positions("ABOVE_BELOW"), .NegatePresetClear("false"), .enable("false"), .NewFFLayout("true")) u_C (
    .clk(or_4_out), .D(C_qn), .Q(C_q), .Qn(C_qn), .reset(or_1_out));  // open: preset
  D_Flip_Flop #(.trigger("falling"), .Pre_Clr_Positions("ABOVE_BELOW"), .NegatePresetClear("false"), .enable("false"), .NewFFLayout("true")) d_ff_1 (
    .clk(or_5_out), .D(d_ff_1_qn), .Q(d_ff_1_q), .Qn(d_ff_1_qn), .reset(or_1_out));  // open: preset
  or or_6 (Q0, A_q, and_7_out);
  or or_7 (Q1, B_q, and_8_out);
  or or_8 (Q2, C_q, and_9_out);
  or or_9 (Q3, d_ff_1_q, and_10_out);
endmodule

module \六十进制计数器  (
  input  CLR,
  input  CPU,
  input  CPD,
  input  ADJ,
  output out_5,
  output out_6,
  output out_7,
  output out_8,
  output out_9,
  output out_10,
  output out_11,
  output out_12,
  output out_13
);

  wire and_1_out, and_2_out, and_3_out, and_4_out, and_6_out, and_7_out, multiplexer_1_out, nand_1_out,
       not_1_out, not_2_out, not_3_out, not_4_out, not_5_out, not_6_out, not_7_out, not_8_out, not_9_out,
       not_10_out, not_11_out, not_12_out, not_13_out, not_14_out, or_1_out, or_2_out;

  and and_1 (and_1_out, CPD, ADJ);
  and and_2 (and_2_out, and_4_out, not_1_out);
  not not_1 (not_1_out, nand_1_out);
  or or_1 (or_1_out, CLR, out_13);
  or or_2 (or_2_out, and_6_out, CLR);
  Multiplexer #(.select(1), .width(1), .disabled("Z"), .enable("false")) multiplexer_1 (
    .in0(and_1_out), .in1(1'b0), .out(multiplexer_1_out), .sel(and_2_out));
  and and_3 (and_3_out, and_4_out, nand_1_out, and_1_out);
  not not_2 (not_2_out, and_7_out);
  \四位二进制可逆计数器  \u_四位二进制可逆计数器_1  (
    .CLR(or_2_out), .CPu(CPU), .Q0(out_5), .CPd(multiplexer_1_out), .Q1(out_6), .Q2(out_7), .Q3(out_8),
    .A(1'b1), .B(1'b0), .C(1'b0), .D(1'b1), .\LD非 (not_2_out));
  not not_3 (not_3_out, out_8);
  \四位二进制可逆计数器  \u_四位二进制可逆计数器_2  (
    .CLR(or_1_out), .CPu(and_6_out), .Q0(out_9), .CPd(and_3_out), .Q1(out_10), .Q2(out_11), .Q3(out_12),
    .A(1'b0), .B(1'b0), .C(1'b0), .D(1'b0), .\LD非 (1'b1));
  not not_4 (not_4_out, out_5);
  not not_5 (not_5_out, out_7);
  not not_6 (not_6_out, out_6);
  and and_4 (and_4_out, not_3_out, not_5_out, not_6_out, not_4_out);
  not not_7 (not_7_out, out_9);
  and and_5 (out_13, not_7_out, out_10, out_11, not_10_out);
  not not_8 (not_8_out, out_5);
  not not_9 (not_9_out, out_7);
  and and_6 (and_6_out, out_8, not_9_out, not_8_out, out_6);
  not not_10 (not_10_out, out_12);
  not not_11 (not_11_out, out_11);
  not not_12 (not_12_out, out_12);
  not not_13 (not_13_out, out_9);
  not not_14 (not_14_out, out_10);
  nand nand_1 (nand_1_out, not_12_out, not_11_out, not_14_out, not_13_out);
  and and_7 (and_7_out, out_8, out_7, out_6, out_5);
endmodule

module \六十进制计数器测试电路  (
  input  in_1,
  input  in_2,
  input  in_3,
  output out_4,
  output out_5,
  output out_6,
  output out_7,
  output out_8,
  output out_9,
  output out_10,
  output out_11,
  output out_12
);

  wire clock_1_out;

  Clock #(.highDuration(1), .lowDuration(1)) clock_1 (.out(clock_1_out));
  Hex_Digit_Display hex_digit_display_1 (.value({out_4, out_5, out_6, out_7}));  // open: dp
  Hex_Digit_Display hex_digit_display_2 (.value({out_8, out_9, out_10, out_11}));  // open: dp
  \六十进制计数器  \u_六十进制计数器_1  (
    .CLR(in_3), .CPU(clock_1_out), .CPD(in_2), .ADJ(in_1), .out_5(out_11), .out_6(out_10), .out_7(out_9),
    .out_8(out_8), .out_9(out_7), .out_10(out_6), .out_11(out_5), .out_12(out_4), .out_13(out_12));
endmodule

module \十二进制计数器或二十四进制的计数器电路  (
  input  CLR,
  input  CPU,
  input  CPD,
  input  ADJ,
  input  in_5,
  output out_6,
  output out_7,
  output out_8,
  output out_9,
  output out_10,
  output out_11,
  output out_12,
  output out_13,
  output out_14
);

  wire and_1_out, and_2_out, and_3_out, and_4_out, and_5_out, and_6_out, and_7_out, and_8_out, and_9_out,
       and_10_out, and_11_out, and_12_out, and_13_out, multiplexer_1_out, \n24转12_1_cout , nand_1_out,
       not_1_out, not_2_out, not_3_out, not_4_out, not_5_out, not_6_out, not_7_out, not_8_out, not_9_out,
       not_10_out, not_11_out, not_12_out, not_13_out, not_14_out, not_15_out, not_16_out, not_17_out,
       not_18_out, not_19_out, not_20_out, not_21_out, not_22_out, not_23_out, or_1_out, or_2_out;
  wire [3:0] \n24转12_1_o4 , \n24转12_1_o8 , \四位二进制可逆计数器_1_q0 , \四位二进制可逆计数器_2_q0 ;

  and and_1 (and_1_out, CPD, ADJ);
  and and_2 (and_2_out, and_5_out, not_1_out);
  not not_1 (not_1_out, nand_1_out);
  or or_1 (or_1_out, CLR, and_4_out);
  or or_2 (or_2_out, and_7_out, and_4_out, CLR);
  Multiplexer #(.select(1), .width(1), .disabled("Z"), .enable("false")) multiplexer_1 (
    .in0(and_1_out), .in1(1'b0), .out(multiplexer_1_out), .sel(and_2_out));
  and and_3 (and_3_out, and_5_out, nand_1_out, and_1_out);
  and and_4 (and_4_out, and_6_out, and_9_out);
  not not_2 (not_2_out, and_8_out);
  \四位二进制可逆计数器  \u_四位二进制可逆计数器_1  (
    .CLR(or_2_out), .CPu(CPU), .Q0(\四位二进制可逆计数器_1_q0 [0]), .CPd(multiplexer_1_out), .Q1(\四位二进制可逆计数器_1_q0 [1]),
    .Q2(\四位二进制可逆计数器_1_q0 [2]), .Q3(\四位二进制可逆计数器_1_q0 [3]), .A(1'b1), .B(1'b0), .C(1'b0), .D(1'b1),
    .\LD非 (not_2_out));
  not not_3 (not_3_out, \四位二进制可逆计数器_1_q0 [3]);
  \四位二进制可逆计数器  \u_四位二进制可逆计数器_2  (
    .CLR(or_1_out), .CPu(and_7_out), .Q0(\四位二进制可逆计数器_2_q0 [0]), .CPd(and_3_out), .Q1(\四位二进制可逆计数器_2_q0 [1]),
    .Q2(\四位二进制可逆计数器_2_q0 [2]), .Q3(\四位二进制可逆计数器_2_q0 [3]), .A(1'b0), .B(1'b0), .C(1'b0), .D(1'b0), .\LD非 (1'b1));
  not not_4 (not_4_out, \四位二进制可逆计数器_1_q0 [2]);
  not not_5 (not_5_out, \四位二进制可逆计数器_1_q0 [1]);
  not not_6 (not_6_out, \四位二进制可逆计数器_1_q0 [0]);
  and and_5 (and_5_out, not_3_out, not_4_out, not_5_out, not_6_out);
  not not_7 (not_7_out, \四位二进制可逆计数器_2_q0 [2]);
  not not_8 (not_8_out, \四位二进制可逆计数器_2_q0 [0]);
  and and_6 (and_6_out, not_8_out, \四位二进制可逆计数器_2_q0 [1], not_7_out, not_11_out);
  not not_9 (not_9_out, \四位二进制可逆计数器_1_q0 [0]);
  not not_10 (not_10_out, \四位二进制可逆计数器_1_q0 [2]);
  and and_7 (and_7_out, \四位二进制可逆计数器_1_q0 [3], not_10_out, not_9_out, \四位二进制可逆计数器_1_q0 [1]);
  not not_11 (not_11_out, \四位二进制可逆计数器_2_q0 [3]);
  not not_12 (not_12_out, \四位二进制可逆计数器_2_q0 [3]);
  not not_13 (not_13_out, \四位二进制可逆计数器_2_q0 [2]);
  not not_14 (not_14_out, \四位二进制可逆计数器_2_q0 [0]);
  not not_15 (not_15_out, \四位二进制可逆计数器_2_q0 [1]);
  nand nand_1 (nand_1_out, not_12_out, not_13_out, not_15_out, not_14_out);
  and and_8 (and_8_out, \四位二进制可逆计数器_1_q0 [3], \四位二进制可逆计数器_1_q0 [2], \四位二进制可逆计数器_1_q0 [1], \四位二进制可逆计数器_1_q0 [0]);
  not not_16 (not_16_out, \四位二进制可逆计数器_1_q0 [0]);
  not not_17 (not_17_out, \四位二进制可逆计数器_1_q0 [1]);
  not not_18 (not_18_out, \四位二进制可逆计数器_1_q0 [3]);
  and and_9 (and_9_out, not_16_out, not_17_out, \四位二进制可逆计数器_1_q0 [2], not_18_out);
  Multiplexer #(.select(1), .width(1), .disabled("Z"), .enable("false")) multiplexer_2 (
    .in0(and_10_out), .in1(and_11_out), .out(out_6), .sel(in_5));
  and and_10 (and_10_out, and_12_out, \n24转12_1_cout );
  \_24转12  \u_24转12_1  (
    .q1(\四位二进制可逆计数器_2_q0 [3]), .o1(\n24转12_1_o4 [3]), .q2(\四位二进制可逆计数器_2_q0 [2]), .o2(\n24转12_1_o4 [2]),
    .q3(\四位二进制可逆计数器_2_q0 [1]), .o3(\n24转12_1_o4 [1]), .q4(\四位二进制可逆计数器_2_q0 [0]), .q5(\四位二进制可逆计数器_1_q0 [3]),
    .q6(\四位二进制可逆计数器_1_q0 [2]), .q7(\四位二进制可逆计数器_1_q0 [1]), .q8(\四位二进制可逆计数器_1_q0 [0]), .o4(\n24转12_1_o4 [0]),
    .o5(\n24转12_1_o8 [3]), .o6(\n24转12_1_o8 [2]), .o7(\n24转12_1_o8 [1]), .o8(\n24转12_1_o8 [0]),
    .cout(\n24转12_1_cout ));
  and and_11 (and_11_out, CPU, and_13_out);
  Multiplexer #(.select(1), .width(4), .disabled("Z"), .enable("false")) multiplexer_3 (
    .in0(\n24转12_1_o8 ), .in1(\四位二进制可逆计数器_1_q0 ), .out({out_10, out_9, out_8, out_7}), .sel(in_5));
  Multiplexer #(.select(1), .width(4), .disabled("Z"), .enable("false")) multiplexer_4 (
    .in0(\n24转12_1_o4 ), .in1(\四位二进制可逆计数器_2_q0 ), .out({out_14, out_13, out_12, out_11}), .sel(in_5));
  and and_12 (and_12_out, not_20_out, out_8, not_21_out, not_19_out, out_11);
  not not_19 (not_19_out, out_10);
  not not_20 (not_20_out, out_7);
  not not_21 (not_21_out, out_9);
  and and_13 (and_13_out, out_7, out_8, not_22_out, not_23_out, out_12);
  not not_22 (not_22_out, out_9);
  not not_23 (not_23_out, out_10);
endmodule

module \十二进制计数器或二十四进制的计数器测试电路  (
  input  in_1,
  input  in_2,
  input  in_3,
  input  in_4,
  input  in_5,
  input  in_6,
  input  in_7,
  output out_8,
  output out_9,
  output out_10,
  output out_11,
  output out_12,
  output out_13,
  output out_14,
  output out_15,
  output out_16,
  output out_17,
  output out_18,
  output out_19
);

  wire \十二进制计数器或二十四进制的计数器电路_1_out_6 ;

  Hex_Digit_Display hex_digit_display_1 (.value({out_8, out_9, out_10, out_11}));  // open: dp
  Hex_Digit_Display hex_digit_display_2 (.value({out_12, out_13, out_14, out_15}));  // open: dp
  \十二进制计数器或二十四进制的计数器电路  \u_十二进制计数器或二十四进制的计数器电路_1  (
    .CLR(in_5), .CPU(in_1), .CPD(in_4), .ADJ(in_2), .out_7(out_15), .out_8(out_14), .out_9(out_13),
    .out_10(out_12), .out_11(out_11), .out_12(out_10), .out_13(out_9), .out_14(out_8), .in_5(in_3),
    .out_6(\十二进制计数器或二十四进制的计数器电路_1_out_6 ));
  \四位二进制可逆计数器  \u_四位二进制可逆计数器_1  (
    .CLR(in_6), .CPu(\十二进制计数器或二十四进制的计数器电路_1_out_6 ), .Q0(out_16), .CPd(in_7), .Q1(out_17), .Q2(out_18),
    .Q3(out_19), .A(1'b0), .B(1'b0), .C(1'b0), .D(1'b0), .\LD非 (1'b1));
endmodule

module \上下午文字显示的电路  (
  input  TT,
  input  AM_FM,
  output [4:0] out_3,
  output [4:0] out_4,
  output [4:0] out_5,
  output [4:0] out_6
);

  wire [19:0] multiplexer_1_out, multiplexer_2_out;

  Multiplexer #(.select(1), .width(20), .disabled("Z"), .enable("false")) multiplexer_1 (
    .in0({20{1'b0}}), .in1(20'hfca1), .out(multiplexer_1_out), .sel(TT));
  Multiplexer #(.select(1), .width(20), .disabled("Z"), .enable("false")) multiplexer_2 (
    .in0({20{1'b0}}), .in1(20'h87e90), .out(multiplexer_2_out), .sel(TT));
  Multiplexer #(.select(1), .width(20), .disabled("Z"), .enable("false")) multiplexer_3 (
    .in0(multiplexer_1_out), .in1(multiplexer_2_out), .out({out_3, out_4, out_5, out_6}), .sel(AM_FM));
endmodule

module \上下午文字显示测试电路  (
  input  in_1,
  input  in_2
);

  wire [4:0] \上下午文字显示的电路_1_out_3 , \上下午文字显示的电路_1_out_4 , \上下午文字显示的电路_1_out_5 , \上下午文字显示的电路_1_out_6 ;

  DotMatrix #(.inputtype("column"), .matrixcols(4), .matrixrows(5), .persist(0), .dotshape("square")) dotmatrix_1 (
    .col0(\上下午文字显示的电路_1_out_3 ), .col1(\上下午文字显示的电路_1_out_4 ), .col2(\上下午文字显示的电路_1_out_5 ),
    .col3(\上下午文字显示的电路_1_out_6 ));
  \上下午文字显示的电路  \u_上下午文字显示的电路_1  (
    .out_3(\上下午文字显示的电路_1_out_3 ), .out_4(\上下午文字显示的电路_1_out_4 ), .out_5(\上下午文字显示的电路_1_out_5 ),
    .out_6(\上下午文字显示的电路_1_out_6 ), .TT(in_2), .AM_FM(in_1));
endmodule

module \电子钟整点报时电路  (
  input  in_1,
  input  in_2,
  input  in_3,
  input  in_4,
  input  in_5,
  input  in_6,
  input  in_7,
  input  in_8,
  input  in_9,
  input  in_10,
  input  in_11,
  input  in_12,
  input  in_13,
  output [3:0] out_14,
  output [3:0] out_15,
  output [3:0] out_16,
  output [3:0] out_17,
  output [3:0] out_18,
  output [3:0] out_19,
  output [4:0] out_20,
  output [4:0] out_21,
  output [4:0] out_22,
  output [4:0] out_23,
  output out_24
);

  wire and_1_out, and_2_out, and_3_out, not_1_out, not_2_out, not_3_out, or_1_out, or_2_out,
       \六十进制计数器_1_out_13 , \六十进制计数器_2_out_13 , \输出电平信号的24或12_1_out_6 ;

  \输出电平信号的24或12  \u_输出电平信号的24或12_1  (
    .CLR(in_13), .CPU(or_1_out), .CPD(in_12), .ADJ(in_6), .out_7(out_15[0]), .out_8(out_15[1]),
    .out_9(out_15[2]), .out_10(out_15[3]), .out_11(out_14[0]), .out_12(out_14[1]), .out_13(out_14[2]),
    .out_14(out_14[3]), .out_6(\输出电平信号的24或12_1_out_6 ), .in_5(in_7));
  \上下午文字显示的电路  \u_上下午文字显示的电路_1  (
    .out_3(out_23), .out_4(out_22), .out_5(out_21), .out_6(out_20), .TT(not_1_out),
    .AM_FM(\输出电平信号的24或12_1_out_6 ));
  not not_1 (not_1_out, in_7);
  or or_1 (or_1_out, in_2, not_2_out);
  \六十进制计数器  \u_六十进制计数器_1  (
    .CLR(in_9), .CPU(or_2_out), .CPD(in_8), .ADJ(in_4), .out_5(out_17[0]), .out_6(out_17[1]),
    .out_7(out_17[2]), .out_8(out_17[3]), .out_9(out_16[0]), .out_10(out_16[1]), .out_11(out_16[2]),
    .out_12(out_16[3]), .out_13(\六十进制计数器_1_out_13 ));
  or or_2 (or_2_out, in_1, not_3_out);
  not not_2 (not_2_out, \六十进制计数器_1_out_13 );
  and and_1 (and_1_out, out_16[2], out_16[0], out_17[3], out_17[0]);
  and and_2 (and_2_out, out_18[2], out_18[0]);
  \六十进制计数器  \u_六十进制计数器_2  (
    .CLR(in_11), .CPU(in_3), .CPD(in_10), .ADJ(in_5), .out_5(out_19[0]), .out_6(out_19[1]),
    .out_7(out_19[2]), .out_8(out_19[3]), .out_9(out_18[0]), .out_10(out_18[1]), .out_11(out_18[2]),
    .out_12(out_18[3]), .out_13(\六十进制计数器_2_out_13 ));
  not not_3 (not_3_out, \六十进制计数器_2_out_13 );
  and and_3 (and_3_out, and_1_out, and_2_out);
  and and_4 (out_24, and_3_out, out_19[0]);
endmodule

module \电子钟整点报时电路测试电路  (
  input  in_1,
  input  in_2,
  input  in_3,
  input  in_4,
  input  in_5,
  input  in_6,
  input  in_7,
  input  in_8,
  input  in_9,
  input  in_10,
  input  in_11,
  input  in_12,
  output out_13
);

  wire clock_1_out;
  wire [3:0] \电子钟整点报时电路_1_out_14 , \电子钟整点报时电路_1_out_15 , \电子钟整点报时电路_1_out_16 , \电子钟整点报时电路_1_out_17 ,
       \电子钟整点报时电路_1_out_18 , \电子钟整点报时电路_1_out_19 ;
  wire [4:0] \电子钟整点报时电路_1_out_20 , \电子钟整点报时电路_1_out_21 , \电子钟整点报时电路_1_out_22 , \电子钟整点报时电路_1_out_23 ;

  DotMatrix #(.inputtype("column"), .matrixcols(4), .matrixrows(5), .persist(0), .dotshape("square")) dotmatrix_1 (
    .col0(\电子钟整点报时电路_1_out_23 ), .col1(\电子钟整点报时电路_1_out_22 ), .col2(\电子钟整点报时电路_1_out_21 ),
    .col3(\电子钟整点报时电路_1_out_20 ));
  Hex_Digit_Display hex_digit_display_1 (.value(\电子钟整点报时电路_1_out_15 ));  // open: dp
  Hex_Digit_Display hex_digit_display_2 (.value(\电子钟整点报时电路_1_out_14 ));  // open: dp
  Hex_Digit_Display hex_digit_display_3 (.value(\电子钟整点报时电路_1_out_16 ));  // open: dp
  Hex_Digit_Display hex_digit_display_4 (.value(\电子钟整点报时电路_1_out_17 ));  // open: dp
  Hex_Digit_Display hex_digit_display_5 (.value(\电子钟整点报时电路_1_out_19 ));  // open: dp
  Hex_Digit_Display hex_digit_display_6 (.value(\电子钟整点报时电路_1_out_18 ));  // open: dp
  \电子钟整点报时电路  \u_电子钟整点报时电路_1  (
    .in_3(clock_1_out), .in_4(in_6), .in_5(in_10), .in_6(in_1), .in_8(in_7), .in_10(in_11), .in_12(in_3),
    .in_1(in_9), .in_2(in_5), .in_7(in_2), .in_9(in_8), .in_11(in_12), .in_13(in_4),
    .out_14(\电子钟整点报时电路_1_out_14 ), .out_15(\电子钟整点报时电路_1_out_15 ), .out_16(\电子钟整点报时电路_1_out_16 ),
    .out_17(\电子钟整点报时电路_1_out_17 ), .out_18(\电子钟整点报时电路_1_out_18 ), .out_19(\电子钟整点报时电路_1_out_19 ),
    .out_24(out_13), .out_20(\电子钟整点报时电路_1_out_20 ), .out_21(\电子钟整点报时电路_1_out_21 ),
    .out_22(\电子钟整点报时电路_1_out_22 ), .out_23(\电子钟整点报时电路_1_out_23 ));
  Clock #(.highDuration(1), .lowDuration(1)) clock_1 (.out(clock_1_out));
endmodule

module \秒脉冲产生电路  (
  input  in_1,
  output out_2
);

  wire not_1_out;

  not not_1 (not_1_out, 1'b0);
  \四位二进制可逆计数器  \u_四位二进制可逆计数器_1  (
    .CLR(out_2), .CPu(in_1), .CPd(1'b0), .Q2(out_2), .A(1'b0), .B(1'b0), .C(1'b0), .D(1'b0), .\LD非 (not_1_out));  // open: Q0, Q1, Q3
endmodule

module \多功能数字钟  (
  input  in_1,
  input  in_2,
  input  cpu,
  input  clr,
  input  adj0,
  input  adj1,
  input  cp,
  output [3:0] out_8,
  output [3:0] out_9,
  output [3:0] out_10,
  output [3:0] out_11,
  output [3:0] out_12,
  output [3:0] out_13,
  output [4:0] out_14,
  output [4:0] out_15,
  output [4:0] out_16,
  output [4:0] out_17,
  output out_18
);

  wire and_1_out, and_2_out, and_3_out, and_4_out, and_5_out, and_6_out, and_7_out, and_8_out,
       multiplexer_1_out, multiplexer_2_out, not_1_out, not_2_out, not_3_out, or_1_out, or_2_out,
       \六十进制计数器_1_out_13 , \六十进制计数器_2_out_13 , \秒脉冲产生电路_1_out_2 , \输出电平信号的24或12_1_out_6 ;

  \输出电平信号的24或12  \u_输出电平信号的24或12_1  (
    .CLR(clr), .CPU(or_1_out), .CPD(in_2), .ADJ(and_1_out), .out_7(out_9[0]), .out_8(out_9[1]),
    .out_9(out_9[2]), .out_10(out_9[3]), .out_11(out_8[0]), .out_12(out_8[1]), .out_13(out_8[2]),
    .out_14(out_8[3]), .out_6(\输出电平信号的24或12_1_out_6 ), .in_5(in_1));
  \上下午文字显示的电路  \u_上下午文字显示的电路_1  (
    .out_3(out_17), .out_4(out_16), .out_5(out_15), .out_6(out_14), .TT(not_1_out),
    .AM_FM(\输出电平信号的24或12_1_out_6 ));
  not not_1 (not_1_out, in_1);
  and and_1 (and_1_out, not_2_out, adj0);
  and and_2 (and_2_out, and_1_out, cpu);
  or or_1 (or_1_out, and_2_out, multiplexer_1_out);
  not not_2 (not_2_out, adj1);
  Multiplexer #(.select(1), .width(1), .disabled("Z"), .enable("false")) multiplexer_1 (
    .in0(\六十进制计数器_1_out_13 ), .in1(1'b0), .out(multiplexer_1_out), .sel(adj0));
  and and_3 (and_3_out, adj0, adj1);
  \六十进制计数器  \u_六十进制计数器_1  (
    .CLR(clr), .CPU(or_2_out), .CPD(in_2), .ADJ(and_3_out), .out_5(out_11[0]), .out_6(out_11[1]),
    .out_7(out_11[2]), .out_8(out_11[3]), .out_9(out_10[0]), .out_10(out_10[1]), .out_11(out_10[2]),
    .out_12(out_10[3]), .out_13(\六十进制计数器_1_out_13 ));
  not not_3 (not_3_out, adj0);
  or or_2 (or_2_out, and_4_out, multiplexer_2_out);
  and and_4 (and_4_out, and_3_out, cpu);
  and and_5 (and_5_out, not_3_out, \秒脉冲产生电路_1_out_2 );
  \秒脉冲产生电路  \u_秒脉冲产生电路_1  (.in_1(cp), .out_2(\秒脉冲产生电路_1_out_2 ));
  Multiplexer #(.select(1), .width(1), .disabled("Z"), .enable("false")) multiplexer_2 (
    .in0(\六十进制计数器_2_out_13 ), .in1(1'b0), .out(multiplexer_2_out), .sel(adj0));
  and and_6 (and_6_out, out_10[2], out_10[0], out_11[3], out_11[0]);
  and and_7 (and_7_out, out_12[2], out_12[0]);
  \六十进制计数器  \u_六十进制计数器_2  (
    .CLR(clr), .CPU(and_5_out), .CPD(1'b0), .ADJ(1'b0), .out_5(out_13[0]), .out_6(out_13[1]),
    .out_7(out_13[2]), .out_8(out_13[3]), .out_9(out_12[0]), .out_10(out_12[1]), .out_11(out_12[2]),
    .out_12(out_12[3]), .out_13(\六十进制计数器_2_out_13 ));
  and and_8 (and_8_out, and_6_out, and_7_out);
  and and_9 (out_18, and_8_out, out_13[0]);
endmodule

module \多功能数字钟测试电路  (
  input  in_1,
  input  in_2,
  input  in_3,
  input  in_4,
  output out_5
);

  wire button_1_out, button_2_out, clock_1_out;
  wire [3:0] \多功能数字钟_1_out_8 , \多功能数字钟_1_out_9 , \多功能数字钟_1_out_10 , \多功能数字钟_1_out_11 , \多功能数字钟_1_out_12 ,
       \多功能数字钟_1_out_13 ;
  wire [4:0] \多功能数字钟_1_out_14 , \多功能数字钟_1_out_15 , \多功能数字钟_1_out_16 , \多功能数字钟_1_out_17 ;

  DotMatrix #(.inputtype("column"), .matrixcols(4), .matrixrows(5), .persist(0), .dotshape("square")) dotmatrix_1 (
    .col0(\多功能数字钟_1_out_17 ), .col1(\多功能数字钟_1_out_16 ), .col2(\多功能数字钟_1_out_15 ), .col3(\多功能数字钟_1_out_14 ));
  Clock #(.highDuration(1), .lowDuration(1)) clock_1 (.out(clock_1_out));
  Hex_Digit_Display hex_digit_display_1 (.value(\多功能数字钟_1_out_8 ));  // open: dp
  Hex_Digit_Display hex_digit_display_2 (.value(\多功能数字钟_1_out_9 ));  // open: dp
  Button button_1 (.out(button_1_out));
  Button button_2 (.out(button_2_out));
  Hex_Digit_Display hex_digit_display_3 (.value(\多功能数字钟_1_out_11 ));  // open: dp
  Hex_Digit_Display hex_digit_display_4 (.value(\多功能数字钟_1_out_10 ));  // open: dp
  Hex_Digit_Display hex_digit_display_5 (.value(\多功能数字钟_1_out_12 ));  // open: dp
  \多功能数字钟  \u_多功能数字钟_1  (
    .in_2(button_2_out), .out_14(\多功能数字钟_1_out_14 ), .out_15(\多功能数字钟_1_out_15 ), .out_16(\多功能数字钟_1_out_16 ),
    .out_17(\多功能数字钟_1_out_17 ), .cpu(button_1_out), .in_1(in_3), .out_8(\多功能数字钟_1_out_8 ),
    .out_9(\多功能数字钟_1_out_9 ), .out_10(\多功能数字钟_1_out_10 ), .out_11(\多功能数字钟_1_out_11 ),
    .out_12(\多功能数字钟_1_out_12 ), .out_13(\多功能数字钟_1_out_13 ), .adj0(in_1), .adj1(in_2), .clr(in_4),
    .cp(clock_1_out), .out_18(out_5));
  Hex_Digit_Display hex_digit_display_6 (.value(\多功能数字钟_1_out_13 ));  // open: dp
endmodule

module \_24转12  (
  input  q1,
  input  q2,
  input  q3,
  input  q4,
  input  q5,
  input  q6,
  input  q7,
  input  q8,
  output o1,
  output o2,
  output o3,
  output o4,
  output o5,
  output o6,
  output o7,
  output o8,
  output cout
);

  wire and_1_out, and_2_out, and_3_out, and_4_out, and_5_out, and_6_out, and_7_out, and_8_out, and_9_out,
       and_10_out, and_11_out, and_12_out, and_13_out, and_14_out, and_15_out, and_16_out, and_17_out,
       and_18_out, and_19_out, and_20_out, and_21_out, and_22_out, and_23_out, and_24_out, and_25_out,
       and_26_out, and_27_out, not_1_out, not_2_out, not_3_out, not_4_out, not_5_out, not_6_out, not_7_out,
       not_8_out, not_9_out, not_10_out, not_11_out, not_12_out, not_13_out, not_14_out, not_15_out,
       not_16_out, not_17_out, not_18_out, not_19_out, not_20_out, not_21_out, not_22_out, not_23_out,
       not_24_out, not_25_out, not_26_out, not_27_out, not_28_out, not_29_out, not_30_out, not_31_out,
       not_32_out, not_33_out, not_34_out, not_35_out, not_36_out, not_37_out, not_38_out, not_39_out,
       not_40_out, not_41_out, not_42_out, not_43_out, not_44_out, not_45_out, not_46_out, not_47_out,
       not_48_out, not_49_out, not_50_out, not_51_out, not_52_out;

  not not_1 (not_1_out, q1);
  not not_2 (not_2_out, q2);
  not not_3 (not_3_out, q3);
  not not_4 (not_4_out, q5);
  not not_5 (not_5_out, q6);
  not not_6 (not_6_out, q7);
  not not_7 (not_7_out, q8);
  not not_8 (not_8_out, q1);
  not not_9 (not_9_out, q2);
  not not_10 (not_10_out, q5);
  not not_11 (not_11_out, q6);
  not not_12 (not_12_out, q8);
  not not_13 (not_13_out, q5);
  not not_14 (not_14_out, q6);
  not not_15 (not_15_out, q7);
  not not_16 (not_16_out, q1);
  not not_17 (not_17_out, q2);
  not not_18 (not_18_out, q4);
  not not_19 (not_19_out, q5);
  not not_20 (not_20_out, q8);
  not not_21 (not_21_out, q4);
  and and_1 (and_1_out, not_21_out, q5);
  not not_22 (not_22_out, q6);
  and and_2 (and_2_out, q3, not_22_out, not_23_out);
  not not_23 (not_23_out, q7);
  not not_24 (not_24_out, q7);
  and and_3 (and_3_out, q3, not_24_out, q8);
  and and_4 (and_4_out, q3, q4, not_25_out);
  not not_25 (not_25_out, q7);
  and and_5 (and_5_out, q2, q3, not_26_out);
  not not_26 (not_26_out, q7);
  and and_6 (and_6_out, q1, q3, not_27_out);
  not not_27 (not_27_out, q7);
  not not_28 (not_28_out, q3);
  and and_7 (and_7_out, not_28_out, not_29_out, q6);
  not not_29 (not_29_out, q4);
  not not_30 (not_30_out, q4);
  and and_8 (and_8_out, not_30_out, q6, q8);
  and and_9 (and_9_out, q6, q7);
  and and_10 (and_10_out, q5, q6);
  and and_11 (and_11_out, q4, q5);
  not not_31 (not_31_out, q4);
  and and_12 (and_12_out, q2, not_31_out, q6);
  not not_32 (not_32_out, q4);
  and and_13 (and_13_out, q1, not_32_out, q6);
  not not_33 (not_33_out, q1);
  not not_34 (not_34_out, q2);
  not not_35 (not_35_out, q3);
  not not_36 (not_36_out, q4);
  not not_37 (not_37_out, q5);
  not not_38 (not_38_out, q6);
  not not_39 (not_39_out, q8);
  not not_40 (not_40_out, q1);
  not not_41 (not_41_out, q2);
  not not_42 (not_42_out, q3);
  not not_43 (not_43_out, q6);
  not not_44 (not_44_out, q8);
  not not_45 (not_45_out, q3);
  not not_46 (not_46_out, q4);
  not not_47 (not_47_out, q7);
  not not_48 (not_48_out, q1);
  not not_49 (not_49_out, q2);
  not not_50 (not_50_out, q5);
  not not_51 (not_51_out, q7);
  not not_52 (not_52_out, q8);
  and and_14 (and_14_out, q4, q7);
  and and_15 (and_15_out, q4, q6);
  and and_16 (and_16_out, q4, q5);
  and and_17 (and_17_out, not_1_out, not_2_out, not_3_out, not_4_out, not_5_out, not_6_out, not_7_out);
  and and_18 (and_18_out, not_8_out, not_9_out, q4, not_10_out, not_11_out, not_12_out);
  and and_19 (and_19_out, q4, not_13_out, not_14_out, not_15_out);
  and and_20 (and_20_out, q3, q7);
  and and_21 (and_21_out, not_16_out, not_17_out, q3, not_18_out, not_19_out, q6, not_20_out);
  and and_22 (and_22_out, not_33_out, not_34_out, not_35_out, not_36_out, not_37_out, not_38_out, not_39_out);
  and and_23 (and_23_out, not_40_out, not_41_out, not_42_out, not_43_out, q7, not_44_out);
  and and_24 (and_24_out, not_45_out, not_46_out, q7);
  and and_25 (and_25_out, q4, q6, not_47_out);
  and and_26 (and_26_out, q4, q5);
  and and_27 (and_27_out, not_48_out, not_49_out, q3, not_50_out, q6, not_51_out, not_52_out);
  or or_1 (cout, and_14_out, and_15_out, and_16_out, q3);
  or or_2 (o4, and_17_out, and_18_out, and_19_out, and_20_out, and_21_out);
  or or_3 (o5, and_1_out, and_2_out, and_3_out, and_4_out, and_5_out, and_6_out);
  or or_4 (o6, and_7_out, and_8_out, and_9_out, and_10_out, and_11_out, and_12_out, and_13_out);
  or or_5 (o7, and_22_out, and_23_out, and_24_out, and_25_out, and_26_out, and_27_out);

  assign o1 = 1'b0;
  assign o2 = 1'b0;
  assign o3 = 1'b0;
  assign o8 = q8;
endmodule

module \输出电平信号的24或12  (
  input  CLR,
  input  CPU,
  input  CPD,
  input  ADJ,
  input  in_5,
  output out_6,
  output out_7,
  output out_8,
  output out_9,
  output out_10,
  output out_11,
  output out_12,
  output out_13,
  output out_14
);

  wire and_1_out, and_2_out, and_3_out, and_4_out, and_5_out, and_6_out, and_7_out, and_8_out, and_9_out,
       multiplexer_1_out, nand_1_out, not_1_out, not_2_out, not_3_out, not_4_out, not_5_out, not_6_out,
       not_7_out, not_8_out, not_9_out, not_10_out, not_11_out, not_12_out, not_13_out, not_14_out,
       not_15_out, not_16_out, not_17_out, not_18_out, or_1_out, or_2_out;
  wire [3:0] \n24转12_1_o4 , \n24转12_1_o8 , \四位二进制可逆计数器_1_q0 , \四位二进制可逆计数器_2_q0 ;

  and and_1 (and_1_out, CPD, ADJ);
  and and_2 (and_2_out, and_5_out, not_1_out);
  not not_1 (not_1_out, nand_1_out);
  or or_1 (or_1_out, CLR, and_4_out);
  or or_2 (or_2_out, and_7_out, and_4_out, CLR);
  Multiplexer #(.select(1), .width(1), .disabled("Z"), .enable("false")) multiplexer_1 (
    .in0(and_1_out), .in1(1'b0), .out(multiplexer_1_out), .sel(and_2_out));
  and and_3 (and_3_out, and_5_out, nand_1_out, and_1_out);
  and and_4 (and_4_out, and_6_out, and_9_out);
  not not_2 (not_2_out, and_8_out);
  \四位二进制可逆计数器  \u_四位二进制可逆计数器_1  (
    .CLR(or_2_out), .CPu(CPU), .Q0(\四位二进制可逆计数器_1_q0 [0]), .CPd(multiplexer_1_out), .Q1(\四位二进制可逆计数器_1_q0 [1]),
    .Q2(\四位二进制可逆计数器_1_q0 [2]), .Q3(\四位二进制可逆计数器_1_q0 [3]), .A(1'b1), .B(1'b0), .C(1'b0), .D(1'b1),
    .\LD非 (not_2_out));
  not not_3 (not_3_out, \四位二进制可逆计数器_1_q0 [3]);
  \四位二进制可逆计数器  \u_四位二进制可逆计数器_2  (
    .CLR(or_1_out), .CPu(and_7_out), .Q0(\四位二进制可逆计数器_2_q0 [0]), .CPd(and_3_out), .Q1(\四位二进制可逆计数器_2_q0 [1]),
    .Q2(\四位二进制可逆计数器_2_q0 [2]), .Q3(\四位二进制可逆计数器_2_q0 [3]), .A(1'b0), .B(1'b0), .C(1'b0), .D(1'b0), .\LD非 (1'b1));
  not not_4 (not_4_out, \四位二进制可逆计数器_1_q0 [2]);
  not not_5 (not_5_out, \四位二进制可逆计数器_1_q0 [1]);
  not not_6 (not_6_out, \四位二进制可逆计数器_1_q0 [0]);
  and and_5 (and_5_out, not_3_out, not_4_out, not_5_out, not_6_out);
  not not_7 (not_7_out, \四位二进制可逆计数器_2_q0 [2]);
  not not_8 (not_8_out, \四位二进制可逆计数器_2_q0 [0]);
  and and_6 (and_6_out, not_8_out, \四位二进制可逆计数器_2_q0 [1], not_7_out, not_11_out);
  not not_9 (not_9_out, \四位二进制可逆计数器_1_q0 [0]);
  not not_10 (not_10_out, \四位二进制可逆计数器_1_q0 [2]);
  and and_7 (and_7_out, \四位二进制可逆计数器_1_q0 [3], not_10_out, not_9_out, \四位二进制可逆计数器_1_q0 [1]);
  not not_11 (not_11_out, \四位二进制可逆计数器_2_q0 [3]);
  not not_12 (not_12_out, \四位二进制可逆计数器_2_q0 [0]);
  not not_13 (not_13_out, \四位二进制可逆计数器_2_q0 [2]);
  not not_14 (not_14_out, \四位二进制可逆计数器_2_q0 [1]);
  not not_15 (not_15_out, \四位二进制可逆计数器_2_q0 [3]);
  nand nand_1 (nand_1_out, not_15_out, not_13_out, not_14_out, not_12_out);
  and and_8 (and_8_out, \四位二进制可逆计数器_1_q0 [3], \四位二进制可逆计数器_1_q0 [2], \四位二进制可逆计数器_1_q0 [1], \四位二进制可逆计数器_1_q0 [0]);
  not not_16 (not_16_out, \四位二进制可逆计数器_1_q0 [1]);
  not not_17 (not_17_out, \四位二进制可逆计数器_1_q0 [0]);
  not not_18 (not_18_out, \四位二进制可逆计数器_1_q0 [3]);
  and and_9 (and_9_out, not_17_out, not_16_out, \四位二进制可逆计数器_1_q0 [2], not_18_out);
  \_24转12  \u_24转12_1  (
    .q1(\四位二进制可逆计数器_2_q0 [3]), .o1(\n24转12_1_o4 [3]), .q2(\四位二进制可逆计数器_2_q0 [2]), .o2(\n24转12_1_o4 [2]),
    .q3(\四位二进制可逆计数器_2_q0 [1]), .o3(\n24转12_1_o4 [1]), .q4(\四位二进制可逆计数器_2_q0 [0]), .q5(\四位二进制可逆计数器_1_q0 [3]),
    .q6(\四位二进制可逆计数器_1_q0 [2]), .q7(\四位二进制可逆计数器_1_q0 [1]), .q8(\四位二进制可逆计数器_1_q0 [0]), .o4(\n24转12_1_o4 [0]),
    .o5(\n24转12_1_o8 [3]), .o6(\n24转12_1_o8 [2]), .o7(\n24转12_1_o8 [1]), .o8(\n24转12_1_o8 [0]), .cout(out_6));
  Multiplexer #(.select(1), .width(4), .disabled("Z"), .enable("false")) multiplexer_2 (
    .in0(\n24转12_1_o8 ), .in1(\四位二进制可逆计数器_1_q0 ), .out({out_10, out_9, out_8, out_7}), .sel(in_5));
  Multiplexer #(.select(1), .width(4), .disabled("Z"), .enable("false")) multiplexer_3 (
    .in0(\n24转12_1_o4 ), .in1(\四位二进制可逆计数器_2_q0 ), .out({out_14, out_13, out_12, out_11}), .sel(in_5));
endmodule
