// Logisim project 实验6-CS1806-U201814655-杨雨鑫.circ as structural Verilog: 10 circuits, main circuit sqrX
module sqrX (
  input  [31:0] a,
  input  [31:0] b,
  input  [31:0] c,
  input  [31:0] d,
  output [31:0] a_prime,
  output [31:0] b_prime,
  output [31:0] c_prime,
  output [31:0] d_prime
);

  wire [31:0] multiplier_1_out, multiplier_2_out, multiplier_3_out, multiplier_4_out, multiplier_5_out,
       multiplier_6_out, multiplier_7_out;

  Multiplier #(.width(32)) multiplier_1 (.a(a), .b(a), .out(multiplier_1_out), .cin({32{1'b0}}));  // open: cout
  Multiplier #(.width(32)) multiplier_2 (.a(b), .b(c), .out(multiplier_2_out), .cin({32{1'b0}}));  // open: cout
  Multiplier #(.width(32)) multiplier_3 (.a(a), .b(b), .out(multiplier_3_out), .cin({32{1'b0}}));  // open: cout
  Multiplier #(.width(32)) multiplier_4 (.a(b), .b(d), .out(multiplier_4_out), .cin({32{1'b0}}));  // open: cout
  Multiplier #(.width(32)) multiplier_5 (.a(a), .b(c), .out(multiplier_5_out), .cin({32{1'b0}}));  // open: cout
  Multiplier #(.width(32)) multiplier_6 (.a(c), .b(d), .out(multiplier_6_out), .cin({32{1'b0}}));  // open: cout
  Multiplier #(.width(32)) multiplier_7 (.a(d), .b(d), .out(multiplier_7_out), .cin({32{1'b0}}));  // open: cout
  Adder #(.width(32)) adder_1 (.a(multiplier_1_out), .b(multiplier_2_out), .out(a_prime), .cin(1'b0));  // open: cout
  Adder #(.width(32)) adder_2 (.a(multiplier_3_out), .b(multiplier_4_out), .out(b_prime), .cin(1'b0));  // open: cout
  Adder #(.width(32)) adder_3 (.a(multiplier_5_out), .b(multiplier_6_out), .out(c_prime), .cin(1'b0));  // open: cout
  Adder #(.width(32)) adder_4 (.a(multiplier_2_out), .b(multiplier_7_out), .out(d_prime), .cin(1'b0));  // open: cout

  // Notes on the sheet:
  //   a*a
  //   b*c
  //   a*b
  //   b*d
  //   a*c
  //   c*d
  //   d*d
endmodule

module sqrX_A (
  input  [31:0] a,
  input  [31:0] b,
  input  [31:0] c,
  input  [31:0] d,
  output [31:0] a_prime,
  output [31:0] b_prime,
  output [31:0] c_prime,
  output [31:0] d_prime
);

  wire [31:0] adder_2_out, adder_4_out, adder_5_out, adder_6_out, multiplier_1_out, multiplier_2_out,
       multiplier_3_out, multiplier_4_out, multiplier_5_out, multiplier_6_out, multiplier_7_out;

  Multiplier #(.width(32)) multiplier_1 (.a(a), .b(a), .out(multiplier_1_out), .cin({32{1'b0}}));  // open: cout
  Multiplier #(.width(32)) multiplier_2 (.a(b), .b(c), .out(multiplier_2_out), .cin({32{1'b0}}));  // open: cout
  Multiplier #(.width(32)) multiplier_3 (.a(a), .b(b), .out(multiplier_3_out), .cin({32{1'b0}}));  // open: cout
  Multiplier #(.width(32)) multiplier_4 (.a(b), .b(d), .out(multiplier_4_out), .cin({32{1'b0}}));  // open: cout
  Multiplier #(.width(32)) multiplier_5 (.a(a), .b(c), .out(multiplier_5_out), .cin({32{1'b0}}));  // open: cout
  Multiplier #(.width(32)) multiplier_6 (.a(c), .b(d), .out(multiplier_6_out), .cin({32{1'b0}}));  // open: cout
  Multiplier #(.width(32)) multiplier_7 (.a(d), .b(d), .out(multiplier_7_out), .cin({32{1'b0}}));  // open: cout
  Adder #(.width(32)) adder_1 (.a(multiplier_3_out), .b(multiplier_4_out), .out(a_prime), .cin(1'b0));  // open: cout
  Adder #(.width(32)) adder_2 (
    .a(multiplier_1_out), .b(multiplier_2_out), .out(adder_2_out), .cin(1'b0));  // open: cout
  Adder #(.width(32)) adder_3 (.a(multiplier_2_out), .b(multiplier_7_out), .out(c_prime), .cin(1'b0));  // open: cout
  Adder #(.width(32)) adder_4 (
    .a(multiplier_5_out), .b(multiplier_6_out), .out(adder_4_out), .cin(1'b0));  // open: cout
  Adder #(.width(32)) adder_5 (.a(multiplier_3_out), .b(adder_2_out), .out(adder_5_out), .cin(1'b0));  // open: cout
  Adder #(.width(32)) adder_6 (.a(multiplier_2_out), .b(adder_4_out), .out(adder_6_out), .cin(1'b0));  // open: cout
  Adder #(.width(32)) adder_7 (.a(adder_5_out), .b(multiplier_4_out), .out(b_prime), .cin(1'b0));  // open: cout
  Adder #(.width(32)) adder_8 (.a(adder_6_out), .b(multiplier_7_out), .out(d_prime), .cin(1'b0));  // open: cout

  // Notes on the sheet:
  //   a*a
  //   b*c
  //   a*b
  //   b*d
  //   a*c
  //   c*d
  //   d*d
endmodule

module \Fibonacci数显示模块  (
  input  [31:0] in_1,
  output [3:0] out_2,
  output [3:0] out_3,
  output [3:0] out_4,
  output [3:0] out_5,
  output [3:0] out_6,
  output [3:0] out_7,
  output [3:0] out_8,
  output [3:0] out_9,
  output [3:0] out_10,
  output [3:0] out_11
);

  wire [31:0] divider_1_rem, divider_2_rem, divider_3_rem, divider_4_rem, divider_5_rem, divider_6_rem,
       divider_7_rem, divider_8_rem, divider_9_rem;
  wire [31:4] divider_1_out, divider_2_out, divider_3_out, divider_4_out, divider_5_out, divider_6_out,
       divider_7_out, divider_8_out, divider_9_out, divider_10_out;

  Divider #(.width(32)) divider_1 (
    .a(in_1), .b(32'h3b9aca00), .out({divider_1_out, out_2}), .rem(divider_1_rem));  // open: upper
  Divider #(.width(32)) divider_2 (
    .a(divider_1_rem), .b(32'h5f5e100), .out({divider_2_out, out_3}), .rem(divider_2_rem));  // open: upper
  Divider #(.width(32)) divider_3 (
    .a(divider_2_rem), .b(32'h989680), .out({divider_3_out, out_4}), .rem(divider_3_rem));  // open: upper
  Divider #(.width(32)) divider_4 (
    .a(divider_3_rem), .b(32'hf4240), .out({divider_4_out, out_5}), .rem(divider_4_rem));  // open: upper
  Divider #(.width(32)) divider_5 (
    .a(divider_4_rem), .b(32'h186a0), .out({divider_5_out, out_6}), .rem(divider_5_rem));  // open: upper
  Divider #(.width(32)) divider_6 (
    .a(divider_5_rem), .b(32'h2710), .out({divider_6_out, out_7}), .rem(divider_6_rem));  // open: upper
  Divider #(.width(32)) divider_7 (
    .a(divider_6_rem), .b(32'h3e8), .out({divider_7_out, out_8}), .rem(divider_7_rem));  // open: upper
  Divider #(.width(32)) divider_8 (
    .a(divider_7_rem), .b(32'h64), .out({divider_8_out, out_9}), .rem(divider_8_rem));  // open: upper
  Divider #(.width(32)) divider_9 (
    .a(divider_8_rem), .b(32'ha), .out({divider_9_out, out_10}), .rem(divider_9_rem));  // open: upper
  Divider #(.width(32)) divider_10 (.a(divider_9_rem), .b(32'h1), .out({divider_10_out, out_11}));  // open: upper, rem

  // Notes on the sheet:
  //   4294967296
endmodule

module \矩阵快速幂迭代模块  (
  input  ni_1,
  input  clr,
  input  clk,
  input  start,
  output [31:0] Fi
);

  wire buffer_1_out, buffer_2_out;
  wire [31:0] multiplexer_1_out, multiplexer_2_out, multiplexer_3_out, multiplexer_4_out, multiplexer_5_out,
       multiplexer_6_out, multiplexer_7_out, multiplexer_8_out, register_1_q, register_3_q, register_4_q,
       sqrx_1_a_prime, sqrx_1_b_prime, sqrx_1_c_prime, sqrx_1_d_prime, sqrx_a_1_a_prime, sqrx_a_1_b_prime,
       sqrx_a_1_c_prime, sqrx_a_1_d_prime;

  buf buffer_1 (buffer_1_out, start);
  buf buffer_2 (buffer_2_out, buffer_1_out);
  Multiplexer #(.select(1), .width(32), .disabled("Z"), .enable("false")) multiplexer_1 (
    .in0({32{1'b0}}), .in1(multiplexer_5_out), .out(multiplexer_1_out), .sel(buffer_2_out));
  Multiplexer #(.select(1), .width(32), .disabled("Z"), .enable("false")) multiplexer_2 (
    .in0(32'h1), .in1(multiplexer_6_out), .out(multiplexer_2_out), .sel(buffer_2_out));
  Multiplexer #(.select(1), .width(32), .disabled("Z"), .enable("false")) multiplexer_3 (
    .in0(32'h1), .in1(multiplexer_7_out), .out(multiplexer_3_out), .sel(buffer_2_out));
  Multiplexer #(.select(1), .width(32), .disabled("Z"), .enable("false")) multiplexer_4 (
    .in0(32'h1), .in1(multiplexer_8_out), .out(multiplexer_4_out), .sel(buffer_2_out));
  Register #(.width(32), .trigger("rising"), .Select("low")) register_1 (
    .D(multiplexer_1_out), .en(1'b1), .Q(register_1_q), .clk(clk), .clr(clr));
  Register #(.width(32), .trigger("rising"), .Select("low")) register_2 (
    .D(multiplexer_2_out), .en(1'b1), .Q(Fi), .clk(clk), .clr(clr));
  Register #(.width(32), .trigger("rising"), .Select("low")) register_3 (
    .D(multiplexer_3_out), .en(1'b1), .Q(register_3_q), .clk(clk), .clr(clr));
  Register #(.width(32), .trigger("rising"), .Select("low")) register_4 (
    .D(multiplexer_4_out), .en(1'b1), .Q(register_4_q), .clk(clk), .clr(clr));
  sqrX sqrx_1 (
    .a(register_1_q), .b(Fi), .c(register_3_q), .d(register_4_q), .a_prime(sqrx_1_a_prime),
    .b_prime(sqrx_1_b_prime), .c_prime(sqrx_1_c_prime), .d_prime(sqrx_1_d_prime));
  sqrX_A sqrx_a_1 (
    .a(register_1_q), .b(Fi), .c(register_3_q), .d(register_4_q), .a_prime(sqrx_a_1_a_prime),
    .b_prime(sqrx_a_1_b_prime), .c_prime(sqrx_a_1_c_prime), .d_prime(sqrx_a_1_d_prime));
  Multiplexer #(.select(1), .width(32), .disabled("Z"), .enable("false")) multiplexer_5 (
    .in0(sqrx_1_a_prime), .in1(sqrx_a_1_a_prime), .out(multiplexer_5_out), .sel(ni_1));
  Multiplexer #(.select(1), .width(32), .disabled("Z"), .enable("false")) multiplexer_6 (
    .in0(sqrx_1_b_prime), .in1(sqrx_a_1_b_prime), .out(multiplexer_6_out), .sel(ni_1));
  Multiplexer #(.select(1), .width(32), .disabled("Z"), .enable("false")) multiplexer_7 (
    .in0(sqrx_1_c_prime), .in1(sqrx_a_1_c_prime), .out(multiplexer_7_out), .sel(ni_1));
  Multiplexer #(.select(1), .width(32), .disabled("Z"), .enable("false")) multiplexer_8 (
    .in0(sqrx_1_d_prime), .in1(sqrx_a_1_d_prime), .out(multiplexer_8_out), .sel(ni_1));
endmodule

module \斐波那契_Fibonacci_数列计算器验证电路  (
  input  [5:0] in_1,
  input  in_2,
  input  in_3
);

  wire [3:0] \斐波那契_fibonacci_数列计算器_1_out_4 , \斐波那契_fibonacci_数列计算器_1_out_5 , \斐波那契_fibonacci_数列计算器_1_out_6 ,
       \斐波那契_fibonacci_数列计算器_1_out_7 , \斐波那契_fibonacci_数列计算器_1_out_8 , \斐波那契_fibonacci_数列计算器_1_out_9 ,
       \斐波那契_fibonacci_数列计算器_1_out_10 , \斐波那契_fibonacci_数列计算器_1_out_11 , \斐波那契_fibonacci_数列计算器_1_out_12 ,
       \斐波那契_fibonacci_数列计算器_1_out_13 ;

  \斐波那契_Fibonacci_数列计算器  \u_斐波那契_fibonacci_数列计算器_1  (
    .in_1(in_1), .in_2(in_2), .in_3(in_3), .out_4(\斐波那契_fibonacci_数列计算器_1_out_4 ),
    .out_5(\斐波那契_fibonacci_数列计算器_1_out_5 ), .out_6(\斐波那契_fibonacci_数列计算器_1_out_6 ),
    .out_7(\斐波那契_fibonacci_数列计算器_1_out_7 ), .out_8(\斐波那契_fibonacci_数列计算器_1_out_8 ),
    .out_9(\斐波那契_fibonacci_数列计算器_1_out_9 ), .out_10(\斐波那契_fibonacci_数列计算器_1_out_10 ),
    .out_11(\斐波那契_fibonacci_数列计算器_1_out_11 ), .out_12(\斐波那契_fibonacci_数列计算器_1_out_12 ),
    .out_13(\斐波那契_fibonacci_数列计算器_1_out_13 ));
  Hex_Digit_Display hex_digit_display_1 (.value(\斐波那契_fibonacci_数列计算器_1_out_4 ));  // open: dp
  Hex_Digit_Display hex_digit_display_2 (.value(\斐波那契_fibonacci_数列计算器_1_out_5 ));  // open: dp
  Hex_Digit_Display hex_digit_display_3 (.value(\斐波那契_fibonacci_数列计算器_1_out_6 ));  // open: dp
  Hex_Digit_Display hex_digit_display_4 (.value(\斐波那契_fibonacci_数列计算器_1_out_7 ));  // open: dp
  Hex_Digit_Display hex_digit_display_5 (.value(\斐波那契_fibonacci_数列计算器_1_out_8 ));  // open: dp
  Hex_Digit_Display hex_digit_display_6 (.value(\斐波那契_fibonacci_数列计算器_1_out_9 ));  // open: dp
  Hex_Digit_Display hex_digit_display_7 (.value(\斐波那契_fibonacci_数列计算器_1_out_10 ));  // open: dp
  Hex_Digit_Display hex_digit_display_8 (.value(\斐波那契_fibonacci_数列计算器_1_out_11 ));  // open: dp
  Hex_Digit_Display hex_digit_display_9 (.value(\斐波那契_fibonacci_数列计算器_1_out_13 ));  // open: dp
  Hex_Digit_Display hex_digit_display_10 (.value(\斐波那契_fibonacci_数列计算器_1_out_12 ));  // open: dp
endmodule

module \sqrX测试电路  (
  input  [31:0] in_1,
  input  [31:0] in_2,
  input  [31:0] in_3,
  input  [31:0] in_4,
  output [31:0] out_5,
  output [31:0] out_6,
  output [31:0] out_7,
  output [31:0] out_8
);

  sqrX sqrx_1 (
    .a(in_1), .b(in_2), .c(in_3), .d(in_4), .a_prime(out_5), .b_prime(out_6), .c_prime(out_7), .d_prime(out_8));
endmodule

module \sqrX_A测试电路  (
  input  [31:0] in_1,
  input  [31:0] in_2,
  input  [31:0] in_3,
  input  [31:0] in_4,
  output [31:0] out_5,
  output [31:0] out_6,
  output [31:0] out_7,
  output [31:0] out_8
);

  sqrX_A sqrx_a_1 (
    .a(in_1), .b(in_2), .c(in_3), .d(in_4), .a_prime(out_5), .b_prime(out_6), .c_prime(out_7), .d_prime(out_8));
endmodule

module \Fibonacci数显示模块测试电路  (
  input  [31:0] in_1
);

  wire [3:0] \fibonacci数显示模块_1_out_2 , \fibonacci数显示模块_1_out_3 , \fibonacci数显示模块_1_out_4 ,
       \fibonacci数显示模块_1_out_5 , \fibonacci数显示模块_1_out_6 , \fibonacci数显示模块_1_out_7 ,
       \fibonacci数显示模块_1_out_8 , \fibonacci数显示模块_1_out_9 , \fibonacci数显示模块_1_out_10 ,
       \fibonacci数显示模块_1_out_11 ;

  \Fibonacci数显示模块  \fibonacci数显示模块_1  (
    .in_1(in_1), .out_2(\fibonacci数显示模块_1_out_2 ), .out_3(\fibonacci数显示模块_1_out_3 ),
    .out_4(\fibonacci数显示模块_1_out_4 ), .out_5(\fibonacci数显示模块_1_out_5 ), .out_6(\fibonacci数显示模块_1_out_6 ),
    .out_7(\fibonacci数显示模块_1_out_7 ), .out_8(\fibonacci数显示模块_1_out_8 ), .out_9(\fibonacci数显示模块_1_out_9 ),
    .out_10(\fibonacci数显示模块_1_out_10 ), .out_11(\fibonacci数显示模块_1_out_11 ));
  Hex_Digit_Display hex_digit_display_1 (.value(\fibonacci数显示模块_1_out_2 ));  // open: dp
  Hex_Digit_Display hex_digit_display_2 (.value(\fibonacci数显示模块_1_out_3 ));  // open: dp
  Hex_Digit_Display hex_digit_display_3 (.value(\fibonacci数显示模块_1_out_5 ));  // open: dp
  Hex_Digit_Display hex_digit_display_4 (.value(\fibonacci数显示模块_1_out_4 ));  // open: dp
  Hex_Digit_Display hex_digit_display_5 (.value(\fibonacci数显示模块_1_out_6 ));  // open: dp
  Hex_Digit_Display hex_digit_display_6 (.value(\fibonacci数显示模块_1_out_7 ));  // open: dp
  Hex_Digit_Display hex_digit_display_7 (.value(\fibonacci数显示模块_1_out_8 ));  // open: dp
  Hex_Digit_Display hex_digit_display_8 (.value(\fibonacci数显示模块_1_out_9 ));  // open: dp
  Hex_Digit_Display hex_digit_display_9 (.value(\fibonacci数显示模块_1_out_11 ));  // open: dp
  Hex_Digit_Display hex_digit_display_10 (.value(\fibonacci数显示模块_1_out_10 ));  // open: dp
endmodule

module controller (
  input  [5:0] n,
  input  clock,
  input  clear,
  output ni_1,
  output clk,
  output start,
  output clear_2
);

  wire buffer_1_out, buffer_2_out, comparator_1_gt, not_1_out, or_1_out, or_2_out;
  wire [5:1] shift_register_1_out;
  wire [7:0] counter_1_q;

  buf buffer_1 (buffer_1_out, buffer_2_out);
  buf buffer_2 (buffer_2_out, clear);
  not not_1 (not_1_out, buffer_1_out);
  or or_1 (or_1_out, clear, clock);
  Shift_Register #(.width(6), .length(6), .parallel("true"), .trigger("falling")) shift_register_1 (
    .shift(not_1_out), .in(n), .clk(or_1_out), .out({shift_register_1_out, ni_1}), .load(buffer_1_out),
    .clr(clear), .d0({{5{1'b0}}, n[0]}), .d1({{5{1'b0}}, n[1]}), .d2({{5{1'b0}}, n[2]}),
    .d3({{5{1'b0}}, n[3]}), .d4({{5{1'b0}}, n[4]}), .d5({{5{1'b0}}, n[5]}));  // open: q0, q1, q2, q3, q4, q5
  Counter #(.width(8), .max('hff), .ongoal("stay"), .trigger("falling"), .behavior("old")) counter_1 (
    .count(1'b1), .Q(counter_1_q), .clk(clock), .clr(clear));  // open: load, D, carry, preset
  Comparator #(.width(8), .mode("unsigned")) comparator_1 (
    .a(8'h6), .b(counter_1_q), .gt(comparator_1_gt));  // open: eq, lt
  and and_1 (clk, comparator_1_gt, clock);
  or or_2 (or_2_out, ni_1, start);
  D_Flip_Flop #(.trigger("rising"), .Pre_Clr_Positions("LEGACY"), .NegatePresetClear("false"), .enable("true"), .NewFFLayout("false")) d_ff_1 (
    .clk(clock), .D(or_2_out), .Q(start), .reset(clear));  // open: Qn, preset, en

  assign clear_2 = clear;
endmodule

module \斐波那契_Fibonacci_数列计算器  (
  input  [5:0] in_1,
  input  in_2,
  input  in_3,
  output [3:0] out_4,
  output [3:0] out_5,
  output [3:0] out_6,
  output [3:0] out_7,
  output [3:0] out_8,
  output [3:0] out_9,
  output [3:0] out_10,
  output [3:0] out_11,
  output [3:0] out_12,
  output [3:0] out_13
);

  wire controller_1_clear_2, controller_1_clk, controller_1_ni_1, controller_1_start;
  wire [5:0] multiplexer_1_out;
  wire [31:0] \矩阵快速幂迭代模块_1_fi ;

  Multiplexer #(.select(1), .width(6), .disabled("Z"), .enable("false")) multiplexer_1 (
    .in0({6{1'b0}}), .in1(in_1), .out(multiplexer_1_out), .sel(in_2));
  controller controller_1 (
    .n(multiplexer_1_out), .clock(in_3), .clear(in_2), .ni_1(controller_1_ni_1), .clk(controller_1_clk),
    .start(controller_1_start), .clear_2(controller_1_clear_2));
  \矩阵快速幂迭代模块  \u_矩阵快速幂迭代模块_1  (
    .ni_1(controller_1_ni_1), .clr(controller_1_clear_2), .clk(controller_1_clk), .start(controller_1_start),
    .Fi(\矩阵快速幂迭代模块_1_fi ));
  \Fibonacci数显示模块  \fibonacci数显示模块_1  (
    .in_1(\矩阵快速幂迭代模块_1_fi ), .out_2(out_4), .out_3(out_5), .out_4(out_6), .out_5(out_7), .out_6(out_8),
    .out_7(out_9), .out_8(out_10), .out_9(out_11), .out_10(out_12), .out_11(out_13));
endmodule
