// Logisim project cpu24.circ as structural Verilog: 26 circuits, main circuit ◇单周期MIPS
module \单周期MIPS  (
  input  IR1,
  input  IR2,
  input  IR3,
  output RegWrite,
  output MemWrite,
  output [31:0] PC,
  output [31:0] IR,
  output [31:0] RDin,
  output [31:0] MDin,
  output [31:0] LedData
);

  wire and_1_out, and_6_out, and_7_out, and_8_out, BGTZ, CLK, clock_2_out, comparator_1_eq, comparator_2_eq,
       comparator_3_eq, comparator_4_eq, comparator_5_eq, comparator_6_gt, comparator_7_eq, comparator_7_lt,
       comparator_8_eq, d_ff_1_q, Go, Halt, IR1_t, IR2_t, IR3_t, IRA, IRB, IRC, mips_alu_1_equal, nand_1_out,
       not_1_out, or_1_out, or_5_out, RST, SH, SignedExt, SRAV, SysCall, W1, W2, W3, \单周期硬布线控制器_1_alu_src ,
       \单周期硬布线控制器_1_beq , \单周期硬布线控制器_1_bne , \单周期硬布线控制器_1_jal , \单周期硬布线控制器_1_jmp , \单周期硬布线控制器_1_jr ,
       \单周期硬布线控制器_1_memtoreg , \单周期硬布线控制器_1_regdst ;
  wire [3:0] adder_1_out_2, \单周期硬布线控制器_1_alu_op ;
  wire [4:0] multiplexer_5_out, multiplexer_6_out, multiplexer_7_out, multiplexer_8_out, multiplexer_11_out;
  wire [12:0] CNT_num;
  wire [15:0] \总周期数 ;
  wire [27:0] adder_1_out, bit_extender_1_out, shifter_1_out;
  wire [31:0] adder_2_out, ALUreslut, bit_extender_2_out, bit_extender_3_out, imm, multiplexer_1_out,
       multiplexer_2_out, multiplexer_3_out, multiplexer_4_out, multiplexer_10_out, multiplexer_12_out,
       multiplexer_14_out, shifter_2_out, SHout, V0, \字数据 ;

  Clock #(.highDuration(1), .lowDuration(1)) clock_1 ();  // open: out
  Button _1 (.out(IRA));
  Button _2 (.out(IRB));
  Button _3 (.out(IRC));
  Multiplexer #(.select(1), .width(32), .disabled("Z"), .enable("false")) multiplexer_1 (
    .in0({adder_1_out_2, adder_1_out}), .in1(adder_2_out), .out(multiplexer_1_out), .sel(or_5_out));
  Button \u_继续运行  (.out(Go));
  LED #(.active("true")) led_1 (.in(W1));
  LED #(.active("true")) led_2 (.in(W2));
  LED #(.active("true")) led_3 (.in(W3));
  Multiplexer #(.select(1), .width(32), .disabled("Z"), .enable("false")) multiplexer_2 (
    .in0(multiplexer_1_out), .in1({adder_1_out_2, shifter_1_out}), .out(multiplexer_2_out),
    .sel(\单周期硬布线控制器_1_jmp ));
  Hex_Digit_Display hex_digit_display_1 (.value(LedData[31:28]));  // open: dp
  Button button_1 (.out(RST));
  Multiplexer #(.select(1), .width(32), .disabled("Z"), .enable("false")) multiplexer_3 (
    .in0(multiplexer_2_out), .in1(V0), .out(multiplexer_3_out), .sel(\单周期硬布线控制器_1_jr ));
  Multiplexer #(.select(1), .width(32), .disabled("Z"), .enable("false")) multiplexer_4 (
    .in0(multiplexer_3_out), .in1(adder_2_out), .out(multiplexer_4_out), .sel(and_6_out));
  or or_1 (or_1_out, Go, ~Halt);  // OR_Gate
  Hex_Digit_Display hex_digit_display_2 (.value(LedData[23:20]));  // open: dp
  Hex_Digit_Display hex_digit_display_3 (.value(LedData[27:24]));  // open: dp
  Register #(.width(32), .trigger("rising"), .Select("low")) u_PC (
    .D(multiplexer_4_out), .en(or_1_out), .Q(PC), .clk(CLK), .clr(RST));
  Hex_Digit_Display hex_digit_display_4 (.value(LedData[19:16]));  // open: dp
  Hex_Digit_Display hex_digit_display_5 (.value(LedData[15:12]));  // open: dp
  // Probe on shifter_1_out
  Comparator #(.width(32), .mode("unsigned")) comparator_1 (.a(V0), .b(32'h22), .eq(comparator_1_eq));  // open: gt, lt
  Comparator #(.width(32), .mode("unsigned")) comparator_2 (.a(V0), .b(32'ha), .eq(comparator_2_eq));  // open: gt, lt
  Comparator #(.width(32), .mode("unsigned")) comparator_3 (.a(V0), .b(32'h27), .eq(comparator_3_eq));  // open: gt, lt
  Comparator #(.width(32), .mode("unsigned")) comparator_4 (.a(V0), .b(32'h25), .eq(comparator_4_eq));  // open: gt, lt
  Comparator #(.width(32), .mode("unsigned")) comparator_5 (.a(V0), .b(32'h26), .eq(comparator_5_eq));  // open: gt, lt
  Hex_Digit_Display hex_digit_display_6 (.value(LedData[7:4]));  // open: dp
  Hex_Digit_Display hex_digit_display_7 (.value(LedData[11:8]));  // open: dp
  // Probe on \总周期数 
  Comparator #(.width(32), .mode("twosComplement")) comparator_6 (
    .a(V0), .b({32{1'b0}}), .gt(comparator_6_gt));  // open: eq, lt
  // Mips_Probe mips_probe_1: pin names not known; wires that end beside it: IR
  Adder #(.width(32)) adder_1 (.a(PC), .b(32'h4), .out({adder_1_out_2, adder_1_out}));  // open: cin, cout
  and and_1 (and_1_out, comparator_1_eq, SysCall);
  // AND_Gate and_2 has open pins: in0=comparator_2_eq, in1=SysCall, out=open
  // AND_Gate and_3 has open pins: in0=comparator_3_eq, in1=SysCall, out=open
  // AND_Gate and_4 has open pins: in0=comparator_4_eq, in1=SysCall, out=open
  // AND_Gate and_5 has open pins: in0=comparator_5_eq, in1=SysCall, out=open
  Hex_Digit_Display hex_digit_display_8 (.value(LedData[3:0]));  // open: dp
  and and_6 (and_6_out, comparator_6_gt, BGTZ);
  ROM #(.addrWidth(10), .dataWidth(32), .Select("high")) rom_1 (.addr(PC[11:2]), .data(IR));
  D_Flip_Flop #(.trigger("high"), .Pre_Clr_Positions("LEGACY"), .NegatePresetClear("false"), .enable("true"), .NewFFLayout("false")) d_ff_1 (.Q(d_ff_1_q));  // open: clk, D, Qn, preset, en, reset
  // Probe on 13'hc
  or or_2 (IR1_t, IR1, IRA);
  Comparator #(.width(13), .mode("twosComplement")) comparator_7 (
    .a(CNT_num), .b(13'hc), .eq(comparator_7_eq), .lt(comparator_7_lt));  // open: gt
  Clock #(.highDuration(1), .lowDuration(1)) clock_2 (.out(clock_2_out));
  Register #(.width(32), .trigger("rising"), .Select("low")) register_1 (
    .D(MDin), .en(and_1_out), .Q(LedData), .clk(CLK), .clr(RST));
  or or_3 (IR2_t, IR2, IRB);
  assign bit_extender_1_out = {{2{1'b0}}, IR[25:0]};  // Bit_Extender bit_extender_1
  Counter #(.width(13), .max('h1fff), .ongoal("stay"), .trigger("rising"), .behavior("old")) counter_1 (
    .count(comparator_7_lt), .Q(CNT_num), .clk(clock_2_out));  // open: load, D, carry, clr, preset
  \单周期硬布线控制器  \u_单周期硬布线控制器_1  (
    .Func(IR[5:0]), .OP(IR[31:26]), .ALU_OP(\单周期硬布线控制器_1_alu_op ), .MemToReg(\单周期硬布线控制器_1_memtoreg ),
    .MemWrite(MemWrite), .ALU_SRC(\单周期硬布线控制器_1_alu_src ), .RegWrite(RegWrite), .SysCALL(SysCall),
    .SignedExt(SignedExt), .RegDst(\单周期硬布线控制器_1_regdst ), .JR(\单周期硬布线控制器_1_jr ), .JMP(\单周期硬布线控制器_1_jmp ),
    .Beq(\单周期硬布线控制器_1_beq ), .JAL(\单周期硬布线控制器_1_jal ), .Bne(\单周期硬布线控制器_1_bne ), .SH(SH), .SRAV(SRAV),
    .BGTZ(BGTZ));
  Multiplexer #(.select(1), .width(5), .disabled("Z"), .enable("false")) multiplexer_5 (
    .in0(IR[25:21]), .in1(5'b00010), .out(multiplexer_5_out), .sel(SysCall));
  Multiplexer #(.select(1), .width(5), .disabled("Z"), .enable("false")) multiplexer_6 (
    .in0(IR[20:16]), .in1(5'b00100), .out(multiplexer_6_out), .sel(SysCall));
  Multiplexer #(.select(1), .width(5), .disabled("Z"), .enable("false")) multiplexer_7 (
    .in0(IR[20:16]), .in1(IR[15:11]), .out(multiplexer_7_out), .sel(\单周期硬布线控制器_1_regdst ));
  nand nand_1 (nand_1_out, d_ff_1_q, comparator_7_eq);
  or or_4 (IR3_t, IR3, IRC);
  Multiplexer #(.select(1), .width(5), .disabled("Z"), .enable("false")) multiplexer_8 (
    .in0(multiplexer_7_out), .in1({5{1'b1}}), .out(multiplexer_8_out), .sel(\单周期硬布线控制器_1_jal ));
  assign bit_extender_2_out = {{16{1'b0}}, IR[15:0]};  // Bit_Extender bit_extender_2
  assign bit_extender_3_out = {{16{IR[15]}}, IR[15:0]};  // Bit_Extender bit_extender_3
  Shifter #(.width(28), .shift("ll")) shifter_1 (.in(bit_extender_1_out), .\dist (5'b00010), .out(shifter_1_out));
  assign CLK = nand_1_out ? clock_2_out : 1'bz;  // Controlled_Buffer controlled_buffer_1
  Pull_Resistor #(.pull(1)) pull_resistor_1 (.node(CLK));
  and and_7 (and_7_out, mips_alu_1_equal, \单周期硬布线控制器_1_beq );
  and and_8 (and_8_out, ~mips_alu_1_equal, \单周期硬布线控制器_1_bne );  // AND_Gate
  MIPS_Regifile mips_regifile_1 (
    .Din(RDin), .Clk(CLK), .R1(V0), .R2(MDin), .WE(RegWrite), .W_num(multiplexer_8_out),
    .R1_num(multiplexer_5_out), .R2_num(multiplexer_6_out));
  Multiplexer #(.select(1), .width(32), .disabled("Z"), .enable("false")) multiplexer_9 (
    .in0(bit_extender_2_out), .in1(bit_extender_3_out), .out(imm), .sel(SignedExt));
  or or_5 (or_5_out, and_7_out, and_8_out);
  Multiplexer #(.select(1), .width(32), .disabled("Z"), .enable("false")) multiplexer_10 (
    .in0(MDin), .in1(imm), .out(multiplexer_10_out), .sel(\单周期硬布线控制器_1_alu_src ));
  Comparator #(.width(32), .mode("twosComplement")) comparator_8 (
    .a(V0), .b(32'h22), .eq(comparator_8_eq));  // open: gt, lt
  // Probe on V0
  Multiplexer #(.select(1), .width(5), .disabled("Z"), .enable("false")) multiplexer_11 (
    .in0(IR[10:6]), .in1(V0[4:0]), .out(multiplexer_11_out), .sel(SRAV));
  Shifter #(.width(32), .shift("ll")) shifter_2 (.in(imm), .\dist (5'b00010), .out(shifter_2_out));
  Adder #(.width(32)) adder_2 (
    .a(shifter_2_out), .b({adder_1_out_2, adder_1_out}), .out(adder_2_out));  // open: cin, cout
  and and_9 (Halt, SysCall, ~comparator_8_eq);  // AND_Gate
  MIPS_ALU mips_alu_1 (
    .X(V0), .Y(multiplexer_10_out), .AluOP(\单周期硬布线控制器_1_alu_op ), .Equal(mips_alu_1_equal),
    .Result(ALUreslut), .shamt(multiplexer_11_out));  // open: Result_2
  Multiplexer #(.select(1), .width(32), .disabled("Z"), .enable("false")) multiplexer_12 (
    .in0(MDin), .in1(SHout), .out(multiplexer_12_out), .sel(SH));
  RAM #(.addrWidth(10), .dataWidth(32), .bus("separate"), .Select("high")) ram_1 (
    .addr(ALUreslut[11:2]), .din(multiplexer_12_out), .data(\字数据 ), .str(MemWrite), .clk(CLK), .clr(RST));  // open: sel, ld
  not not_1 (not_1_out, Halt);
  Multiplexer #(.select(1), .width(32), .disabled("Z"), .enable("false")) multiplexer_13 (
    .in0({\字数据 [31:16], MDin[15:0]}), .in1({MDin[15:0], \字数据 [15:0]}), .out(SHout), .sel(ALUreslut[1]));
  Register #(.width(16), .trigger("rising"), .Select("low")) register_2 (
    .en(not_1_out), .Q(\总周期数 ), .clk(CLK), .clr(RST));  // open: D
  Multiplexer #(.select(1), .width(32), .disabled("Z"), .enable("false")) multiplexer_14 (
    .in0(ALUreslut), .in1(\字数据 ), .out(multiplexer_14_out), .sel(\单周期硬布线控制器_1_memtoreg ));
  Multiplexer #(.select(1), .width(32), .disabled("Z"), .enable("false")) multiplexer_15 (
    .in0(multiplexer_14_out), .in1({adder_1_out_2, adder_1_out}), .out(RDin), .sel(\单周期硬布线控制器_1_jal ));
  // LCD_Video lcd_video_1: pin names not known

  // Notes on the sheet:
  //   中断源
  //   中断等待指示
  //   总复位信号应将除ROM以外所有存储组件全部清零
  //   数码管输出
  //   数码管输出应该用寄存器锁存，否则显示数据只能一闪而过
  //   指令存储器
  //   指令字
  //   contents of rom_1 (hex, n*v repeats v):
  //   20090000 200b0020 20110001 20120001 a5310000 112020 20020022 c 2328820 21290002 216bffff 1560fff8
  //   200b0010 20090000 8d310000 112020 20020022 c 21290004 216bffff 1560fff9 2002000a c
  //   控制位
  //   暂停节拍，不能为0
  //   OP
  //   Func
  //   rs
  //   rt
  //   rd
  //   shamt
  //   imm16
  //   戳工具置1进入计数暂停模式，ctrl+k时钟自动运行到对应节拍暂停
  //   ctrl+k关闭时钟连续运行，将控制位置零，进入单步调试模式调试
  //   用这个时钟源需要去掉电路中的其他时钟源
  //   JMP
  //   JR
  //   OP
  //   Func
  //   Syscall
  //   Beq
  //   Bne
  //   MemToReg
  //   MemWrite
  //   AluOP
  //   AluSrcB
  //   RegWrite
  //   JAL
  //   RegDst
  //   可计数暂停的时钟源
  //   为方便自动评测，需要输出PC，IR，寄存器堆写如数据RDin
  //   RAM写使能MemWrite、RAM写入数据MDin等信号
endmodule

// 单周期硬布线控制器
module \单周期硬布线控制器  (
  input  [5:0] OP,
  input  [5:0] Func,
  output [3:0] ALU_OP,
  output MemToReg,
  output MemWrite,
  output ALU_SRC,
  output RegWrite,
  output SysCALL,
  output SignedExt,
  output RegDst,
  output Beq,
  output Bne,
  output JR,
  output JMP,
  output JAL,
  output SH,
  output SRAV,
  output BGTZ
);

  \运算控制器自动生成  \u_运算控制器自动生成_1  (
    .OP0(OP[0]), .OP1(OP[1]), .OP2(OP[2]), .OP3(OP[3]), .OP4(OP[4]), .OP5(OP[5]), .F0(Func[0]), .F1(Func[1]),
    .F2(Func[2]), .F3(Func[3]), .F4(Func[4]), .F5(Func[5]), .S0(ALU_OP[0]), .S1(ALU_OP[1]), .S2(ALU_OP[2]),
    .S3(ALU_OP[3]));
  \控制信号自动生成  \u_控制信号自动生成_1  (
    .OP0(OP[0]), .OP1(OP[1]), .OP2(OP[2]), .OP3(OP[3]), .OP4(OP[4]), .OP5(OP[5]), .F0(Func[0]), .F1(Func[1]),
    .F2(Func[2]), .F3(Func[3]), .F4(Func[4]), .F5(Func[5]), .MemToReg(MemToReg), .MemWrite(MemWrite),
    .ALU_SRC(ALU_SRC), .RegWrite(RegWrite), .SysCALL(SysCALL), .SignedExt(SignedExt), .RegDst(RegDst),
    .BEQ(Beq), .BNE(Bne), .JR(JR), .JUMP(JMP), .JAL(JAL), .SH(SH), .SRAV(SRAV), .BGTZ(BGTZ));

  // Other names for the same wires on the sheet: OP_CODE[5:0] = OP

  // Notes on the sheet:
  //   运算器控制器，根据指令生成运算器功能选择信号
  //   控制信号生成，产生数据通路需要的其他控制信号
endmodule

// 运算器控制器
module \运算控制器自动生成  (
  input  OP0,
  input  OP1,
  input  OP2,
  input  OP3,
  input  OP4,
  input  OP5,
  input  F0,
  input  F1,
  input  F2,
  input  F3,
  input  F4,
  input  F5,
  output S0,
  output S1,
  output S2,
  output S3
);

  wire and_1_out, and_2_out, and_3_out, and_4_out, and_5_out, and_6_out, and_7_out, and_8_out, and_9_out,
       and_10_out, and_11_out, and_12_out, and_13_out, and_14_out, and_15_out, and_16_out, and_17_out,
       and_18_out, and_19_out, and_20_out, and_21_out, and_22_out, and_23_out, and_24_out, and_25_out,
       and_26_out, and_27_out, and_28_out, and_29_out, and_30_out, and_31_out, and_32_out, and_33_out,
       and_34_out, and_35_out, and_36_out, and_37_out, and_38_out, and_39_out, not_1_out, not_2_out,
       not_3_out, not_4_out, not_5_out, not_6_out, not_7_out, not_8_out, not_9_out, not_10_out, not_11_out,
       not_12_out, not_13_out, not_14_out, not_15_out, not_16_out, not_17_out, not_18_out, not_19_out,
       not_20_out, not_21_out, not_22_out, not_23_out, not_24_out, not_25_out, not_26_out, not_27_out,
       not_28_out, not_29_out, not_30_out, not_31_out, not_32_out, not_33_out, not_34_out, not_35_out,
       not_36_out, not_37_out, not_38_out, not_39_out, not_40_out, not_41_out, not_42_out, not_43_out,
       not_44_out, not_45_out, not_46_out, not_47_out, not_48_out, not_49_out, not_50_out, not_51_out,
       not_52_out, not_53_out, not_54_out, not_55_out, not_56_out, not_57_out, not_58_out, not_59_out,
       not_60_out, not_61_out, not_62_out, not_63_out, not_64_out, not_65_out, not_66_out, not_67_out,
       not_68_out, not_69_out, not_70_out, not_71_out, not_72_out, not_73_out, not_74_out, not_75_out,
       not_76_out, not_77_out, not_78_out, not_79_out, not_80_out, not_81_out, not_82_out, not_83_out,
       not_84_out, not_85_out, not_86_out, not_87_out, not_88_out, not_89_out, not_90_out, not_91_out,
       not_92_out, not_93_out, not_94_out, not_95_out, not_96_out, not_97_out, not_98_out, not_99_out,
       not_100_out, not_101_out, not_102_out, not_103_out, not_104_out, not_105_out, not_106_out,
       not_107_out, not_108_out, not_109_out, not_110_out, not_111_out, not_112_out, not_113_out,
       not_114_out, not_115_out, not_116_out, not_117_out, not_118_out, not_119_out, not_120_out,
       not_121_out, not_122_out, not_123_out, not_124_out, not_125_out, not_126_out, not_127_out,
       not_128_out, not_129_out, not_130_out, not_131_out, not_132_out, not_133_out, not_134_out,
       not_135_out, not_136_out, not_137_out, not_138_out, not_139_out, not_140_out, not_141_out,
       not_142_out, not_143_out, not_144_out, not_145_out, not_146_out, not_147_out, not_148_out,
       not_149_out, not_150_out, not_151_out, not_152_out, not_153_out, not_154_out, not_155_out,
       not_156_out, not_157_out, not_158_out, not_159_out, not_160_out, not_161_out, not_162_out,
       not_163_out, not_164_out, not_165_out, not_166_out, not_167_out, not_168_out, not_169_out,
       not_170_out, not_171_out, not_172_out, not_173_out, not_174_out, not_175_out, not_176_out,
       not_177_out, not_178_out, not_179_out, not_180_out, not_181_out, not_182_out, not_183_out,
       not_184_out, not_185_out, not_186_out, not_187_out, not_188_out, not_189_out, not_190_out,
       not_191_out, not_192_out, not_193_out, not_194_out, not_195_out, not_196_out, not_197_out,
       not_198_out, not_199_out, not_200_out, not_201_out, not_202_out, not_203_out, not_204_out,
       not_205_out, not_206_out, not_207_out, not_208_out, not_209_out, not_210_out, not_211_out,
       not_212_out, not_213_out, not_214_out, not_215_out, not_216_out, not_217_out, not_218_out,
       not_219_out, not_220_out, not_221_out, not_222_out, not_223_out, not_224_out, not_225_out,
       not_226_out, not_227_out, not_228_out, not_229_out, not_230_out, not_231_out, not_232_out,
       not_233_out, not_234_out, not_235_out, not_236_out, not_237_out, not_238_out, not_239_out,
       not_240_out, not_241_out, not_242_out, not_243_out, not_244_out, not_245_out, not_246_out,
       not_247_out, not_248_out, not_249_out, not_250_out, not_251_out, not_252_out, not_253_out,
       not_254_out, not_255_out, not_256_out, not_257_out;

  not not_1 (not_1_out, OP5);
  not not_2 (not_2_out, OP4);
  not not_3 (not_3_out, OP3);
  not not_4 (not_4_out, OP2);
  not not_5 (not_5_out, OP1);
  not not_6 (not_6_out, OP0);
  not not_7 (not_7_out, F5);
  not not_8 (not_8_out, F4);
  not not_9 (not_9_out, F3);
  not not_10 (not_10_out, F2);
  not not_11 (not_11_out, OP5);
  not not_12 (not_12_out, OP4);
  not not_13 (not_13_out, OP3);
  not not_14 (not_14_out, OP2);
  not not_15 (not_15_out, OP1);
  not not_16 (not_16_out, OP0);
  not not_17 (not_17_out, F4);
  not not_18 (not_18_out, F3);
  not not_19 (not_19_out, F2);
  not not_20 (not_20_out, F1);
  not not_21 (not_21_out, F0);
  not not_22 (not_22_out, OP5);
  not not_23 (not_23_out, OP4);
  not not_24 (not_24_out, OP3);
  not not_25 (not_25_out, OP2);
  not not_26 (not_26_out, OP1);
  not not_27 (not_27_out, OP0);
  not not_28 (not_28_out, F4);
  not not_29 (not_29_out, F3);
  not not_30 (not_30_out, F2);
  not not_31 (not_31_out, F1);
  not not_32 (not_32_out, OP5);
  not not_33 (not_33_out, OP4);
  not not_34 (not_34_out, OP3);
  not not_35 (not_35_out, OP2);
  not not_36 (not_36_out, OP1);
  not not_37 (not_37_out, OP0);
  not not_38 (not_38_out, F4);
  not not_39 (not_39_out, F3);
  not not_40 (not_40_out, F1);
  not not_41 (not_41_out, F0);
  not not_42 (not_42_out, OP5);
  not not_43 (not_43_out, OP4);
  not not_44 (not_44_out, OP3);
  not not_45 (not_45_out, OP2);
  not not_46 (not_46_out, OP1);
  not not_47 (not_47_out, OP0);
  not not_48 (not_48_out, F4);
  not not_49 (not_49_out, F2);
  not not_50 (not_50_out, F0);
  not not_51 (not_51_out, OP5);
  not not_52 (not_52_out, OP4);
  not not_53 (not_53_out, OP2);
  not not_54 (not_54_out, OP1);
  not not_55 (not_55_out, OP0);
  not not_56 (not_56_out, OP5);
  not not_57 (not_57_out, OP4);
  not not_58 (not_58_out, OP1);
  not not_59 (not_59_out, OP0);
  not not_60 (not_60_out, OP5);
  not not_61 (not_61_out, OP4);
  not not_62 (not_62_out, OP2);
  not not_63 (not_63_out, OP1);
  not not_64 (not_64_out, OP5);
  not not_65 (not_65_out, OP4);
  not not_66 (not_66_out, OP2);
  not not_67 (not_67_out, OP0);
  not not_68 (not_68_out, OP4);
  not not_69 (not_69_out, OP3);
  not not_70 (not_70_out, OP2);
  not not_71 (not_71_out, OP4);
  not not_72 (not_72_out, OP2);
  not not_73 (not_73_out, OP5);
  not not_74 (not_74_out, OP4);
  not not_75 (not_75_out, OP3);
  not not_76 (not_76_out, OP2);
  not not_77 (not_77_out, OP1);
  not not_78 (not_78_out, OP0);
  not not_79 (not_79_out, F5);
  not not_80 (not_80_out, F4);
  not not_81 (not_81_out, F3);
  not not_82 (not_82_out, OP5);
  not not_83 (not_83_out, OP4);
  not not_84 (not_84_out, OP0);
  not not_85 (not_85_out, OP4);
  not not_86 (not_86_out, OP2);
  not not_87 (not_87_out, OP1);
  not not_88 (not_88_out, OP5);
  not not_89 (not_89_out, OP4);
  not not_90 (not_90_out, OP3);
  not not_91 (not_91_out, OP2);
  not not_92 (not_92_out, OP1);
  not not_93 (not_93_out, OP0);
  not not_94 (not_94_out, F5);
  not not_95 (not_95_out, F4);
  not not_96 (not_96_out, F3);
  not not_97 (not_97_out, F2);
  not not_98 (not_98_out, F0);
  not not_99 (not_99_out, OP5);
  not not_100 (not_100_out, OP4);
  not not_101 (not_101_out, OP3);
  not not_102 (not_102_out, OP2);
  not not_103 (not_103_out, OP1);
  not not_104 (not_104_out, OP0);
  not not_105 (not_105_out, F4);
  not not_106 (not_106_out, F3);
  not not_107 (not_107_out, F2);
  not not_108 (not_108_out, F0);
  not not_109 (not_109_out, OP5);
  not not_110 (not_110_out, OP4);
  not not_111 (not_111_out, OP3);
  not not_112 (not_112_out, OP2);
  not not_113 (not_113_out, OP1);
  not not_114 (not_114_out, OP0);
  not not_115 (not_115_out, F4);
  not not_116 (not_116_out, F3);
  not not_117 (not_117_out, F1);
  not not_118 (not_118_out, F0);
  not not_119 (not_119_out, OP5);
  not not_120 (not_120_out, OP4);
  not not_121 (not_121_out, OP3);
  not not_122 (not_122_out, OP2);
  not not_123 (not_123_out, OP1);
  not not_124 (not_124_out, OP0);
  not not_125 (not_125_out, F4);
  not not_126 (not_126_out, F3);
  not not_127 (not_127_out, OP5);
  not not_128 (not_128_out, OP4);
  not not_129 (not_129_out, OP3);
  not not_130 (not_130_out, OP2);
  not not_131 (not_131_out, OP1);
  not not_132 (not_132_out, OP0);
  not not_133 (not_133_out, F4);
  not not_134 (not_134_out, F2);
  not not_135 (not_135_out, F0);
  not not_136 (not_136_out, OP5);
  not not_137 (not_137_out, OP4);
  not not_138 (not_138_out, OP1);
  not not_139 (not_139_out, OP0);
  not not_140 (not_140_out, OP5);
  not not_141 (not_141_out, OP4);
  not not_142 (not_142_out, OP2);
  not not_143 (not_143_out, OP0);
  not not_144 (not_144_out, OP5);
  not not_145 (not_145_out, OP4);
  not not_146 (not_146_out, OP3);
  not not_147 (not_147_out, OP2);
  not not_148 (not_148_out, OP1);
  not not_149 (not_149_out, OP0);
  not not_150 (not_150_out, F4);
  not not_151 (not_151_out, F3);
  not not_152 (not_152_out, F2);
  not not_153 (not_153_out, F1);
  not not_154 (not_154_out, F0);
  not not_155 (not_155_out, OP5);
  not not_156 (not_156_out, OP4);
  not not_157 (not_157_out, OP3);
  not not_158 (not_158_out, OP2);
  not not_159 (not_159_out, OP1);
  not not_160 (not_160_out, OP0);
  not not_161 (not_161_out, F4);
  not not_162 (not_162_out, F3);
  not not_163 (not_163_out, F2);
  not not_164 (not_164_out, F1);
  not not_165 (not_165_out, OP5);
  not not_166 (not_166_out, OP4);
  not not_167 (not_167_out, OP3);
  not not_168 (not_168_out, OP2);
  not not_169 (not_169_out, OP1);
  not not_170 (not_170_out, OP0);
  not not_171 (not_171_out, F4);
  not not_172 (not_172_out, F3);
  not not_173 (not_173_out, F2);
  not not_174 (not_174_out, F0);
  not not_175 (not_175_out, OP5);
  not not_176 (not_176_out, OP4);
  not not_177 (not_177_out, OP3);
  not not_178 (not_178_out, OP2);
  not not_179 (not_179_out, OP1);
  not not_180 (not_180_out, OP0);
  not not_181 (not_181_out, F4);
  not not_182 (not_182_out, F3);
  not not_183 (not_183_out, F1);
  not not_184 (not_184_out, F0);
  not not_185 (not_185_out, OP5);
  not not_186 (not_186_out, OP4);
  not not_187 (not_187_out, OP3);
  not not_188 (not_188_out, OP2);
  not not_189 (not_189_out, OP1);
  not not_190 (not_190_out, OP0);
  not not_191 (not_191_out, F4);
  not not_192 (not_192_out, F2);
  not not_193 (not_193_out, OP5);
  not not_194 (not_194_out, OP4);
  not not_195 (not_195_out, OP2);
  not not_196 (not_196_out, OP1);
  not not_197 (not_197_out, OP0);
  not not_198 (not_198_out, OP5);
  not not_199 (not_199_out, OP4);
  not not_200 (not_200_out, OP1);
  not not_201 (not_201_out, OP0);
  not not_202 (not_202_out, OP5);
  not not_203 (not_203_out, OP4);
  not not_204 (not_204_out, OP2);
  not not_205 (not_205_out, OP1);
  not not_206 (not_206_out, OP4);
  not not_207 (not_207_out, OP3);
  not not_208 (not_208_out, OP2);
  not not_209 (not_209_out, OP4);
  not not_210 (not_210_out, OP2);
  not not_211 (not_211_out, OP4);
  not not_212 (not_212_out, OP2);
  not not_213 (not_213_out, OP1);
  not not_214 (not_214_out, OP5);
  not not_215 (not_215_out, OP4);
  not not_216 (not_216_out, OP3);
  not not_217 (not_217_out, OP2);
  not not_218 (not_218_out, OP1);
  not not_219 (not_219_out, OP0);
  not not_220 (not_220_out, F4);
  not not_221 (not_221_out, F3);
  not not_222 (not_222_out, F1);
  not not_223 (not_223_out, OP5);
  not not_224 (not_224_out, OP4);
  not not_225 (not_225_out, OP3);
  not not_226 (not_226_out, OP2);
  not not_227 (not_227_out, OP1);
  not not_228 (not_228_out, OP0);
  not not_229 (not_229_out, F4);
  not not_230 (not_230_out, F3);
  not not_231 (not_231_out, OP5);
  not not_232 (not_232_out, OP4);
  not not_233 (not_233_out, OP3);
  not not_234 (not_234_out, OP2);
  not not_235 (not_235_out, OP1);
  not not_236 (not_236_out, OP0);
  not not_237 (not_237_out, F4);
  not not_238 (not_238_out, F2);
  not not_239 (not_239_out, F0);
  not not_240 (not_240_out, OP5);
  not not_241 (not_241_out, OP4);
  not not_242 (not_242_out, OP3);
  not not_243 (not_243_out, OP2);
  not not_244 (not_244_out, OP1);
  not not_245 (not_245_out, OP0);
  not not_246 (not_246_out, F4);
  not not_247 (not_247_out, F2);
  not not_248 (not_248_out, OP5);
  not not_249 (not_249_out, OP4);
  not not_250 (not_250_out, OP2);
  not not_251 (not_251_out, OP0);
  not not_252 (not_252_out, OP5);
  not not_253 (not_253_out, OP4);
  not not_254 (not_254_out, OP1);
  not not_255 (not_255_out, OP5);
  not not_256 (not_256_out, OP4);
  not not_257 (not_257_out, OP0);
  and and_1 (and_1_out, not_1_out, not_2_out, not_3_out, not_4_out, not_5_out, not_6_out, not_7_out, not_8_out, not_9_out, not_10_out, F1, F0);
  and and_2 (and_2_out, not_11_out, not_12_out, not_13_out, not_14_out, not_15_out, not_16_out, F5, not_17_out, not_18_out, not_19_out, not_20_out, not_21_out);
  and and_3 (and_3_out, not_22_out, not_23_out, not_24_out, not_25_out, not_26_out, not_27_out, F5, not_28_out, not_29_out, not_30_out, not_31_out, F0);
  and and_4 (and_4_out, not_32_out, not_33_out, not_34_out, not_35_out, not_36_out, not_37_out, F5, not_38_out, not_39_out, F2, not_40_out, not_41_out);
  and and_5 (and_5_out, not_42_out, not_43_out, not_44_out, not_45_out, not_46_out, not_47_out, F5, not_48_out, F3, not_49_out, F1, not_50_out);
  and and_6 (and_6_out, not_51_out, not_52_out, OP3, not_53_out, not_54_out, not_55_out);
  and and_7 (and_7_out, not_56_out, not_57_out, OP3, OP2, not_58_out, not_59_out);
  and and_8 (and_8_out, not_60_out, not_61_out, OP3, not_62_out, not_63_out, OP0);
  and and_9 (and_9_out, not_64_out, not_65_out, OP3, not_66_out, OP1, not_67_out);
  and and_10 (and_10_out, OP5, not_68_out, not_69_out, not_70_out, OP1, OP0);
  and and_11 (and_11_out, OP5, not_71_out, OP3, not_72_out, OP1, OP0);
  and and_12 (and_12_out, not_73_out, not_74_out, not_75_out, not_76_out, not_77_out, not_78_out, not_79_out, not_80_out, not_81_out, F2, F1, F0);
  and and_13 (and_13_out, not_82_out, not_83_out, OP3, OP2, OP1, not_84_out);
  and and_14 (and_14_out, OP5, not_85_out, OP3, not_86_out, not_87_out, OP0);
  and and_15 (and_15_out, not_88_out, not_89_out, not_90_out, not_91_out, not_92_out, not_93_out, not_94_out, not_95_out, not_96_out, not_97_out, F1, not_98_out);
  and and_16 (and_16_out, not_99_out, not_100_out, not_101_out, not_102_out, not_103_out, not_104_out, F5, not_105_out, not_106_out, not_107_out, F1, not_108_out);
  and and_17 (and_17_out, not_109_out, not_110_out, not_111_out, not_112_out, not_113_out, not_114_out, F5, not_115_out, not_116_out, F2, not_117_out, not_118_out);
  and and_18 (and_18_out, not_119_out, not_120_out, not_121_out, not_122_out, not_123_out, not_124_out, F5, not_125_out, not_126_out, F2, F1, F0);
  and and_19 (and_19_out, not_127_out, not_128_out, not_129_out, not_130_out, not_131_out, not_132_out, F5, not_133_out, F3, not_134_out, F1, not_135_out);
  and and_20 (and_20_out, not_136_out, not_137_out, OP3, OP2, not_138_out, not_139_out);
  and and_21 (and_21_out, not_140_out, not_141_out, OP3, not_142_out, OP1, not_143_out);
  and and_22 (and_22_out, not_144_out, not_145_out, not_146_out, not_147_out, not_148_out, not_149_out, F5, not_150_out, not_151_out, not_152_out, not_153_out, not_154_out);
  and and_23 (and_23_out, not_155_out, not_156_out, not_157_out, not_158_out, not_159_out, not_160_out, F5, not_161_out, not_162_out, not_163_out, not_164_out, F0);
  and and_24 (and_24_out, not_165_out, not_166_out, not_167_out, not_168_out, not_169_out, not_170_out, F5, not_171_out, not_172_out, not_173_out, F1, not_174_out);
  and and_25 (and_25_out, not_175_out, not_176_out, not_177_out, not_178_out, not_179_out, not_180_out, F5, not_181_out, not_182_out, F2, not_183_out, not_184_out);
  and and_26 (and_26_out, not_185_out, not_186_out, not_187_out, not_188_out, not_189_out, not_190_out, F5, not_191_out, F3, not_192_out, F1, F0);
  and and_27 (and_27_out, not_193_out, not_194_out, OP3, not_195_out, not_196_out, not_197_out);
  and and_28 (and_28_out, not_198_out, not_199_out, OP3, OP2, not_200_out, not_201_out);
  and and_29 (and_29_out, not_202_out, not_203_out, OP3, not_204_out, not_205_out, OP0);
  and and_30 (and_30_out, OP5, not_206_out, not_207_out, not_208_out, OP1, OP0);
  and and_31 (and_31_out, OP5, not_209_out, OP3, not_210_out, OP1, OP0);
  and and_32 (and_32_out, OP5, not_211_out, OP3, not_212_out, not_213_out, OP0);
  and and_33 (and_33_out, not_214_out, not_215_out, not_216_out, not_217_out, not_218_out, not_219_out, F5, not_220_out, not_221_out, F2, not_222_out, F0);
  and and_34 (and_34_out, not_223_out, not_224_out, not_225_out, not_226_out, not_227_out, not_228_out, F5, not_229_out, not_230_out, F2, F1, F0);
  and and_35 (and_35_out, not_231_out, not_232_out, not_233_out, not_234_out, not_235_out, not_236_out, F5, not_237_out, F3, not_238_out, F1, not_239_out);
  and and_36 (and_36_out, not_240_out, not_241_out, not_242_out, not_243_out, not_244_out, not_245_out, F5, not_246_out, F3, not_247_out, F1, F0);
  and and_37 (and_37_out, not_248_out, not_249_out, OP3, not_250_out, OP1, not_251_out);
  and and_38 (and_38_out, not_252_out, not_253_out, OP3, OP2, not_254_out, OP0);
  and and_39 (and_39_out, not_255_out, not_256_out, OP3, OP2, OP1, not_257_out);
  or or_1 (S1, and_15_out, and_16_out, and_17_out, and_18_out, and_19_out, and_20_out, and_21_out);
  or or_2 (S2, and_22_out, and_23_out, and_24_out, and_25_out, and_26_out, and_27_out, and_28_out, and_29_out, and_30_out, and_31_out, and_32_out);
  or or_3 (S3, and_33_out, and_34_out, and_35_out, and_36_out, and_37_out, and_38_out, and_39_out);
  or or_4 (S0, and_1_out, and_2_out, and_3_out, and_4_out, and_5_out, and_6_out, and_7_out, and_8_out, and_9_out, and_10_out, and_11_out, and_12_out, and_13_out, and_14_out);
endmodule

// 控制信号生成
module \控制信号自动生成  (
  input  OP0,
  input  OP1,
  input  OP2,
  input  OP3,
  input  OP4,
  input  OP5,
  input  F0,
  input  F1,
  input  F2,
  input  F3,
  input  F4,
  input  F5,
  output MemToReg,
  output MemWrite,
  output ALU_SRC,
  output RegWrite,
  output SysCALL,
  output SignedExt,
  output RegDst,
  output BEQ,
  output BNE,
  output JR,
  output JUMP,
  output JAL,
  output SH,
  output SRAV,
  output BGTZ
);

  wire and_3_out, and_4_out, and_5_out, and_6_out, and_7_out, and_8_out, and_9_out, and_10_out, and_11_out,
       and_12_out, and_13_out, and_14_out, and_16_out, and_17_out, and_18_out, and_19_out, and_20_out,
       and_21_out, and_22_out, and_23_out, and_24_out, and_25_out, and_29_out, and_30_out, not_1_out,
       not_2_out, not_3_out, not_4_out, not_5_out, not_6_out, not_7_out, not_8_out, not_9_out, not_10_out,
       not_11_out, not_12_out, not_13_out, not_14_out, not_15_out, not_16_out, not_17_out, not_18_out,
       not_19_out, not_20_out, not_21_out, not_22_out, not_23_out, not_24_out, not_25_out, not_26_out,
       not_27_out, not_28_out, not_29_out, not_30_out, not_31_out, not_32_out, not_33_out, not_34_out,
       not_35_out, not_36_out, not_37_out, not_38_out, not_39_out, not_40_out, not_41_out, not_42_out,
       not_43_out, not_44_out, not_45_out, not_46_out, not_47_out, not_48_out, not_49_out, not_50_out,
       not_51_out, not_52_out, not_53_out, not_54_out, not_55_out, not_56_out, not_57_out, not_58_out,
       not_59_out, not_60_out, not_61_out, not_62_out, not_63_out, not_64_out, not_65_out, not_66_out,
       not_67_out, not_68_out, not_69_out, not_70_out, not_71_out, not_72_out, not_73_out, not_74_out,
       not_75_out, not_76_out, not_77_out, not_78_out, not_79_out, not_80_out, not_81_out, not_82_out,
       not_83_out, not_84_out, not_85_out, not_86_out, not_87_out, not_88_out, not_89_out, not_90_out,
       not_91_out, not_92_out, not_93_out, not_94_out, not_95_out, not_96_out, not_97_out, not_98_out,
       not_99_out, not_100_out, not_101_out, not_102_out, not_103_out, not_104_out, not_105_out, not_106_out,
       not_107_out, not_108_out, not_109_out, not_110_out, not_111_out, not_112_out, not_113_out,
       not_114_out, not_115_out, not_116_out, not_117_out, not_118_out, not_119_out, not_120_out,
       not_121_out, not_122_out, not_123_out, not_124_out, not_125_out, not_126_out, not_127_out,
       not_128_out, not_129_out, not_130_out, not_131_out, not_132_out, not_133_out, not_134_out,
       not_135_out, not_136_out, not_137_out, not_138_out, not_139_out, not_140_out, not_141_out,
       not_142_out, not_143_out, not_144_out, not_145_out, not_146_out, not_147_out, not_148_out,
       not_149_out, not_150_out, not_151_out, not_152_out, not_153_out, not_154_out, not_155_out,
       not_156_out, not_157_out, not_158_out, not_159_out, not_160_out, not_161_out, not_162_out,
       not_163_out, not_164_out, not_165_out, not_166_out, not_167_out, not_168_out, not_169_out,
       not_170_out, not_171_out, not_172_out, not_173_out, not_174_out, not_175_out, not_176_out,
       not_177_out, not_178_out, not_179_out, not_180_out, not_181_out, not_182_out, not_183_out,
       not_184_out, not_185_out, not_186_out, not_187_out, not_188_out, not_189_out, not_190_out, not_191_out;

  not not_1 (not_1_out, OP2);
  not not_2 (not_2_out, OP3);
  not not_3 (not_3_out, OP4);
  not not_4 (not_4_out, OP2);
  not not_5 (not_5_out, OP4);
  not not_6 (not_6_out, OP0);
  not not_7 (not_7_out, OP4);
  not not_8 (not_8_out, OP5);
  not not_9 (not_9_out, OP1);
  not not_10 (not_10_out, OP4);
  not not_11 (not_11_out, OP5);
  not not_12 (not_12_out, OP1);
  not not_13 (not_13_out, OP2);
  not not_14 (not_14_out, OP4);
  not not_15 (not_15_out, OP2);
  not not_16 (not_16_out, OP4);
  not not_17 (not_17_out, OP0);
  not not_18 (not_18_out, OP1);
  not not_19 (not_19_out, OP2);
  not not_20 (not_20_out, OP4);
  not not_21 (not_21_out, OP5);
  not not_22 (not_22_out, F0);
  not not_23 (not_23_out, F2);
  not not_24 (not_24_out, F3);
  not not_25 (not_25_out, F4);
  not not_26 (not_26_out, OP0);
  not not_27 (not_27_out, OP1);
  not not_28 (not_28_out, OP2);
  not not_29 (not_29_out, OP4);
  not not_30 (not_30_out, OP5);
  not not_31 (not_31_out, F1);
  not not_32 (not_32_out, F3);
  not not_33 (not_33_out, F4);
  not not_34 (not_34_out, OP0);
  not not_35 (not_35_out, OP1);
  not not_36 (not_36_out, OP2);
  not not_37 (not_37_out, OP4);
  not not_38 (not_38_out, OP5);
  not not_39 (not_39_out, F2);
  not not_40 (not_40_out, F4);
  not not_41 (not_41_out, OP0);
  not not_42 (not_42_out, OP1);
  not not_43 (not_43_out, OP2);
  not not_44 (not_44_out, OP4);
  not not_45 (not_45_out, OP5);
  not not_46 (not_46_out, F3);
  not not_47 (not_47_out, F4);
  not not_48 (not_48_out, F5);
  not not_49 (not_49_out, OP0);
  not not_50 (not_50_out, OP1);
  not not_51 (not_51_out, OP2);
  not not_52 (not_52_out, OP4);
  not not_53 (not_53_out, OP5);
  not not_54 (not_54_out, F3);
  not not_55 (not_55_out, F4);
  not not_56 (not_56_out, OP0);
  not not_57 (not_57_out, OP4);
  not not_58 (not_58_out, OP5);
  not not_59 (not_59_out, OP1);
  not not_60 (not_60_out, OP4);
  not not_61 (not_61_out, OP5);
  not not_62 (not_62_out, OP2);
  not not_63 (not_63_out, OP3);
  not not_64 (not_64_out, OP4);
  not not_65 (not_65_out, OP0);
  not not_66 (not_66_out, OP1);
  not not_67 (not_67_out, OP2);
  not not_68 (not_68_out, OP3);
  not not_69 (not_69_out, OP4);
  not not_70 (not_70_out, OP5);
  not not_71 (not_71_out, F0);
  not not_72 (not_72_out, F1);
  not not_73 (not_73_out, F4);
  not not_74 (not_74_out, F5);
  not not_75 (not_75_out, OP5);
  not not_76 (not_76_out, OP4);
  not not_77 (not_77_out, OP3);
  not not_78 (not_78_out, OP1);
  not not_79 (not_79_out, OP5);
  not not_80 (not_80_out, OP4);
  not not_81 (not_81_out, OP2);
  not not_82 (not_82_out, OP1);
  not not_83 (not_83_out, OP0);
  not not_84 (not_84_out, OP5);
  not not_85 (not_85_out, OP4);
  not not_86 (not_86_out, OP2);
  not not_87 (not_87_out, OP1);
  not not_88 (not_88_out, OP5);
  not not_89 (not_89_out, OP4);
  not not_90 (not_90_out, OP2);
  not not_91 (not_91_out, OP0);
  not not_92 (not_92_out, OP5);
  not not_93 (not_93_out, OP4);
  not not_94 (not_94_out, OP3);
  not not_95 (not_95_out, OP0);
  not not_96 (not_96_out, OP1);
  not not_97 (not_97_out, OP2);
  not not_98 (not_98_out, OP3);
  not not_99 (not_99_out, OP4);
  not not_100 (not_100_out, OP5);
  not not_101 (not_101_out, F0);
  not not_102 (not_102_out, F2);
  not not_103 (not_103_out, F3);
  not not_104 (not_104_out, F4);
  not not_105 (not_105_out, OP0);
  not not_106 (not_106_out, OP1);
  not not_107 (not_107_out, OP2);
  not not_108 (not_108_out, OP3);
  not not_109 (not_109_out, OP4);
  not not_110 (not_110_out, OP5);
  not not_111 (not_111_out, F1);
  not not_112 (not_112_out, F3);
  not not_113 (not_113_out, F4);
  not not_114 (not_114_out, OP0);
  not not_115 (not_115_out, OP1);
  not not_116 (not_116_out, OP2);
  not not_117 (not_117_out, OP3);
  not not_118 (not_118_out, OP4);
  not not_119 (not_119_out, OP5);
  not not_120 (not_120_out, F2);
  not not_121 (not_121_out, F4);
  not not_122 (not_122_out, OP0);
  not not_123 (not_123_out, OP1);
  not not_124 (not_124_out, OP2);
  not not_125 (not_125_out, OP3);
  not not_126 (not_126_out, OP4);
  not not_127 (not_127_out, OP5);
  not not_128 (not_128_out, F3);
  not not_129 (not_129_out, F4);
  not not_130 (not_130_out, F5);
  not not_131 (not_131_out, OP0);
  not not_132 (not_132_out, OP1);
  not not_133 (not_133_out, OP2);
  not not_134 (not_134_out, OP3);
  not not_135 (not_135_out, OP4);
  not not_136 (not_136_out, OP5);
  not not_137 (not_137_out, F3);
  not not_138 (not_138_out, F4);
  not not_139 (not_139_out, OP0);
  not not_140 (not_140_out, OP1);
  not not_141 (not_141_out, OP3);
  not not_142 (not_142_out, OP4);
  not not_143 (not_143_out, OP5);
  not not_144 (not_144_out, OP1);
  not not_145 (not_145_out, OP3);
  not not_146 (not_146_out, OP4);
  not not_147 (not_147_out, OP5);
  not not_148 (not_148_out, OP0);
  not not_149 (not_149_out, OP1);
  not not_150 (not_150_out, OP2);
  not not_151 (not_151_out, OP3);
  not not_152 (not_152_out, OP4);
  not not_153 (not_153_out, OP5);
  not not_154 (not_154_out, F0);
  not not_155 (not_155_out, F1);
  not not_156 (not_156_out, F2);
  not not_157 (not_157_out, F4);
  not not_158 (not_158_out, F5);
  not not_159 (not_159_out, OP0);
  not not_160 (not_160_out, OP2);
  not not_161 (not_161_out, OP3);
  not not_162 (not_162_out, OP4);
  not not_163 (not_163_out, OP5);
  not not_164 (not_164_out, F0);
  not not_165 (not_165_out, F1);
  not not_166 (not_166_out, F2);
  not not_167 (not_167_out, F4);
  not not_168 (not_168_out, F5);
  not not_169 (not_169_out, OP2);
  not not_170 (not_170_out, OP3);
  not not_171 (not_171_out, OP4);
  not not_172 (not_172_out, OP5);
  not not_173 (not_173_out, OP2);
  not not_174 (not_174_out, OP3);
  not not_175 (not_175_out, OP4);
  not not_176 (not_176_out, OP5);
  not not_177 (not_177_out, OP1);
  not not_178 (not_178_out, OP2);
  not not_179 (not_179_out, OP4);
  not not_180 (not_180_out, OP0);
  not not_181 (not_181_out, OP1);
  not not_182 (not_182_out, OP2);
  not not_183 (not_183_out, OP3);
  not not_184 (not_184_out, OP4);
  not not_185 (not_185_out, OP5);
  not not_186 (not_186_out, F3);
  not not_187 (not_187_out, F4);
  not not_188 (not_188_out, F5);
  not not_189 (not_189_out, OP3);
  not not_190 (not_190_out, OP4);
  not not_191 (not_191_out, OP5);
  and and_1 (MemToReg, OP0, OP1, not_1_out, not_2_out, not_3_out, OP5);
  and and_2 (MemWrite, OP0, not_4_out, OP3, not_5_out, OP5);
  and and_3 (and_3_out, not_6_out, OP3, not_7_out, not_8_out);
  and and_4 (and_4_out, not_9_out, OP3, not_10_out, not_11_out);
  and and_5 (and_5_out, OP0, not_12_out, not_13_out, OP3, not_14_out);
  and and_6 (and_6_out, OP0, OP1, not_15_out, not_16_out, OP5);
  and and_7 (and_7_out, not_17_out, not_18_out, not_19_out, not_20_out, not_21_out, not_22_out, not_23_out, not_24_out, not_25_out);
  and and_8 (and_8_out, not_26_out, not_27_out, not_28_out, not_29_out, not_30_out, not_31_out, not_32_out, not_33_out, F5);
  and and_9 (and_9_out, not_34_out, not_35_out, not_36_out, not_37_out, not_38_out, F1, not_39_out, F3, not_40_out, F5);
  and and_10 (and_10_out, not_41_out, not_42_out, not_43_out, not_44_out, not_45_out, F0, F1, not_46_out, not_47_out, not_48_out);
  and and_11 (and_11_out, not_49_out, not_50_out, not_51_out, not_52_out, not_53_out, F0, F1, F2, not_54_out, not_55_out);
  and and_12 (and_12_out, not_56_out, OP3, not_57_out, not_58_out);
  and and_13 (and_13_out, not_59_out, OP3, not_60_out, not_61_out);
  and and_14 (and_14_out, OP0, OP1, not_62_out, not_63_out, not_64_out);
  and and_15 (SysCALL, not_65_out, not_66_out, not_67_out, not_68_out, not_69_out, not_70_out, not_71_out, not_72_out, F2, F3, not_73_out, not_74_out);
  and and_16 (and_16_out, not_75_out, not_76_out, not_77_out, OP2, not_78_out, OP0);
  and and_17 (and_17_out, not_79_out, not_80_out, OP3, not_81_out, not_82_out, not_83_out);
  and and_18 (and_18_out, not_84_out, not_85_out, OP3, not_86_out, not_87_out, OP0);
  and and_19 (and_19_out, not_88_out, not_89_out, OP3, not_90_out, OP1, not_91_out);
  and and_20 (and_20_out, not_92_out, not_93_out, not_94_out, OP2, OP1, OP0);
  and and_21 (and_21_out, not_95_out, not_96_out, not_97_out, not_98_out, not_99_out, not_100_out, not_101_out, not_102_out, not_103_out, not_104_out);
  and and_22 (and_22_out, not_105_out, not_106_out, not_107_out, not_108_out, not_109_out, not_110_out, not_111_out, not_112_out, not_113_out, F5);
  and and_23 (and_23_out, not_114_out, not_115_out, not_116_out, not_117_out, not_118_out, not_119_out, F1, not_120_out, F3, not_121_out, F5);
  and and_24 (and_24_out, not_122_out, not_123_out, not_124_out, not_125_out, not_126_out, not_127_out, F0, F1, not_128_out, not_129_out, not_130_out);
  and and_25 (and_25_out, not_131_out, not_132_out, not_133_out, not_134_out, not_135_out, not_136_out, F0, F1, F2, not_137_out, not_138_out);
  and and_26 (BEQ, not_139_out, not_140_out, OP2, not_141_out, not_142_out, not_143_out);
  and and_27 (BNE, OP0, not_144_out, OP2, not_145_out, not_146_out, not_147_out);
  and and_28 (JR, not_148_out, not_149_out, not_150_out, not_151_out, not_152_out, not_153_out, not_154_out, not_155_out, not_156_out, F3, not_157_out, not_158_out);
  and and_29 (and_29_out, not_159_out, not_160_out, not_161_out, not_162_out, not_163_out, not_164_out, not_165_out, not_166_out, F3, not_167_out, not_168_out);
  and and_30 (and_30_out, OP1, not_169_out, not_170_out, not_171_out, not_172_out);
  and and_31 (JAL, OP0, OP1, not_173_out, not_174_out, not_175_out, not_176_out);
  and and_32 (SH, OP0, not_177_out, not_178_out, OP3, not_179_out, OP5);
  and and_33 (SRAV, not_180_out, not_181_out, not_182_out, not_183_out, not_184_out, not_185_out, F0, F1, F2, not_186_out, not_187_out, not_188_out);
  and and_34 (BGTZ, OP0, OP1, OP2, not_189_out, not_190_out, not_191_out);
  or or_1 (ALU_SRC, and_3_out, and_4_out, and_5_out, and_6_out);
  or or_2 (RegWrite, and_7_out, and_8_out, and_9_out, and_10_out, and_11_out, and_12_out, and_13_out, and_14_out);
  or or_3 (SignedExt, and_16_out, and_17_out, and_18_out, and_19_out, and_20_out);
  or or_4 (RegDst, and_21_out, and_22_out, and_23_out, and_24_out, and_25_out);
  or or_5 (JUMP, and_29_out, and_30_out);
endmodule

// ALU
module MIPS_ALU (
  input  [4:0] shamt,
  input  [31:0] X,
  input  [31:0] Y,
  input  [3:0] AluOP,
  output Equal,
  output [31:0] Result,
  output [31:0] Result_2
);

  wire [0:0] comparator_1_lt, comparator_2_lt;
  wire [31:0] adder_1_out, AND_out, divider_1_out, divider_1_rem, multiplier_1_cout, multiplier_1_out,
       NOR_out, OR_out, shifter_1_out, shifter_2_out, shifter_3_out, subtractor_1_out, XOR_out;

  assign AND_out = X & Y;  // AND_Gate AND, 32 bits wide
  assign OR_out = X | Y;  // OR_Gate OR, 32 bits wide
  Shifter #(.width(32), .shift("ll")) shifter_1 (.in(Y), .\dist (shamt), .out(shifter_1_out));
  Shifter #(.width(32), .shift("ar")) shifter_2 (.in(Y), .\dist (shamt), .out(shifter_2_out));
  Shifter #(.width(32), .shift("lr")) shifter_3 (.in(Y), .\dist (shamt), .out(shifter_3_out));
  Multiplier #(.width(32)) multiplier_1 (.a(X), .b(Y), .out(multiplier_1_out), .cout(multiplier_1_cout));  // open: cin
  Divider #(.width(32)) divider_1 (.a(X), .b(Y), .out(divider_1_out), .rem(divider_1_rem));  // open: upper
  Adder #(.width(32)) adder_1 (.a(X), .b(Y), .out(adder_1_out));  // open: cin, cout
  Subtractor #(.width(32)) subtractor_1 (.a(X), .b(Y), .out(subtractor_1_out));  // open: bin, bout
  assign XOR_out = X ^ Y;  // XOR_Gate XOR, 32 bits wide
  assign NOR_out = ~(X | Y);  // NOR_Gate NOR, 32 bits wide
  Comparator #(.width(32), .mode("twosComplement")) comparator_1 (
    .a(X), .b(Y), .eq(Equal), .lt(comparator_1_lt[0]));  // open: gt
  Comparator #(.width(32), .mode("unsigned")) comparator_2 (.a(X), .b(Y), .lt(comparator_2_lt[0]));  // open: gt, eq
  Multiplexer #(.select(4), .width(32), .disabled("Z"), .enable("false")) multiplexer_1 (
    .in0(shifter_1_out), .in1(shifter_2_out), .in2(shifter_3_out), .in3(multiplier_1_out),
    .in4(divider_1_out), .in5(adder_1_out), .in6(subtractor_1_out), .in7(AND_out), .in8(OR_out),
    .in9(XOR_out), .in10(NOR_out), .in11({{31{1'b0}}, comparator_1_lt[0]}),
    .in12({{31{1'b0}}, comparator_2_lt[0]}), .in13({32{1'b0}}), .in14({32{1'b0}}), .in15({32{1'b0}}),
    .out(Result), .sel(AluOP));
  Multiplexer #(.select(4), .width(32), .disabled("Z"), .enable("false")) multiplexer_2 (
    .in0({32{1'b0}}), .in1({32{1'b0}}), .in2({32{1'b0}}), .in3(multiplier_1_cout), .in4(divider_1_rem),
    .in5({32{1'b0}}), .in6({32{1'b0}}), .in7({32{1'b0}}), .in8({32{1'b0}}), .in9({32{1'b0}}),
    .in10({32{1'b0}}), .in11({32{1'b0}}), .in12({32{1'b0}}), .in13({32{1'b0}}), .in14({32{1'b0}}),
    .in15({32{1'b0}}), .out(Result_2), .sel(AluOP));

  // Other names for the same wires on the sheet: Result2[31:0] = Result_2; S[3:0] = AluOP

  // Notes on the sheet:
  //   不要改变此引脚区域内容，也不要改变ALU封装形式
  //   输入引脚
  //   输出引脚
endmodule

module MIPS_Regifile (
  input  [31:0] Din,
  input  Clk,
  input  WE,
  input  [4:0] R1_num,
  input  [4:0] W_num,
  input  [4:0] R2_num,
  output [31:0] R1,
  output [31:0] R2
);

  // RegisterFile registerfile_1: pin names not known; wires that end beside it: Din, Clk, WE, W_num, R1_num, R2_num, R1, R2
endmodule

module \理想流水线  (
  output RegWrite,
  output MemWrite,
  output [31:0] IF_PC,
  output [31:0] ID_PC,
  output [31:0] EX_PC,
  output [31:0] M_PC,
  output [31:0] WB_PC,
  output [31:0] RDin,
  output [31:0] MDin,
  output [31:0] LedData
);

  wire and_1_out, and_2_out, CLK, clock_1_out, clock_2_out, comparator_1_eq, comparator_1_lt, d_ff_1_q,
       ex_mem_1_memtoreg_2, ex_mem_1_memwrite_4, ex_mem_1_regwrite_2, Go, id_ex_1_alusrcb_2, id_ex_1_beq_2,
       id_ex_1_bne_2, id_ex_1_memtoreg_2, id_ex_1_memwrite_2, id_ex_1_regwrite_2, id_ex_1_sys_2, IR1, IR2,
       IR3, mem_wb_1_memtoreg_2, mips_alu_1_equal, nand_1_out, not_1_out, or_1_out, or_2_out, or_3_out, RST,
       Syscall, W1, W2, W3, \单周期硬布线控制器_1_alu_src , \单周期硬布线控制器_1_beq , \单周期硬布线控制器_1_bne ,
       \单周期硬布线控制器_1_memtoreg , \单周期硬布线控制器_1_memwrite , \单周期硬布线控制器_1_regdst , \单周期硬布线控制器_1_regwrite ,
       \单周期硬布线控制器_1_syscall ;
  wire [3:0] id_ex_1_aluop_2, \单周期硬布线控制器_1_alu_op ;
  wire [4:0] ex_mem_1_writereg_num_2, id_ex_1_writereg_num_2, mem_wb_1_writereg_num_2, multiplexer_2_out;
  wire [12:0] CNT_num;
  wire [15:0] \LoadUse次数 , \总周期数 , \插入气泡数 , \无条件分支数 , \条件分支成功数 ;
  wire [31:0] adder_1_out, adder_2_out, bit_extender_1_out, EX_IR, ex_mem_1_ir_mem, ex_mem_1_result_2,
       id_ex_1_ir_id_2, id_ex_1_rs_2, id_ex_1_rt_2, id_ex_1_signimm_2, ID_IR, if_id_1_ir_2, IF_IR, MEM_IR,
       mem_wb_1_rd_2, mem_wb_1_result_2, mips_alu_1_result, mips_probe_5_p1, mips_regifile_1_r1,
       mips_regifile_1_r2, multiplexer_1_out, multiplexer_3_out, ram_1_data, shifter_1_out, WB_IR;

  Button \u_总复位  (.out(RST));
  Button _1 (.out(IR1));
  Button _2 (.out(IR2));
  Button _3 (.out(IR3));
  // Probe on \总周期数 
  // Probe on \总周期数 
  Button \u_继续运行  (.out(Go));
  LED #(.active("true")) led_1 (.in(W1));
  LED #(.active("true")) led_2 (.in(W2));
  LED #(.active("true")) led_3 (.in(W3));
  Hex_Digit_Display hex_digit_display_1 (.value(LedData[31:28]));  // open: dp
  // Probe on IF_PC[19:0]
  // Mips_Probe mips_probe_1: pin names not known; wires that end beside it: IF_IR
  not not_1 (not_1_out, Syscall);
  Multiplexer #(.select(1), .width(32), .disabled("Z"), .enable("false")) multiplexer_1 (
    .in0(adder_1_out), .in1(adder_2_out), .out(multiplexer_1_out), .sel(or_3_out));
  or or_1 (or_1_out, ~Syscall, Go);  // OR_Gate
  Hex_Digit_Display hex_digit_display_2 (.value(LedData[27:24]));  // open: dp
  Hex_Digit_Display hex_digit_display_3 (.value(LedData[23:20]));  // open: dp
  // Probe on ID_PC[19:0]
  // Mips_Probe mips_probe_2: pin names not known; wires that end beside it: ID_IR
  Counter #(.width(16), .max('hffff), .ongoal("wrap"), .trigger("rising"), .behavior("new")) counter_1 (
    .count(not_1_out), .Q(\总周期数 ), .clk(CLK), .clr(RST));  // open: load, D, carry, preset, down
  Register #(.width(32), .trigger("rising"), .Select("low")) register_1 (
    .D(multiplexer_1_out), .en(or_1_out), .Q(IF_PC), .clk(CLK));  // open: clr
  Hex_Digit_Display hex_digit_display_4 (.value(LedData[15:12]));  // open: dp
  Hex_Digit_Display hex_digit_display_5 (.value(LedData[19:16]));  // open: dp
  Hex_Digit_Display hex_digit_display_6 (.value(LedData[11:8]));  // open: dp
  Hex_Digit_Display hex_digit_display_7 (.value(LedData[7:4]));  // open: dp
  Clock #(.highDuration(1), .lowDuration(1)) clock_1 (.out(clock_1_out));
  // Probe on EX_PC[19:0]
  // Mips_Probe mips_probe_3: pin names not known; wires that end beside it: clock_1_out, EX_IR, CLK
  Adder #(.width(32)) adder_1 (.a(IF_PC), .b(32'h4), .out(adder_1_out));  // open: cin, cout
  Hex_Digit_Display hex_digit_display_8 (.value(LedData[3:0]));  // open: dp
  // Probe on \总周期数 
  // Probe on M_PC[19:0]
  // Mips_Probe mips_probe_4: pin names not known; wires that end beside it: MEM_IR
  // Mips_Probe mips_probe_5: pin names not known; wires that end beside it: mips_probe_5_p1
  ROM #(.addrWidth(10), .dataWidth(32), .Select("high")) rom_1 (.addr(IF_PC[11:2]), .data(mips_probe_5_p1));
  // Probe on \总周期数 
  // Probe on \无条件分支数 
  // Probe on \条件分支成功数 
  // Probe on \插入气泡数 
  // Probe on \LoadUse次数 
  // Probe on if_id_1_ir_2
  // Probe on IF_PC[11:0]
  // Probe on WB_PC[19:0]
  // Mips_Probe mips_probe_6: pin names not known; wires that end beside it: WB_IR
  IF_ID if_id_1 (
    .IR(mips_probe_5_p1), .PC_4(IF_PC), .IR_2(if_id_1_ir_2), .PC_4_ID(ID_PC), .CLK(CLK), .EN(or_2_out));  // open: RST
  or or_2 (or_2_out, ~Syscall, Go);  // OR_Gate
  // Probe on ID_PC[11:0]
  // Probe on EX_PC[11:0]
  // Probe on M_PC[11:0]
  D_Flip_Flop #(.trigger("high"), .Pre_Clr_Positions("LEGACY"), .NegatePresetClear("false"), .enable("true"), .NewFFLayout("false")) d_ff_1 (.Q(d_ff_1_q));  // open: clk, D, Qn, preset, en, reset
  // Probe on 13'hc
  \单周期硬布线控制器  \u_单周期硬布线控制器_1  (
    .Func(if_id_1_ir_2[5:0]), .OP(if_id_1_ir_2[31:26]), .ALU_OP(\单周期硬布线控制器_1_alu_op ),
    .MemToReg(\单周期硬布线控制器_1_memtoreg ), .MemWrite(\单周期硬布线控制器_1_memwrite ), .ALU_SRC(\单周期硬布线控制器_1_alu_src ),
    .RegWrite(\单周期硬布线控制器_1_regwrite ), .SysCALL(\单周期硬布线控制器_1_syscall ), .RegDst(\单周期硬布线控制器_1_regdst ),
    .Beq(\单周期硬布线控制器_1_beq ), .Bne(\单周期硬布线控制器_1_bne ));  // open: SignedExt, JR, JMP, JAL, SH, SRAV, BGTZ
  // Probe on WB_PC[11:0]
  Comparator #(.width(13), .mode("twosComplement")) comparator_1 (
    .a(CNT_num), .b(13'hc), .eq(comparator_1_eq), .lt(comparator_1_lt));  // open: gt
  Clock #(.highDuration(1), .lowDuration(1)) clock_2 (.out(clock_2_out));
  Multiplexer #(.select(1), .width(5), .disabled("Z"), .enable("false")) multiplexer_2 (
    .in0(if_id_1_ir_2[20:16]), .in1(if_id_1_ir_2[15:11]), .out(multiplexer_2_out), .sel(\单周期硬布线控制器_1_regdst ));
  assign bit_extender_1_out = {{16{if_id_1_ir_2[15]}}, if_id_1_ir_2[15:0]};  // Bit_Extender bit_extender_1
  nand nand_1 (nand_1_out, d_ff_1_q, comparator_1_eq);
  Counter #(.width(13), .max('h1fff), .ongoal("stay"), .trigger("rising"), .behavior("old")) counter_2 (
    .count(comparator_1_lt), .Q(CNT_num), .clk(clock_2_out));  // open: load, D, carry, clr, preset
  MIPS_Regifile mips_regifile_1 (
    .Din(RDin), .Clk(CLK), .R1(mips_regifile_1_r1), .R2(mips_regifile_1_r2), .WE(RegWrite),
    .W_num(mem_wb_1_writereg_num_2), .R1_num(if_id_1_ir_2[25:21]), .R2_num(if_id_1_ir_2[20:16]));
  assign CLK = nand_1_out ? clock_2_out : 1'bz;  // Controlled_Buffer controlled_buffer_1
  Pull_Resistor #(.pull(1)) pull_resistor_1 (.node(CLK));
  ID_EX id_ex_1 (
    .BEQ(\单周期硬布线控制器_1_beq ), .BNE(\单周期硬布线控制器_1_bne ), .MemToReg(\单周期硬布线控制器_1_memtoreg ),
    .MemWrite(\单周期硬布线控制器_1_memwrite ), .AluOP(\单周期硬布线控制器_1_alu_op ), .AluSrcB(\单周期硬布线控制器_1_alu_src ),
    .RegWrite(\单周期硬布线控制器_1_regwrite ), .RS(mips_regifile_1_r1), .RT(mips_regifile_1_r2),
    .WriteReg_num(multiplexer_2_out), .SignImm(bit_extender_1_out), .IR_ID(if_id_1_ir_2), .PC_4_ID(ID_PC),
    .BEQ_2(id_ex_1_beq_2), .BNE_2(id_ex_1_bne_2), .MemToReg_2(id_ex_1_memtoreg_2),
    .MemWrite_2(id_ex_1_memwrite_2), .AluOP_2(id_ex_1_aluop_2), .AluSrcB_2(id_ex_1_alusrcb_2),
    .RegWrite_2(id_ex_1_regwrite_2), .RS_2(id_ex_1_rs_2), .RT_2(id_ex_1_rt_2),
    .WriteReg_num_2(id_ex_1_writereg_num_2), .SignImm_2(id_ex_1_signimm_2), .IR_ID_2(id_ex_1_ir_id_2),
    .PC_4_ID_2(EX_PC), .CLK(CLK), .sys(\单周期硬布线控制器_1_syscall ), .sys_2(id_ex_1_sys_2), .in_22(or_2_out));  // open: jal, jal_2, JMP, JMP_2, JR, JR_2, RST, FwdA, FwdA_2, FwdB, FwdB_2
  // Probe on id_ex_1_ir_id_2
  or or_3 (or_3_out, and_1_out, and_2_out);
  and and_1 (and_1_out, id_ex_1_beq_2, mips_alu_1_equal);
  and and_2 (and_2_out, ~mips_alu_1_equal, id_ex_1_bne_2);  // AND_Gate
  Multiplexer #(.select(1), .width(32), .disabled("Z"), .enable("false")) multiplexer_3 (
    .in0(id_ex_1_rt_2), .in1(id_ex_1_signimm_2), .out(multiplexer_3_out), .sel(id_ex_1_alusrcb_2));
  Shifter #(.width(32), .shift("ll")) shifter_1 (.in(id_ex_1_signimm_2), .\dist (5'b00010), .out(shifter_1_out));
  MIPS_ALU mips_alu_1 (
    .X(id_ex_1_rs_2), .Y(multiplexer_3_out), .AluOP(id_ex_1_aluop_2), .Equal(mips_alu_1_equal),
    .Result(mips_alu_1_result), .shamt(id_ex_1_ir_id_2[10:6]));  // open: Result_2
  Adder #(.width(32)) adder_2 (.a(shifter_1_out), .b(EX_PC), .out(adder_2_out));  // open: cin, cout
  EX_MEM ex_mem_1 (
    .RegWrite(id_ex_1_regwrite_2), .MemToReg(id_ex_1_memtoreg_2), .MemWrite(id_ex_1_memwrite_2),
    .IR_EX(id_ex_1_ir_id_2), .Result(mips_alu_1_result), .WriteData(id_ex_1_rt_2),
    .WriteReg_num(id_ex_1_writereg_num_2), .PC_4_EX(EX_PC), .RegWrite_2(ex_mem_1_regwrite_2),
    .MemToReg_2(ex_mem_1_memtoreg_2), .MemWrite_3(MemWrite), .IR_MEM(ex_mem_1_ir_mem),
    .Result_2(ex_mem_1_result_2), .WriteData_2(MDin), .WriteReg_num_2(ex_mem_1_writereg_num_2),
    .PC_4_MEM(M_PC), .CLK(CLK), .MemWrite_2(id_ex_1_sys_2), .MemWrite_4(ex_mem_1_memwrite_4), .in_13(or_2_out));  // open: RST, jal, jal_2, v0, v0_2
  // Probe on ex_mem_1_ir_mem
  RAM #(.addrWidth(10), .dataWidth(32), .bus("separate"), .Select("high")) ram_1 (
    .addr(ex_mem_1_result_2[11:2]), .din(MDin), .data(ram_1_data), .str(MemWrite), .clk(CLK));  // open: sel, ld, clr
  Register #(.width(32), .trigger("rising"), .Select("low")) register_2 (
    .D(MDin), .Q(LedData), .clk(CLK), .clr(RST));  // open: en
  MEM_WB mem_wb_1 (
    .RegWrite(ex_mem_1_regwrite_2), .MemToReg(ex_mem_1_memtoreg_2), .Result(ex_mem_1_result_2),
    .RD(ram_1_data), .WriteReg_num(ex_mem_1_writereg_num_2), .IR_MEM(ex_mem_1_ir_mem), .PC_4_MEM(M_PC),
    .RegWrite_2(RegWrite), .MemToReg_2(mem_wb_1_memtoreg_2), .Result_2(mem_wb_1_result_2),
    .RD_2(mem_wb_1_rd_2), .WriteReg_num_2(mem_wb_1_writereg_num_2), .PC_4_WB(WB_PC), .CLK(CLK),
    .sys(ex_mem_1_memwrite_4), .sys_2(Syscall), .in_12(or_2_out));  // open: IR_WB, RST, jal, jal_2, v0, v0_2
  Multiplexer #(.select(1), .width(32), .disabled("Z"), .enable("false")) multiplexer_4 (
    .in0(mem_wb_1_result_2), .in1(mem_wb_1_rd_2), .out(RDin), .sel(mem_wb_1_memtoreg_2));

  // Other names for the same wires on the sheet: MEM_PC[31:0] = M_PC

  // Notes on the sheet:
  //   中断源
  //   时空图监测，可删除
  //   中断等待指示
  //   数码管输出
  //   指令存储器
  //   contents of rom_1 (hex, n*v repeats v):
  //   20100000 20110000 20120000 20130000 36100000 36310001 36520002 36730003 ae100000 ae110004 ae120008
  //   ae13000c 2002000a 20110000 20120000 20130000 c
  //   控制位
  //   rs
  //   rt
  //   rd
  //   流水调试日志用
  //   暂停节拍，不能为0
  //   戳工具置1进入计数暂停模式，ctrl+k时钟自动运行到对应节拍暂停
  //   ctrl+k关闭时钟连续运行，将控制位置零，进入单步调试模式调试
  //   用这个时钟源需要去掉电路中的其他时钟源
  //   可计数暂停的时钟源
  //   为方便自动评测，需要输出流水线各段保存的PC值，注意是PC不是PC+4，另外ID段寄存器写入信息，Mem段内存写入信息也要输出
endmodule

module \气泡流水线  (
  output RegWrite,
  output MemWrite,
  output [31:0] IF_PC,
  output [31:0] ID_PC,
  output [31:0] EX_PC,
  output [31:0] M_PC,
  output [31:0] WB_PC,
  output [31:0] RDin,
  output [31:0] MDin,
  output [31:0] LedData
);

  wire and_3_out, and_4_out, and_5_out, branch, CLK, clock_1_out, clock_2_out, comparator_1_eq,
       comparator_2_eq, comparator_2_lt, d_ff_1_q, EN, ex_mem_1_jal_2, ex_mem_1_memtoreg_2,
       ex_mem_1_memwrite_4, ex_mem_1_regwrite_2, Go, halt, id_ex_1_alusrcb_2, id_ex_1_beq_2, id_ex_1_bne_2,
       id_ex_1_jal_2, id_ex_1_memtoreg_2, id_ex_1_memwrite_2, id_ex_1_regwrite_2, id_ex_1_sys_2, IR1, IR2,
       IR3, JMP, JR, LedOut, mem_wb_1_jal_2, mem_wb_1_memtoreg_2, mips_alu_1_equal, nand_1_out, not_1_out,
       not_2_out, not_3_out, or_2_out, RST, Stall, Syscall, W1, W2, W3, \单周期硬布线控制器_1_alu_src ,
       \单周期硬布线控制器_1_beq , \单周期硬布线控制器_1_bne , \单周期硬布线控制器_1_jal , \单周期硬布线控制器_1_jmp , \单周期硬布线控制器_1_jr ,
       \单周期硬布线控制器_1_memtoreg , \单周期硬布线控制器_1_memwrite , \单周期硬布线控制器_1_regdst , \单周期硬布线控制器_1_regwrite ,
       \单周期硬布线控制器_1_syscall , \控制逻辑_1_flushid_ex , \控制逻辑_1_flushif_id ;
  wire [3:0] id_ex_1_aluop_2, \单周期硬布线控制器_1_alu_op ;
  wire [4:0] ex_mem_1_writereg_num_2, id_ex_1_writereg_num_2, mem_wb_1_writereg_num_2, multiplexer_6_out,
       multiplexer_7_out, RS, RT;
  wire [12:0] CNT_num;
  wire [15:0] \LoadUse次数 , \总周期数 , \插入气泡数 , \无条件分支数 , \条件分支成功数 ;
  wire [27:0] adder_1_out, bit_extender_2_out;
  wire [31:0] adder_2_out, adder_3_out, adder_4_out, bit_extender_1_out, EX_IR, ex_mem_1_ir_mem,
       ex_mem_1_result_2, ex_mem_1_v0_2, id_ex_1_ir_id_2, id_ex_1_rt_2, id_ex_1_signimm_2, ID_IR,
       if_id_1_ir_2, IF_IR, MEM_IR, mem_wb_1_rd_2, mem_wb_1_result_2, mips_alu_1_result, mips_probe_6_p1,
       mips_regifile_1_r1, mips_regifile_1_r2, multiplexer_1_out, multiplexer_2_out, multiplexer_3_out,
       multiplexer_8_out, multiplexer_9_out, ram_1_data, rv0, shifter_1_out, shifter_2_out, V0, WB_IR;

  Button \u_总复位  (.out(RST));
  Button _1 (.out(IR1));
  Button _2 (.out(IR2));
  Button _3 (.out(IR3));
  // Probe on \总周期数 
  // Probe on \总周期数 
  Button \u_继续运行  (.out(Go));
  LED #(.active("true")) led_1 (.in(W1));
  LED #(.active("true")) led_2 (.in(W2));
  LED #(.active("true")) led_3 (.in(W3));
  Hex_Digit_Display hex_digit_display_1 (.value(LedData[31:28]));  // open: dp
  // Probe on IF_PC[19:0]
  // Mips_Probe mips_probe_1: pin names not known; wires that end beside it: IF_IR
  Multiplexer #(.select(1), .width(32), .disabled("Z"), .enable("false")) multiplexer_1 (
    .in0({shifter_2_out[31:28], adder_1_out}), .in1(adder_3_out), .out(multiplexer_1_out), .sel(branch));
  Hex_Digit_Display hex_digit_display_2 (.value(LedData[23:20]));  // open: dp
  Hex_Digit_Display hex_digit_display_3 (.value(LedData[27:24]));  // open: dp
  // Probe on ID_PC[19:0]
  // Mips_Probe mips_probe_2: pin names not known; wires that end beside it: ID_IR
  Comparator #(.width(32), .mode("twosComplement")) comparator_1 (
    .a(rv0), .b(32'h22), .eq(comparator_1_eq));  // open: gt, lt
  not not_1 (not_1_out, halt);
  Multiplexer #(.select(1), .width(32), .disabled("Z"), .enable("false")) multiplexer_2 (
    .in0(multiplexer_1_out), .in1(shifter_2_out), .out(multiplexer_2_out), .sel(JMP));
  Multiplexer #(.select(1), .width(32), .disabled("Z"), .enable("false")) multiplexer_3 (
    .in0(multiplexer_2_out), .in1(V0), .out(multiplexer_3_out), .sel(JR));
  Hex_Digit_Display hex_digit_display_4 (.value(LedData[15:12]));  // open: dp
  Hex_Digit_Display hex_digit_display_5 (.value(LedData[19:16]));  // open: dp
  Hex_Digit_Display hex_digit_display_6 (.value(LedData[11:8]));  // open: dp
  Hex_Digit_Display hex_digit_display_7 (.value(LedData[7:4]));  // open: dp
  Clock #(.highDuration(1), .lowDuration(1)) clock_1 (.out(clock_1_out));
  // Probe on EX_PC[19:0]
  // Mips_Probe mips_probe_3: pin names not known; wires that end beside it: clock_1_out, EX_IR, CLK
  and and_1 (LedOut, Syscall, comparator_1_eq);
  and and_2 (halt, Syscall, ~comparator_1_eq);  // AND_Gate
  Counter #(.width(16), .max('hffff), .ongoal("wrap"), .trigger("rising"), .behavior("new")) counter_1 (
    .count(not_1_out), .Q(\总周期数 ), .clk(CLK), .clr(RST));  // open: load, D, carry, preset, down
  Register #(.width(32), .trigger("rising"), .Select("low")) register_1 (
    .D(MDin), .Q(LedData), .clk(CLK), .clr(RST));  // open: en
  Register #(.width(32), .trigger("rising"), .Select("low")) register_2 (
    .D(multiplexer_3_out), .en(and_3_out), .Q(IF_PC), .clk(CLK));  // open: clr
  Hex_Digit_Display hex_digit_display_8 (.value(LedData[3:0]));  // open: dp
  not not_2 (not_2_out, Stall);
  // Probe on \总周期数 
  // Probe on M_PC[19:0]
  // Mips_Probe mips_probe_4: pin names not known; wires that end beside it: MEM_IR
  Adder #(.width(32)) adder_1 (.a(IF_PC), .b(32'h4), .out({shifter_2_out[31:28], adder_1_out}));  // open: cin, cout
  and and_3 (and_3_out, not_2_out, EN);
  or or_1 (EN, ~halt, Go);  // OR_Gate
  // Probe on \总周期数 
  // Probe on \无条件分支数 
  // Probe on \条件分支成功数 
  // Probe on \插入气泡数 
  // Probe on \LoadUse次数 
  // Probe on IF_PC[11:0]
  // Probe on WB_PC[19:0]
  // Mips_Probe mips_probe_5: pin names not known; wires that end beside it: WB_IR
  // Mips_Probe mips_probe_6: pin names not known; wires that end beside it: mips_probe_6_p1
  ROM #(.addrWidth(10), .dataWidth(32), .Select("high")) rom_1 (.addr(IF_PC[11:2]), .data(mips_probe_6_p1));
  // Probe on EX_PC[11:0]
  // Probe on ID_PC[11:0]
  // Probe on M_PC[11:0]
  D_Flip_Flop #(.trigger("high"), .Pre_Clr_Positions("LEGACY"), .NegatePresetClear("false"), .enable("true"), .NewFFLayout("false")) d_ff_1 (.Q(d_ff_1_q));  // open: clk, D, Qn, preset, en, reset
  // Probe on 13'hc
  // Probe on if_id_1_ir_2
  IF_ID if_id_1 (
    .IR(mips_probe_6_p1), .PC_4(IF_PC), .IR_2(if_id_1_ir_2), .PC_4_ID(ID_PC), .CLK(CLK),
    .RST(\控制逻辑_1_flushif_id ), .EN(and_3_out));
  // Probe on WB_PC[11:0]
  Comparator #(.width(13), .mode("twosComplement")) comparator_2 (
    .a(CNT_num), .b(13'hc), .eq(comparator_2_eq), .lt(comparator_2_lt));  // open: gt
  Clock #(.highDuration(1), .lowDuration(1)) clock_2 (.out(clock_2_out));
  nand nand_1 (nand_1_out, d_ff_1_q, comparator_2_eq);
  Counter #(.width(13), .max('h1fff), .ongoal("stay"), .trigger("rising"), .behavior("old")) counter_2 (
    .count(comparator_2_lt), .Q(CNT_num), .clk(clock_2_out));  // open: load, D, carry, clr, preset
  \单周期硬布线控制器  \u_单周期硬布线控制器_1  (
    .Func(if_id_1_ir_2[5:0]), .OP(if_id_1_ir_2[31:26]), .ALU_OP(\单周期硬布线控制器_1_alu_op ),
    .MemToReg(\单周期硬布线控制器_1_memtoreg ), .MemWrite(\单周期硬布线控制器_1_memwrite ), .ALU_SRC(\单周期硬布线控制器_1_alu_src ),
    .RegWrite(\单周期硬布线控制器_1_regwrite ), .SysCALL(\单周期硬布线控制器_1_syscall ), .RegDst(\单周期硬布线控制器_1_regdst ),
    .JR(\单周期硬布线控制器_1_jr ), .JMP(\单周期硬布线控制器_1_jmp ), .Beq(\单周期硬布线控制器_1_beq ), .JAL(\单周期硬布线控制器_1_jal ),
    .Bne(\单周期硬布线控制器_1_bne ));  // open: SignedExt, SH, SRAV, BGTZ
  Multiplexer #(.select(1), .width(5), .disabled("Z"), .enable("false")) multiplexer_4 (
    .in0(if_id_1_ir_2[25:21]), .in1(5'b00010), .out(RS), .sel(\单周期硬布线控制器_1_syscall ));
  Multiplexer #(.select(1), .width(5), .disabled("Z"), .enable("false")) multiplexer_5 (
    .in0(if_id_1_ir_2[20:16]), .in1(5'b00100), .out(RT), .sel(\单周期硬布线控制器_1_syscall ));
  Multiplexer #(.select(1), .width(5), .disabled("Z"), .enable("false")) multiplexer_6 (
    .in0(if_id_1_ir_2[20:16]), .in1(if_id_1_ir_2[15:11]), .out(multiplexer_6_out), .sel(\单周期硬布线控制器_1_regdst ));
  Multiplexer #(.select(1), .width(5), .disabled("Z"), .enable("false")) multiplexer_7 (
    .in0(multiplexer_6_out), .in1({5{1'b1}}), .out(multiplexer_7_out), .sel(\单周期硬布线控制器_1_jal ));
  assign CLK = nand_1_out ? clock_2_out : 1'bz;  // Controlled_Buffer controlled_buffer_1
  // Probe on RS
  assign bit_extender_1_out = {{16{if_id_1_ir_2[15]}}, if_id_1_ir_2[15:0]};  // Bit_Extender bit_extender_1
  Pull_Resistor #(.pull(1)) pull_resistor_1 (.node(CLK));
  not not_3 (not_3_out, CLK);
  MIPS_Regifile mips_regifile_1 (
    .Din(RDin), .Clk(not_3_out), .R1(mips_regifile_1_r1), .R2(mips_regifile_1_r2), .WE(RegWrite),
    .W_num(mem_wb_1_writereg_num_2), .R1_num(RS), .R2_num(RT));
  // Mips_Probe mips_probe_7: pin names not known; wires that end beside it: if_id_1_ir_2
  ID_EX id_ex_1 (
    .BEQ(\单周期硬布线控制器_1_beq ), .BNE(\单周期硬布线控制器_1_bne ), .MemToReg(\单周期硬布线控制器_1_memtoreg ),
    .MemWrite(\单周期硬布线控制器_1_memwrite ), .AluOP(\单周期硬布线控制器_1_alu_op ), .AluSrcB(\单周期硬布线控制器_1_alu_src ),
    .RegWrite(\单周期硬布线控制器_1_regwrite ), .RS(mips_regifile_1_r1), .RT(mips_regifile_1_r2),
    .WriteReg_num(multiplexer_7_out), .SignImm(bit_extender_1_out), .IR_ID(if_id_1_ir_2), .PC_4_ID(ID_PC),
    .BEQ_2(id_ex_1_beq_2), .BNE_2(id_ex_1_bne_2), .MemToReg_2(id_ex_1_memtoreg_2),
    .MemWrite_2(id_ex_1_memwrite_2), .AluOP_2(id_ex_1_aluop_2), .AluSrcB_2(id_ex_1_alusrcb_2),
    .RegWrite_2(id_ex_1_regwrite_2), .RS_2(V0), .RT_2(id_ex_1_rt_2), .WriteReg_num_2(id_ex_1_writereg_num_2),
    .SignImm_2(id_ex_1_signimm_2), .IR_ID_2(id_ex_1_ir_id_2), .PC_4_ID_2(EX_PC), .CLK(CLK),
    .sys(\单周期硬布线控制器_1_syscall ), .sys_2(id_ex_1_sys_2), .in_22(EN), .jal(\单周期硬布线控制器_1_jal ),
    .jal_2(id_ex_1_jal_2), .JMP(\单周期硬布线控制器_1_jmp ), .JMP_2(JMP), .JR(\单周期硬布线控制器_1_jr ), .JR_2(JR),
    .RST(\控制逻辑_1_flushid_ex ));  // open: FwdA, FwdA_2, FwdB, FwdB_2
  \控制逻辑  \u_控制逻辑_1  (
    .MEM_WriteReg_num(ex_mem_1_writereg_num_2), .EX_WriteReg_num(id_ex_1_writereg_num_2), .Stall(Stall),
    .FlushID_EX(\控制逻辑_1_flushid_ex ), .FlushIF_ID(\控制逻辑_1_flushif_id ), .rs(RS), .IR(if_id_1_ir_2), .rt(RT),
    .MEM_RegWrite(ex_mem_1_regwrite_2), .EX_RegWrite(id_ex_1_regwrite_2), .branch(or_2_out));
  or or_2 (or_2_out, id_ex_1_jal_2, JMP, JR, branch);
  or or_3 (branch, and_4_out, and_5_out);
  and and_4 (and_4_out, id_ex_1_beq_2, mips_alu_1_equal);
  and and_5 (and_5_out, ~mips_alu_1_equal, id_ex_1_bne_2);  // AND_Gate
  Multiplexer #(.select(1), .width(32), .disabled("Z"), .enable("false")) multiplexer_8 (
    .in0(id_ex_1_rt_2), .in1(id_ex_1_signimm_2), .out(multiplexer_8_out), .sel(id_ex_1_alusrcb_2));
  Adder #(.width(32)) adder_2 (.a(EX_PC), .b(32'h4), .out(adder_2_out));  // open: cin, cout
  MIPS_ALU mips_alu_1 (
    .X(V0), .Y(multiplexer_8_out), .AluOP(id_ex_1_aluop_2), .Equal(mips_alu_1_equal),
    .Result(mips_alu_1_result), .shamt(id_ex_1_ir_id_2[10:6]));  // open: Result_2
  Shifter #(.width(32), .shift("ll")) shifter_1 (.in(id_ex_1_signimm_2), .\dist (5'b00010), .out(shifter_1_out));
  // Mips_Probe mips_probe_8: pin names not known; wires that end beside it: id_ex_1_ir_id_2
  Adder #(.width(32)) adder_3 (.a(shifter_1_out), .b(adder_2_out), .out(adder_3_out));  // open: cin, cout
  EX_MEM ex_mem_1 (
    .RegWrite(id_ex_1_regwrite_2), .MemToReg(id_ex_1_memtoreg_2), .MemWrite(id_ex_1_memwrite_2),
    .IR_EX(id_ex_1_ir_id_2), .Result(mips_alu_1_result), .WriteData(id_ex_1_rt_2),
    .WriteReg_num(id_ex_1_writereg_num_2), .PC_4_EX(EX_PC), .RegWrite_2(ex_mem_1_regwrite_2),
    .MemToReg_2(ex_mem_1_memtoreg_2), .MemWrite_3(MemWrite), .IR_MEM(ex_mem_1_ir_mem),
    .Result_2(ex_mem_1_result_2), .WriteData_2(MDin), .WriteReg_num_2(ex_mem_1_writereg_num_2),
    .PC_4_MEM(M_PC), .CLK(CLK), .MemWrite_2(id_ex_1_sys_2), .MemWrite_4(ex_mem_1_memwrite_4), .in_13(EN),
    .jal(id_ex_1_jal_2), .jal_2(ex_mem_1_jal_2), .v0(V0), .v0_2(ex_mem_1_v0_2));  // open: RST
  // Probe on ex_mem_1_ir_mem
  // Mips_Probe mips_probe_9: pin names not known; wires that end beside it: ex_mem_1_ir_mem
  assign bit_extender_2_out = {{2{1'b0}}, id_ex_1_ir_id_2[25:0]};  // Bit_Extender bit_extender_2
  RAM #(.addrWidth(10), .dataWidth(32), .bus("separate"), .Select("high")) ram_1 (
    .addr(ex_mem_1_result_2[11:2]), .din(MDin), .data(ram_1_data), .str(MemWrite), .clk(CLK));  // open: sel, ld, clr
  Shifter #(.width(28), .shift("ll")) shifter_2 (.in(bit_extender_2_out), .\dist (5'b00010), .out(shifter_2_out[27:0]));
  MEM_WB mem_wb_1 (
    .RegWrite(ex_mem_1_regwrite_2), .MemToReg(ex_mem_1_memtoreg_2), .Result(ex_mem_1_result_2),
    .RD(ram_1_data), .WriteReg_num(ex_mem_1_writereg_num_2), .IR_MEM(ex_mem_1_ir_mem), .PC_4_MEM(M_PC),
    .RegWrite_2(RegWrite), .MemToReg_2(mem_wb_1_memtoreg_2), .Result_2(mem_wb_1_result_2),
    .RD_2(mem_wb_1_rd_2), .WriteReg_num_2(mem_wb_1_writereg_num_2), .PC_4_WB(WB_PC), .CLK(CLK),
    .sys(ex_mem_1_memwrite_4), .sys_2(Syscall), .in_12(EN), .jal(ex_mem_1_jal_2), .jal_2(mem_wb_1_jal_2),
    .v0(ex_mem_1_v0_2), .v0_2(rv0));  // open: IR_WB, RST
  Multiplexer #(.select(1), .width(32), .disabled("Z"), .enable("false")) multiplexer_9 (
    .in0(mem_wb_1_result_2), .in1(mem_wb_1_rd_2), .out(multiplexer_9_out), .sel(mem_wb_1_memtoreg_2));
  Adder #(.width(32)) adder_4 (.a(WB_PC), .b(32'h4), .out(adder_4_out));  // open: cin, cout
  Multiplexer #(.select(1), .width(32), .disabled("Z"), .enable("false")) multiplexer_10 (
    .in0(multiplexer_9_out), .in1(adder_4_out), .out(RDin), .sel(mem_wb_1_jal_2));

  // Other names for the same wires on the sheet: MEM_PC[31:0] = M_PC

  // Notes on the sheet:
  //   中断源
  //   时空图监测，可删除
  //   中断等待指示
  //   数码管输出
  //   指令存储器
  //   contents of rom_1 (hex, n*v repeats v):
  //   20110001 8000c05 20110001 20120002 20130003 8000c09 20110001 20120002 20130003 8000c0d 20110001
  //   20120002 20130003 8000c11 20110001 20120002 20130003 c000cb8 20100001 20110001 118fc0 112020
  //   20020022 c 118882 12200001 8000c15 112020 20020022 c 20110001 118880 112020 20020022 c 12200001
  //   8000c1f 20110001 118fc0 112020 20020022 c 1188c3 112020 20020022 c 118903 112020 20020022 c 118903
  //   112020 20020022 c 118903 112020 20020022 c 118903 112020 20020022 c 118903 112020 20020022 c 118903
  //   112020 20020022 c 118903 112020 20020022 c 20100001 109fc0 139fc3 8021 2012000c 24160003 26100001
  //   3210000f 20080008 20090001 139900 2709825 132020 20020022 c 1094022 1500fff9 22100001 2018000f
  //   2188024 108700 20080008 20090001 139902 2709825 132021 20020022 c 1094022 1500fff9 108702 2c9b022
  //   12c00001 8000c50 4020 1084027 84400 3508ffff 82021 20020022 c 2010ffff 20110000 ae300000 22100001
  //   22310004 ae300000 22100001 22310004 ae300000 22100001 22310004 ae300000 22100001 22310004 ae300000
  //   22100001 22310004 ae300000 22100001 22310004 ae300000 22100001 22310004 ae300000 22100001 22310004
  //   ae300000 22100001 22310004 ae300000 22100001 22310004 ae300000 22100001 22310004 ae300000 22100001
  //   22310004 ae300000 22100001 22310004 ae300000 22100001 22310004 ae300000 22100001 22310004 ae300000
  //   22100001 22310004 22100001 8020 2011003c 8e130000 8e340000 274402a 11000002 ae330000 ae140000
  //   2231fffc 1611fff8 102020 20020022 c 22100004 2011003c 1611fff2 20020032 c 20100000 22100001 102020
  //   20020022 c 22100002 102020 20020022 c 22100003 102020 20020022 c 22100004 102020 20020022 c 22100005
  //   102020 20020022 c 22100006 102020 20020022 c 22100007 102020 20020022 c 22100008 102020 20020022
  //   20020022 c 3e00008
  //   控制位
  //   流水调试日志用
  //   暂停节拍，不能为0
  //   戳工具置1进入计数暂停模式，ctrl+k时钟自动运行到对应节拍暂停
  //   ctrl+k关闭时钟连续运行，将控制位置零，进入单步调试模式调试
  //   rs
  //   rt
  //   rd
  //   可计数暂停的时钟源
  //   为方便自动评测，需要输出流水线各段保存的PC值，注意是PC不是PC+4，另外ID段寄存器写入信息，Mem段内存写入信息也要输出
endmodule

module \重定向流水线  (
  output RegWrite,
  output MemWrite,
  output [31:0] IF_PC,
  output [31:0] ID_PC,
  output [31:0] EX_PC,
  output [31:0] M_PC,
  output [31:0] WB_PC,
  output [31:0] RDin,
  output [31:0] MDin,
  output [31:0] LedData
);

  wire and_4_out, and_5_out, and_6_out, BGTZ, BGTZ1, BGTZ_A, branch, CLK, clock_1_out, clock_2_out,
       comparator_1_gt, comparator_2_eq, comparator_3_eq, comparator_3_lt, d_ff_1_q, EN, EX_BEQ, EX_BNE,
       EX_Branch, EX_BranchTaken, ex_mem_1_jal_2, ex_mem_1_memtoreg_2, ex_mem_1_memwrite_4,
       ex_mem_1_regwrite_2, EX_PredictJump, EX_PreErr, Go, halt, id_ex_1_alusrcb_2, id_ex_1_jal_2,
       id_ex_1_memtoreg_2, id_ex_1_memwrite_2, id_ex_1_regwrite_2, id_ex_1_sys_2, ID_EXRST, IR1, IR2, IR3,
       JMP, JR, LedOut, mem_wb_1_jal_2, mem_wb_1_memtoreg_2, mips_alu_1_equal, multiplexer_11_out,
       multiplexer_12_out, multiplexer_13_out, multiplexer_14_out, nand_1_out, not_1_out, not_2_out,
       not_3_out, PredictJump, register_4_q, register_5_q, RST, SH, SH1, SignedExt, SRAV, SRAV1, Stall,
       Syscall, W1, W2, W3, \单周期硬布线控制器_1_jmp , \单周期硬布线控制器_2_alu_src , \单周期硬布线控制器_2_beq , \单周期硬布线控制器_2_bne ,
       \单周期硬布线控制器_2_jal , \单周期硬布线控制器_2_jmp , \单周期硬布线控制器_2_jr , \单周期硬布线控制器_2_memtoreg ,
       \单周期硬布线控制器_2_memwrite , \单周期硬布线控制器_2_regdst , \单周期硬布线控制器_2_regwrite , \单周期硬布线控制器_2_syscall ,
       \重定向控制器_1_if_id_clr ;
  wire [1:0] FwdA, FwdB, id_ex_1_fwda_2, id_ex_1_fwdb_2;
  wire [3:0] id_ex_1_aluop_2, \单周期硬布线控制器_2_alu_op ;
  wire [4:0] ex_mem_1_writereg_num_2, id_ex_1_writereg_num_2, mem_wb_1_writereg_num_2, multiplexer_6_out,
       multiplexer_9_out, RS, RT, shamt;
  wire [12:0] CNT_num;
  wire [15:0] \LoadUse次数 , \总周期数 , \插入气泡数 , \无条件分支数 , \条件分支成功数 ;
  wire [31:0] adder_2_out, adder_4_out, ALU_A, ALUreslut, bit_extender_1_out, bit_extender_2_out,
       EX_BranchAddr, EX_IR, ex_mem_1_v0_2, id_ex_1_rt_2, id_ex_1_signimm_2, ID_IR, IF_IR, JumpAddr,
       LedData_in, M_IR, mem_wb_1_rd_2, mem_wb_1_result_2, mips_alu_1_result, mips_regifile_1_r1,
       mips_regifile_1_r2, multiplexer_1_out, multiplexer_2_out, multiplexer_3_out, multiplexer_4_out,
       multiplexer_5_out, multiplexer_10_out, multiplexer_15_out, multiplexer_17_out, multiplexer_20_out,
       PC_4, register_1_q, rv0, shifter_1_out, SHout, V0, WB_IR, \字数据 ;

  Button \u_总复位  (.out(RST));
  Button _1 (.out(IR1));
  Button _2 (.out(IR2));
  Button _3 (.out(IR3));
  // Probe on \总周期数 
  // Probe on \总周期数 
  Button \u_继续运行  (.out(Go));
  LED #(.active("true")) led_1 (.in(W1));
  LED #(.active("true")) led_2 (.in(W2));
  LED #(.active("true")) led_3 (.in(W3));
  Comparator #(.width(32), .mode("twosComplement")) comparator_1 (
    .a(ALU_A), .b({32{1'b0}}), .gt(comparator_1_gt));  // open: eq, lt
  Hex_Digit_Display hex_digit_display_1 (.value(LedData[31:28]));  // open: dp
  // Probe on IF_PC[19:0]
  // Mips_Probe mips_probe_1: pin names not known; wires that end beside it: IF_IR
  and and_1 (BGTZ_A, comparator_1_gt, BGTZ);
  or or_1 (EX_BranchTaken, branch, BGTZ_A);
  Hex_Digit_Display hex_digit_display_2 (.value(LedData[23:20]));  // open: dp
  Hex_Digit_Display hex_digit_display_3 (.value(LedData[27:24]));  // open: dp
  // Probe on ID_PC[19:0]
  // Mips_Probe mips_probe_2: pin names not known; wires that end beside it: ID_IR
  Multiplexer #(.select(1), .width(32), .disabled("Z"), .enable("false")) multiplexer_1 (
    .in0(adder_2_out), .in1(EX_BranchAddr), .out(multiplexer_1_out), .sel(EX_BranchTaken));
  Hex_Digit_Display hex_digit_display_4 (.value(LedData[15:12]));  // open: dp
  Hex_Digit_Display hex_digit_display_5 (.value(LedData[19:16]));  // open: dp
  Multiplexer #(.select(1), .width(32), .disabled("Z"), .enable("false")) multiplexer_2 (
    .in0(multiplexer_4_out), .in1(multiplexer_1_out), .out(multiplexer_2_out), .sel(EX_PreErr));
  Multiplexer #(.select(1), .width(32), .disabled("Z"), .enable("false")) multiplexer_3 (
    .in0(multiplexer_2_out), .in1({PC_4[31:28], IF_IR[25:0], 2'b00}), .out(multiplexer_3_out),
    .sel(\单周期硬布线控制器_1_jmp ));
  xor xor_1 (EX_PreErr, EX_BranchTaken, EX_PredictJump);
  or or_2 (EX_Branch, BGTZ, EX_BEQ, EX_BNE);
  Hex_Digit_Display hex_digit_display_6 (.value(LedData[7:4]));  // open: dp
  Hex_Digit_Display hex_digit_display_7 (.value(LedData[11:8]));  // open: dp
  Clock #(.highDuration(1), .lowDuration(1)) clock_1 (.out(clock_1_out));
  // Probe on EX_PC[19:0]
  // Mips_Probe mips_probe_3: pin names not known; wires that end beside it: clock_1_out, EX_IR, CLK
  Comparator #(.width(32), .mode("twosComplement")) comparator_2 (
    .a(rv0), .b(32'h22), .eq(comparator_2_eq));  // open: gt, lt
  not not_1 (not_1_out, halt);
  Register #(.width(32), .trigger("rising"), .Select("low")) register_1 (
    .D(MDin), .Q(register_1_q), .clk(CLK));  // open: en, clr
  Hex_Digit_Display hex_digit_display_8 (.value(LedData[3:0]));  // open: dp
  and and_2 (LedOut, Syscall, comparator_2_eq);
  and and_3 (halt, Syscall, ~comparator_2_eq);  // AND_Gate
  Counter #(.width(16), .max('hffff), .ongoal("wrap"), .trigger("rising"), .behavior("new")) counter_1 (
    .count(not_1_out), .Q(\总周期数 ), .clk(CLK), .clr(RST));  // open: load, D, carry, preset, down
  Register #(.width(32), .trigger("rising"), .Select("low")) register_2 (
    .D(register_1_q), .en(LedOut), .Q(LedData), .clk(CLK), .clr(RST));
  Multiplexer #(.select(1), .width(32), .disabled("Z"), .enable("false")) multiplexer_4 (
    .in0(PC_4), .in1(JumpAddr), .out(multiplexer_4_out), .sel(PredictJump));
  Multiplexer #(.select(1), .width(32), .disabled("Z"), .enable("false")) multiplexer_5 (
    .in0(multiplexer_3_out), .in1(V0), .out(multiplexer_5_out), .sel(JR));
  // Probe on \总周期数 
  // Probe on M_PC[19:0]
  // Mips_Probe mips_probe_4: pin names not known; wires that end beside it: M_IR
  Register #(.width(32), .trigger("rising"), .Select("low")) register_3 (
    .D(multiplexer_5_out), .en(and_4_out), .Q(IF_PC), .clk(CLK));  // open: clr
  not not_2 (not_2_out, Stall);
  BTB btb_1 (
    .PC(IF_PC), .EX_PC(EX_PC), .EX_BranchAddr(EX_BranchAddr), .CLK(CLK), .EX_Branch(EX_Branch),
    .EX_BranchTaken(EX_BranchTaken), .IF_IR(IF_IR), .ID_IR(ID_IR), .EX_IR(EX_IR), .M_IR(M_IR), .WB_IR(WB_IR),
    .PredictJump(PredictJump), .JumpAddr(JumpAddr));
  // Probe on \总周期数 
  // Probe on \无条件分支数 
  // Probe on \条件分支成功数 
  // Probe on \插入气泡数 
  // Probe on \LoadUse次数 
  // Probe on IF_PC[11:0]
  // Probe on WB_PC[19:0]
  // Mips_Probe mips_probe_5: pin names not known; wires that end beside it: WB_IR
  Adder #(.width(32)) adder_1 (.a(IF_PC), .b(32'h4), .out(PC_4));  // open: cin, cout
  and and_4 (and_4_out, not_2_out, EN);
  or or_3 (EN, ~halt, Go);  // OR_Gate
  // Probe on ID_PC[11:0]
  // Probe on EX_PC[11:0]
  \单周期硬布线控制器  \u_单周期硬布线控制器_1  (
    .Func(IF_IR[5:0]), .OP(IF_IR[31:26]), .JMP(\单周期硬布线控制器_1_jmp ));  // open: ALU_OP, MemToReg, MemWrite, ALU_SRC, RegWrite, SysCALL, SignedExt, RegDst, JR, Beq, JAL, Bne, SH, SRAV, BGTZ
  ROM #(.addrWidth(10), .dataWidth(32), .Select("high")) rom_1 (.addr(IF_PC[11:2]), .data(IF_IR));
  // Probe on M_PC[11:0]
  D_Flip_Flop #(.trigger("high"), .Pre_Clr_Positions("LEGACY"), .NegatePresetClear("false"), .enable("true"), .NewFFLayout("false")) d_ff_1 (.Q(d_ff_1_q));  // open: clk, D, Qn, preset, en, reset
  // Probe on 13'h2bc
  // Mips_Probe mips_probe_6: pin names not known; wires that end beside it: IF_IR
  // Probe on WB_PC[11:0]
  Comparator #(.width(13), .mode("twosComplement")) comparator_3 (
    .a(CNT_num), .b(13'h2bc), .eq(comparator_3_eq), .lt(comparator_3_lt));  // open: gt
  Clock #(.highDuration(1), .lowDuration(1)) clock_2 (.out(clock_2_out));
  \重定向控制器  \u_重定向控制器_1  (
    .EX_WriteReg_num(id_ex_1_writereg_num_2), .MEM_WriteReg_num(ex_mem_1_writereg_num_2), .RsForward(FwdA),
    .RtForward(FwdB), .Stall(Stall), .ID_EX_CLR(ID_EXRST), .IF_ID_CLR(\重定向控制器_1_if_id_clr ), .rs(RS),
    .IR(ID_IR), .rt(RT), .EX_MemtoReg(id_ex_1_memtoreg_2), .EX_RegWrite(id_ex_1_regwrite_2), .branch(JR),
    .MEM_RegWrite(ex_mem_1_regwrite_2), .PredictError(EX_PreErr));  // open: PC_EN
  IF_ID if_id_1 (
    .IR(IF_IR), .PC_4(IF_PC), .IR_2(ID_IR), .PC_4_ID(ID_PC), .CLK(CLK), .RST(\重定向控制器_1_if_id_clr ),
    .EN(and_4_out));
  nand nand_1 (nand_1_out, d_ff_1_q, comparator_3_eq);
  Counter #(.width(13), .max('h1fff), .ongoal("stay"), .trigger("rising"), .behavior("old")) counter_2 (
    .count(comparator_3_lt), .Q(CNT_num), .clk(clock_2_out));  // open: load, D, carry, clr, preset
  assign CLK = nand_1_out ? clock_2_out : 1'bz;  // Controlled_Buffer controlled_buffer_1
  // Probe on RS
  Multiplexer #(.select(1), .width(5), .disabled("Z"), .enable("false")) multiplexer_6 (
    .in0(ID_IR[20:16]), .in1(ID_IR[15:11]), .out(multiplexer_6_out), .sel(\单周期硬布线控制器_2_regdst ));
  Pull_Resistor #(.pull(1)) pull_resistor_1 (.node(CLK));
  \单周期硬布线控制器  \u_单周期硬布线控制器_2  (
    .Func(ID_IR[5:0]), .OP(ID_IR[31:26]), .ALU_OP(\单周期硬布线控制器_2_alu_op ), .MemToReg(\单周期硬布线控制器_2_memtoreg ),
    .MemWrite(\单周期硬布线控制器_2_memwrite ), .ALU_SRC(\单周期硬布线控制器_2_alu_src ), .RegWrite(\单周期硬布线控制器_2_regwrite ),
    .SysCALL(\单周期硬布线控制器_2_syscall ), .SignedExt(SignedExt), .RegDst(\单周期硬布线控制器_2_regdst ),
    .JR(\单周期硬布线控制器_2_jr ), .JMP(\单周期硬布线控制器_2_jmp ), .Beq(\单周期硬布线控制器_2_beq ), .JAL(\单周期硬布线控制器_2_jal ),
    .Bne(\单周期硬布线控制器_2_bne ), .SH(SH1), .SRAV(SRAV1), .BGTZ(BGTZ1));
  Multiplexer #(.select(1), .width(5), .disabled("Z"), .enable("false")) multiplexer_7 (
    .in0(ID_IR[25:21]), .in1(5'b00010), .out(RS), .sel(\单周期硬布线控制器_2_syscall ));
  Multiplexer #(.select(1), .width(5), .disabled("Z"), .enable("false")) multiplexer_8 (
    .in0(ID_IR[20:16]), .in1(5'b00100), .out(RT), .sel(\单周期硬布线控制器_2_syscall ));
  Multiplexer #(.select(1), .width(5), .disabled("Z"), .enable("false")) multiplexer_9 (
    .in0(multiplexer_6_out), .in1({5{1'b1}}), .out(multiplexer_9_out), .sel(\单周期硬布线控制器_2_jal ));
  assign bit_extender_1_out = {{16{1'b0}}, ID_IR[15:0]};  // Bit_Extender bit_extender_1
  assign bit_extender_2_out = {{16{ID_IR[15]}}, ID_IR[15:0]};  // Bit_Extender bit_extender_2
  not not_3 (not_3_out, CLK);
  Multiplexer #(.select(1), .width(32), .disabled("Z"), .enable("false")) multiplexer_10 (
    .in0(bit_extender_1_out), .in1(bit_extender_2_out), .out(multiplexer_10_out), .sel(SignedExt));
  Multiplexer #(.select(1), .width(1), .disabled("Z"), .enable("false")) multiplexer_11 (
    .in0(PredictJump), .in1(1'b0), .out(multiplexer_11_out), .sel(ID_EXRST));
  Multiplexer #(.select(1), .width(1), .disabled("Z"), .enable("false")) multiplexer_12 (
    .in0(SH1), .in1(1'b0), .out(multiplexer_12_out), .sel(ID_EXRST));
  Multiplexer #(.select(1), .width(1), .disabled("Z"), .enable("false")) multiplexer_13 (
    .in0(SRAV1), .in1(1'b0), .out(multiplexer_13_out), .sel(ID_EXRST));
  Multiplexer #(.select(1), .width(1), .disabled("Z"), .enable("false")) multiplexer_14 (
    .in0(BGTZ1), .in1(1'b0), .out(multiplexer_14_out), .sel(ID_EXRST));
  MIPS_Regifile mips_regifile_1 (
    .Din(RDin), .Clk(not_3_out), .R1(mips_regifile_1_r1), .R2(mips_regifile_1_r2), .WE(RegWrite),
    .W_num(mem_wb_1_writereg_num_2), .R1_num(RS), .R2_num(RT));
  // Mips_Probe mips_probe_7: pin names not known; wires that end beside it: ID_IR
  Register #(.width(1), .trigger("rising"), .Select("low")) register_4 (
    .D(multiplexer_11_out), .en(EN), .Q(register_4_q), .clk(CLK));  // open: clr
  Register #(.width(1), .trigger("rising"), .Select("low")) register_5 (
    .D(multiplexer_12_out), .en(EN), .Q(register_5_q), .clk(CLK));  // open: clr
  Register #(.width(1), .trigger("rising"), .Select("low")) register_6 (
    .D(multiplexer_13_out), .en(EN), .Q(SRAV), .clk(CLK));  // open: clr
  Register #(.width(1), .trigger("rising"), .Select("low")) register_7 (
    .D(multiplexer_14_out), .en(EN), .Q(BGTZ), .clk(CLK));  // open: clr
  ID_EX id_ex_1 (
    .BEQ(\单周期硬布线控制器_2_beq ), .BNE(\单周期硬布线控制器_2_bne ), .MemToReg(\单周期硬布线控制器_2_memtoreg ),
    .MemWrite(\单周期硬布线控制器_2_memwrite ), .AluOP(\单周期硬布线控制器_2_alu_op ), .AluSrcB(\单周期硬布线控制器_2_alu_src ),
    .RegWrite(\单周期硬布线控制器_2_regwrite ), .RS(mips_regifile_1_r1), .RT(mips_regifile_1_r2),
    .WriteReg_num(multiplexer_9_out), .SignImm(multiplexer_10_out), .IR_ID(ID_IR), .PC_4_ID(ID_PC),
    .BEQ_2(EX_BEQ), .BNE_2(EX_BNE), .MemToReg_2(id_ex_1_memtoreg_2), .MemWrite_2(id_ex_1_memwrite_2),
    .AluOP_2(id_ex_1_aluop_2), .AluSrcB_2(id_ex_1_alusrcb_2), .RegWrite_2(id_ex_1_regwrite_2), .RS_2(V0),
    .RT_2(id_ex_1_rt_2), .WriteReg_num_2(id_ex_1_writereg_num_2), .SignImm_2(id_ex_1_signimm_2),
    .IR_ID_2(EX_IR), .PC_4_ID_2(EX_PC), .CLK(CLK), .sys(\单周期硬布线控制器_2_syscall ), .sys_2(id_ex_1_sys_2),
    .in_22(EN), .jal(\单周期硬布线控制器_2_jal ), .jal_2(id_ex_1_jal_2), .JMP(\单周期硬布线控制器_2_jmp ), .JMP_2(JMP),
    .JR(\单周期硬布线控制器_2_jr ), .JR_2(JR), .RST(ID_EXRST), .FwdA(FwdA), .FwdA_2(id_ex_1_fwda_2), .FwdB(FwdB),
    .FwdB_2(id_ex_1_fwdb_2));
  Register #(.width(1), .trigger("rising"), .Select("low")) register_8 (
    .D(register_4_q), .Q(EX_PredictJump), .clk(CLK));  // open: en, clr
  Register #(.width(1), .trigger("rising"), .Select("low")) register_9 (
    .D(register_5_q), .Q(SH), .clk(CLK));  // open: en, clr
  or or_4 (branch, and_5_out, and_6_out);
  and and_5 (and_5_out, EX_BEQ, mips_alu_1_equal);
  and and_6 (and_6_out, ~mips_alu_1_equal, EX_BNE);  // AND_Gate
  Multiplexer #(.select(2), .width(32), .disabled("Z"), .enable("false")) multiplexer_15 (
    .in0(id_ex_1_rt_2), .in1(RDin), .in2(ALUreslut), .out(multiplexer_15_out), .sel(id_ex_1_fwdb_2));  // open: in3
  Multiplexer #(.select(2), .width(32), .disabled("Z"), .enable("false")) multiplexer_16 (
    .in0(V0), .in1(RDin), .in2(ALUreslut), .out(ALU_A), .sel(id_ex_1_fwda_2));  // open: in3
  Multiplexer #(.select(1), .width(32), .disabled("Z"), .enable("false")) multiplexer_17 (
    .in0(multiplexer_15_out), .in1(id_ex_1_signimm_2), .out(multiplexer_17_out), .sel(id_ex_1_alusrcb_2));
  Adder #(.width(32)) adder_2 (.a(EX_PC), .b(32'h4), .out(adder_2_out));  // open: cin, cout
  MIPS_ALU mips_alu_1 (
    .X(ALU_A), .Y(multiplexer_17_out), .AluOP(id_ex_1_aluop_2), .Equal(mips_alu_1_equal),
    .Result(mips_alu_1_result), .shamt(shamt));  // open: Result_2
  Shifter #(.width(32), .shift("ll")) shifter_1 (.in(id_ex_1_signimm_2), .\dist (5'b00010), .out(shifter_1_out));
  Adder #(.width(32)) adder_3 (.a(shifter_1_out), .b(adder_2_out), .out(EX_BranchAddr));  // open: cin, cout
  // Mips_Probe mips_probe_8: pin names not known; wires that end beside it: EX_IR
  Multiplexer #(.select(1), .width(5), .disabled("Z"), .enable("false")) multiplexer_18 (
    .in0(EX_IR[10:6]), .in1(V0[4:0]), .out(shamt), .sel(SRAV));
  EX_MEM ex_mem_1 (
    .RegWrite(id_ex_1_regwrite_2), .MemToReg(id_ex_1_memtoreg_2), .MemWrite(id_ex_1_memwrite_2),
    .IR_EX(EX_IR), .Result(mips_alu_1_result), .WriteData(multiplexer_15_out),
    .WriteReg_num(id_ex_1_writereg_num_2), .PC_4_EX(EX_PC), .RegWrite_2(ex_mem_1_regwrite_2),
    .MemToReg_2(ex_mem_1_memtoreg_2), .MemWrite_3(MemWrite), .IR_MEM(M_IR), .Result_2(ALUreslut),
    .WriteData_2(MDin), .WriteReg_num_2(ex_mem_1_writereg_num_2), .PC_4_MEM(M_PC), .CLK(CLK),
    .MemWrite_2(id_ex_1_sys_2), .MemWrite_4(ex_mem_1_memwrite_4), .in_13(EN), .jal(id_ex_1_jal_2),
    .jal_2(ex_mem_1_jal_2), .v0(ALU_A), .v0_2(ex_mem_1_v0_2));  // open: RST
  // Probe on M_IR
  // Mips_Probe mips_probe_9: pin names not known; wires that end beside it: M_IR
  Multiplexer #(.select(1), .width(32), .disabled("Z"), .enable("false")) multiplexer_19 (
    .in0(MDin), .in1(SHout), .out(LedData_in), .sel(SH));
  RAM #(.addrWidth(10), .dataWidth(32), .bus("separate"), .Select("high")) ram_1 (
    .addr(ALUreslut[11:2]), .din(LedData_in), .data(\字数据 ), .str(MemWrite), .clk(CLK));  // open: sel, ld, clr
  MEM_WB mem_wb_1 (
    .RegWrite(ex_mem_1_regwrite_2), .MemToReg(ex_mem_1_memtoreg_2), .Result(ALUreslut), .RD(\字数据 ),
    .WriteReg_num(ex_mem_1_writereg_num_2), .IR_MEM(M_IR), .PC_4_MEM(M_PC), .RegWrite_2(RegWrite),
    .MemToReg_2(mem_wb_1_memtoreg_2), .Result_2(mem_wb_1_result_2), .RD_2(mem_wb_1_rd_2),
    .WriteReg_num_2(mem_wb_1_writereg_num_2), .IR_WB(WB_IR), .PC_4_WB(WB_PC), .CLK(CLK),
    .sys(ex_mem_1_memwrite_4), .sys_2(Syscall), .in_12(EN), .jal(ex_mem_1_jal_2), .jal_2(mem_wb_1_jal_2),
    .v0(ex_mem_1_v0_2), .v0_2(rv0));  // open: RST
  // Probe on ALUreslut
  // Mips_Probe mips_probe_10: pin names not known; wires that end beside it: WB_IR
  Multiplexer #(.select(1), .width(32), .disabled("Z"), .enable("false")) multiplexer_20 (
    .in0(mem_wb_1_result_2), .in1(mem_wb_1_rd_2), .out(multiplexer_20_out), .sel(mem_wb_1_memtoreg_2));
  Multiplexer #(.select(1), .width(32), .disabled("Z"), .enable("false")) multiplexer_21 (
    .in0(multiplexer_20_out), .in1(adder_4_out), .out(RDin), .sel(mem_wb_1_jal_2));
  Adder #(.width(32)) adder_4 (.a(WB_PC), .b(32'h4), .out(adder_4_out));  // open: cin, cout
  Multiplexer #(.select(1), .width(32), .disabled("Z"), .enable("false")) multiplexer_22 (
    .in0({\字数据 [31:16], MDin[15:0]}), .in1({MDin[15:0], \字数据 [15:0]}), .out(SHout), .sel(ALUreslut[1]));

  // Other names for the same wires on the sheet: MEM_IR[31:0] = M_IR; MEM_PC[31:0] = M_PC; PC[31:0] = IF_PC

  // Notes on the sheet:
  //   中断源
  //   时空图监测，可删除
  //   中断等待指示
  //   数码管输出
  //   指令存储器
  //   控制位
  //   contents of rom_1 (hex, n*v repeats v):
  //   20110001 8000005 20110001 20120002 20130003 8000009 20110001 20120002 20130003 800000d 20110001
  //   20120002 20130003 8000011 20110001 20120002 20130003 c0000f8 20100001 20110001 118fc0 112020
  //   20020022 c 118882 12200001 8000015 112020 20020022 c 20110001 118880 112020 20020022 c 12200001
  //   800001f 20110001 118fc0 112020 20020022 c 1188c3 112020 20020022 c 118903 112020 20020022 c 118903
  //   112020 20020022 c 118903 112020 20020022 c 118903 112020 20020022 c 118903 112020 20020022 c 118903
  //   112020 20020022 c 118903 112020 20020022 c 20100001 109fc0 139fc3 8021 2012000c 24160003 26100001
  //   3210000f 20080008 20090001 139900 2709825 132020 20020022 c 1094022 1500fff9 22100001 2018000f
  //   2188024 108700 20080008 20090001 139902 2709825 132021 20020022 c 1094022 1500fff9 108702 2c9b022
  //   12c00001 8000050 4020 1084027 84400 3508ffff 82021 20020022 c 2010ffff 20110000 ae300000 22100001
  //   22310004 ae300000 22100001 22310004 ae300000 22100001 22310004 ae300000 22100001 22310004 ae300000
  //   22100001 22310004 ae300000 22100001 22310004 ae300000 22100001 22310004 ae300000 22100001 22310004
  //   ae300000 22100001 22310004 ae300000 22100001 22310004 ae300000 22100001 22310004 ae300000 22100001
  //   22310004 ae300000 22100001 22310004 ae300000 22100001 22310004 ae300000 22100001 22310004 ae300000
  //   22100001 22310004 22100001 8020 2011003c 8e130000 8e340000 274402a 11000002 ae330000 ae140000
  //   2231fffc 1611fff8 102020 20020022 c 22100004 2011003c 1611fff2 20020032 c 20080001 20090003 20110876
  //   118d00 112020 20020022 c 200b0008 1118807 1318807 112020 20020022 c 216bffff 1560fff9 2002000a c
  //   2008ffff 20117777 112020 20020022 c 200b0010 3a31ffff 112020 20020022 c 216bffff 1560fffa 2002000a c
  //   20090000 200b0020 20110001 20120001 a5310000 112020 20020022 c 2328820 21290002 216bffff 1560fff8
  //   200b0010 20090000 8d310000 112020 20020022 c 21290004 216bffff 1560fff9 2002000a c 2011000f 112020
  //   20020022 c 2231ffff 1e20fffb 2002000a c 2002000a c 20100000 22100001 102020 20020022 c 22100002
  //   102020 20020022 c 22100003 102020 20020022 c 22100004 102020 20020022 c 22100005 102020 20020022 c
  //   22100006 102020 20020022 c 22100007 102020 20020022 c 22100008 102020 20020022 20020022 c 3e00008
  //   流水调试日志用
  //   暂停节拍，不能为0
  //   戳工具置1进入计数暂停模式，ctrl+k时钟自动运行到对应节拍暂停
  //   ctrl+k关闭时钟连续运行，将控制位置零，进入单步调试模式调试
  //   rs
  //   rt
  //   rd
  //   可计数暂停的时钟源
  //   为方便自动评测，需要输出流水线各段保存的PC值，注意是PC不是PC+4，另外ID段寄存器写入信息，Mem段内存写入信息也要输出
  //   shamt
endmodule

module \中断按键参考电路  (
  input  \同步清零信号 ,
  output \与中断屏蔽位与 
);

  wire \_1号中断_out , and_1_out, clock_1_out, d_ff_1_q, or_1_out, or_2_out;

  Clock #(.highDuration(1), .lowDuration(1)) clock_1 (.out(clock_1_out));
  Button \_1号中断  (.out(\_1号中断_out ));
  or or_1 (or_1_out, \与中断屏蔽位与 , d_ff_1_q);
  LED #(.active("true")) \_1号中断等待指示灯  (.in(or_1_out));
  D_Flip_Flop #(.trigger("rising"), .Pre_Clr_Positions("LEGACY"), .NegatePresetClear("false"), .enable("true"), .NewFFLayout("false")) d_ff_1 (
    .clk(\_1号中断_out ), .D(1'b1), .Q(d_ff_1_q), .reset(\与中断屏蔽位与 ));  // open: Qn, preset, en
  or or_2 (or_2_out, d_ff_1_q, \与中断屏蔽位与 );
  and and_1 (and_1_out, or_2_out, ~\同步清零信号 );  // AND_Gate
  D_Flip_Flop #(.trigger("rising"), .Pre_Clr_Positions("LEGACY"), .NegatePresetClear("false"), .enable("true"), .NewFFLayout("false")) IR1 (
    .clk(clock_1_out), .D(and_1_out), .Q(\与中断屏蔽位与 ));  // open: Qn, preset, en, reset

  // Notes on the sheet:
  //   中断信号采样参考电路
  //   Reset 
endmodule
module \单周期MIPS_单级中断  (
  input  IR1,
  input  IR2,
  input  IR3,
  input  in_4,
  output RegWrite,
  output MemWrite,
  output [31:0] PC,
  output [31:0] IR,
  output [31:0] RDin,
  output [31:0] MDin,
  output [31:0] LedData
);

  wire _1_out, _2_out, _3_out, and_1_out, and_3_out, and_4_out, and_5_out, and_6_out, and_7_out,
       buffer_1_out, buffer_2_out, CLK, clock_2_out, CLR1, CLR2, CLR3, comparator_1_eq, comparator_2_eq,
       comparator_3_eq, comparator_4_eq, comparator_5_eq, comparator_5_lt, comparator_7_eq,
       controlled_inverter_1_out, controlled_inverter_2_out, controlled_inverter_3_out, d_ff_1_q, d_ff_2_q,
       d_ff_3_q, d_ff_4_q, ERET, Go, Halt, IE, INT, INT1, INT2, INT3, IR1_t, IR2_t, IR3_t, IRA, IRC, LedOut,
       mips_alu_1_equal, nand_1_out, not_1_out, or_1_out, or_2_out, or_4_out, or_5_out, or_7_out, or_11_out,
       or_12_out, or_14_out, or_15_out, RST, SignedExt, SysCall, W1, W2, W3, \单周期硬布线控制器_1_alu_src ,
       \单周期硬布线控制器_1_beq , \单周期硬布线控制器_1_bne , \单周期硬布线控制器_1_jal , \单周期硬布线控制器_1_jmp , \单周期硬布线控制器_1_jr ,
       \单周期硬布线控制器_1_memtoreg , \单周期硬布线控制器_1_regdst ;
  wire [1:0] priority_encoder_1_out, priority_encoder_2_out, register_1_q;
  wire [3:0] \单周期硬布线控制器_1_alu_op ;
  wire [4:0] multiplexer_7_out, multiplexer_8_out, multiplexer_9_out, multiplexer_10_out;
  wire [9:0] multiplexer_13_out, \内存原地址 ;
  wire [12:0] CNT_num;
  wire [15:0] \总周期数 ;
  wire [27:0] adder_1_out, bit_extender_1_out;
  wire [31:0] adder_2_out, bit_extender_2_out, bit_extender_3_out, EPCout, mips_alu_1_result,
       multiplexer_1_out, multiplexer_2_out, multiplexer_4_out, multiplexer_5_out, multiplexer_11_out,
       multiplexer_12_out, multiplexer_15_out, ret, shifter_1_out, shifter_2_out, undriven, V0, \中断入口地址 ;

  Clock #(.highDuration(1), .lowDuration(1)) clock_1 ();  // open: out
  Button _1 (.out(_1_out));
  Button _2 (.out(_2_out));
  Button _3 (.out(_3_out));
  Button \u_继续运行  (.out(Go));
  LED #(.active("true")) led_1 (.in(W1));
  LED #(.active("true")) led_2 (.in(W2));
  LED #(.active("true")) led_3 (.in(W3));
  or or_1 (or_1_out, INT1, INT2, INT3);
  or or_2 (or_2_out, INT1, INT2, INT3);
  Hex_Digit_Display hex_digit_display_1 (.value(LedData[31:28]));  // open: dp
  Comparator #(.width(16), .mode("twosComplement")) comparator_1 (
    .a(16'h23b), .b(\总周期数 ), .eq(comparator_1_eq));  // open: gt, lt
  Comparator #(.width(16), .mode("twosComplement")) comparator_2 (
    .a(\总周期数 ), .b(16'h1), .eq(comparator_2_eq));  // open: gt, lt
  Comparator #(.width(16), .mode("twosComplement")) comparator_3 (
    .a(\总周期数 ), .b(16'h4), .eq(comparator_3_eq));  // open: gt, lt
  Comparator #(.width(16), .mode("twosComplement")) comparator_4 (
    .a(\总周期数 ), .b(16'h7), .eq(comparator_4_eq));  // open: gt, lt
  or or_3 (W1, INT1, d_ff_1_q);
  Hex_Digit_Display hex_digit_display_2 (.value(LedData[27:24]));  // open: dp
  Hex_Digit_Display hex_digit_display_3 (.value(LedData[23:20]));  // open: dp
  or or_4 (or_4_out, comparator_1_eq, comparator_2_eq);
  assign controlled_inverter_1_out = or_4_out ? ~CLK : 1'bz;  // Controlled_Inverter controlled_inverter_1
  assign controlled_inverter_2_out = comparator_3_eq ? ~CLK : 1'bz;  // Controlled_Inverter controlled_inverter_2
  assign controlled_inverter_3_out = comparator_4_eq ? ~CLK : 1'bz;  // Controlled_Inverter controlled_inverter_3
  D_Flip_Flop #(.trigger("rising"), .Pre_Clr_Positions("LEGACY"), .NegatePresetClear("false"), .enable("true"), .NewFFLayout("false")) d_ff_1 (
    .clk(IR1_t), .D(1'b1), .Q(d_ff_1_q), .reset(INT1));  // open: Qn, preset, en
  and and_1 (and_1_out, or_1_out, ~ERET);  // AND_Gate
  and and_2 (INT, ~IE, or_2_out);  // AND_Gate
  Hex_Digit_Display hex_digit_display_4 (.value(LedData[19:16]));  // open: dp
  Hex_Digit_Display hex_digit_display_5 (.value(LedData[15:12]));  // open: dp
  Pull_Resistor #(.pull(0)) pull_resistor_1 (.node(controlled_inverter_1_out));
  Pull_Resistor #(.pull(0)) pull_resistor_2 (.node(controlled_inverter_2_out));
  Pull_Resistor #(.pull(0)) pull_resistor_3 (.node(controlled_inverter_3_out));
  Multiplexer #(.select(1), .width(32), .disabled("Z"), .enable("false")) multiplexer_1 (
    .in0({shifter_1_out[31:28], adder_1_out}), .in1(adder_2_out), .out(multiplexer_1_out), .sel(or_12_out));
  or or_5 (or_5_out, d_ff_1_q, INT1);
  Register #(.width(1), .trigger("rising"), .Select("low")) u_IE (.D(and_1_out), .Q(IE), .clk(CLK));  // open: en, clr
  Hex_Digit_Display hex_digit_display_6 (.value(LedData[11:8]));  // open: dp
  Hex_Digit_Display hex_digit_display_7 (.value(LedData[7:4]));  // open: dp
  // Probe on \总周期数 
  Multiplexer #(.select(1), .width(32), .disabled("Z"), .enable("false")) multiplexer_2 (
    .in0(multiplexer_1_out), .in1(shifter_1_out), .out(multiplexer_2_out), .sel(\单周期硬布线控制器_1_jmp ));
  and and_3 (and_3_out, or_5_out, ~CLR1);  // AND_Gate
  Hex_Digit_Display hex_digit_display_8 (.value(LedData[3:0]));  // open: dp
  Multiplexer #(.select(1), .width(32), .disabled("Z"), .enable("false")) multiplexer_3 (
    .in0(multiplexer_2_out), .in1(V0), .out(ret), .sel(\单周期硬布线控制器_1_jr ));
  D_Flip_Flop #(.trigger("rising"), .Pre_Clr_Positions("LEGACY"), .NegatePresetClear("false"), .enable("true"), .NewFFLayout("false")) u_IR1 (
    .clk(CLK), .D(and_3_out), .Q(INT1));  // open: Qn, preset, en, reset
  Button button_1 (.out(RST));
  buf buffer_1 (buffer_1_out, INT);
  buf buffer_2 (buffer_2_out, buffer_1_out);
  Multiplexer #(.select(1), .width(32), .disabled("Z"), .enable("false")) multiplexer_4 (
    .in0(ret), .in1(\中断入口地址 ), .out(multiplexer_4_out), .sel(buffer_2_out));
  Priority_Encoder #(.select(2), .disabled("Z")) priority_encoder_1 (
    .in0(INT1), .in1(INT2), .in2(INT3), .out(priority_encoder_1_out));  // open: in3, gs, en_out, en_in
  Register #(.width(2), .trigger("rising"), .Select("low")) register_1 (
    .D(priority_encoder_1_out), .en(INT), .Q(register_1_q), .clk(CLK));  // open: clr
  Demultiplexer #(.select(2), .width(1), .tristate("false"), .disabled("Z"), .enable("false")) demultiplexer_1 (
    .out0(CLR1), .out1(CLR2), .out2(CLR3), .in(ERET), .sel(register_1_q));  // open: out3
  or or_6 (IR1_t, IR1, IRA);
  Multiplexer #(.select(1), .width(32), .disabled("Z"), .enable("false")) multiplexer_5 (
    .in0(multiplexer_4_out), .in1(EPCout), .out(multiplexer_5_out), .sel(ERET));
  or or_7 (or_7_out, Go, ~Halt);  // OR_Gate
  Multiplexer #(.select(2), .width(32), .disabled("Z"), .enable("false")) multiplexer_6 (
    .in0(32'h30ac), .in1(32'h3150), .in2(32'h31f4), .out(\中断入口地址 ), .sel(priority_encoder_1_out));  // open: in3
  or or_8 (IR2_t, IR2, in_4);
  Register #(.width(32), .trigger("rising"), .Select("low")) u_PC (
    .D(multiplexer_5_out), .en(or_7_out), .Q(PC), .clk(CLK), .clr(RST));
  // Probe on shifter_1_out[27:0]
  // Probe on priority_encoder_1_out
  Adder #(.width(32)) adder_1 (.a(PC), .b(32'h4), .out({shifter_1_out[31:28], adder_1_out}));  // open: cin, cout
  or or_9 (IR3_t, IR3, IRC);
  // Mips_Probe mips_probe_1: pin names not known; wires that end beside it: IR
  or or_10 (W2, INT2, d_ff_3_q);
  ROM #(.addrWidth(10), .dataWidth(32), .Select("high")) rom_1 (.addr(PC[11:2]), .data(IR));
  D_Flip_Flop #(.trigger("high"), .Pre_Clr_Positions("LEGACY"), .NegatePresetClear("false"), .enable("true"), .NewFFLayout("false")) d_ff_2 (.Q(d_ff_2_q));  // open: clk, D, Qn, preset, en, reset
  D_Flip_Flop #(.trigger("rising"), .Pre_Clr_Positions("LEGACY"), .NegatePresetClear("false"), .enable("true"), .NewFFLayout("false")) d_ff_3 (
    .clk(IR2_t), .D(1'b1), .Q(d_ff_3_q), .reset(INT2));  // open: Qn, preset, en
  // Probe on 13'hc
  or or_11 (or_11_out, d_ff_3_q, INT2);
  and and_4 (and_4_out, or_11_out, ~CLR2);  // AND_Gate
  Register #(.width(32), .trigger("rising"), .Select("low")) EPC (
    .D(ret), .en(INT), .Q(EPCout), .clk(CLK));  // open: clr
  assign bit_extender_1_out = {{2{1'b0}}, IR[25:0]};  // Bit_Extender bit_extender_1
  Comparator #(.width(13), .mode("twosComplement")) comparator_5 (
    .a(CNT_num), .b(13'hc), .eq(comparator_5_eq), .lt(comparator_5_lt));  // open: gt
  Clock #(.highDuration(1), .lowDuration(1)) clock_2 (.out(clock_2_out));
  D_Flip_Flop #(.trigger("rising"), .Pre_Clr_Positions("LEGACY"), .NegatePresetClear("false"), .enable("true"), .NewFFLayout("false")) IR1_2 (
    .clk(CLK), .D(and_4_out), .Q(INT2));  // open: Qn, preset, en, reset
  Multiplexer #(.select(1), .width(5), .disabled("Z"), .enable("false")) multiplexer_7 (
    .in0(IR[25:21]), .in1(5'b00010), .out(multiplexer_7_out), .sel(SysCall));
  Multiplexer #(.select(1), .width(5), .disabled("Z"), .enable("false")) multiplexer_8 (
    .in0(IR[20:16]), .in1(5'b00100), .out(multiplexer_8_out), .sel(SysCall));
  Multiplexer #(.select(1), .width(5), .disabled("Z"), .enable("false")) multiplexer_9 (
    .in0(IR[20:16]), .in1(IR[15:11]), .out(multiplexer_9_out), .sel(\单周期硬布线控制器_1_regdst ));
  nand nand_1 (nand_1_out, d_ff_2_q, comparator_5_eq);
  Counter #(.width(13), .max('h1fff), .ongoal("stay"), .trigger("rising"), .behavior("old")) counter_1 (
    .count(comparator_5_lt), .Q(CNT_num), .clk(clock_2_out));  // open: load, D, carry, clr, preset
  \单周期硬布线控制器  \u_单周期硬布线控制器_1  (
    .Func(IR[5:0]), .OP(IR[31:26]), .ALU_OP(\单周期硬布线控制器_1_alu_op ), .MemToReg(\单周期硬布线控制器_1_memtoreg ),
    .MemWrite(MemWrite), .ALU_SRC(\单周期硬布线控制器_1_alu_src ), .RegWrite(RegWrite), .SysCALL(SysCall),
    .SignedExt(SignedExt), .RegDst(\单周期硬布线控制器_1_regdst ), .JR(\单周期硬布线控制器_1_jr ), .JMP(\单周期硬布线控制器_1_jmp ),
    .Beq(\单周期硬布线控制器_1_beq ), .JAL(\单周期硬布线控制器_1_jal ), .Bne(\单周期硬布线控制器_1_bne ));  // open: SH, SRAV, BGTZ
  Multiplexer #(.select(1), .width(5), .disabled("Z"), .enable("false")) multiplexer_10 (
    .in0(multiplexer_9_out), .in1({5{1'b1}}), .out(multiplexer_10_out), .sel(\单周期硬布线控制器_1_jal ));
  Shifter #(.width(28), .shift("ll")) shifter_1 (.in(bit_extender_1_out), .\dist (5'b00010), .out(shifter_1_out[27:0]));
  assign CLK = nand_1_out ? clock_2_out : 1'bz;  // Controlled_Buffer controlled_buffer_1
  Pull_Resistor #(.pull(1)) pull_resistor_4 (.node(CLK));
  assign bit_extender_2_out = {{16{IR[15]}}, IR[15:0]};  // Bit_Extender bit_extender_2
  and and_5 (and_5_out, mips_alu_1_equal, \单周期硬布线控制器_1_beq );
  and and_6 (and_6_out, ~mips_alu_1_equal, \单周期硬布线控制器_1_bne );  // AND_Gate
  MIPS_Regifile mips_regifile_1 (
    .Din(RDin), .Clk(CLK), .R1(V0), .R2(MDin), .WE(RegWrite), .W_num(multiplexer_10_out),
    .R1_num(multiplexer_7_out), .R2_num(multiplexer_8_out));
  or or_12 (or_12_out, and_5_out, and_6_out);
  Multiplexer #(.select(1), .width(32), .disabled("Z"), .enable("false")) multiplexer_11 (
    .in0(MDin), .in1(bit_extender_2_out), .out(multiplexer_11_out), .sel(\单周期硬布线控制器_1_alu_src ));
  Comparator #(.width(32), .mode("twosComplement")) comparator_6 (.a(IR), .b(32'h42000018), .eq(ERET));  // open: gt, lt
  or or_13 (W3, INT3, d_ff_4_q);
  // Probe on V0
  Shifter #(.width(32), .shift("ll")) shifter_2 (.in(bit_extender_2_out), .\dist (5'b00010), .out(shifter_2_out));
  D_Flip_Flop #(.trigger("rising"), .Pre_Clr_Positions("LEGACY"), .NegatePresetClear("false"), .enable("true"), .NewFFLayout("false")) d_ff_4 (
    .clk(IR3_t), .D(1'b1), .Q(d_ff_4_q), .reset(INT3));  // open: Qn, preset, en
  Adder #(.width(32)) adder_2 (
    .a(shifter_2_out), .b({shifter_1_out[31:28], adder_1_out}), .out(adder_2_out));  // open: cin, cout
  or or_14 (or_14_out, d_ff_4_q, INT3);
  and and_7 (and_7_out, or_14_out, ~CLR3);  // AND_Gate
  MIPS_ALU mips_alu_1 (
    .X(V0), .Y(multiplexer_11_out), .AluOP(\单周期硬布线控制器_1_alu_op ), .Equal(mips_alu_1_equal),
    .Result({mips_alu_1_result[31:12], \内存原地址 , mips_alu_1_result[1:0]}), .shamt(IR[10:6]));  // open: Result_2
  D_Flip_Flop #(.trigger("rising"), .Pre_Clr_Positions("LEGACY"), .NegatePresetClear("false"), .enable("true"), .NewFFLayout("false")) IR1_3 (
    .clk(CLK), .D(and_7_out), .Q(INT3));  // open: Qn, preset, en, reset
  Comparator #(.width(32), .mode("twosComplement")) comparator_7 (
    .a(V0), .b(32'h22), .eq(comparator_7_eq));  // open: gt, lt
  // Probe on MDin
  Button _2_2 (.out(in_4));
  Button _3_2 (.out(IRC));
  and and_8 (LedOut, SysCall, comparator_7_eq);
  and and_9 (Halt, SysCall, ~comparator_7_eq);  // AND_Gate
  Register #(.width(32), .trigger("rising"), .Select("low")) register_2 (
    .D(MDin), .en(LedOut), .Q(LedData), .clk(CLK), .clr(RST));
  Priority_Encoder #(.select(2), .disabled("Z")) priority_encoder_2 (
    .in0(1'b0), .in1(1'b0), .in2(INT2), .in3(INT3), .out(priority_encoder_2_out));  // open: gs, en_out, en_in
  // Probe on priority_encoder_2_out
  assign bit_extender_3_out = {{30{1'b0}}, priority_encoder_2_out};  // Bit_Extender bit_extender_3
  Button _1_2 (.out(IRA));
  Multiplexer #(.select(1), .width(32), .disabled("Z"), .enable("false")) multiplexer_12 (
    .in0({mips_alu_1_result[31:12], \内存原地址 , mips_alu_1_result[1:0]}), .in1(undriven),
    .out(multiplexer_12_out), .sel(\单周期硬布线控制器_1_memtoreg ));
  Multiplexer #(.select(1), .width(10), .disabled("Z"), .enable("false")) multiplexer_13 (
    .in0(10'h1), .in1({10{1'b0}}), .out(multiplexer_13_out), .sel(INT));
  LED #(.active("true")) led_4 (.in(W1));
  LED #(.active("true")) led_5 (.in(W2));
  LED #(.active("true")) led_6 (.in(W3));
  not not_1 (not_1_out, Halt);
  Multiplexer #(.select(1), .width(32), .disabled("Z"), .enable("false")) multiplexer_14 (
    .in0(multiplexer_12_out), .in1({shifter_1_out[31:28], adder_1_out}), .out(RDin), .sel(\单周期硬布线控制器_1_jal ));
  Multiplexer #(.select(1), .width(32), .disabled("Z"), .enable("false")) multiplexer_15 (
    .in0(MDin), .in1(bit_extender_3_out), .out(multiplexer_15_out), .sel(INT));
  or or_15 (or_15_out, INT, MemWrite);
  Counter #(.width(16), .max('hffff), .ongoal("wrap"), .trigger("rising"), .behavior("new")) counter_2 (
    .count(not_1_out), .Q(\总周期数 ), .clk(CLK), .clr(RST));  // open: load, D, carry, preset, down
  RAM #(.addrWidth(10), .dataWidth(32), .bus("separate"), .Select("high")) ram_1 (
    .addr(multiplexer_13_out), .din(multiplexer_15_out), .str(or_15_out), .clk(CLK), .clr(RST));  // open: data, sel, ld

  // Other names for the same wires on the sheet: IRB = in_4; writemem[31:0] = MDin

  // Notes on the sheet:
  //   中断源
  //   中断等待指示
  //   总复位信号应将除ROM以外所有存储组件全部清零
  //   单级中断测试信号模拟器
  //   数码管输出
  //   中断信号采样参考电路
  //   数码管输出应该用寄存器锁存，否则显示数据只能一闪而过
  //   Reset 
  //   指令存储器
  //   contents of rom_1 (hex, n*v repeats v):
  //   201d07d0 20100001 109fc0 139fc3 8021 2012000c 24160008 26100001 3210000f 20080008 20090001 139900
  //   2709825 132020 20020022 c 1094022 1500fff9 22100001 2018000f 2188024 108700 20080008 20090001 139902
  //   2709825 132021 20020022 c 1094022 1500fff9 108702 2c9b022 12c00001 8000c07 4020 1084027 84400
  //   3508ffff 82021 20020022 c 8000c01 afa20000 23bd0004 afa40000 23bd0004 afb00000 23bd0004 afb30000
  //   23bd0004 afb40000 23bd0004 afb50000 23bd0004 afb60000 23bd0004 20160001 20140003 20150001 168020
  //   108100 2149825 132020 20020022 c 1600fffa 295a022 1680fff7 23bdfffc 8fb60000 23bdfffc 8fb50000
  //   23bdfffc 8fb40000 23bdfffc 8fb30000 23bdfffc 8fb00000 23bdfffc 8fa40000 23bdfffc 8fa20000 42000018
  //   afa20000 23bd0004 afa40000 23bd0004 afb00000 23bd0004 afb30000 23bd0004 afb40000 23bd0004 afb50000
  //   23bd0004 afb60000 23bd0004 20160002 20140003 20150001 168020 108100 2149825 132020 20020022 c
  //   1600fffa 295a022 1680fff7 23bdfffc 8fb60000 23bdfffc 8fb50000 23bdfffc 8fb40000 23bdfffc 8fb30000
  //   23bdfffc 8fb00000 23bdfffc 8fa40000 23bdfffc 8fa20000 42000018 afa20000 23bd0004 afa40000 23bd0004
  //   afb00000 23bd0004 afb30000 23bd0004 afb40000 23bd0004 afb50000 23bd0004 afb60000 23bd0004 20160003
  //   20140003 20150001 168020 108100 2149825 132020 20020022 c 1600fffa 295a022 1680fff7 23bdfffc
  //   8fb60000 23bdfffc 8fb50000 23bdfffc 8fb40000 23bdfffc 8fb30000 23bdfffc 8fb00000 23bdfffc 8fa40000
  //   23bdfffc 8fa20000 42000018
  //   控制位
  //   暂停节拍，不能为0
  //   中断信号采样参考电路
  //   OP
  //   Func
  //   rs
  //   rt
  //   rd
  //   指令字
  //   shamt
  //   imm16
  //   用这个时钟源需要去掉电路中的其他时钟源
  //   为方便自动评测，需要输出PC，IR，寄存器堆写如数据RDin
  //   戳工具置1进入计数暂停模式，ctrl+k时钟自动运行到对应节拍暂停
  //   ctrl+k关闭时钟连续运行，将控制位置零，进入单步调试模式调试
  //   Reset 
  //   RAM写使能MemWrite、RAM写入数据MDin等信号
  //   JMP
  //   JR
  //   OP
  //   Func
  //   Beq
  //   Bne
  //   MemToReg
  //   MemWrite
  //   AluOP
  //   AluSrcB
  //   RegWrite
  //   JAL
  //   RegDst
  //   Syscall
  //   可计数暂停的时钟源
  //   中断信号采样参考电路
  //   Reset 
endmodule

module \单周期MIPS_多级中断  (
  input  IR1,
  input  IR2,
  input  IR3,
  output RegWrite,
  output MemWrite,
  output [31:0] PC,
  output [31:0] IR,
  output [31:0] RDin,
  output [31:0] MDin,
  output [31:0] LedData
);

  wire and_5_out, and_7_out, and_8_out, and_9_out, and_10_out, CLK, clock_1_out, clock_2_out, CLR1, CLR2,
       CLR3, comparator_1_eq, comparator_2_eq, comparator_3_eq, comparator_4_eq, comparator_5_eq,
       comparator_6_eq, comparator_7_eq, comparator_9_gt, comparator_10_eq, comparator_10_lt,
       controlled_inverter_1_out, controlled_inverter_2_out, controlled_inverter_3_out, d_ff_1_q, d_ff_2_q,
       d_ff_3_q, d_ff_4_q, ERET, Go, Halt, IE, INT, INT1, INT2, INT3, IR1_t, IR2_t, IR3_t, IRA, IRB, IRC,
       LedOut, MFC0, MFCMTC, mips_alu_1_equal, MTC0, nand_1_out, not_1_out, not_2_out, or_2_out, or_3_out,
       or_5_out, or_9_out, or_10_out, or_12_out, or_13_out, or_14_out, or_15_out, or_16_out, RST, SignedExt,
       SysCall, W1, W2, W3, \单周期硬布线控制器_1_alu_src , \单周期硬布线控制器_1_beq , \单周期硬布线控制器_1_bne , \单周期硬布线控制器_1_jal ,
       \单周期硬布线控制器_1_jmp , \单周期硬布线控制器_1_jr , \单周期硬布线控制器_1_memtoreg , \单周期硬布线控制器_1_regdst ;
  wire [1:0] cur_IntNo, multiplexer_13_out, multiplexer_15_out, multiplexer_17_out, priority_encoder_1_out,
       register_4_q, register_7_q;
  wire [3:0] \单周期硬布线控制器_1_alu_op ;
  wire [4:0] multiplexer_7_out, multiplexer_8_out, multiplexer_9_out, multiplexer_10_out;
  wire [12:0] CNT_num;
  wire [15:0] \总周期数 ;
  wire [27:0] bit_extender_1_out, shifter_1_out;
  wire [31:0] adder_1_out, adder_2_out, bit_extender_2_out, EPCout, mips_alu_1_result, multiplexer_1_out,
       multiplexer_2_out, multiplexer_4_out, multiplexer_5_out, multiplexer_11_out, multiplexer_12_out,
       multiplexer_14_out, multiplexer_16_out, multiplexer_18_out, ram_1_data, register_3_q, register_6_q,
       ret, shifter_2_out, V0, \中断入口地址 ;

  Clock #(.highDuration(1), .lowDuration(1)) clock_1 (.out(clock_1_out));
  Button _1 (.out(IRA));
  Button _2 (.out(IRB));
  Button _3 (.out(IRC));
  Button \u_继续运行  (.out(Go));
  LED #(.active("true")) led_1 (.in(W1));
  LED #(.active("true")) led_2 (.in(W2));
  LED #(.active("true")) led_3 (.in(W3));
  Hex_Digit_Display hex_digit_display_1 (.value(LedData[31:28]));  // open: dp
  Comparator #(.width(16), .mode("twosComplement")) comparator_1 (
    .a(16'h23b), .b(\总周期数 ), .eq(comparator_1_eq));  // open: gt, lt
  Comparator #(.width(16), .mode("twosComplement")) comparator_2 (
    .a(\总周期数 ), .b(16'h1), .eq(comparator_2_eq));  // open: gt, lt
  Comparator #(.width(16), .mode("twosComplement")) comparator_3 (
    .a(\总周期数 ), .b(16'h4), .eq(comparator_3_eq));  // open: gt, lt
  Comparator #(.width(16), .mode("twosComplement")) comparator_4 (
    .a(\总周期数 ), .b(16'h7), .eq(comparator_4_eq));  // open: gt, lt
  or or_1 (W1, INT1, d_ff_1_q);
  Comparator #(.width(32), .mode("twosComplement")) comparator_5 (
    .a(V0), .b(32'h22), .eq(comparator_5_eq));  // open: gt, lt
  Comparator #(.width(5), .mode("twosComplement")) comparator_6 (
    .a(IR[25:21]), .b({5{1'b0}}), .eq(comparator_6_eq));  // open: gt, lt
  Comparator #(.width(5), .mode("twosComplement")) comparator_7 (
    .a(IR[25:21]), .b(5'b00100), .eq(comparator_7_eq));  // open: gt, lt
  Comparator #(.width(6), .mode("twosComplement")) comparator_8 (
    .a(IR[31:26]), .b(6'b010000), .eq(MFCMTC));  // open: gt, lt
  Hex_Digit_Display hex_digit_display_2 (.value(LedData[27:24]));  // open: dp
  Hex_Digit_Display hex_digit_display_3 (.value(LedData[23:20]));  // open: dp
  or or_2 (or_2_out, comparator_1_eq, comparator_2_eq);
  assign controlled_inverter_1_out = or_2_out ? ~CLK : 1'bz;  // Controlled_Inverter controlled_inverter_1
  assign controlled_inverter_2_out = comparator_3_eq ? ~CLK : 1'bz;  // Controlled_Inverter controlled_inverter_2
  assign controlled_inverter_3_out = comparator_4_eq ? ~CLK : 1'bz;  // Controlled_Inverter controlled_inverter_3
  D_Flip_Flop #(.trigger("rising"), .Pre_Clr_Positions("LEGACY"), .NegatePresetClear("false"), .enable("true"), .NewFFLayout("false")) d_ff_1 (
    .clk(IR1_t), .D(1'b1), .Q(d_ff_1_q), .reset(INT1));  // open: Qn, preset, en
  and and_1 (LedOut, SysCall, comparator_5_eq);
  and and_2 (Halt, SysCall, ~comparator_5_eq);  // AND_Gate
  Hex_Digit_Display hex_digit_display_4 (.value(LedData[19:16]));  // open: dp
  Hex_Digit_Display hex_digit_display_5 (.value(LedData[15:12]));  // open: dp
  Pull_Resistor #(.pull(0)) pull_resistor_1 (.node(controlled_inverter_1_out));
  Pull_Resistor #(.pull(0)) pull_resistor_2 (.node(controlled_inverter_2_out));
  Pull_Resistor #(.pull(0)) pull_resistor_3 (.node(controlled_inverter_3_out));
  Multiplexer #(.select(1), .width(32), .disabled("Z"), .enable("false")) multiplexer_1 (
    .in0(adder_1_out), .in1(adder_2_out), .out(multiplexer_1_out), .sel(or_10_out));
  or or_3 (or_3_out, d_ff_1_q, INT1);
  and and_3 (MFC0, comparator_6_eq, MFCMTC);
  and and_4 (MTC0, comparator_7_eq, MFCMTC);
  Hex_Digit_Display hex_digit_display_6 (.value(LedData[11:8]));  // open: dp
  Hex_Digit_Display hex_digit_display_7 (.value(LedData[7:4]));  // open: dp
  // Probe on \总周期数 
  Multiplexer #(.select(1), .width(32), .disabled("Z"), .enable("false")) multiplexer_2 (
    .in0(multiplexer_1_out), .in1({adder_1_out[31:28], shifter_1_out}), .out(multiplexer_2_out),
    .sel(\单周期硬布线控制器_1_jmp ));
  and and_5 (and_5_out, or_3_out, ~CLR1);  // AND_Gate
  Pull_Resistor #(.pull(0)) pull_resistor_4 (.node(CLR1));
  Hex_Digit_Display hex_digit_display_8 (.value(LedData[3:0]));  // open: dp
  Multiplexer #(.select(1), .width(32), .disabled("Z"), .enable("false")) multiplexer_3 (
    .in0(multiplexer_2_out), .in1(V0), .out(ret), .sel(\单周期硬布线控制器_1_jr ));
  D_Flip_Flop #(.trigger("rising"), .Pre_Clr_Positions("LEGACY"), .NegatePresetClear("false"), .enable("true"), .NewFFLayout("false")) u_IR1 (
    .clk(CLK), .D(and_5_out), .Q(INT1));  // open: Qn, preset, en, reset
  Button button_1 (.out(RST));
  Multiplexer #(.select(1), .width(32), .disabled("Z"), .enable("false")) multiplexer_4 (
    .in0(ret), .in1(\中断入口地址 ), .out(multiplexer_4_out), .sel(INT));
  or or_4 (IR1_t, IR1, IRA);
  Multiplexer #(.select(1), .width(32), .disabled("Z"), .enable("false")) multiplexer_5 (
    .in0(multiplexer_4_out), .in1(EPCout), .out(multiplexer_5_out), .sel(ERET));
  or or_5 (or_5_out, Go, ~Halt);  // OR_Gate
  Priority_Encoder #(.select(2), .disabled("Z")) priority_encoder_1 (
    .in1(INT1), .in2(INT2), .in3(INT3), .out(priority_encoder_1_out));  // open: in0, gs, en_out, en_in
  or or_6 (IR2_t, IR2, IRB);
  Register #(.width(32), .trigger("rising"), .Select("low")) u_PC (
    .D(multiplexer_5_out), .en(or_5_out), .Q(PC), .clk(CLK), .clr(RST));
  // Probe on shifter_1_out
  // Probe on priority_encoder_1_out
  Multiplexer #(.select(2), .width(32), .disabled("Z"), .enable("false")) multiplexer_6 (
    .in1(32'h30ac), .in2(32'h3158), .in3(32'h3204), .out(\中断入口地址 ), .sel(priority_encoder_1_out));  // open: in0
  Adder #(.width(32)) adder_1 (.a(PC), .b(32'h4), .out(adder_1_out));  // open: cin, cout
  not not_1 (not_1_out, IE);
  Comparator #(.width(2), .mode("unsigned")) comparator_9 (
    .a(priority_encoder_1_out), .b(cur_IntNo), .gt(comparator_9_gt));  // open: eq, lt
  or or_7 (IR3_t, IR3, IRC);
  // Mips_Probe mips_probe_1: pin names not known; wires that end beside it: IR
  or or_8 (W2, INT2, d_ff_3_q);
  and and_6 (INT, not_1_out, comparator_9_gt);
  ROM #(.addrWidth(10), .dataWidth(32), .Select("high")) rom_1 (.addr(PC[11:2]), .data(IR));
  D_Flip_Flop #(.trigger("high"), .Pre_Clr_Positions("LEGACY"), .NegatePresetClear("false"), .enable("true"), .NewFFLayout("false")) d_ff_2 (.Q(d_ff_2_q));  // open: clk, D, Qn, preset, en, reset
  D_Flip_Flop #(.trigger("rising"), .Pre_Clr_Positions("LEGACY"), .NegatePresetClear("false"), .enable("true"), .NewFFLayout("false")) d_ff_3 (
    .clk(IR2_t), .D(1'b1), .Q(d_ff_3_q), .reset(INT2));  // open: Qn, preset, en
  // Probe on 13'hc
  or or_9 (or_9_out, d_ff_3_q, INT2);
  and and_7 (and_7_out, or_9_out, ~CLR2);  // AND_Gate
  Pull_Resistor #(.pull(0)) pull_resistor_5 (.node(CLR2));
  Demultiplexer #(.select(2), .width(1), .tristate("false"), .disabled("Z"), .enable("false")) demultiplexer_1 (
    .out1(CLR1), .out2(CLR2), .out3(CLR3), .in(ERET), .sel(priority_encoder_1_out));  // open: out0
  assign bit_extender_1_out = {{2{1'b0}}, IR[25:0]};  // Bit_Extender bit_extender_1
  Comparator #(.width(13), .mode("twosComplement")) comparator_10 (
    .a(CNT_num), .b(13'hc), .eq(comparator_10_eq), .lt(comparator_10_lt));  // open: gt
  Clock #(.highDuration(1), .lowDuration(1)) clock_2 (.out(clock_2_out));
  D_Flip_Flop #(.trigger("rising"), .Pre_Clr_Positions("LEGACY"), .NegatePresetClear("false"), .enable("true"), .NewFFLayout("false")) IR1_2 (
    .clk(CLK), .D(and_7_out), .Q(INT2));  // open: Qn, preset, en, reset
  Pull_Resistor #(.pull(0)) pull_resistor_6 (.node(priority_encoder_1_out));
  Multiplexer #(.select(1), .width(5), .disabled("Z"), .enable("false")) multiplexer_7 (
    .in0(IR[25:21]), .in1(5'b00010), .out(multiplexer_7_out), .sel(SysCall));
  Multiplexer #(.select(1), .width(5), .disabled("Z"), .enable("false")) multiplexer_8 (
    .in0(IR[20:16]), .in1(5'b00100), .out(multiplexer_8_out), .sel(SysCall));
  Multiplexer #(.select(1), .width(5), .disabled("Z"), .enable("false")) multiplexer_9 (
    .in0(IR[20:16]), .in1(IR[15:11]), .out(multiplexer_9_out), .sel(\单周期硬布线控制器_1_regdst ));
  nand nand_1 (nand_1_out, d_ff_2_q, comparator_10_eq);
  Counter #(.width(13), .max('h1fff), .ongoal("stay"), .trigger("rising"), .behavior("old")) counter_1 (
    .count(comparator_10_lt), .Q(CNT_num), .clk(clock_2_out));  // open: load, D, carry, clr, preset
  \单周期硬布线控制器  \u_单周期硬布线控制器_1  (
    .Func(IR[5:0]), .OP(IR[31:26]), .ALU_OP(\单周期硬布线控制器_1_alu_op ), .MemToReg(\单周期硬布线控制器_1_memtoreg ),
    .MemWrite(MemWrite), .ALU_SRC(\单周期硬布线控制器_1_alu_src ), .RegWrite(RegWrite), .SysCALL(SysCall),
    .SignedExt(SignedExt), .RegDst(\单周期硬布线控制器_1_regdst ), .JR(\单周期硬布线控制器_1_jr ), .JMP(\单周期硬布线控制器_1_jmp ),
    .Beq(\单周期硬布线控制器_1_beq ), .JAL(\单周期硬布线控制器_1_jal ), .Bne(\单周期硬布线控制器_1_bne ));  // open: SH, SRAV, BGTZ
  Multiplexer #(.select(1), .width(5), .disabled("Z"), .enable("false")) multiplexer_10 (
    .in0(multiplexer_9_out), .in1({5{1'b1}}), .out(multiplexer_10_out), .sel(\单周期硬布线控制器_1_jal ));
  Shifter #(.width(28), .shift("ll")) shifter_1 (.in(bit_extender_1_out), .\dist (5'b00010), .out(shifter_1_out));
  assign CLK = nand_1_out ? clock_2_out : 1'bz;  // Controlled_Buffer controlled_buffer_1
  Pull_Resistor #(.pull(1)) pull_resistor_7 (.node(CLK));
  assign bit_extender_2_out = {{16{IR[15]}}, IR[15:0]};  // Bit_Extender bit_extender_2
  and and_8 (and_8_out, mips_alu_1_equal, \单周期硬布线控制器_1_beq );
  and and_9 (and_9_out, ~mips_alu_1_equal, \单周期硬布线控制器_1_bne );  // AND_Gate
  MIPS_Regifile mips_regifile_1 (
    .Din(RDin), .Clk(CLK), .R1(V0), .R2(MDin), .WE(RegWrite), .W_num(multiplexer_10_out),
    .R1_num(multiplexer_7_out), .R2_num(multiplexer_8_out));
  or or_10 (or_10_out, and_8_out, and_9_out);
  Multiplexer #(.select(1), .width(32), .disabled("Z"), .enable("false")) multiplexer_11 (
    .in0(MDin), .in1(bit_extender_2_out), .out(multiplexer_11_out), .sel(\单周期硬布线控制器_1_alu_src ));
  Comparator #(.width(32), .mode("twosComplement")) comparator_11 (
    .a(IR), .b(32'h42000018), .eq(ERET));  // open: gt, lt
  or or_11 (W3, INT3, d_ff_4_q);
  // Probe on V0
  Shifter #(.width(32), .shift("ll")) shifter_2 (.in(bit_extender_2_out), .\dist (5'b00010), .out(shifter_2_out));
  D_Flip_Flop #(.trigger("rising"), .Pre_Clr_Positions("LEGACY"), .NegatePresetClear("false"), .enable("true"), .NewFFLayout("false")) d_ff_4 (
    .clk(IR3_t), .D(1'b1), .Q(d_ff_4_q), .reset(INT3));  // open: Qn, preset, en
  Adder #(.width(32)) adder_2 (.a(shifter_2_out), .b(adder_1_out), .out(adder_2_out));  // open: cin, cout
  or or_12 (or_12_out, d_ff_4_q, INT3);
  and and_10 (and_10_out, or_12_out, ~CLR3);  // AND_Gate
  Pull_Resistor #(.pull(0)) pull_resistor_8 (.node(CLR3));
  Multiplexer #(.select(1), .width(32), .disabled("Z"), .enable("false")) multiplexer_12 (
    .in0(ret), .in1(register_3_q), .out(multiplexer_12_out), .sel(ERET));
  or or_13 (or_13_out, INT, ERET);
  Multiplexer #(.select(1), .width(2), .disabled("Z"), .enable("false")) multiplexer_13 (
    .in0(priority_encoder_1_out), .in1(register_4_q), .out(multiplexer_13_out), .sel(ERET));
  or or_14 (or_14_out, INT, ERET);
  MIPS_ALU mips_alu_1 (
    .X(V0), .Y(multiplexer_11_out), .AluOP(\单周期硬布线控制器_1_alu_op ), .Equal(mips_alu_1_equal),
    .Result(mips_alu_1_result), .shamt(IR[10:6]));  // open: Result_2
  D_Flip_Flop #(.trigger("rising"), .Pre_Clr_Positions("LEGACY"), .NegatePresetClear("false"), .enable("true"), .NewFFLayout("false")) IR1_3 (
    .clk(CLK), .D(and_10_out), .Q(INT3));  // open: Qn, preset, en, reset
  Register #(.width(32), .trigger("rising"), .Select("low")) register_1 (
    .D(multiplexer_12_out), .en(or_13_out), .Q(EPCout), .clk(CLK));  // open: clr
  Register #(.width(2), .trigger("rising"), .Select("low")) register_2 (
    .D(multiplexer_13_out), .en(or_14_out), .Q(cur_IntNo), .clk(CLK));  // open: clr
  Multiplexer #(.select(1), .width(32), .disabled("Z"), .enable("false")) multiplexer_14 (
    .in0(EPCout), .in1(register_6_q), .out(multiplexer_14_out), .sel(ERET));
  Multiplexer #(.select(1), .width(2), .disabled("Z"), .enable("false")) multiplexer_15 (
    .in0(cur_IntNo), .in1(register_7_q), .out(multiplexer_15_out), .sel(ERET));
  // Probe on MDin
  or or_15 (or_15_out, INT, MTC0);
  or or_16 (or_16_out, INT, MTC0, ERET, MFC0);
  Register #(.width(32), .trigger("rising"), .Select("low")) register_3 (
    .D(multiplexer_14_out), .en(or_13_out), .Q(register_3_q), .clk(CLK));  // open: clr
  Register #(.width(2), .trigger("rising"), .Select("low")) register_4 (
    .D(multiplexer_15_out), .en(or_14_out), .Q(register_4_q), .clk(CLK));  // open: clr
  Register #(.width(32), .trigger("rising"), .Select("low")) register_5 (
    .D(MDin), .en(LedOut), .Q(LedData), .clk(CLK), .clr(RST));
  Register #(.width(1), .trigger("rising"), .Select("low")) u_IE (
    .D(or_15_out), .en(or_16_out), .Q(IE), .clk(CLK));  // open: clr
  Multiplexer #(.select(1), .width(32), .disabled("Z"), .enable("false")) multiplexer_16 (
    .in0(register_3_q), .in1({32{1'b0}}), .out(multiplexer_16_out), .sel(ERET));
  Multiplexer #(.select(1), .width(2), .disabled("Z"), .enable("false")) multiplexer_17 (
    .in0(register_4_q), .in1(2'b00), .out(multiplexer_17_out), .sel(ERET));
  RAM #(.addrWidth(10), .dataWidth(32), .bus("separate"), .Select("high")) ram_1 (
    .addr(mips_alu_1_result[11:2]), .din(MDin), .data(ram_1_data), .str(MemWrite), .clk(CLK), .clr(RST));  // open: sel, ld
  Register #(.width(32), .trigger("rising"), .Select("low")) register_6 (
    .D(multiplexer_16_out), .en(or_13_out), .Q(register_6_q), .clk(CLK));  // open: clr
  Register #(.width(2), .trigger("rising"), .Select("low")) register_7 (
    .D(multiplexer_17_out), .en(or_14_out), .Q(register_7_q), .clk(CLK));  // open: clr
  Multiplexer #(.select(1), .width(32), .disabled("Z"), .enable("false")) multiplexer_18 (
    .in0(mips_alu_1_result), .in1(ram_1_data), .out(multiplexer_18_out), .sel(\单周期硬布线控制器_1_memtoreg ));
  not not_2 (not_2_out, Halt);
  Multiplexer #(.select(1), .width(32), .disabled("Z"), .enable("false")) multiplexer_19 (
    .in0(multiplexer_18_out), .in1(adder_1_out), .out(RDin), .sel(\单周期硬布线控制器_1_jal ));
  Counter #(.width(16), .max('hffff), .ongoal("wrap"), .trigger("rising"), .behavior("new")) counter_2 (
    .count(not_2_out), .Q(\总周期数 ), .clk(CLK), .clr(RST));  // open: load, D, carry, preset, down

  // Other names for the same wires on the sheet: rs[4:0] = IR[25:21]; OP[5:0] = IR[31:26]

  // Notes on the sheet:
  //   中断源
  //   中断等待指示
  //   总复位信号应将除ROM以外所有存储组件全部清零
  //   单级中断测试信号模拟器
  //   数码管输出
  //   中断信号采样参考电路
  //   数码管输出应该用寄存器锁存，否则显示数据只能一闪而过
  //   Reset 
  //   指令存储器
  //   contents of rom_1 (hex, n*v repeats v):
  //   201d07d0 20100001 109fc0 139fc3 8021 2012000c 24160008 26100001 3210000f 20080008 20090001 139900
  //   2709825 132020 20020022 c 1094022 1500fff9 22100001 2018000f 2188024 108700 20080008 20090001 139902
  //   2709825 132021 20020022 c 1094022 1500fff9 108702 2c9b022 12c00001 8000c07 4020 1084027 84400
  //   3508ffff 82021 20020022 c 8000c01 afa20000 23bd0004 afa40000 23bd0004 afb00000 23bd0004 afb30000
  //   23bd0004 afb40000 23bd0004 afb50000 23bd0004 afb60000 23bd0004 40000000 20160001 20140003 20150001
  //   168020 108100 2149825 132020 20020022 c 1600fffa 295a022 1680fff7 40800000 23bdfffc 8fb60000
  //   23bdfffc 8fb50000 23bdfffc 8fb40000 23bdfffc 8fb30000 23bdfffc 8fb00000 23bdfffc 8fa40000 23bdfffc
  //   8fa20000 42000018 afa20000 23bd0004 afa40000 23bd0004 afb00000 23bd0004 afb30000 23bd0004 afb40000
  //   23bd0004 afb50000 23bd0004 afb60000 23bd0004 40000000 20160002 20140003 20150001 168020 108100
  //   2149825 132020 20020022 c 1600fffa 295a022 1680fff7 40800000 23bdfffc 8fb60000 23bdfffc 8fb50000
  //   23bdfffc 8fb40000 23bdfffc 8fb30000 23bdfffc 8fb00000 23bdfffc 8fa40000 23bdfffc 8fa20000 42000018
  //   afa20000 23bd0004 afa40000 23bd0004 afb00000 23bd0004 afb30000 23bd0004 afb40000 23bd0004 afb50000
  //   23bd0004 afb60000 23bd0004 40000000 20160003 20140003 20150001 168020 108100 2149825 132020 20020022
  //   c 1600fffa 295a022 1680fff7 40800000 23bdfffc 8fb60000 23bdfffc 8fb50000 23bdfffc 8fb40000 23bdfffc
  //   8fb30000 23bdfffc 8fb00000 23bdfffc 8fa40000 23bdfffc 8fa20000 42000018
  //   控制位
  //   暂停节拍，不能为0
  //   中断信号采样参考电路
  //   OP
  //   Func
  //   rs
  //   rt
  //   rd
  //   指令字
  //   shamt
  //   imm16
  //   用这个时钟源需要去掉电路中的其他时钟源
  //   为方便自动评测，需要输出PC，IR，寄存器堆写如数据RDin
  //   戳工具置1进入计数暂停模式，ctrl+k时钟自动运行到对应节拍暂停
  //   ctrl+k关闭时钟连续运行，将控制位置零，进入单步调试模式调试
  //   Reset 
  //   RAM写使能MemWrite、RAM写入数据MDin等信号
  //   JMP
  //   JR
  //   OP
  //   Func
  //   Beq
  //   Bne
  //   MemToReg
  //   MemWrite
  //   AluOP
  //   AluSrcB
  //   RegWrite
  //   JAL
  //   RegDst
  //   Syscall
  //   可计数暂停的时钟源
  //   中断信号采样参考电路
  //   Reset 
  //   被打断的中断服务号
  //   被打断的中断服务号
endmodule

module \封装正确性测试  (
);

  wire IR1, IR2, IR3, MemW, RegW;
  wire [31:0] EX_PC, ID_PC, IF_PC, IR, LED, MDin, MDinr, MEM_PC, PC, RDin, RDinr, WB_PC;

  \单周期MIPS  \u_单周期mips_1  (
    .RegWrite(RegW), .MemWrite(MemW), .PC(PC), .IR(IR), .RDin(RDin), .MDin(MDin), .LedData(LED));  // open: IR1, IR2, IR3
  \气泡流水线  \u_气泡流水线_1  (
    .RegWrite(RegW), .MemWrite(MemW), .IF_PC(IF_PC), .ID_PC(ID_PC), .EX_PC(EX_PC), .M_PC(MEM_PC),
    .WB_PC(WB_PC), .RDin(RDinr), .MDin(MDinr), .LedData(LED));
  \单周期MIPS_单级中断  \u_单周期mips_单级中断_1  (
    .IR1(IR1), .IR2(IR2), .IR3(IR3), .RegWrite(RegW), .MemWrite(MemW), .PC(PC), .IR(IR), .RDin(RDin),
    .MDin(MDin), .LedData(LED));  // open: in_4
  \理想流水线  \u_理想流水线_1  (
    .RegWrite(RegW), .MemWrite(MemW), .IF_PC(IF_PC), .ID_PC(ID_PC), .EX_PC(EX_PC), .M_PC(MEM_PC),
    .WB_PC(WB_PC), .RDin(RDinr), .MDin(MDinr), .LedData(LED));
  \重定向流水线  \u_重定向流水线_1  (
    .RegWrite(RegW), .MemWrite(MemW), .IF_PC(IF_PC), .ID_PC(ID_PC), .EX_PC(EX_PC), .M_PC(MEM_PC),
    .WB_PC(WB_PC), .RDin(RDinr), .MDin(MDinr), .LedData(LED));
  \单周期MIPS_多级中断  \u_单周期mips_多级中断_1  (
    .IR1(IR1), .IR2(IR2), .IR3(IR3), .RegWrite(RegW), .MemWrite(MemW), .PC(PC), .IR(IR), .RDin(RDin),
    .MDin(MDin), .LedData(LED));

  // Notes on the sheet:
  //   单周期封装测试
  //   气泡流水封装测试
  //   单周期+单级中断封装测试
  //   请检查上面封装有无位宽不匹配，引脚标签是否和连接的标签相对应，否则无法在educoder平台上正确测试
  //   理想流水封装测试
  //   重定向流水封装测试
  //   单周期+多级中断封装测试
endmodule

module IF_ID (
  input  EN,
  input  [31:0] IR,
  input  [31:0] PC_4,
  input  CLK,
  input  RST,
  output [31:0] IR_2,
  output [31:0] PC_4_ID
);

  wire [31:0] multiplexer_1_out, multiplexer_2_out;

  Pull_Resistor #(.pull(0)) pull_resistor_1 (.node(RST));
  Multiplexer #(.select(1), .width(32), .disabled("Z"), .enable("false")) multiplexer_1 (
    .in0(IR), .in1({32{1'b0}}), .out(multiplexer_1_out), .sel(RST));
  Multiplexer #(.select(1), .width(32), .disabled("Z"), .enable("false")) multiplexer_2 (
    .in0(PC_4), .in1({32{1'b0}}), .out(multiplexer_2_out), .sel(RST));
  Register #(.width(32), .trigger("rising"), .Select("low")) register_1 (
    .D(multiplexer_1_out), .en(EN), .Q(IR_2), .clk(CLK));  // open: clr
  Register #(.width(32), .trigger("rising"), .Select("low")) register_2 (
    .D(multiplexer_2_out), .en(EN), .Q(PC_4_ID), .clk(CLK));  // open: clr
endmodule

module ID_EX (
  input  JMP,
  input  JR,
  input  jal,
  input  sys,
  input  BEQ,
  input  BNE,
  input  MemToReg,
  input  MemWrite,
  input  [3:0] AluOP,
  input  AluSrcB,
  input  RegWrite,
  input  [31:0] RS,
  input  [31:0] RT,
  input  [4:0] WriteReg_num,
  input  [31:0] SignImm,
  input  [31:0] IR_ID,
  input  [31:0] PC_4_ID,
  input  [1:0] FwdA,
  input  [1:0] FwdB,
  input  RST,
  input  CLK,
  input  in_22,
  output JMP_2,
  output JR_2,
  output jal_2,
  output sys_2,
  output BEQ_2,
  output BNE_2,
  output MemToReg_2,
  output MemWrite_2,
  output [3:0] AluOP_2,
  output AluSrcB_2,
  output RegWrite_2,
  output [31:0] RS_2,
  output [31:0] RT_2,
  output [4:0] WriteReg_num_2,
  output [31:0] SignImm_2,
  output [31:0] IR_ID_2,
  output [31:0] PC_4_ID_2,
  output [1:0] FwdA_2,
  output [1:0] FwdB_2
);

  wire multiplexer_1_out, multiplexer_2_out, multiplexer_3_out, multiplexer_4_out, multiplexer_5_out,
       multiplexer_6_out, multiplexer_7_out, multiplexer_8_out, multiplexer_10_out, multiplexer_11_out;
  wire [1:0] multiplexer_18_out, multiplexer_19_out;
  wire [3:0] multiplexer_9_out;
  wire [4:0] multiplexer_14_out;
  wire [31:0] multiplexer_12_out, multiplexer_13_out, multiplexer_15_out, multiplexer_16_out,
       multiplexer_17_out;

  Pull_Resistor #(.pull(0)) pull_resistor_1 (.node(RST));
  Multiplexer #(.select(1), .width(1), .disabled("Z"), .enable("false")) multiplexer_1 (
    .in0(JMP), .in1(1'b0), .out(multiplexer_1_out), .sel(RST));
  Multiplexer #(.select(1), .width(1), .disabled("Z"), .enable("false")) multiplexer_2 (
    .in0(JR), .in1(1'b0), .out(multiplexer_2_out), .sel(RST));
  Multiplexer #(.select(1), .width(1), .disabled("Z"), .enable("false")) multiplexer_3 (
    .in0(jal), .in1(1'b0), .out(multiplexer_3_out), .sel(RST));
  Multiplexer #(.select(1), .width(1), .disabled("Z"), .enable("false")) multiplexer_4 (
    .in0(sys), .in1(1'b0), .out(multiplexer_4_out), .sel(RST));
  Multiplexer #(.select(1), .width(1), .disabled("Z"), .enable("false")) multiplexer_5 (
    .in0(BEQ), .in1(1'b0), .out(multiplexer_5_out), .sel(RST));
  Multiplexer #(.select(1), .width(1), .disabled("Z"), .enable("false")) multiplexer_6 (
    .in0(BNE), .in1(1'b0), .out(multiplexer_6_out), .sel(RST));
  Multiplexer #(.select(1), .width(1), .disabled("Z"), .enable("false")) multiplexer_7 (
    .in0(MemToReg), .in1(1'b0), .out(multiplexer_7_out), .sel(RST));
  Multiplexer #(.select(1), .width(1), .disabled("Z"), .enable("false")) multiplexer_8 (
    .in0(MemWrite), .in1(1'b0), .out(multiplexer_8_out), .sel(RST));
  Multiplexer #(.select(1), .width(4), .disabled("Z"), .enable("false")) multiplexer_9 (
    .in0(AluOP), .in1(4'b0000), .out(multiplexer_9_out), .sel(RST));
  Multiplexer #(.select(1), .width(1), .disabled("Z"), .enable("false")) multiplexer_10 (
    .in0(AluSrcB), .in1(1'b0), .out(multiplexer_10_out), .sel(RST));
  Multiplexer #(.select(1), .width(1), .disabled("Z"), .enable("false")) multiplexer_11 (
    .in0(RegWrite), .in1(1'b0), .out(multiplexer_11_out), .sel(RST));
  Multiplexer #(.select(1), .width(32), .disabled("Z"), .enable("false")) multiplexer_12 (
    .in0(RS), .in1({32{1'b0}}), .out(multiplexer_12_out), .sel(RST));
  Multiplexer #(.select(1), .width(32), .disabled("Z"), .enable("false")) multiplexer_13 (
    .in0(RT), .in1({32{1'b0}}), .out(multiplexer_13_out), .sel(RST));
  Multiplexer #(.select(1), .width(5), .disabled("Z"), .enable("false")) multiplexer_14 (
    .in0(WriteReg_num), .in1({5{1'b0}}), .out(multiplexer_14_out), .sel(RST));
  Multiplexer #(.select(1), .width(32), .disabled("Z"), .enable("false")) multiplexer_15 (
    .in0(SignImm), .in1({32{1'b0}}), .out(multiplexer_15_out), .sel(RST));
  Multiplexer #(.select(1), .width(32), .disabled("Z"), .enable("false")) multiplexer_16 (
    .in0(IR_ID), .in1({32{1'b0}}), .out(multiplexer_16_out), .sel(RST));
  Multiplexer #(.select(1), .width(32), .disabled("Z"), .enable("false")) multiplexer_17 (
    .in0(PC_4_ID), .in1({32{1'b0}}), .out(multiplexer_17_out), .sel(RST));
  Multiplexer #(.select(1), .width(2), .disabled("Z"), .enable("false")) multiplexer_18 (
    .in0(FwdA), .in1(2'b00), .out(multiplexer_18_out), .sel(RST));
  Multiplexer #(.select(1), .width(2), .disabled("Z"), .enable("false")) multiplexer_19 (
    .in0(FwdB), .in1(2'b00), .out(multiplexer_19_out), .sel(RST));
  Register #(.width(1), .trigger("rising"), .Select("low")) register_1 (
    .D(multiplexer_1_out), .en(in_22), .Q(JMP_2), .clk(CLK));  // open: clr
  Register #(.width(1), .trigger("rising"), .Select("low")) register_2 (
    .D(multiplexer_2_out), .en(in_22), .Q(JR_2), .clk(CLK));  // open: clr
  Register #(.width(1), .trigger("rising"), .Select("low")) register_3 (
    .D(multiplexer_3_out), .en(in_22), .Q(jal_2), .clk(CLK));  // open: clr
  Register #(.width(1), .trigger("rising"), .Select("low")) register_4 (
    .D(multiplexer_4_out), .en(in_22), .Q(sys_2), .clk(CLK));  // open: clr
  Register #(.width(1), .trigger("rising"), .Select("low")) register_5 (
    .D(multiplexer_5_out), .en(in_22), .Q(BEQ_2), .clk(CLK));  // open: clr
  Register #(.width(1), .trigger("rising"), .Select("low")) register_6 (
    .D(multiplexer_6_out), .en(in_22), .Q(BNE_2), .clk(CLK));  // open: clr
  Register #(.width(1), .trigger("rising"), .Select("low")) register_7 (
    .D(multiplexer_7_out), .en(in_22), .Q(MemToReg_2), .clk(CLK));  // open: clr
  Register #(.width(1), .trigger("rising"), .Select("low")) register_8 (
    .D(multiplexer_8_out), .en(in_22), .Q(MemWrite_2), .clk(CLK));  // open: clr
  Register #(.width(4), .trigger("rising"), .Select("low")) register_9 (
    .D(multiplexer_9_out), .en(in_22), .Q(AluOP_2), .clk(CLK));  // open: clr
  Register #(.width(1), .trigger("rising"), .Select("low")) register_10 (
    .D(multiplexer_10_out), .en(in_22), .Q(AluSrcB_2), .clk(CLK));  // open: clr
  Register #(.width(1), .trigger("rising"), .Select("low")) register_11 (
    .D(multiplexer_11_out), .en(in_22), .Q(RegWrite_2), .clk(CLK));  // open: clr
  Register #(.width(32), .trigger("rising"), .Select("low")) register_12 (
    .D(multiplexer_12_out), .en(in_22), .Q(RS_2), .clk(CLK));  // open: clr
  Register #(.width(32), .trigger("rising"), .Select("low")) register_13 (
    .D(multiplexer_13_out), .en(in_22), .Q(RT_2), .clk(CLK));  // open: clr
  Register #(.width(5), .trigger("rising"), .Select("low")) register_14 (
    .D(multiplexer_14_out), .en(in_22), .Q(WriteReg_num_2), .clk(CLK));  // open: clr
  Register #(.width(32), .trigger("rising"), .Select("low")) register_15 (
    .D(multiplexer_15_out), .en(in_22), .Q(SignImm_2), .clk(CLK));  // open: clr
  Register #(.width(32), .trigger("rising"), .Select("low")) register_16 (
    .D(multiplexer_16_out), .en(in_22), .Q(IR_ID_2), .clk(CLK));  // open: clr
  Register #(.width(32), .trigger("rising"), .Select("low")) register_17 (
    .D(multiplexer_17_out), .en(in_22), .Q(PC_4_ID_2), .clk(CLK));  // open: clr
  Register #(.width(2), .trigger("rising"), .Select("low")) register_18 (
    .D(multiplexer_18_out), .en(in_22), .Q(FwdA_2), .clk(CLK));  // open: clr
  Register #(.width(2), .trigger("rising"), .Select("low")) register_19 (
    .D(multiplexer_19_out), .en(in_22), .Q(FwdB_2), .clk(CLK));  // open: clr
endmodule

module EX_MEM (
  input  jal,
  input  RegWrite,
  input  MemToReg,
  input  MemWrite,
  input  [31:0] IR_EX,
  input  [31:0] Result,
  input  [31:0] WriteData,
  input  [4:0] WriteReg_num,
  input  [31:0] PC_4_EX,
  input  MemWrite_2,
  input  [31:0] v0,
  input  RST,
  input  in_13,
  input  CLK,
  output jal_2,
  output RegWrite_2,
  output MemToReg_2,
  output MemWrite_3,
  output [31:0] IR_MEM,
  output [31:0] Result_2,
  output [31:0] WriteData_2,
  output [4:0] WriteReg_num_2,
  output [31:0] PC_4_MEM,
  output MemWrite_4,
  output [31:0] v0_2
);

  wire multiplexer_1_out, multiplexer_2_out, multiplexer_3_out, multiplexer_4_out, multiplexer_10_out;
  wire [4:0] multiplexer_8_out;
  wire [31:0] multiplexer_5_out, multiplexer_6_out, multiplexer_7_out, multiplexer_9_out, multiplexer_11_out;

  Pull_Resistor #(.pull(0)) pull_resistor_1 (.node(RST));
  Multiplexer #(.select(1), .width(1), .disabled("Z"), .enable("false")) multiplexer_1 (
    .in0(jal), .in1(1'b0), .out(multiplexer_1_out), .sel(RST));
  Multiplexer #(.select(1), .width(1), .disabled("Z"), .enable("false")) multiplexer_2 (
    .in0(RegWrite), .in1(1'b0), .out(multiplexer_2_out), .sel(RST));
  Multiplexer #(.select(1), .width(1), .disabled("Z"), .enable("false")) multiplexer_3 (
    .in0(MemToReg), .in1(1'b0), .out(multiplexer_3_out), .sel(RST));
  Multiplexer #(.select(1), .width(1), .disabled("Z"), .enable("false")) multiplexer_4 (
    .in0(MemWrite), .in1(1'b0), .out(multiplexer_4_out), .sel(RST));
  Multiplexer #(.select(1), .width(32), .disabled("Z"), .enable("false")) multiplexer_5 (
    .in0(IR_EX), .in1({32{1'b0}}), .out(multiplexer_5_out), .sel(RST));
  Multiplexer #(.select(1), .width(32), .disabled("Z"), .enable("false")) multiplexer_6 (
    .in0(Result), .in1({32{1'b0}}), .out(multiplexer_6_out), .sel(RST));
  Multiplexer #(.select(1), .width(32), .disabled("Z"), .enable("false")) multiplexer_7 (
    .in0(WriteData), .in1({32{1'b0}}), .out(multiplexer_7_out), .sel(RST));
  Multiplexer #(.select(1), .width(5), .disabled("Z"), .enable("false")) multiplexer_8 (
    .in0(WriteReg_num), .in1({5{1'b0}}), .out(multiplexer_8_out), .sel(RST));
  Multiplexer #(.select(1), .width(32), .disabled("Z"), .enable("false")) multiplexer_9 (
    .in0(PC_4_EX), .in1({32{1'b0}}), .out(multiplexer_9_out), .sel(RST));
  Multiplexer #(.select(1), .width(1), .disabled("Z"), .enable("false")) multiplexer_10 (
    .in0(MemWrite_2), .in1(1'b0), .out(multiplexer_10_out), .sel(RST));
  Multiplexer #(.select(1), .width(32), .disabled("Z"), .enable("false")) multiplexer_11 (
    .in0(v0), .in1({32{1'b0}}), .out(multiplexer_11_out), .sel(RST));
  Register #(.width(1), .trigger("rising"), .Select("low")) register_1 (
    .D(multiplexer_1_out), .en(in_13), .Q(jal_2), .clk(CLK));  // open: clr
  Register #(.width(1), .trigger("rising"), .Select("low")) register_2 (
    .D(multiplexer_2_out), .en(in_13), .Q(RegWrite_2), .clk(CLK));  // open: clr
  Register #(.width(1), .trigger("rising"), .Select("low")) register_3 (
    .D(multiplexer_3_out), .en(in_13), .Q(MemToReg_2), .clk(CLK));  // open: clr
  Register #(.width(1), .trigger("rising"), .Select("low")) register_4 (
    .D(multiplexer_4_out), .en(in_13), .Q(MemWrite_3), .clk(CLK));  // open: clr
  Register #(.width(32), .trigger("rising"), .Select("low")) register_5 (
    .D(multiplexer_5_out), .en(in_13), .Q(IR_MEM), .clk(CLK));  // open: clr
  Register #(.width(32), .trigger("rising"), .Select("low")) register_6 (
    .D(multiplexer_6_out), .en(in_13), .Q(Result_2), .clk(CLK));  // open: clr
  Register #(.width(32), .trigger("rising"), .Select("low")) register_7 (
    .D(multiplexer_7_out), .en(in_13), .Q(WriteData_2), .clk(CLK));  // open: clr
  Register #(.width(5), .trigger("rising"), .Select("low")) register_8 (
    .D(multiplexer_8_out), .en(in_13), .Q(WriteReg_num_2), .clk(CLK));  // open: clr
  Register #(.width(32), .trigger("rising"), .Select("low")) register_9 (
    .D(multiplexer_9_out), .en(in_13), .Q(PC_4_MEM), .clk(CLK));  // open: clr
  Register #(.width(1), .trigger("rising"), .Select("low")) register_10 (
    .D(multiplexer_10_out), .en(in_13), .Q(MemWrite_4), .clk(CLK));  // open: clr
  Register #(.width(32), .trigger("rising"), .Select("low")) register_11 (
    .D(multiplexer_11_out), .en(in_13), .Q(v0_2), .clk(CLK));  // open: clr
endmodule

module MEM_WB (
  input  jal,
  input  RegWrite,
  input  MemToReg,
  input  sys,
  input  [31:0] Result,
  input  [31:0] RD,
  input  [4:0] WriteReg_num,
  input  [31:0] IR_MEM,
  input  [31:0] PC_4_MEM,
  input  [31:0] v0,
  input  RST,
  input  in_12,
  input  CLK,
  output jal_2,
  output RegWrite_2,
  output MemToReg_2,
  output sys_2,
  output [31:0] Result_2,
  output [31:0] RD_2,
  output [4:0] WriteReg_num_2,
  output [31:0] IR_WB,
  output [31:0] PC_4_WB,
  output [31:0] v0_2
);

  wire multiplexer_1_out, multiplexer_2_out, multiplexer_3_out, multiplexer_4_out;
  wire [4:0] multiplexer_7_out;
  wire [31:0] multiplexer_5_out, multiplexer_6_out, multiplexer_8_out, multiplexer_9_out, multiplexer_10_out;

  Pull_Resistor #(.pull(0)) pull_resistor_1 (.node(RST));
  Multiplexer #(.select(1), .width(1), .disabled("Z"), .enable("false")) multiplexer_1 (
    .in0(jal), .in1(1'b0), .out(multiplexer_1_out), .sel(RST));
  Multiplexer #(.select(1), .width(1), .disabled("Z"), .enable("false")) multiplexer_2 (
    .in0(RegWrite), .in1(1'b0), .out(multiplexer_2_out), .sel(RST));
  Multiplexer #(.select(1), .width(1), .disabled("Z"), .enable("false")) multiplexer_3 (
    .in0(MemToReg), .in1(1'b0), .out(multiplexer_3_out), .sel(RST));
  Multiplexer #(.select(1), .width(1), .disabled("Z"), .enable("false")) multiplexer_4 (
    .in0(sys), .in1(1'b0), .out(multiplexer_4_out), .sel(RST));
  Multiplexer #(.select(1), .width(32), .disabled("Z"), .enable("false")) multiplexer_5 (
    .in0(Result), .in1({32{1'b0}}), .out(multiplexer_5_out), .sel(RST));
  Multiplexer #(.select(1), .width(32), .disabled("Z"), .enable("false")) multiplexer_6 (
    .in0(RD), .in1({32{1'b0}}), .out(multiplexer_6_out), .sel(RST));
  Multiplexer #(.select(1), .width(5), .disabled("Z"), .enable("false")) multiplexer_7 (
    .in0(WriteReg_num), .in1({5{1'b0}}), .out(multiplexer_7_out), .sel(RST));
  Multiplexer #(.select(1), .width(32), .disabled("Z"), .enable("false")) multiplexer_8 (
    .in0(IR_MEM), .in1({32{1'b0}}), .out(multiplexer_8_out), .sel(RST));
  Multiplexer #(.select(1), .width(32), .disabled("Z"), .enable("false")) multiplexer_9 (
    .in0(PC_4_MEM), .in1({32{1'b0}}), .out(multiplexer_9_out), .sel(RST));
  Multiplexer #(.select(1), .width(32), .disabled("Z"), .enable("false")) multiplexer_10 (
    .in0(v0), .in1({32{1'b0}}), .out(multiplexer_10_out), .sel(RST));
  Register #(.width(1), .trigger("rising"), .Select("low")) register_1 (
    .D(multiplexer_1_out), .en(in_12), .Q(jal_2), .clk(CLK));  // open: clr
  Register #(.width(1), .trigger("rising"), .Select("low")) register_2 (
    .D(multiplexer_2_out), .en(in_12), .Q(RegWrite_2), .clk(CLK));  // open: clr
  Register #(.width(1), .trigger("rising"), .Select("low")) register_3 (
    .D(multiplexer_3_out), .en(in_12), .Q(MemToReg_2), .clk(CLK));  // open: clr
  Register #(.width(1), .trigger("rising"), .Select("low")) register_4 (
    .D(multiplexer_4_out), .en(in_12), .Q(sys_2), .clk(CLK));  // open: clr
  Register #(.width(32), .trigger("rising"), .Select("low")) register_5 (
    .D(multiplexer_5_out), .en(in_12), .Q(Result_2), .clk(CLK));  // open: clr
  Register #(.width(32), .trigger("rising"), .Select("low")) register_6 (
    .D(multiplexer_6_out), .en(in_12), .Q(RD_2), .clk(CLK));  // open: clr
  Register #(.width(5), .trigger("rising"), .Select("low")) register_7 (
    .D(multiplexer_7_out), .en(in_12), .Q(WriteReg_num_2), .clk(CLK));  // open: clr
  Register #(.width(32), .trigger("rising"), .Select("low")) register_8 (
    .D(multiplexer_8_out), .en(in_12), .Q(IR_WB), .clk(CLK));  // open: clr
  Register #(.width(32), .trigger("rising"), .Select("low")) register_9 (
    .D(multiplexer_9_out), .en(in_12), .Q(PC_4_WB), .clk(CLK));  // open: clr
  Register #(.width(32), .trigger("rising"), .Select("low")) register_10 (
    .D(multiplexer_10_out), .en(in_12), .Q(v0_2), .clk(CLK));  // open: clr
endmodule

module \控制逻辑  (
  input  branch,
  input  [31:0] IR,
  input  [4:0] MEM_WriteReg_num,
  input  [4:0] rs,
  input  [4:0] rt,
  input  [4:0] EX_WriteReg_num,
  input  EX_RegWrite,
  input  MEM_RegWrite,
  output FlushID_EX,
  output FlushIF_ID,
  output Stall
);

  wire and_1_out, and_2_out, and_3_out, and_4_out, comparator_1_gt, comparator_1_lt, comparator_2_gt,
       comparator_2_lt, comparator_3_eq, comparator_4_eq, comparator_5_eq, comparator_6_eq, rs__0, RsUsed,
       rt__0, RtUsed;

  Pull_Resistor #(.pull(0)) pull_resistor_1 (.node(rs));
  rstused rstused_1 (
    .OP0(IR[26]), .OP1(IR[27]), .OP2(IR[28]), .OP3(IR[29]), .OP4(IR[30]), .OP5(IR[31]), .F0(IR[0]),
    .F1(IR[1]), .F2(IR[2]), .F3(IR[3]), .F4(IR[4]), .F5(IR[5]), .RSUSED(RsUsed), .RTUSED(RtUsed));
  Comparator #(.width(5), .mode("twosComplement")) comparator_1 (
    .a(rs), .b({5{1'b0}}), .gt(comparator_1_gt), .lt(comparator_1_lt));  // open: eq
  Comparator #(.width(5), .mode("twosComplement")) comparator_2 (
    .a(rt), .b({5{1'b0}}), .gt(comparator_2_gt), .lt(comparator_2_lt));  // open: eq
  or or_1 (rs__0, comparator_1_gt, comparator_1_lt);
  or or_2 (rt__0, comparator_2_gt, comparator_2_lt);
  and and_1 (and_1_out, rs__0, RsUsed, MEM_RegWrite, comparator_3_eq);
  Comparator #(.width(5), .mode("twosComplement")) comparator_3 (
    .a(MEM_WriteReg_num), .b(rs), .eq(comparator_3_eq));  // open: gt, lt
  Comparator #(.width(5), .mode("twosComplement")) comparator_4 (
    .a(MEM_WriteReg_num), .b(rt), .eq(comparator_4_eq));  // open: gt, lt
  Comparator #(.width(5), .mode("twosComplement")) comparator_5 (
    .a(EX_WriteReg_num), .b(rs), .eq(comparator_5_eq));  // open: gt, lt
  Comparator #(.width(5), .mode("twosComplement")) comparator_6 (
    .a(EX_WriteReg_num), .b(rt), .eq(comparator_6_eq));  // open: gt, lt
  or or_3 (Stall, and_1_out, and_2_out, and_3_out, and_4_out);
  and and_2 (and_2_out, rt__0, RtUsed, MEM_RegWrite, comparator_4_eq);
  and and_3 (and_3_out, rs__0, RsUsed, EX_RegWrite, comparator_5_eq);
  and and_4 (and_4_out, rt__0, RtUsed, EX_RegWrite, comparator_6_eq);
  or or_4 (FlushID_EX, Stall, branch);

  assign FlushIF_ID = branch;

  // Notes on the sheet:
  //   op
  //   Func
endmodule

module rstused (
  input  OP0,
  input  OP1,
  input  OP2,
  input  OP3,
  input  OP4,
  input  OP5,
  input  F0,
  input  F1,
  input  F2,
  input  F3,
  input  F4,
  input  F5,
  output RSUSED,
  output RTUSED
);

  wire and_1_out, and_2_out, and_3_out, and_4_out, and_5_out, and_6_out, and_7_out, and_8_out, and_9_out,
       and_10_out, and_11_out, and_12_out, and_13_out, and_14_out, and_15_out, and_16_out, and_17_out,
       and_18_out, and_19_out, and_20_out, and_21_out, and_22_out, and_23_out, and_24_out, and_25_out,
       and_26_out, and_27_out, and_28_out, and_29_out, and_30_out, and_31_out, and_32_out, and_33_out,
       not_1_out, not_2_out, not_3_out, not_4_out, not_5_out, not_6_out, not_7_out, not_8_out, not_9_out,
       not_10_out, not_11_out, not_12_out, not_13_out, not_14_out, not_15_out, not_16_out, not_17_out,
       not_18_out, not_19_out, not_20_out, not_21_out, not_22_out, not_23_out, not_24_out, not_25_out,
       not_26_out, not_27_out, not_28_out, not_29_out, not_30_out, not_31_out, not_32_out, not_33_out,
       not_34_out, not_35_out, not_36_out, not_37_out, not_38_out, not_39_out, not_40_out, not_41_out,
       not_42_out, not_43_out, not_44_out, not_45_out, not_46_out, not_47_out, not_48_out, not_49_out,
       not_50_out, not_51_out, not_52_out, not_53_out, not_54_out, not_55_out, not_56_out, not_57_out,
       not_58_out, not_59_out, not_60_out, not_61_out, not_62_out, not_63_out, not_64_out, not_65_out,
       not_66_out, not_67_out, not_68_out, not_69_out, not_70_out, not_71_out, not_72_out, not_73_out,
       not_74_out, not_75_out, not_76_out, not_77_out, not_78_out, not_79_out, not_80_out, not_81_out,
       not_82_out, not_83_out, not_84_out, not_85_out, not_86_out, not_87_out, not_88_out, not_89_out,
       not_90_out, not_91_out, not_92_out, not_93_out, not_94_out, not_95_out, not_96_out, not_97_out,
       not_98_out, not_99_out, not_100_out, not_101_out, not_102_out, not_103_out, not_104_out, not_105_out,
       not_106_out, not_107_out, not_108_out, not_109_out, not_110_out, not_111_out, not_112_out,
       not_113_out, not_114_out, not_115_out, not_116_out, not_117_out, not_118_out, not_119_out,
       not_120_out, not_121_out, not_122_out, not_123_out, not_124_out, not_125_out, not_126_out,
       not_127_out, not_128_out, not_129_out, not_130_out, not_131_out, not_132_out, not_133_out,
       not_134_out, not_135_out, not_136_out, not_137_out, not_138_out, not_139_out, not_140_out,
       not_141_out, not_142_out, not_143_out, not_144_out, not_145_out, not_146_out, not_147_out,
       not_148_out, not_149_out, not_150_out, not_151_out, not_152_out, not_153_out, not_154_out,
       not_155_out, not_156_out, not_157_out, not_158_out, not_159_out, not_160_out, not_161_out,
       not_162_out, not_163_out, not_164_out, not_165_out, not_166_out, not_167_out, not_168_out,
       not_169_out, not_170_out, not_171_out, not_172_out, not_173_out, not_174_out, not_175_out,
       not_176_out, not_177_out, not_178_out, not_179_out, not_180_out, not_181_out, not_182_out,
       not_183_out, not_184_out, not_185_out, not_186_out, not_187_out, not_188_out, not_189_out,
       not_190_out, not_191_out, not_192_out, not_193_out, not_194_out, not_195_out, not_196_out,
       not_197_out, not_198_out, not_199_out, not_200_out, not_201_out, not_202_out, not_203_out,
       not_204_out, not_205_out, not_206_out, not_207_out;

  not not_1 (not_1_out, OP5);
  not not_2 (not_2_out, OP4);
  not not_3 (not_3_out, OP3);
  not not_4 (not_4_out, OP2);
  not not_5 (not_5_out, OP1);
  not not_6 (not_6_out, OP0);
  not not_7 (not_7_out, F4);
  not not_8 (not_8_out, F3);
  not not_9 (not_9_out, F2);
  not not_10 (not_10_out, F1);
  not not_11 (not_11_out, F0);
  not not_12 (not_12_out, OP5);
  not not_13 (not_13_out, OP4);
  not not_14 (not_14_out, OP3);
  not not_15 (not_15_out, OP2);
  not not_16 (not_16_out, OP1);
  not not_17 (not_17_out, OP0);
  not not_18 (not_18_out, F4);
  not not_19 (not_19_out, F3);
  not not_20 (not_20_out, F2);
  not not_21 (not_21_out, F1);
  not not_22 (not_22_out, OP5);
  not not_23 (not_23_out, OP4);
  not not_24 (not_24_out, OP3);
  not not_25 (not_25_out, OP2);
  not not_26 (not_26_out, OP1);
  not not_27 (not_27_out, OP0);
  not not_28 (not_28_out, F4);
  not not_29 (not_29_out, F3);
  not not_30 (not_30_out, F2);
  not not_31 (not_31_out, F0);
  not not_32 (not_32_out, OP5);
  not not_33 (not_33_out, OP4);
  not not_34 (not_34_out, OP3);
  not not_35 (not_35_out, OP2);
  not not_36 (not_36_out, OP1);
  not not_37 (not_37_out, OP0);
  not not_38 (not_38_out, F4);
  not not_39 (not_39_out, F3);
  not not_40 (not_40_out, F1);
  not not_41 (not_41_out, F0);
  not not_42 (not_42_out, OP5);
  not not_43 (not_43_out, OP4);
  not not_44 (not_44_out, OP3);
  not not_45 (not_45_out, OP2);
  not not_46 (not_46_out, OP1);
  not not_47 (not_47_out, OP0);
  not not_48 (not_48_out, F4);
  not not_49 (not_49_out, F3);
  not not_50 (not_50_out, F1);
  not not_51 (not_51_out, OP5);
  not not_52 (not_52_out, OP4);
  not not_53 (not_53_out, OP3);
  not not_54 (not_54_out, OP2);
  not not_55 (not_55_out, OP1);
  not not_56 (not_56_out, OP0);
  not not_57 (not_57_out, F4);
  not not_58 (not_58_out, F3);
  not not_59 (not_59_out, OP5);
  not not_60 (not_60_out, OP4);
  not not_61 (not_61_out, OP3);
  not not_62 (not_62_out, OP2);
  not not_63 (not_63_out, OP1);
  not not_64 (not_64_out, OP0);
  not not_65 (not_65_out, F4);
  not not_66 (not_66_out, F2);
  not not_67 (not_67_out, F0);
  not not_68 (not_68_out, OP5);
  not not_69 (not_69_out, OP4);
  not not_70 (not_70_out, OP3);
  not not_71 (not_71_out, OP2);
  not not_72 (not_72_out, OP1);
  not not_73 (not_73_out, OP0);
  not not_74 (not_74_out, F4);
  not not_75 (not_75_out, F2);
  not not_76 (not_76_out, OP5);
  not not_77 (not_77_out, OP4);
  not not_78 (not_78_out, OP3);
  not not_79 (not_79_out, OP2);
  not not_80 (not_80_out, OP1);
  not not_81 (not_81_out, OP0);
  not not_82 (not_82_out, F5);
  not not_83 (not_83_out, F4);
  not not_84 (not_84_out, F2);
  not not_85 (not_85_out, F1);
  not not_86 (not_86_out, F0);
  not not_87 (not_87_out, OP5);
  not not_88 (not_88_out, OP4);
  not not_89 (not_89_out, OP3);
  not not_90 (not_90_out, OP2);
  not not_91 (not_91_out, OP1);
  not not_92 (not_92_out, OP0);
  not not_93 (not_93_out, F5);
  not not_94 (not_94_out, F4);
  not not_95 (not_95_out, F1);
  not not_96 (not_96_out, F0);
  not not_97 (not_97_out, OP5);
  not not_98 (not_98_out, OP4);
  not not_99 (not_99_out, OP3);
  not not_100 (not_100_out, OP1);
  not not_101 (not_101_out, OP0);
  not not_102 (not_102_out, OP5);
  not not_103 (not_103_out, OP4);
  not not_104 (not_104_out, OP3);
  not not_105 (not_105_out, OP1);
  not not_106 (not_106_out, OP5);
  not not_107 (not_107_out, OP4);
  not not_108 (not_108_out, OP2);
  not not_109 (not_109_out, OP1);
  not not_110 (not_110_out, OP0);
  not not_111 (not_111_out, OP5);
  not not_112 (not_112_out, OP4);
  not not_113 (not_113_out, OP1);
  not not_114 (not_114_out, OP0);
  not not_115 (not_115_out, OP5);
  not not_116 (not_116_out, OP4);
  not not_117 (not_117_out, OP2);
  not not_118 (not_118_out, OP1);
  not not_119 (not_119_out, OP5);
  not not_120 (not_120_out, OP4);
  not not_121 (not_121_out, OP2);
  not not_122 (not_122_out, OP0);
  not not_123 (not_123_out, OP5);
  not not_124 (not_124_out, OP4);
  not not_125 (not_125_out, OP1);
  not not_126 (not_126_out, OP4);
  not not_127 (not_127_out, OP3);
  not not_128 (not_128_out, OP2);
  not not_129 (not_129_out, OP4);
  not not_130 (not_130_out, OP2);
  not not_131 (not_131_out, OP5);
  not not_132 (not_132_out, OP4);
  not not_133 (not_133_out, OP3);
  not not_134 (not_134_out, OP2);
  not not_135 (not_135_out, OP1);
  not not_136 (not_136_out, OP0);
  not not_137 (not_137_out, F5);
  not not_138 (not_138_out, F4);
  not not_139 (not_139_out, F3);
  not not_140 (not_140_out, OP5);
  not not_141 (not_141_out, OP4);
  not not_142 (not_142_out, OP0);
  not not_143 (not_143_out, OP4);
  not not_144 (not_144_out, OP2);
  not not_145 (not_145_out, OP1);
  not not_146 (not_146_out, OP5);
  not not_147 (not_147_out, OP4);
  not not_148 (not_148_out, OP3);
  not not_149 (not_149_out, OP0);
  not not_150 (not_150_out, OP1);
  not not_151 (not_151_out, OP3);
  not not_152 (not_152_out, OP4);
  not not_153 (not_153_out, OP5);
  not not_154 (not_154_out, F0);
  not not_155 (not_155_out, F2);
  not not_156 (not_156_out, F3);
  not not_157 (not_157_out, F4);
  not not_158 (not_158_out, OP0);
  not not_159 (not_159_out, OP1);
  not not_160 (not_160_out, OP3);
  not not_161 (not_161_out, OP4);
  not not_162 (not_162_out, OP5);
  not not_163 (not_163_out, F1);
  not not_164 (not_164_out, F3);
  not not_165 (not_165_out, F4);
  not not_166 (not_166_out, OP0);
  not not_167 (not_167_out, OP1);
  not not_168 (not_168_out, OP3);
  not not_169 (not_169_out, OP4);
  not not_170 (not_170_out, OP5);
  not not_171 (not_171_out, F0);
  not not_172 (not_172_out, F1);
  not not_173 (not_173_out, F4);
  not not_174 (not_174_out, F5);
  not not_175 (not_175_out, OP0);
  not not_176 (not_176_out, OP1);
  not not_177 (not_177_out, OP3);
  not not_178 (not_178_out, OP4);
  not not_179 (not_179_out, OP5);
  not not_180 (not_180_out, F2);
  not not_181 (not_181_out, F4);
  not not_182 (not_182_out, OP0);
  not not_183 (not_183_out, OP1);
  not not_184 (not_184_out, OP3);
  not not_185 (not_185_out, OP4);
  not not_186 (not_186_out, OP5);
  not not_187 (not_187_out, F3);
  not not_188 (not_188_out, F4);
  not not_189 (not_189_out, F5);
  not not_190 (not_190_out, OP0);
  not not_191 (not_191_out, OP1);
  not not_192 (not_192_out, OP3);
  not not_193 (not_193_out, OP4);
  not not_194 (not_194_out, OP5);
  not not_195 (not_195_out, F3);
  not not_196 (not_196_out, F4);
  not not_197 (not_197_out, OP1);
  not not_198 (not_198_out, OP3);
  not not_199 (not_199_out, OP4);
  not not_200 (not_200_out, OP5);
  not not_201 (not_201_out, OP2);
  not not_202 (not_202_out, OP4);
  not not_203 (not_203_out, OP3);
  not not_204 (not_204_out, OP4);
  not not_205 (not_205_out, OP5);
  not not_206 (not_206_out, OP2);
  not not_207 (not_207_out, OP4);
  and and_1 (and_1_out, not_1_out, not_2_out, not_3_out, not_4_out, not_5_out, not_6_out, F5, not_7_out, not_8_out, not_9_out, not_10_out, not_11_out);
  and and_2 (and_2_out, not_12_out, not_13_out, not_14_out, not_15_out, not_16_out, not_17_out, F5, not_18_out, not_19_out, not_20_out, not_21_out, F0);
  and and_3 (and_3_out, not_22_out, not_23_out, not_24_out, not_25_out, not_26_out, not_27_out, F5, not_28_out, not_29_out, not_30_out, F1, not_31_out);
  and and_4 (and_4_out, not_32_out, not_33_out, not_34_out, not_35_out, not_36_out, not_37_out, F5, not_38_out, not_39_out, F2, not_40_out, not_41_out);
  and and_5 (and_5_out, not_42_out, not_43_out, not_44_out, not_45_out, not_46_out, not_47_out, F5, not_48_out, not_49_out, F2, not_50_out, F0);
  and and_6 (and_6_out, not_51_out, not_52_out, not_53_out, not_54_out, not_55_out, not_56_out, F5, not_57_out, not_58_out, F2, F1, F0);
  and and_7 (and_7_out, not_59_out, not_60_out, not_61_out, not_62_out, not_63_out, not_64_out, F5, not_65_out, F3, not_66_out, F1, not_67_out);
  and and_8 (and_8_out, not_68_out, not_69_out, not_70_out, not_71_out, not_72_out, not_73_out, F5, not_74_out, F3, not_75_out, F1, F0);
  and and_9 (and_9_out, not_76_out, not_77_out, not_78_out, not_79_out, not_80_out, not_81_out, not_82_out, not_83_out, F3, not_84_out, not_85_out, not_86_out);
  and and_10 (and_10_out, not_87_out, not_88_out, not_89_out, not_90_out, not_91_out, not_92_out, not_93_out, not_94_out, F3, F2, not_95_out, not_96_out);
  and and_11 (and_11_out, not_97_out, not_98_out, not_99_out, OP2, not_100_out, not_101_out);
  and and_12 (and_12_out, not_102_out, not_103_out, not_104_out, OP2, not_105_out, OP0);
  and and_13 (and_13_out, not_106_out, not_107_out, OP3, not_108_out, not_109_out, not_110_out);
  and and_14 (and_14_out, not_111_out, not_112_out, OP3, OP2, not_113_out, not_114_out);
  and and_15 (and_15_out, not_115_out, not_116_out, OP3, not_117_out, not_118_out, OP0);
  and and_16 (and_16_out, not_119_out, not_120_out, OP3, not_121_out, OP1, not_122_out);
  and and_17 (and_17_out, not_123_out, not_124_out, OP3, OP2, not_125_out, OP0);
  and and_18 (and_18_out, OP5, not_126_out, not_127_out, not_128_out, OP1, OP0);
  and and_19 (and_19_out, OP5, not_129_out, OP3, not_130_out, OP1, OP0);
  and and_20 (and_20_out, not_131_out, not_132_out, not_133_out, not_134_out, not_135_out, not_136_out, not_137_out, not_138_out, not_139_out, F2, F1, F0);
  and and_21 (and_21_out, not_140_out, not_141_out, OP3, OP2, OP1, not_142_out);
  and and_22 (and_22_out, OP5, not_143_out, OP3, not_144_out, not_145_out, OP0);
  and and_23 (and_23_out, not_146_out, not_147_out, not_148_out, OP2, OP1, OP0);
  and and_24 (and_24_out, not_149_out, not_150_out, not_151_out, not_152_out, not_153_out, not_154_out, not_155_out, not_156_out, not_157_out);
  and and_25 (and_25_out, not_158_out, not_159_out, not_160_out, not_161_out, not_162_out, not_163_out, not_164_out, not_165_out, F5);
  and and_26 (and_26_out, not_166_out, not_167_out, not_168_out, not_169_out, not_170_out, not_171_out, not_172_out, F2, F3, not_173_out, not_174_out);
  and and_27 (and_27_out, not_175_out, not_176_out, not_177_out, not_178_out, not_179_out, F1, not_180_out, F3, not_181_out, F5);
  and and_28 (and_28_out, not_182_out, not_183_out, not_184_out, not_185_out, not_186_out, F0, F1, not_187_out, not_188_out, not_189_out);
  and and_29 (and_29_out, not_190_out, not_191_out, not_192_out, not_193_out, not_194_out, F0, F1, F2, not_195_out, not_196_out);
  and and_30 (and_30_out, not_197_out, OP2, not_198_out, not_199_out, not_200_out);
  and and_31 (and_31_out, OP0, not_201_out, OP3, not_202_out, OP5);
  and and_32 (and_32_out, OP0, OP2, not_203_out, not_204_out, not_205_out);
  and and_33 (and_33_out, OP0, OP1, not_206_out, not_207_out, OP5);
  or or_1 (RTUSED, and_24_out, and_25_out, and_26_out, and_27_out, and_28_out, and_29_out, and_30_out, and_31_out, and_32_out, and_33_out);
  or or_2 (RSUSED, and_1_out, and_2_out, and_3_out, and_4_out, and_5_out, and_6_out, and_7_out, and_8_out, and_9_out, and_10_out, and_11_out, and_12_out, and_13_out, and_14_out, and_15_out, and_16_out, and_17_out, and_18_out, and_19_out, and_20_out, and_21_out, and_22_out, and_23_out);
endmodule

module \重定向控制器  (
  input  branch,
  input  PredictError,
  input  [31:0] IR,
  input  EX_MemtoReg,
  input  [4:0] rs,
  input  [4:0] rt,
  input  [4:0] EX_WriteReg_num,
  input  [4:0] MEM_WriteReg_num,
  input  EX_RegWrite,
  input  MEM_RegWrite,
  output ID_EX_CLR,
  output IF_ID_CLR,
  output Stall,
  output PC_EN,
  output [1:0] RsForward,
  output [1:0] RtForward
);

  wire and_1_out, and_2_out, and_3_out, and_4_out, and_5_out, and_6_out, comparator_1_gt, comparator_1_lt,
       comparator_2_gt, comparator_2_lt, comparator_3_eq, comparator_4_eq, comparator_5_eq, comparator_6_eq,
       rs__0, RsUsed, rt__0, RtUsed;
  wire [1:0] priority_encoder_1_out, priority_encoder_2_out;

  Pull_Resistor #(.pull(0)) pull_resistor_1 (.node(rs));
  rstused rstused_1 (
    .OP0(IR[26]), .OP1(IR[27]), .OP2(IR[28]), .OP3(IR[29]), .OP4(IR[30]), .OP5(IR[31]), .F0(IR[0]),
    .F1(IR[1]), .F2(IR[2]), .F3(IR[3]), .F4(IR[4]), .F5(IR[5]), .RSUSED(RsUsed), .RTUSED(RtUsed));
  Comparator #(.width(5), .mode("twosComplement")) comparator_1 (
    .a(rs), .b({5{1'b0}}), .gt(comparator_1_gt), .lt(comparator_1_lt));  // open: eq
  Comparator #(.width(5), .mode("twosComplement")) comparator_2 (
    .a(rt), .b({5{1'b0}}), .gt(comparator_2_gt), .lt(comparator_2_lt));  // open: eq
  or or_1 (rs__0, comparator_1_gt, comparator_1_lt);
  or or_2 (rt__0, comparator_2_gt, comparator_2_lt);
  and and_1 (and_1_out, RsUsed, rs__0, EX_MemtoReg, comparator_3_eq);
  Comparator #(.width(5), .mode("twosComplement")) comparator_3 (
    .a(EX_WriteReg_num), .b(rs), .eq(comparator_3_eq));  // open: gt, lt
  Comparator #(.width(5), .mode("twosComplement")) comparator_4 (
    .a(EX_WriteReg_num), .b(rt), .eq(comparator_4_eq));  // open: gt, lt
  Comparator #(.width(5), .mode("twosComplement")) comparator_5 (
    .a(MEM_WriteReg_num), .b(rs), .eq(comparator_5_eq));  // open: gt, lt
  Comparator #(.width(5), .mode("twosComplement")) comparator_6 (
    .a(MEM_WriteReg_num), .b(rt), .eq(comparator_6_eq));  // open: gt, lt
  or or_3 (Stall, and_1_out, and_2_out);
  not not_1 (PC_EN, Stall);
  and and_2 (and_2_out, EX_MemtoReg, comparator_4_eq, RtUsed, rt__0);
  or or_4 (ID_EX_CLR, Stall, PredictError, branch);
  and and_3 (and_3_out, comparator_3_eq, RsUsed, rs__0, EX_RegWrite);
  and and_4 (and_4_out, comparator_4_eq, RtUsed, rt__0, EX_RegWrite);
  or or_5 (IF_ID_CLR, PredictError, branch);
  and and_5 (and_5_out, comparator_5_eq, RsUsed, rs__0, MEM_RegWrite);
  and and_6 (and_6_out, comparator_6_eq, RtUsed, rt__0, MEM_RegWrite);
  Priority_Encoder #(.select(2), .disabled("Z")) priority_encoder_1 (
    .in0(1'b0), .in1(1'b0), .in2(and_6_out), .in3(and_4_out), .out(priority_encoder_1_out), .en_in(1'b1));  // open: gs, en_out
  Priority_Encoder #(.select(2), .disabled("Z")) priority_encoder_2 (
    .in0(1'b0), .in1(1'b0), .in2(and_5_out), .in3(and_3_out), .out(priority_encoder_2_out), .en_in(1'b1));  // open: gs, en_out
  // Probe on priority_encoder_1_out
  // Probe on priority_encoder_2_out
  Multiplexer #(.select(2), .width(2), .disabled("Z"), .enable("false")) multiplexer_1 (
    .in0(2'b00), .in1(2'b00), .in2(2'b01), .in3(2'b10), .out(RsForward), .sel(priority_encoder_2_out));
  Multiplexer #(.select(2), .width(2), .disabled("Z"), .enable("false")) multiplexer_2 (
    .in0(2'b00), .in1(2'b00), .in2(2'b01), .in3(2'b10), .out(RtForward), .sel(priority_encoder_1_out));
  Pull_Resistor #(.pull(0)) pull_resistor_2 (.node(RsForward));
  Pull_Resistor #(.pull(0)) pull_resistor_3 (.node(RtForward));

  // Notes on the sheet:
  //   op
  //   Func
endmodule

module \EX重定向  (
  output RegWrite,
  output MemWrite,
  output [31:0] IF_PC,
  output [31:0] ID_PC,
  output [31:0] EX_PC,
  output [31:0] M_PC,
  output [31:0] WB_PC,
  output [31:0] RDin,
  output [31:0] MDin,
  output [31:0] LedData
);

  wire and_3_out, and_4_out, and_5_out, branch, CLK, clock_1_out, clock_2_out, comparator_1_eq,
       comparator_2_eq, comparator_2_lt, d_ff_1_q, EN, ex_mem_1_jal_2, ex_mem_1_memtoreg_2,
       ex_mem_1_memwrite_4, ex_mem_1_regwrite_2, Go, halt, id_ex_1_alusrcb_2, id_ex_1_beq_2, id_ex_1_bne_2,
       id_ex_1_jal_2, id_ex_1_memtoreg_2, id_ex_1_memwrite_2, id_ex_1_regwrite_2, id_ex_1_sys_2, IR1, IR2,
       IR3, JMP, JR, LedOut, mem_wb_1_jal_2, mem_wb_1_memtoreg_2, mips_alu_1_equal, nand_1_out, not_1_out,
       not_2_out, not_3_out, or_2_out, RST, Stall, Syscall, W1, W2, W3, \单周期硬布线控制器_1_alu_src ,
       \单周期硬布线控制器_1_beq , \单周期硬布线控制器_1_bne , \单周期硬布线控制器_1_jal , \单周期硬布线控制器_1_jmp , \单周期硬布线控制器_1_jr ,
       \单周期硬布线控制器_1_memtoreg , \单周期硬布线控制器_1_memwrite , \单周期硬布线控制器_1_regdst , \单周期硬布线控制器_1_regwrite ,
       \单周期硬布线控制器_1_syscall , \重定向控制器_1_id_ex_clr , \重定向控制器_1_if_id_clr ;
  wire [1:0] FwdA, FwdB, id_ex_1_fwda_2, id_ex_1_fwdb_2;
  wire [3:0] id_ex_1_aluop_2, \单周期硬布线控制器_1_alu_op ;
  wire [4:0] ex_mem_1_writereg_num_2, id_ex_1_writereg_num_2, mem_wb_1_writereg_num_2, multiplexer_4_out,
       multiplexer_7_out, RS, RT;
  wire [12:0] CNT_num;
  wire [15:0] \LoadUse次数 , \总周期数 , \插入气泡数 , \无条件分支数 , \条件分支成功数 ;
  wire [27:0] bit_extender_2_out, shifter_2_out;
  wire [31:0] adder_1_out, adder_2_out, adder_3_out, adder_4_out, bit_extender_1_out, EX_IR, ex_mem_1_ir_mem,
       ex_mem_1_result_2, ex_mem_1_v0_2, id_ex_1_ir_id_2, id_ex_1_rt_2, id_ex_1_signimm_2, ID_IR,
       if_id_1_ir_2, IF_IR, MEM_IR, mem_wb_1_ir_wb, mem_wb_1_rd_2, mem_wb_1_result_2, mips_alu_1_result,
       mips_regifile_1_r1, mips_regifile_1_r2, multiplexer_1_out, multiplexer_2_out, multiplexer_3_out,
       multiplexer_8_out, multiplexer_9_out, multiplexer_10_out, multiplexer_11_out, ram_1_data, rom_1_data,
       rv0, shifter_1_out, V0, WB_IR;

  Button \u_总复位  (.out(RST));
  Button _1 (.out(IR1));
  Button _2 (.out(IR2));
  Button _3 (.out(IR3));
  // Probe on \总周期数 
  // Probe on \总周期数 
  Button \u_继续运行  (.out(Go));
  LED #(.active("true")) led_1 (.in(W1));
  LED #(.active("true")) led_2 (.in(W2));
  LED #(.active("true")) led_3 (.in(W3));
  Hex_Digit_Display hex_digit_display_1 (.value(LedData[31:28]));  // open: dp
  // Probe on IF_PC[19:0]
  // Mips_Probe mips_probe_1: pin names not known; wires that end beside it: IF_IR
  Hex_Digit_Display hex_digit_display_2 (.value(LedData[27:24]));  // open: dp
  Hex_Digit_Display hex_digit_display_3 (.value(LedData[23:20]));  // open: dp
  // Probe on ID_PC[19:0]
  // Mips_Probe mips_probe_2: pin names not known; wires that end beside it: ID_IR
  Multiplexer #(.select(1), .width(32), .disabled("Z"), .enable("false")) multiplexer_1 (
    .in0(adder_1_out), .in1(adder_3_out), .out(multiplexer_1_out), .sel(branch));
  Hex_Digit_Display hex_digit_display_4 (.value(LedData[19:16]));  // open: dp
  Hex_Digit_Display hex_digit_display_5 (.value(LedData[15:12]));  // open: dp
  Multiplexer #(.select(1), .width(32), .disabled("Z"), .enable("false")) multiplexer_2 (
    .in0(multiplexer_1_out), .in1({adder_1_out[31:28], shifter_2_out}), .out(multiplexer_2_out), .sel(JMP));
  Hex_Digit_Display hex_digit_display_6 (.value(LedData[11:8]));  // open: dp
  Hex_Digit_Display hex_digit_display_7 (.value(LedData[7:4]));  // open: dp
  Clock #(.highDuration(1), .lowDuration(1)) clock_1 (.out(clock_1_out));
  // Probe on EX_PC[19:0]
  // Mips_Probe mips_probe_3: pin names not known; wires that end beside it: clock_1_out, EX_IR, CLK
  Comparator #(.width(32), .mode("twosComplement")) comparator_1 (
    .a(rv0), .b(32'h22), .eq(comparator_1_eq));  // open: gt, lt
  not not_1 (not_1_out, halt);
  Multiplexer #(.select(1), .width(32), .disabled("Z"), .enable("false")) multiplexer_3 (
    .in0(multiplexer_2_out), .in1(V0), .out(multiplexer_3_out), .sel(JR));
  Hex_Digit_Display hex_digit_display_8 (.value(LedData[3:0]));  // open: dp
  and and_1 (LedOut, Syscall, comparator_1_eq);
  and and_2 (halt, Syscall, ~comparator_1_eq);  // AND_Gate
  Counter #(.width(16), .max('hffff), .ongoal("wrap"), .trigger("rising"), .behavior("new")) counter_1 (
    .count(not_1_out), .Q(\总周期数 ), .clk(CLK), .clr(RST));  // open: load, D, carry, preset, down
  Register #(.width(32), .trigger("rising"), .Select("low")) register_1 (
    .D(MDin), .Q(LedData), .clk(CLK), .clr(RST));  // open: en
  // Probe on \总周期数 
  // Probe on M_PC[19:0]
  // Mips_Probe mips_probe_4: pin names not known; wires that end beside it: MEM_IR
  Register #(.width(32), .trigger("rising"), .Select("low")) register_2 (
    .D(multiplexer_3_out), .en(and_3_out), .Q(IF_PC), .clk(CLK));  // open: clr
  not not_2 (not_2_out, Stall);
  // Probe on \总周期数 
  // Probe on \无条件分支数 
  // Probe on \条件分支成功数 
  // Probe on \插入气泡数 
  // Probe on \LoadUse次数 
  // Probe on IF_PC[11:0]
  // Probe on WB_PC[19:0]
  // Mips_Probe mips_probe_5: pin names not known; wires that end beside it: WB_IR
  Adder #(.width(32)) adder_1 (.a(IF_PC), .b(32'h4), .out(adder_1_out));  // open: cin, cout
  and and_3 (and_3_out, not_2_out, EN);
  or or_1 (EN, ~halt, Go);  // OR_Gate
  // Probe on EX_PC[11:0]
  // Probe on ID_PC[11:0]
  ROM #(.addrWidth(10), .dataWidth(32), .Select("high")) rom_1 (.addr(IF_PC[11:2]), .data(rom_1_data));
  // Probe on M_PC[11:0]
  D_Flip_Flop #(.trigger("high"), .Pre_Clr_Positions("LEGACY"), .NegatePresetClear("false"), .enable("true"), .NewFFLayout("false")) d_ff_1 (.Q(d_ff_1_q));  // open: clk, D, Qn, preset, en, reset
  // Probe on 13'h15
  // Mips_Probe mips_probe_6: pin names not known; wires that end beside it: rom_1_data
  // Probe on WB_PC[11:0]
  Comparator #(.width(13), .mode("twosComplement")) comparator_2 (
    .a(CNT_num), .b(13'h15), .eq(comparator_2_eq), .lt(comparator_2_lt));  // open: gt
  Clock #(.highDuration(1), .lowDuration(1)) clock_2 (.out(clock_2_out));
  \重定向控制器  \u_重定向控制器_1  (
    .EX_WriteReg_num(id_ex_1_writereg_num_2), .MEM_WriteReg_num(ex_mem_1_writereg_num_2), .RsForward(FwdA),
    .RtForward(FwdB), .Stall(Stall), .ID_EX_CLR(\重定向控制器_1_id_ex_clr ), .IF_ID_CLR(\重定向控制器_1_if_id_clr ),
    .rs(RS), .IR(if_id_1_ir_2), .rt(RT), .EX_MemtoReg(id_ex_1_memtoreg_2), .EX_RegWrite(id_ex_1_regwrite_2),
    .branch(or_2_out), .MEM_RegWrite(ex_mem_1_regwrite_2));  // open: PC_EN, PredictError
  IF_ID if_id_1 (
    .IR(rom_1_data), .PC_4(IF_PC), .IR_2(if_id_1_ir_2), .PC_4_ID(ID_PC), .CLK(CLK),
    .RST(\重定向控制器_1_if_id_clr ), .EN(and_3_out));
  nand nand_1 (nand_1_out, d_ff_1_q, comparator_2_eq);
  Counter #(.width(13), .max('h1fff), .ongoal("stay"), .trigger("rising"), .behavior("old")) counter_2 (
    .count(comparator_2_lt), .Q(CNT_num), .clk(clock_2_out));  // open: load, D, carry, clr, preset
  // Probe on if_id_1_ir_2
  assign CLK = nand_1_out ? clock_2_out : 1'bz;  // Controlled_Buffer controlled_buffer_1
  // Probe on RS
  Multiplexer #(.select(1), .width(5), .disabled("Z"), .enable("false")) multiplexer_4 (
    .in0(if_id_1_ir_2[20:16]), .in1(if_id_1_ir_2[15:11]), .out(multiplexer_4_out), .sel(\单周期硬布线控制器_1_regdst ));
  Pull_Resistor #(.pull(1)) pull_resistor_1 (.node(CLK));
  \单周期硬布线控制器  \u_单周期硬布线控制器_1  (
    .Func(if_id_1_ir_2[5:0]), .OP(if_id_1_ir_2[31:26]), .ALU_OP(\单周期硬布线控制器_1_alu_op ),
    .MemToReg(\单周期硬布线控制器_1_memtoreg ), .MemWrite(\单周期硬布线控制器_1_memwrite ), .ALU_SRC(\单周期硬布线控制器_1_alu_src ),
    .RegWrite(\单周期硬布线控制器_1_regwrite ), .SysCALL(\单周期硬布线控制器_1_syscall ), .RegDst(\单周期硬布线控制器_1_regdst ),
    .JR(\单周期硬布线控制器_1_jr ), .JMP(\单周期硬布线控制器_1_jmp ), .Beq(\单周期硬布线控制器_1_beq ), .JAL(\单周期硬布线控制器_1_jal ),
    .Bne(\单周期硬布线控制器_1_bne ));  // open: SignedExt, SH, SRAV, BGTZ
  Multiplexer #(.select(1), .width(5), .disabled("Z"), .enable("false")) multiplexer_5 (
    .in0(if_id_1_ir_2[25:21]), .in1(5'b00010), .out(RS), .sel(\单周期硬布线控制器_1_syscall ));
  Multiplexer #(.select(1), .width(5), .disabled("Z"), .enable("false")) multiplexer_6 (
    .in0(if_id_1_ir_2[20:16]), .in1(5'b00100), .out(RT), .sel(\单周期硬布线控制器_1_syscall ));
  Multiplexer #(.select(1), .width(5), .disabled("Z"), .enable("false")) multiplexer_7 (
    .in0(multiplexer_4_out), .in1({5{1'b1}}), .out(multiplexer_7_out), .sel(\单周期硬布线控制器_1_jal ));
  not not_3 (not_3_out, CLK);
  assign bit_extender_1_out = {{16{if_id_1_ir_2[15]}}, if_id_1_ir_2[15:0]};  // Bit_Extender bit_extender_1
  // Mips_Probe mips_probe_7: pin names not known; wires that end beside it: if_id_1_ir_2
  MIPS_Regifile mips_regifile_1 (
    .Din(RDin), .Clk(not_3_out), .R1(mips_regifile_1_r1), .R2(mips_regifile_1_r2), .WE(RegWrite),
    .W_num(mem_wb_1_writereg_num_2), .R1_num(RS), .R2_num(RT));
  ID_EX id_ex_1 (
    .BEQ(\单周期硬布线控制器_1_beq ), .BNE(\单周期硬布线控制器_1_bne ), .MemToReg(\单周期硬布线控制器_1_memtoreg ),
    .MemWrite(\单周期硬布线控制器_1_memwrite ), .AluOP(\单周期硬布线控制器_1_alu_op ), .AluSrcB(\单周期硬布线控制器_1_alu_src ),
    .RegWrite(\单周期硬布线控制器_1_regwrite ), .RS(mips_regifile_1_r1), .RT(mips_regifile_1_r2),
    .WriteReg_num(multiplexer_7_out), .SignImm(bit_extender_1_out), .IR_ID(if_id_1_ir_2), .PC_4_ID(ID_PC),
    .BEQ_2(id_ex_1_beq_2), .BNE_2(id_ex_1_bne_2), .MemToReg_2(id_ex_1_memtoreg_2),
    .MemWrite_2(id_ex_1_memwrite_2), .AluOP_2(id_ex_1_aluop_2), .AluSrcB_2(id_ex_1_alusrcb_2),
    .RegWrite_2(id_ex_1_regwrite_2), .RS_2(V0), .RT_2(id_ex_1_rt_2), .WriteReg_num_2(id_ex_1_writereg_num_2),
    .SignImm_2(id_ex_1_signimm_2), .IR_ID_2(id_ex_1_ir_id_2), .PC_4_ID_2(EX_PC), .CLK(CLK),
    .sys(\单周期硬布线控制器_1_syscall ), .sys_2(id_ex_1_sys_2), .in_22(EN), .jal(\单周期硬布线控制器_1_jal ),
    .jal_2(id_ex_1_jal_2), .JMP(\单周期硬布线控制器_1_jmp ), .JMP_2(JMP), .JR(\单周期硬布线控制器_1_jr ), .JR_2(JR),
    .RST(\重定向控制器_1_id_ex_clr ), .FwdA(FwdA), .FwdA_2(id_ex_1_fwda_2), .FwdB(FwdB), .FwdB_2(id_ex_1_fwdb_2));
  or or_2 (or_2_out, id_ex_1_jal_2, JMP, JR, branch);
  or or_3 (branch, and_5_out, and_4_out);
  and and_4 (and_4_out, ~mips_alu_1_equal, id_ex_1_bne_2);  // AND_Gate
  and and_5 (and_5_out, id_ex_1_beq_2, mips_alu_1_equal);
  Multiplexer #(.select(2), .width(32), .disabled("Z"), .enable("false")) multiplexer_8 (
    .in0(id_ex_1_rt_2), .in1(RDin), .in2(ex_mem_1_result_2), .out(multiplexer_8_out), .sel(id_ex_1_fwdb_2));  // open: in3
  Multiplexer #(.select(2), .width(32), .disabled("Z"), .enable("false")) multiplexer_9 (
    .in0(V0), .in1(RDin), .in2(ex_mem_1_result_2), .out(multiplexer_9_out), .sel(id_ex_1_fwda_2));  // open: in3
  Multiplexer #(.select(1), .width(32), .disabled("Z"), .enable("false")) multiplexer_10 (
    .in0(multiplexer_8_out), .in1(id_ex_1_signimm_2), .out(multiplexer_10_out), .sel(id_ex_1_alusrcb_2));
  Adder #(.width(32)) adder_2 (.a(EX_PC), .b(32'h4), .out(adder_2_out));  // open: cin, cout
  MIPS_ALU mips_alu_1 (
    .X(multiplexer_9_out), .Y(multiplexer_10_out), .AluOP(id_ex_1_aluop_2), .Equal(mips_alu_1_equal),
    .Result(mips_alu_1_result), .shamt(id_ex_1_ir_id_2[10:6]));  // open: Result_2
  Shifter #(.width(32), .shift("ll")) shifter_1 (.in(id_ex_1_signimm_2), .\dist (5'b00010), .out(shifter_1_out));
  Adder #(.width(32)) adder_3 (.a(shifter_1_out), .b(adder_2_out), .out(adder_3_out));  // open: cin, cout
  // Mips_Probe mips_probe_8: pin names not known; wires that end beside it: id_ex_1_ir_id_2
  EX_MEM ex_mem_1 (
    .RegWrite(id_ex_1_regwrite_2), .MemToReg(id_ex_1_memtoreg_2), .MemWrite(id_ex_1_memwrite_2),
    .IR_EX(id_ex_1_ir_id_2), .Result(mips_alu_1_result), .WriteData(multiplexer_8_out),
    .WriteReg_num(id_ex_1_writereg_num_2), .PC_4_EX(EX_PC), .RegWrite_2(ex_mem_1_regwrite_2),
    .MemToReg_2(ex_mem_1_memtoreg_2), .MemWrite_3(MemWrite), .IR_MEM(ex_mem_1_ir_mem),
    .Result_2(ex_mem_1_result_2), .WriteData_2(MDin), .WriteReg_num_2(ex_mem_1_writereg_num_2),
    .PC_4_MEM(M_PC), .CLK(CLK), .MemWrite_2(id_ex_1_sys_2), .MemWrite_4(ex_mem_1_memwrite_4), .in_13(EN),
    .jal(id_ex_1_jal_2), .jal_2(ex_mem_1_jal_2), .v0(multiplexer_9_out), .v0_2(ex_mem_1_v0_2));  // open: RST
  // Probe on ex_mem_1_ir_mem
  assign bit_extender_2_out = {{2{1'b0}}, id_ex_1_ir_id_2[25:0]};  // Bit_Extender bit_extender_2
  // Mips_Probe mips_probe_9: pin names not known; wires that end beside it: ex_mem_1_ir_mem
  Shifter #(.width(28), .shift("ll")) shifter_2 (.in(bit_extender_2_out), .\dist (5'b00010), .out(shifter_2_out));
  RAM #(.addrWidth(10), .dataWidth(32), .bus("separate"), .Select("high")) ram_1 (
    .addr(ex_mem_1_result_2[11:2]), .din(MDin), .data(ram_1_data), .str(MemWrite), .clk(CLK));  // open: sel, ld, clr
  MEM_WB mem_wb_1 (
    .RegWrite(ex_mem_1_regwrite_2), .MemToReg(ex_mem_1_memtoreg_2), .Result(ex_mem_1_result_2),
    .RD(ram_1_data), .WriteReg_num(ex_mem_1_writereg_num_2), .IR_MEM(ex_mem_1_ir_mem), .PC_4_MEM(M_PC),
    .RegWrite_2(RegWrite), .MemToReg_2(mem_wb_1_memtoreg_2), .Result_2(mem_wb_1_result_2),
    .RD_2(mem_wb_1_rd_2), .WriteReg_num_2(mem_wb_1_writereg_num_2), .IR_WB(mem_wb_1_ir_wb), .PC_4_WB(WB_PC),
    .CLK(CLK), .sys(ex_mem_1_memwrite_4), .sys_2(Syscall), .in_12(EN), .jal(ex_mem_1_jal_2),
    .jal_2(mem_wb_1_jal_2), .v0(ex_mem_1_v0_2), .v0_2(rv0));  // open: RST
  // Probe on ex_mem_1_result_2
  // Mips_Probe mips_probe_10: pin names not known; wires that end beside it: mem_wb_1_ir_wb
  Multiplexer #(.select(1), .width(32), .disabled("Z"), .enable("false")) multiplexer_11 (
    .in0(mem_wb_1_result_2), .in1(mem_wb_1_rd_2), .out(multiplexer_11_out), .sel(mem_wb_1_memtoreg_2));
  Multiplexer #(.select(1), .width(32), .disabled("Z"), .enable("false")) multiplexer_12 (
    .in0(multiplexer_11_out), .in1(adder_4_out), .out(RDin), .sel(mem_wb_1_jal_2));
  Adder #(.width(32)) adder_4 (.a(WB_PC), .b(32'h4), .out(adder_4_out));  // open: cin, cout

  // Other names for the same wires on the sheet: MEM_PC[31:0] = M_PC

  // Notes on the sheet:
  //   中断源
  //   时空图监测，可删除
  //   中断等待指示
  //   数码管输出
  //   指令存储器
  //   控制位
  //   contents of rom_1 (hex, n*v repeats v):
  //   20110001 8000c05 20110001 20120002 20130003 8000c09 20110001 20120002 20130003 8000c0d 20110001
  //   20120002 20130003 8000c11 20110001 20120002 20130003 c000cb8 20100001 20110001 118fc0 112020
  //   20020022 c 118882 12200001 8000c15 112020 20020022 c 20110001 118880 112020 20020022 c 12200001
  //   8000c1f 20110001 118fc0 112020 20020022 c 1188c3 112020 20020022 c 118903 112020 20020022 c 118903
  //   112020 20020022 c 118903 112020 20020022 c 118903 112020 20020022 c 118903 112020 20020022 c 118903
  //   112020 20020022 c 118903 112020 20020022 c 20100001 109fc0 139fc3 8021 2012000c 24160003 26100001
  //   3210000f 20080008 20090001 139900 2709825 132020 20020022 c 1094022 1500fff9 22100001 2018000f
  //   2188024 108700 20080008 20090001 139902 2709825 132021 20020022 c 1094022 1500fff9 108702 2c9b022
  //   12c00001 8000c50 4020 1084027 84400 3508ffff 82021 20020022 c 2010ffff 20110000 ae300000 22100001
  //   22310004 ae300000 22100001 22310004 ae300000 22100001 22310004 ae300000 22100001 22310004 ae300000
  //   22100001 22310004 ae300000 22100001 22310004 ae300000 22100001 22310004 ae300000 22100001 22310004
  //   ae300000 22100001 22310004 ae300000 22100001 22310004 ae300000 22100001 22310004 ae300000 22100001
  //   22310004 ae300000 22100001 22310004 ae300000 22100001 22310004 ae300000 22100001 22310004 ae300000
  //   22100001 22310004 22100001 8020 2011003c 8e130000 8e340000 274402a 11000002 ae330000 ae140000
  //   2231fffc 1611fff8 102020 20020022 c 22100004 2011003c 1611fff2 20020032 c 20100000 22100001 102020
  //   20020022 c 22100002 102020 20020022 c 22100003 102020 20020022 c 22100004 102020 20020022 c 22100005
  //   102020 20020022 c 22100006 102020 20020022 c 22100007 102020 20020022 c 22100008 102020 20020022
  //   20020022 c 3e00008
  //   流水调试日志用
  //   暂停节拍，不能为0
  //   戳工具置1进入计数暂停模式，ctrl+k时钟自动运行到对应节拍暂停
  //   ctrl+k关闭时钟连续运行，将控制位置零，进入单步调试模式调试
  //   rs
  //   rt
  //   rd
  //   可计数暂停的时钟源
  //   为方便自动评测，需要输出流水线各段保存的PC值，注意是PC不是PC+4，另外ID段寄存器写入信息，Mem段内存写入信息也要输出
endmodule
module BTB (
  input  [31:0] PC,
  input  [31:0] EX_PC,
  input  [31:0] EX_BranchAddr,
  input  CLK,
  input  EX_Branch,
  input  EX_BranchTaken,
  input  [31:0] IF_IR,
  input  [31:0] ID_IR,
  input  [31:0] EX_IR,
  input  [31:0] M_IR,
  input  [31:0] WB_IR,
  output PredictJump,
  output [31:0] JumpAddr
);

  wire and_1_out, and_2_out, and_3_out, and_4_out, and_5_out, and_6_out, and_7_out, and_8_out, and_9_out,
       and_28_out, and_29_out, and_30_out, and_31_out, and_32_out, and_33_out, and_34_out, and_35_out,
       and_36_out, and_37_out, and_38_out, and_39_out, and_40_out, and_41_out, and_42_out, and_43_out,
       comparator_1_eq, comparator_2_eq, comparator_3_eq, comparator_4_eq, comparator_5_eq, comparator_6_eq,
       comparator_7_eq, comparator_8_eq, comparator_9_eq, comparator_10_eq, comparator_11_eq,
       comparator_12_eq, comparator_13_eq, comparator_14_eq, comparator_15_eq, comparator_16_eq,
       decoder_2_out0, decoder_2_out1, decoder_2_out2, decoder_2_out3, hit, L1, L2, L3, L4, L5, L6, L7, L8,
       Miss, multiplexer_4_out, not_1_out, not_2_out, not_3_out, not_4_out, not_5_out, not_6_out, not_7_out,
       not_8_out, not_9_out, or_1_out, or_3_out, or_4_out, or_5_out, or_6_out, or_7_out, or_8_out, or_9_out,
       or_10_out, pc_hit, priority_encoder_1_gs, V1, V2, V3, V4, V5, V6, V7, V8, X1, X2, X3, X4, X5, X6, X7,
       X8, Y1, Y2, Y3, Y4, Y5, Y6, Y7, Y8;
  wire [1:0] controlled_buffer_10_out, controlled_buffer_18_out, controlled_buffer_26_out,
       controlled_buffer_35_out, History_2_q, History_3_q, History_4_q, History_5_q, History_6_q,
       History_7_q, History_8_q, History_Curr, History_q, History_Update;
  wire [2:0] compare_1_max_num, compare_2_max_num, compare_3_max_num, compare_4_max_num, compare_5_max_num,
       compare_6_max_num, LRU, multiplexer_2_out, priority_encoder_1_out;
  wire [15:0] A1, A2, A3, A4, A5, A6, A7, A8, compare_1_max, compare_2_max, compare_3_max, compare_4_max,
       compare_5_max, compare_6_max;
  wire [31:0] controlled_buffer_1_out, data_2_q, data_3_q, data_4_q, data_5_q, data_6_q, data_7_q, data_8_q,
       data_q, tag, tag1, tag2, tag3, tag4, tag5, tag6, tag7, tag8;

  and and_1 (and_1_out, Miss, EX_Branch);
  and and_2 (and_2_out, and_1_out, X1);
  and and_3 (and_3_out, and_1_out, X2);
  and and_4 (and_4_out, and_1_out, X3);
  and and_5 (and_5_out, and_1_out, X4);
  and and_6 (and_6_out, and_1_out, X5);
  and and_7 (and_7_out, and_1_out, X6);
  and and_8 (and_8_out, and_1_out, X7);
  and and_9 (and_9_out, and_1_out, X8);
  Register #(.width(1), .trigger("rising"), .Select("low")) valid (
    .D(1'b1), .en(and_2_out), .Q(V1), .clk(CLK));  // open: clr
  Register #(.width(1), .trigger("rising"), .Select("low")) valid_2 (
    .D(1'b1), .en(and_3_out), .Q(V2), .clk(CLK));  // open: clr
  Register #(.width(1), .trigger("rising"), .Select("low")) valid_3 (
    .D(1'b1), .en(and_4_out), .Q(V3), .clk(CLK));  // open: clr
  Register #(.width(1), .trigger("rising"), .Select("low")) valid_4 (
    .D(1'b1), .en(and_5_out), .Q(V4), .clk(CLK));  // open: clr
  Register #(.width(1), .trigger("rising"), .Select("low")) valid_5 (
    .D(1'b1), .en(and_6_out), .Q(V5), .clk(CLK));  // open: clr
  Register #(.width(1), .trigger("rising"), .Select("low")) valid_6 (
    .D(1'b1), .en(and_7_out), .Q(V6), .clk(CLK));  // open: clr
  Register #(.width(1), .trigger("rising"), .Select("low")) valid_7 (
    .D(1'b1), .en(and_8_out), .Q(V7), .clk(CLK));  // open: clr
  Register #(.width(1), .trigger("rising"), .Select("low")) valid_8 (
    .D(1'b1), .en(and_9_out), .Q(V8), .clk(CLK));  // open: clr
  Register #(.width(32), .trigger("rising"), .Select("low")) u_tag (
    .D(EX_PC), .en(and_2_out), .Q(tag1), .clk(CLK));  // open: clr
  Register #(.width(32), .trigger("rising"), .Select("low")) tag_2 (
    .D(EX_PC), .en(and_3_out), .Q(tag2), .clk(CLK));  // open: clr
  Register #(.width(32), .trigger("rising"), .Select("low")) tag_3 (
    .D(EX_PC), .en(and_4_out), .Q(tag3), .clk(CLK));  // open: clr
  Register #(.width(32), .trigger("rising"), .Select("low")) tag_4 (
    .D(EX_PC), .en(and_5_out), .Q(tag4), .clk(CLK));  // open: clr
  Register #(.width(32), .trigger("rising"), .Select("low")) tag_5 (
    .D(EX_PC), .en(and_6_out), .Q(tag5), .clk(CLK));  // open: clr
  Register #(.width(32), .trigger("rising"), .Select("low")) tag_6 (
    .D(EX_PC), .en(and_7_out), .Q(tag6), .clk(CLK));  // open: clr
  Register #(.width(32), .trigger("rising"), .Select("low")) tag_7 (
    .D(EX_PC), .en(and_8_out), .Q(tag7), .clk(CLK));  // open: clr
  Register #(.width(32), .trigger("rising"), .Select("low")) tag_8 (
    .D(EX_PC), .en(and_9_out), .Q(tag8), .clk(CLK));  // open: clr
  and and_10 (L1, V1, EX_Branch, comparator_1_eq);
  Comparator #(.width(32), .mode("twosComplement")) comparator_1 (
    .a(EX_PC), .b(tag1), .eq(comparator_1_eq));  // open: gt, lt
  and and_11 (L2, V2, EX_Branch, comparator_2_eq);
  Comparator #(.width(32), .mode("twosComplement")) comparator_2 (
    .a(EX_PC), .b(tag2), .eq(comparator_2_eq));  // open: gt, lt
  and and_12 (L3, V3, EX_Branch, comparator_3_eq);
  Comparator #(.width(32), .mode("twosComplement")) comparator_3 (
    .a(EX_PC), .b(tag3), .eq(comparator_3_eq));  // open: gt, lt
  and and_13 (L4, V4, EX_Branch, comparator_4_eq);
  Comparator #(.width(32), .mode("twosComplement")) comparator_4 (
    .a(EX_PC), .b(tag4), .eq(comparator_4_eq));  // open: gt, lt
  and and_14 (L5, V5, EX_Branch, comparator_5_eq);
  Comparator #(.width(32), .mode("twosComplement")) comparator_5 (
    .a(EX_PC), .b(tag5), .eq(comparator_5_eq));  // open: gt, lt
  and and_15 (L6, V6, EX_Branch, comparator_6_eq);
  Comparator #(.width(32), .mode("twosComplement")) comparator_6 (
    .a(EX_PC), .b(tag6), .eq(comparator_6_eq));  // open: gt, lt
  and and_16 (L7, V7, EX_Branch, comparator_7_eq);
  Comparator #(.width(32), .mode("twosComplement")) comparator_7 (
    .a(EX_PC), .b(tag7), .eq(comparator_7_eq));  // open: gt, lt
  and and_17 (L8, V8, EX_Branch, comparator_8_eq);
  Comparator #(.width(32), .mode("twosComplement")) comparator_8 (
    .a(EX_PC), .b(tag8), .eq(comparator_8_eq));  // open: gt, lt
  Register #(.width(32), .trigger("rising"), .Select("low")) data (
    .D(EX_BranchAddr), .en(and_2_out), .Q(data_q), .clk(CLK));  // open: clr
  Register #(.width(32), .trigger("rising"), .Select("low")) data_2 (
    .D(EX_BranchAddr), .en(and_3_out), .Q(data_2_q), .clk(CLK));  // open: clr
  Register #(.width(32), .trigger("rising"), .Select("low")) data_3 (
    .D(EX_BranchAddr), .en(and_4_out), .Q(data_3_q), .clk(CLK));  // open: clr
  Register #(.width(32), .trigger("rising"), .Select("low")) data_4 (
    .D(EX_BranchAddr), .en(and_5_out), .Q(data_4_q), .clk(CLK));  // open: clr
  Register #(.width(32), .trigger("rising"), .Select("low")) data_5 (
    .D(EX_BranchAddr), .en(and_6_out), .Q(data_5_q), .clk(CLK));  // open: clr
  Register #(.width(32), .trigger("rising"), .Select("low")) data_6 (
    .D(EX_BranchAddr), .en(and_7_out), .Q(data_6_q), .clk(CLK));  // open: clr
  Register #(.width(32), .trigger("rising"), .Select("low")) data_7 (
    .D(EX_BranchAddr), .en(and_8_out), .Q(data_7_q), .clk(CLK));  // open: clr
  Register #(.width(32), .trigger("rising"), .Select("low")) data_8 (
    .D(EX_BranchAddr), .en(and_9_out), .Q(data_8_q), .clk(CLK));  // open: clr
  assign controlled_buffer_1_out = Y1 ? data_q : 32'bz;  // Controlled_Buffer controlled_buffer_1
  assign controlled_buffer_1_out = Y2 ? data_2_q : 32'bz;  // Controlled_Buffer controlled_buffer_2
  assign controlled_buffer_1_out = Y3 ? data_3_q : 32'bz;  // Controlled_Buffer controlled_buffer_3
  assign controlled_buffer_1_out = Y4 ? data_4_q : 32'bz;  // Controlled_Buffer controlled_buffer_4
  assign controlled_buffer_1_out = Y5 ? data_5_q : 32'bz;  // Controlled_Buffer controlled_buffer_5
  assign controlled_buffer_1_out = Y6 ? data_6_q : 32'bz;  // Controlled_Buffer controlled_buffer_6
  assign controlled_buffer_1_out = Y7 ? data_7_q : 32'bz;  // Controlled_Buffer controlled_buffer_7
  assign controlled_buffer_1_out = Y8 ? data_8_q : 32'bz;  // Controlled_Buffer controlled_buffer_8
  // Mips_Probe mips_probe_1: pin names not known; wires that end beside it: IF_IR
  // Mips_Probe mips_probe_2: pin names not known; wires that end beside it: ID_IR
  assign JumpAddr = pc_hit ? controlled_buffer_1_out : 32'bz;  // Controlled_Buffer controlled_buffer_9
  // Mips_Probe mips_probe_3: pin names not known; wires that end beside it: EX_IR
  Comparator #(.width(32), .mode("twosComplement")) comparator_9 (
    .a(PC), .b(tag1), .eq(comparator_9_eq));  // open: gt, lt
  Comparator #(.width(32), .mode("twosComplement")) comparator_10 (
    .a(PC), .b(tag2), .eq(comparator_10_eq));  // open: gt, lt
  Comparator #(.width(32), .mode("twosComplement")) comparator_11 (
    .a(PC), .b(tag3), .eq(comparator_11_eq));  // open: gt, lt
  Comparator #(.width(32), .mode("twosComplement")) comparator_12 (
    .a(PC), .b(tag4), .eq(comparator_12_eq));  // open: gt, lt
  Comparator #(.width(32), .mode("twosComplement")) comparator_13 (
    .a(PC), .b(tag5), .eq(comparator_13_eq));  // open: gt, lt
  Comparator #(.width(32), .mode("twosComplement")) comparator_14 (
    .a(PC), .b(tag6), .eq(comparator_14_eq));  // open: gt, lt
  Comparator #(.width(32), .mode("twosComplement")) comparator_15 (
    .a(PC), .b(tag7), .eq(comparator_15_eq));  // open: gt, lt
  Comparator #(.width(32), .mode("twosComplement")) comparator_16 (
    .a(PC), .b(tag8), .eq(comparator_16_eq));  // open: gt, lt
  // Mips_Probe mips_probe_4: pin names not known; wires that end beside it: M_IR
  and and_18 (Y1, comparator_9_eq, V1);
  and and_19 (Y2, comparator_10_eq, V2);
  and and_20 (Y3, comparator_11_eq, V3);
  and and_21 (Y4, comparator_12_eq, V4);
  and and_22 (Y5, comparator_13_eq, V5);
  and and_23 (Y6, comparator_14_eq, V6);
  and and_24 (Y7, comparator_15_eq, V7);
  and and_25 (Y8, comparator_16_eq, V8);
  // Mips_Probe mips_probe_5: pin names not known; wires that end beside it: WB_IR
  Multiplexer #(.select(1), .width(32), .disabled("Z"), .enable("false")) multiplexer_1 (
    .in0(PC), .in1(EX_PC), .out(tag), .sel(EX_Branch));
  and and_26 (Miss, not_9_out, EX_Branch);
  not not_1 (not_1_out, V1);
  not not_2 (not_2_out, V2);
  not not_3 (not_3_out, V3);
  not not_4 (not_4_out, V4);
  not not_5 (not_5_out, V5);
  not not_6 (not_6_out, V6);
  not not_7 (not_7_out, V7);
  not not_8 (not_8_out, V8);
  not not_9 (not_9_out, hit);
  or or_1 (or_1_out, L1, L2, L3, L4, L5, L6, L7, L8);
  and and_27 (hit, or_1_out, EX_Branch);
  Priority_Encoder #(.select(3), .disabled("Z")) priority_encoder_1 (
    .in0(not_1_out), .in1(not_2_out), .in2(not_3_out), .in3(not_4_out), .in4(not_5_out), .in5(not_6_out),
    .in6(not_7_out), .in7(not_8_out), .out(priority_encoder_1_out), .gs(priority_encoder_1_gs));  // open: en_out, en_in
  Decoder #(.select(3), .tristate("false"), .disabled("Z"), .enable("false")) decoder_1 (
    .out0(X1), .out1(X2), .out2(X3), .out3(X4), .out4(X5), .out5(X6), .out6(X7), .out7(X8),
    .sel(multiplexer_2_out));
  Multiplexer #(.select(1), .width(3), .disabled("Z"), .enable("false")) multiplexer_2 (
    .in0(LRU), .in1(priority_encoder_1_out), .out(multiplexer_2_out), .sel(priority_encoder_1_gs));
  or or_2 (pc_hit, Y1, Y2, Y3, Y4, Y5, Y6, Y7, Y8);
  compare compare_1 (.Y(A2), .X(A1), .Y_num(3'b001), .X_num(3'b000), .MAX(compare_1_max), .Max_num(compare_1_max_num));
  compare compare_2 (.Y(A4), .X(A3), .Y_num(3'b011), .X_num(3'b010), .MAX(compare_2_max), .Max_num(compare_2_max_num));
  compare compare_3 (.Y(A6), .X(A5), .Y_num(3'b101), .X_num(3'b100), .MAX(compare_3_max), .Max_num(compare_3_max_num));
  compare compare_4 (.Y(A8), .X(A7), .Y_num(3'b111), .X_num(3'b110), .MAX(compare_4_max), .Max_num(compare_4_max_num));
  Decoder #(.select(2), .tristate("false"), .disabled("Z"), .enable("false")) decoder_2 (
    .out0(decoder_2_out0), .out1(decoder_2_out1), .out2(decoder_2_out2), .out3(decoder_2_out3),
    .sel(History_Curr));
  compare compare_5 (
    .Y(compare_2_max), .X(compare_1_max), .Y_num(compare_2_max_num), .X_num(compare_1_max_num),
    .MAX(compare_5_max), .Max_num(compare_5_max_num));
  compare compare_6 (
    .Y(compare_4_max), .X(compare_3_max), .Y_num(compare_4_max_num), .X_num(compare_3_max_num),
    .MAX(compare_6_max), .Max_num(compare_6_max_num));
  compare compare_7 (
    .Y(compare_6_max), .X(compare_5_max), .Y_num(compare_6_max_num), .X_num(compare_5_max_num), .Max_num(LRU));  // open: MAX
  and and_28 (and_28_out, decoder_2_out0, EX_BranchTaken);
  and and_29 (and_29_out, decoder_2_out0, ~EX_BranchTaken);  // AND_Gate
  and and_30 (and_30_out, decoder_2_out1, EX_BranchTaken);
  and and_31 (and_31_out, decoder_2_out1, ~EX_BranchTaken);  // AND_Gate
  and and_32 (and_32_out, decoder_2_out2, EX_BranchTaken);
  and and_33 (and_33_out, decoder_2_out2, ~EX_BranchTaken);  // AND_Gate
  and and_34 (and_34_out, decoder_2_out3, EX_BranchTaken);
  and and_35 (and_35_out, decoder_2_out3, ~EX_BranchTaken);  // AND_Gate
  Counter #(.width(16), .max('hffff), .ongoal("wrap"), .trigger("rising"), .behavior("new")) counter_1 (
    .Q(A1), .clk(CLK), .clr(L1));  // open: load, D, count, carry, preset, down
  Counter #(.width(16), .max('hffff), .ongoal("wrap"), .trigger("rising"), .behavior("new")) counter_2 (
    .Q(A2), .clk(CLK), .clr(L2));  // open: load, D, count, carry, preset, down
  Counter #(.width(16), .max('hffff), .ongoal("wrap"), .trigger("rising"), .behavior("new")) counter_3 (
    .Q(A3), .clk(CLK), .clr(L3));  // open: load, D, count, carry, preset, down
  Counter #(.width(16), .max('hffff), .ongoal("wrap"), .trigger("rising"), .behavior("new")) counter_4 (
    .Q(A4), .clk(CLK), .clr(L4));  // open: load, D, count, carry, preset, down
  Counter #(.width(16), .max('hffff), .ongoal("wrap"), .trigger("rising"), .behavior("new")) counter_5 (
    .Q(A5), .clk(CLK), .clr(L5));  // open: load, D, count, carry, preset, down
  Counter #(.width(16), .max('hffff), .ongoal("wrap"), .trigger("rising"), .behavior("new")) counter_6 (
    .Q(A6), .clk(CLK), .clr(L6));  // open: load, D, count, carry, preset, down
  Counter #(.width(16), .max('hffff), .ongoal("wrap"), .trigger("rising"), .behavior("new")) counter_7 (
    .Q(A7), .clk(CLK), .clr(L7));  // open: load, D, count, carry, preset, down
  Counter #(.width(16), .max('hffff), .ongoal("wrap"), .trigger("rising"), .behavior("new")) counter_8 (
    .Q(A8), .clk(CLK), .clr(L8));  // open: load, D, count, carry, preset, down
  assign controlled_buffer_10_out = and_28_out ? 2'b01 : 2'bz;  // Controlled_Buffer controlled_buffer_10
  assign controlled_buffer_10_out = and_29_out ? 2'b00 : 2'bz;  // Controlled_Buffer controlled_buffer_11
  assign controlled_buffer_10_out = and_30_out ? 2'b10 : 2'bz;  // Controlled_Buffer controlled_buffer_12
  assign controlled_buffer_10_out = and_31_out ? 2'b00 : 2'bz;  // Controlled_Buffer controlled_buffer_13
  assign controlled_buffer_10_out = and_32_out ? 2'b10 : 2'bz;  // Controlled_Buffer controlled_buffer_14
  assign controlled_buffer_10_out = and_33_out ? 2'b11 : 2'bz;  // Controlled_Buffer controlled_buffer_15
  assign controlled_buffer_10_out = and_34_out ? 2'b10 : 2'bz;  // Controlled_Buffer controlled_buffer_16
  assign controlled_buffer_10_out = and_35_out ? 2'b00 : 2'bz;  // Controlled_Buffer controlled_buffer_17
  Multiplexer #(.select(1), .width(2), .disabled("Z"), .enable("false")) multiplexer_3 (
    .in0(2'b11), .in1(controlled_buffer_10_out), .out(History_Update), .sel(hit));
  and and_36 (and_36_out, Miss, X1);
  and and_37 (and_37_out, Miss, X2);
  and and_38 (and_38_out, Miss, X3);
  and and_39 (and_39_out, Miss, X4);
  and and_40 (and_40_out, Miss, X5);
  and and_41 (and_41_out, Miss, X6);
  and and_42 (and_42_out, Miss, X7);
  and and_43 (and_43_out, Miss, X8);
  or or_3 (or_3_out, and_36_out, L1);
  or or_4 (or_4_out, and_37_out, L2);
  or or_5 (or_5_out, and_38_out, L3);
  or or_6 (or_6_out, and_39_out, L4);
  or or_7 (or_7_out, and_40_out, L5);
  or or_8 (or_8_out, and_41_out, L6);
  or or_9 (or_9_out, and_42_out, L7);
  or or_10 (or_10_out, and_43_out, L8);
  Register #(.width(2), .trigger("rising"), .Select("low")) History (
    .D(History_Update), .en(or_3_out), .Q(History_q), .clk(CLK));  // open: clr
  Register #(.width(2), .trigger("rising"), .Select("low")) History_2 (
    .D(History_Update), .en(or_4_out), .Q(History_2_q), .clk(CLK));  // open: clr
  Register #(.width(2), .trigger("rising"), .Select("low")) History_3 (
    .D(History_Update), .en(or_5_out), .Q(History_3_q), .clk(CLK));  // open: clr
  Register #(.width(2), .trigger("rising"), .Select("low")) History_4 (
    .D(History_Update), .en(or_6_out), .Q(History_4_q), .clk(CLK));  // open: clr
  Register #(.width(2), .trigger("rising"), .Select("low")) History_5 (
    .D(History_Update), .en(or_7_out), .Q(History_5_q), .clk(CLK));  // open: clr
  Register #(.width(2), .trigger("rising"), .Select("low")) History_6 (
    .D(History_Update), .en(or_8_out), .Q(History_6_q), .clk(CLK));  // open: clr
  Register #(.width(2), .trigger("rising"), .Select("low")) History_7 (
    .D(History_Update), .en(or_9_out), .Q(History_7_q), .clk(CLK));  // open: clr
  Register #(.width(2), .trigger("rising"), .Select("low")) History_8 (
    .D(History_Update), .en(or_10_out), .Q(History_8_q), .clk(CLK));  // open: clr
  assign controlled_buffer_18_out = Y1 ? History_q : 2'bz;  // Controlled_Buffer controlled_buffer_18
  assign controlled_buffer_18_out = Y2 ? History_2_q : 2'bz;  // Controlled_Buffer controlled_buffer_19
  assign controlled_buffer_18_out = Y3 ? History_3_q : 2'bz;  // Controlled_Buffer controlled_buffer_20
  assign controlled_buffer_18_out = Y4 ? History_4_q : 2'bz;  // Controlled_Buffer controlled_buffer_21
  assign controlled_buffer_18_out = Y5 ? History_5_q : 2'bz;  // Controlled_Buffer controlled_buffer_22
  assign controlled_buffer_18_out = Y6 ? History_6_q : 2'bz;  // Controlled_Buffer controlled_buffer_23
  assign controlled_buffer_18_out = Y7 ? History_7_q : 2'bz;  // Controlled_Buffer controlled_buffer_24
  assign controlled_buffer_18_out = Y8 ? History_8_q : 2'bz;  // Controlled_Buffer controlled_buffer_25
  assign controlled_buffer_26_out = L1 ? History_q : 2'bz;  // Controlled_Buffer controlled_buffer_26
  assign controlled_buffer_26_out = L2 ? History_2_q : 2'bz;  // Controlled_Buffer controlled_buffer_27
  assign controlled_buffer_26_out = L3 ? History_3_q : 2'bz;  // Controlled_Buffer controlled_buffer_28
  assign controlled_buffer_26_out = L4 ? History_4_q : 2'bz;  // Controlled_Buffer controlled_buffer_29
  assign controlled_buffer_26_out = L5 ? History_5_q : 2'bz;  // Controlled_Buffer controlled_buffer_30
  assign controlled_buffer_26_out = L6 ? History_6_q : 2'bz;  // Controlled_Buffer controlled_buffer_31
  assign controlled_buffer_26_out = L7 ? History_7_q : 2'bz;  // Controlled_Buffer controlled_buffer_32
  assign controlled_buffer_26_out = L8 ? History_8_q : 2'bz;  // Controlled_Buffer controlled_buffer_33
  assign History_Curr = hit ? controlled_buffer_26_out : 2'bz;  // Controlled_Buffer controlled_buffer_34
  assign controlled_buffer_35_out = pc_hit ? controlled_buffer_18_out : 2'bz;  // Controlled_Buffer controlled_buffer_35
  Multiplexer #(.select(2), .width(1), .disabled("Z"), .enable("false")) multiplexer_4 (
    .in0(1'b0), .in1(1'b0), .in2(1'b1), .in3(1'b1), .out(multiplexer_4_out), .sel(controlled_buffer_35_out));
  Multiplexer #(.select(1), .width(1), .disabled("Z"), .enable("false")) multiplexer_5 (
    .in0(1'b0), .in1(multiplexer_4_out), .out(PredictJump), .sel(pc_hit));

  // Other names for the same wires on the sheet: MEM_IR[31:0] = M_IR
endmodule

module compare (
  input  [15:0] Y,
  input  [15:0] X,
  input  [2:0] Y_num,
  input  [2:0] X_num,
  output [15:0] MAX,
  output [2:0] Max_num
);

  wire comparator_1_eq, comparator_1_gt, or_1_out;

  Multiplexer #(.select(1), .width(16), .disabled("Z"), .enable("false")) multiplexer_1 (
    .in0(Y), .in1(X), .out(MAX), .sel(or_1_out));
  Comparator #(.width(16), .mode("unsigned")) comparator_1 (
    .a(X), .b(Y), .gt(comparator_1_gt), .eq(comparator_1_eq));  // open: lt
  or or_1 (or_1_out, comparator_1_gt, comparator_1_eq);
  Multiplexer #(.select(1), .width(3), .disabled("Z"), .enable("false")) multiplexer_2 (
    .in0(Y_num), .in1(X_num), .out(Max_num), .sel(or_1_out));

  // Notes on the sheet:
  //   输出两个输入中的较大值，并输出较大值的3位编号
endmodule

module LCDtest (
  input  Reset,
  input  CLK,
  input  EN
);

  wire lcd_video_1_p4, lcd_video_1_p6, lcd_video_1_p8;

  // LCD_Video lcd_video_1: pin names not known; wires that end beside it: Reset, CLK, EN, lcd_video_1_p4, lcd_video_1_p4, lcd_video_1_p6, lcd_video_1_p6, lcd_video_1_p8, lcd_video_1_p8
endmodule

module \团队中断逻辑  (
  input  CLK,
  input  IR1,
  input  IR2,
  input  [31:0] IR,
  input  [31:0] \入口1 ,
  input  [31:0] \入口2 ,
  output LIGHT1,
  output LIGHT2
);

  wire and_1_out, and_2_out, and_4_out, CLR1, CLR2, d_ff_1_q, d_ff_2_q, ERET, IE, INT, INT1, INT2, or_2_out,
       or_3_out, or_4_out, or_6_out;
  wire [1:0] priority_encoder_1_out, register_1_q;
  wire [31:0] EPCout, ret, \中断入口地址 ;

  or or_1 (LIGHT1, INT1, d_ff_1_q);
  D_Flip_Flop #(.trigger("rising"), .Pre_Clr_Positions("LEGACY"), .NegatePresetClear("false"), .enable("true"), .NewFFLayout("false")) d_ff_1 (
    .clk(IR1), .D(1'b1), .Q(d_ff_1_q), .reset(INT1));  // open: Qn, preset, en
  or or_2 (or_2_out, d_ff_1_q, INT1);
  or or_3 (or_3_out, INT1, INT2);
  or or_4 (or_4_out, INT1, INT2);
  and and_1 (and_1_out, or_2_out, ~CLR1);  // AND_Gate
  and and_2 (and_2_out, or_3_out, ~ERET);  // AND_Gate
  and and_3 (INT, ~IE, or_4_out);  // AND_Gate
  D_Flip_Flop #(.trigger("rising"), .Pre_Clr_Positions("LEGACY"), .NegatePresetClear("false"), .enable("true"), .NewFFLayout("false")) u_IR1 (
    .clk(CLK), .D(and_1_out), .Q(INT1));  // open: Qn, preset, en, reset
  Register #(.width(1), .trigger("rising"), .Select("low")) u_IE (.D(and_2_out), .Q(IE), .clk(CLK));  // open: en, clr
  or or_5 (LIGHT2, INT2, d_ff_2_q);
  D_Flip_Flop #(.trigger("rising"), .Pre_Clr_Positions("LEGACY"), .NegatePresetClear("false"), .enable("true"), .NewFFLayout("false")) d_ff_2 (
    .clk(IR2), .D(1'b1), .Q(d_ff_2_q), .reset(INT2));  // open: Qn, preset, en
  or or_6 (or_6_out, d_ff_2_q, INT2);
  Priority_Encoder #(.select(2), .disabled("Z")) priority_encoder_1 (
    .in0(INT1), .in1(INT2), .out(priority_encoder_1_out));  // open: in2, in3, gs, en_out, en_in
  Register #(.width(32), .trigger("rising"), .Select("low")) EPC (
    .D(ret), .en(INT), .Q(EPCout), .clk(CLK));  // open: clr
  and and_4 (and_4_out, or_6_out, ~CLR2);  // AND_Gate
  // Probe on priority_encoder_1_out
  Multiplexer #(.select(2), .width(32), .disabled("Z"), .enable("false")) multiplexer_1 (
    .in0(\入口1 ), .in1(\入口2 ), .out(\中断入口地址 ), .sel(priority_encoder_1_out));  // open: in2, in3
  D_Flip_Flop #(.trigger("rising"), .Pre_Clr_Positions("LEGACY"), .NegatePresetClear("false"), .enable("true"), .NewFFLayout("false")) IR1_2 (
    .clk(CLK), .D(and_4_out), .Q(INT2));  // open: Qn, preset, en, reset
  Register #(.width(2), .trigger("rising"), .Select("low")) register_1 (
    .D(priority_encoder_1_out), .en(INT), .Q(register_1_q), .clk(CLK));  // open: clr
  Demultiplexer #(.select(2), .width(1), .tristate("false"), .disabled("Z"), .enable("false")) demultiplexer_1 (
    .out0(CLR1), .out1(CLR2), .in(ERET), .sel(register_1_q));  // open: out2, out3
  Comparator #(.width(32), .mode("twosComplement")) comparator_1 (.a(IR), .b(32'h42000018), .eq(ERET));  // open: gt, lt

  // Other names for the same wires on the sheet: entrence1[31:0] = \入口1 ; entrence2[31:0] = \入口2 ; W1 = LIGHT1;
  //   W2 = LIGHT2

  // Notes on the sheet:
  //   中断信号采样参考电路
  //   Reset 
  //   中断信号采样参考电路
  //   Reset 
endmodule

module \显示勾  (
  input  in_1,
  input  in_2,
  input  in_3,
  input  [6:0] in_4,
  input  [6:0] in_5,
  input  [15:0] in_6
);

  // LCD_Video lcd_video_1: pin names not known; wires that end beside it: in_1, in_2, in_3, in_4, in_5, in_6
endmodule
