// Logisim project cpu24团队任务.circ as structural Verilog: 28 circuits, main circuit ◇单周期MIPS
module \单周期MIPS  (
  input  IR1,
  input  IR2,
  input  IR3,
  output RegWrite,
  output MemWrite,
  output [31:0] PC,
  output [31:0] IR,
  output [31:0] RDin,
  output [31:0] MDin,
  output [31:0] LedData
);

  wire and_3_out, and_4_out, and_5_out, CLK, clock_2_out, comparator_1_eq, comparator_2_eq, comparator_2_lt,
       d_ff_1_q, Go, halt, IR1_t, IR2_t, IR3_t, IRA, IRB, IRC, led_en, mips_alu_1_equal, nand_1_out,
       not_1_out, not_2_out, or_3_out, or_5_out, SB, SignedExt, SRAV, syscall, W1, W2, W3,
       \单周期硬布线控制器_1_alu_src , \单周期硬布线控制器_1_beq , \单周期硬布线控制器_1_bgtz , \单周期硬布线控制器_1_bne , \单周期硬布线控制器_1_jal ,
       \单周期硬布线控制器_1_jmp , \单周期硬布线控制器_1_jr , \单周期硬布线控制器_1_memtoreg , \单周期硬布线控制器_1_regdst ;
  wire [3:0] multiplexer_10_out, \单周期硬布线控制器_1_alu_op ;
  wire [4:0] multiplexer_4_out, multiplexer_6_out, multiplexer_7_out, multiplexer_8_out, multiplexer_11_out,
       multiplexer_15_out;
  wire [12:0] CNT_num;
  wire [15:0] \总周期数 ;
  wire [31:0] adder_2_out, Address, and_6_out, bit_extender_1_out, bit_extender_2_out, MDinByte, MDout,
       multiplexer_1_out, multiplexer_2_out, multiplexer_3_out, multiplexer_5_out, multiplexer_9_out,
       multiplexer_12_out, multiplexer_13_out, multiplexer_16_out, PC_4, R_rs, shifter_1_out, shifter_2_out;

  Clock #(.highDuration(1), .lowDuration(1)) clock_1 ();  // open: out
  Button _1 (.out(IRA));
  Button _2 (.out(IRB));
  Button _3 (.out(IRC));
  Button \u_继续运行  (.out(Go));
  LED #(.active("true")) led_1 (.in(W1));
  LED #(.active("true")) led_2 (.in(W2));
  LED #(.active("true")) led_3 (.in(W3));
  Hex_Digit_Display hex_digit_display_1 (.value(LedData[31:28]));  // open: dp
  Hex_Digit_Display hex_digit_display_2 (.value(LedData[23:20]));  // open: dp
  Hex_Digit_Display hex_digit_display_3 (.value(LedData[27:24]));  // open: dp
  Hex_Digit_Display hex_digit_display_4 (.value(LedData[15:12]));  // open: dp
  Hex_Digit_Display hex_digit_display_5 (.value(LedData[19:16]));  // open: dp
  Hex_Digit_Display hex_digit_display_6 (.value(LedData[7:4]));  // open: dp
  Hex_Digit_Display hex_digit_display_7 (.value(LedData[11:8]));  // open: dp
  // Probe on \总周期数 
  Hex_Digit_Display hex_digit_display_8 (.value(LedData[3:0]));  // open: dp
  Multiplexer #(.select(1), .width(32), .disabled("Z"), .enable("false")) multiplexer_1 (
    .in0(PC_4), .in1(adder_2_out), .out(multiplexer_1_out), .sel(or_5_out));
  or or_1 (IR1_t, IR1, IRA);
  Multiplexer #(.select(1), .width(32), .disabled("Z"), .enable("false")) multiplexer_2 (
    .in0(multiplexer_1_out), .in1({PC_4[31:28], IR[25:0], 2'b00}), .out(multiplexer_2_out),
    .sel(\单周期硬布线控制器_1_jmp ));
  or or_2 (IR2_t, IR2, IRB);
  Multiplexer #(.select(1), .width(32), .disabled("Z"), .enable("false")) multiplexer_3 (
    .in0(multiplexer_2_out), .in1(R_rs), .out(multiplexer_3_out), .sel(\单周期硬布线控制器_1_jr ));
  or or_3 (or_3_out, ~halt, Go);  // OR_Gate
  or or_4 (IR3_t, IR3, IRC);
  Register #(.width(32), .trigger("rising"), .Select("low")) u_PC (
    .D(multiplexer_3_out), .en(or_3_out), .Q(PC), .clk(CLK));  // open: clr
  ROM #(.addrWidth(10), .dataWidth(32), .Select("high")) rom_1 (.addr(PC[11:2]), .data(IR));
  Adder #(.width(32)) adder_1 (.a(PC), .b(32'h4), .out(PC_4));  // open: cin, cout
  Comparator #(.width(32), .mode("twosComplement")) comparator_1 (
    .a(R_rs), .b(32'h22), .eq(comparator_1_eq));  // open: gt, lt
  not not_1 (not_1_out, halt);
  D_Flip_Flop #(.trigger("high"), .Pre_Clr_Positions("LEGACY"), .NegatePresetClear("false"), .enable("true"), .NewFFLayout("false")) d_ff_1 (.Q(d_ff_1_q));  // open: clk, D, Qn, preset, en, reset
  // Probe on 13'hc
  // Mips_Probe mips_probe_1: pin names not known; wires that end beside it: IR
  Counter #(.width(16), .max('hffff), .ongoal("wrap"), .trigger("rising"), .behavior("new")) counter_1 (
    .count(not_1_out), .Q(\总周期数 ), .clk(CLK));  // open: load, D, carry, clr, preset, down
  Comparator #(.width(13), .mode("twosComplement")) comparator_2 (
    .a(CNT_num), .b(13'hc), .eq(comparator_2_eq), .lt(comparator_2_lt));  // open: gt
  Clock #(.highDuration(1), .lowDuration(1)) clock_2 (.out(clock_2_out));
  Counter #(.width(13), .max('h1fff), .ongoal("stay"), .trigger("rising"), .behavior("old")) counter_2 (
    .count(comparator_2_lt), .Q(CNT_num), .clk(clock_2_out));  // open: load, D, carry, clr, preset
  and and_1 (led_en, syscall, comparator_1_eq);
  and and_2 (halt, syscall, ~comparator_1_eq);  // AND_Gate
  nand nand_1 (nand_1_out, d_ff_1_q, comparator_2_eq);
  assign bit_extender_1_out = {{16{1'b0}}, IR[15:0]};  // Bit_Extender bit_extender_1
  assign bit_extender_2_out = {{16{IR[15]}}, IR[15:0]};  // Bit_Extender bit_extender_2
  assign CLK = nand_1_out ? clock_2_out : 1'bz;  // Controlled_Buffer controlled_buffer_1
  Pull_Resistor #(.pull(1)) pull_resistor_1 (.node(CLK));
  \单周期硬布线控制器  \u_单周期硬布线控制器_1  (
    .Func(IR[5:0]), .OP(IR[31:26]), .ALU_OP(\单周期硬布线控制器_1_alu_op ), .MemToReg(\单周期硬布线控制器_1_memtoreg ),
    .MemWrite(MemWrite), .ALU_SRC(\单周期硬布线控制器_1_alu_src ), .RegWrite(RegWrite), .SysCALL(syscall),
    .SignedExt(SignedExt), .RegDst(\单周期硬布线控制器_1_regdst ), .JR(\单周期硬布线控制器_1_jr ), .JMP(\单周期硬布线控制器_1_jmp ),
    .Beq(\单周期硬布线控制器_1_beq ), .JAL(\单周期硬布线控制器_1_jal ), .Bne(\单周期硬布线控制器_1_bne ), .BGTZ(\单周期硬布线控制器_1_bgtz ),
    .SRAV(SRAV), .SB(SB));
  Multiplexer #(.select(1), .width(5), .disabled("Z"), .enable("false")) multiplexer_4 (
    .in0(IR[20:16]), .in1(IR[15:11]), .out(multiplexer_4_out), .sel(\单周期硬布线控制器_1_regdst ));
  Multiplexer #(.select(1), .width(32), .disabled("Z"), .enable("false")) multiplexer_5 (
    .in0(bit_extender_1_out), .in1(bit_extender_2_out), .out(multiplexer_5_out), .sel(SignedExt));
  Register #(.width(32), .trigger("rising"), .Select("low")) register_1 (
    .D(MDin), .en(led_en), .Q(LedData), .clk(CLK));  // open: clr
  Multiplexer #(.select(1), .width(5), .disabled("Z"), .enable("false")) multiplexer_6 (
    .in0(multiplexer_4_out), .in1({5{1'b1}}), .out(multiplexer_6_out), .sel(\单周期硬布线控制器_1_jal ));
  Multiplexer #(.select(1), .width(5), .disabled("Z"), .enable("false")) multiplexer_7 (
    .in0(IR[25:21]), .in1(5'b00010), .out(multiplexer_7_out), .sel(syscall));
  Multiplexer #(.select(1), .width(5), .disabled("Z"), .enable("false")) multiplexer_8 (
    .in0(IR[20:16]), .in1(5'b00100), .out(multiplexer_8_out), .sel(syscall));
  MIPS_Regifile mips_regifile_1 (
    .Din(RDin), .Clk(CLK), .R1(R_rs), .R2(MDin), .WE(RegWrite), .W_num(multiplexer_6_out),
    .R1_num(multiplexer_7_out), .R2_num(multiplexer_8_out));
  Multiplexer #(.select(1), .width(32), .disabled("Z"), .enable("false")) multiplexer_9 (
    .in0(MDin), .in1(multiplexer_5_out), .out(multiplexer_9_out), .sel(\单周期硬布线控制器_1_alu_src ));
  Multiplexer #(.select(1), .width(4), .disabled("Z"), .enable("false")) multiplexer_10 (
    .in0(\单周期硬布线控制器_1_alu_op ), .in1(4'b0101), .out(multiplexer_10_out), .sel(SB));
  Shifter #(.width(32), .shift("ll")) shifter_1 (.in(bit_extender_2_out), .\dist (5'b00010), .out(shifter_1_out));
  not not_2 (not_2_out, mips_alu_1_equal);
  and and_3 (and_3_out, \单周期硬布线控制器_1_beq , mips_alu_1_equal);
  MIPS_ALU mips_alu_1 (
    .X(R_rs), .Y(multiplexer_9_out), .AluOP(multiplexer_10_out), .Equal(mips_alu_1_equal), .Result(Address),
    .shamt(multiplexer_11_out));  // open: Result_2
  Multiplexer #(.select(1), .width(5), .disabled("Z"), .enable("false")) multiplexer_11 (
    .in0(IR[10:6]), .in1(R_rs[4:0]), .out(multiplexer_11_out), .sel(SRAV));
  Adder #(.width(32)) adder_2 (.a(shifter_1_out), .b(PC_4), .out(adder_2_out));  // open: cin, cout
  or or_5 (or_5_out, and_4_out, and_5_out, and_3_out);
  and and_4 (and_4_out, \单周期硬布线控制器_1_bne , not_2_out);
  and and_5 (and_5_out, \单周期硬布线控制器_1_bgtz , ~Address[0]);  // AND_Gate
  Multiplexer #(.select(1), .width(32), .disabled("Z"), .enable("false")) multiplexer_12 (
    .in0(MDin), .in1(MDinByte), .out(multiplexer_12_out), .sel(SB));
  Multiplexer #(.select(1), .width(32), .disabled("Z"), .enable("false")) multiplexer_13 (
    .in0(Address), .in1(MDout), .out(multiplexer_13_out), .sel(\单周期硬布线控制器_1_memtoreg ));
  RAM #(.addrWidth(10), .dataWidth(32), .bus("separate"), .Select("high")) ram_1 (
    .addr(Address[11:2]), .din(multiplexer_12_out), .data(MDout), .str(MemWrite), .clk(CLK));  // open: sel, ld, clr
  Multiplexer #(.select(1), .width(32), .disabled("Z"), .enable("false")) multiplexer_14 (
    .in0(multiplexer_13_out), .in1(PC_4), .out(RDin), .sel(\单周期硬布线控制器_1_jal ));
  // Probe on MDin[14:8]
  // LCD_Video lcd_video_1: pin names not known; wires that end beside it: CLK, led_en, MDin[14:8], MDin[6:0], {16{1'b1}}
  // Probe on MDin[6:0]
  Multiplexer #(.select(2), .width(5), .disabled("Z"), .enable("false")) multiplexer_15 (
    .in0({5{1'b0}}), .in1(5'b01000), .in2(5'b10000), .in3(5'b11000), .out(multiplexer_15_out),
    .sel(Address[1:0]));
  Multiplexer #(.select(2), .width(32), .disabled("Z"), .enable("false")) multiplexer_16 (
    .in0(32'hff), .in1(32'hff00), .in2(32'hff0000), .in3(32'hff000000), .out(multiplexer_16_out),
    .sel(Address[1:0]));
  Shifter #(.width(32), .shift("ll")) shifter_2 (.in(MDin), .\dist (multiplexer_15_out), .out(shifter_2_out));
  assign MDinByte = shifter_2_out | and_6_out;  // OR_Gate or_6, 32 bits wide
  assign and_6_out = MDout & ~multiplexer_16_out;  // AND_Gate and_6, 32 bits wide

  // Other names for the same wires on the sheet: 指令字[31:0] = IR; R_v0[31:0] = R_rs

  // Notes on the sheet:
  //   中断源
  //   中断等待指示
  //   总复位信号应将除ROM以外所有存储组件全部清零
  //   数码管输出
  //   数码管输出应该用寄存器锁存，否则显示数据只能一闪而过
  //   指令存储器
  //   contents of rom_1 (hex, n*v repeats v):
  //   22100000 22310032 22520000 102200 922020 20020022 c 112200 922020 20020022 c 22100001 20010001
  //   2218822 22520001 1611fff3 20020000 c
  //   为方便自动评测，需要输出PC，IR，寄存器堆写如数据RDin
  //   控制位
  //   暂停节拍，不能为0
  //   OP
  //   Func
  //   rs
  //   指令字
  //   rt
  //   rd
  //   RAM写使能MemWrite、RAM写入数据MDin等信号
  //   戳工具置1进入计数暂停模式，ctrl+k时钟自动运行到对应节拍暂停
  //   ctrl+k关闭时钟连续运行，将控制位置零，进入单步调试模式调试
  //   用这个时钟源需要去掉电路中的其他时钟源
  //   JMP
  //   JR
  //   OP
  //   Func
  //   Syscall
  //   可计数暂停的时钟源
  //   Beq
  //   BGTZ
  //   Bne
  //   MemToReg
  //   MemWrite
  //   AluOP
  //   AluSrcB
  //   RegWrite
  //   JAL
  //   RegDst
endmodule

// 单周期硬布线控制器
module \单周期硬布线控制器  (
  input  [5:0] OP,
  input  [5:0] Func,
  output [3:0] ALU_OP,
  output MemToReg,
  output MemWrite,
  output ALU_SRC,
  output RegWrite,
  output SysCALL,
  output SignedExt,
  output RegDst,
  output Beq,
  output Bne,
  output JR,
  output JMP,
  output JAL,
  output BGTZ,
  output SRAV,
  output SB
);

  \运算控制器自动生成  \u_运算控制器自动生成_1  (
    .OP0(OP[0]), .OP1(OP[1]), .OP2(OP[2]), .OP3(OP[3]), .OP4(OP[4]), .OP5(OP[5]), .F0(Func[0]), .F1(Func[1]),
    .F2(Func[2]), .F3(Func[3]), .F4(Func[4]), .F5(Func[5]), .S0(ALU_OP[0]), .S1(ALU_OP[1]), .S2(ALU_OP[2]),
    .S3(ALU_OP[3]));
  \控制信号自动生成  \u_控制信号自动生成_1  (
    .OP0(OP[0]), .MemToReg(MemToReg), .OP1(OP[1]), .OP2(OP[2]), .OP3(OP[3]), .OP4(OP[4]),
    .MemWrite(MemWrite), .OP5(OP[5]), .F0(Func[0]), .F1(Func[1]), .F2(Func[2]), .F3(Func[3]), .F4(Func[4]),
    .ALU_SRC(ALU_SRC), .F5(Func[5]), .RegWrite(RegWrite), .SysCALL(SysCALL), .SignedExt(SignedExt),
    .RegDst(RegDst), .BEQ(Beq), .BNE(Bne), .JR(JR), .JUMP(JMP), .JAL(JAL), .BGTZ(BGTZ), .SRAV(SRAV), .SB(SB));

  // Other names for the same wires on the sheet: OP_CODE[5:0] = OP

  // Notes on the sheet:
  //   运算器控制器，根据指令生成运算器功能选择信号
  //   控制信号生成，产生数据通路需要的其他控制信号
endmodule

// 运算器控制器
module \运算控制器自动生成  (
  input  OP0,
  input  OP1,
  input  OP2,
  input  OP3,
  input  OP4,
  input  OP5,
  input  F0,
  input  F1,
  input  F2,
  input  F3,
  input  F4,
  input  F5,
  output S0,
  output S1,
  output S2,
  output S3
);

  wire and_1_out, and_2_out, and_3_out, and_4_out, and_5_out, and_6_out, and_7_out, and_8_out, and_9_out,
       and_10_out, and_11_out, and_12_out, and_13_out, and_14_out, and_15_out, and_16_out, and_17_out,
       and_18_out, and_19_out, and_20_out, and_21_out, and_22_out, and_23_out, and_24_out, and_25_out,
       and_26_out, and_27_out, and_28_out, and_29_out, and_30_out, and_31_out, and_32_out, and_33_out,
       and_34_out, and_35_out, and_36_out, and_37_out, and_38_out, and_39_out, and_40_out, and_41_out,
       and_42_out, not_1_out, not_2_out, not_3_out, not_4_out, not_5_out, not_6_out, not_7_out, not_8_out,
       not_9_out, not_10_out, not_11_out, not_12_out, not_13_out, not_14_out, not_15_out, not_16_out,
       not_17_out, not_18_out, not_19_out, not_20_out, not_21_out, not_22_out, not_23_out, not_24_out,
       not_25_out, not_26_out, not_27_out, not_28_out, not_29_out, not_30_out, not_31_out, not_32_out,
       not_33_out, not_34_out, not_35_out, not_36_out, not_37_out, not_38_out, not_39_out, not_40_out,
       not_41_out, not_42_out, not_43_out, not_44_out, not_45_out, not_46_out, not_47_out, not_48_out,
       not_49_out, not_50_out, not_51_out, not_52_out, not_53_out, not_54_out, not_55_out, not_56_out,
       not_57_out, not_58_out, not_59_out, not_60_out, not_61_out, not_62_out, not_63_out, not_64_out,
       not_65_out, not_66_out, not_67_out, not_68_out, not_69_out, not_70_out, not_71_out, not_72_out,
       not_73_out, not_74_out, not_75_out, not_76_out, not_77_out, not_78_out, not_79_out, not_80_out,
       not_81_out, not_82_out, not_83_out, not_84_out, not_85_out, not_86_out, not_87_out, not_88_out,
       not_89_out, not_90_out, not_91_out, not_92_out, not_93_out, not_94_out, not_95_out, not_96_out,
       not_97_out, not_98_out, not_99_out, not_100_out, not_101_out, not_102_out, not_103_out, not_104_out,
       not_105_out, not_106_out, not_107_out, not_108_out, not_109_out, not_110_out, not_111_out,
       not_112_out, not_113_out, not_114_out, not_115_out, not_116_out, not_117_out, not_118_out,
       not_119_out, not_120_out, not_121_out, not_122_out, not_123_out, not_124_out, not_125_out,
       not_126_out, not_127_out, not_128_out, not_129_out, not_130_out, not_131_out, not_132_out,
       not_133_out, not_134_out, not_135_out, not_136_out, not_137_out, not_138_out, not_139_out,
       not_140_out, not_141_out, not_142_out, not_143_out, not_144_out, not_145_out, not_146_out,
       not_147_out, not_148_out, not_149_out, not_150_out, not_151_out, not_152_out, not_153_out,
       not_154_out, not_155_out, not_156_out, not_157_out, not_158_out, not_159_out, not_160_out,
       not_161_out, not_162_out, not_163_out, not_164_out, not_165_out, not_166_out, not_167_out,
       not_168_out, not_169_out, not_170_out, not_171_out, not_172_out, not_173_out, not_174_out,
       not_175_out, not_176_out, not_177_out, not_178_out, not_179_out, not_180_out, not_181_out,
       not_182_out, not_183_out, not_184_out, not_185_out, not_186_out, not_187_out, not_188_out,
       not_189_out, not_190_out, not_191_out, not_192_out, not_193_out, not_194_out, not_195_out,
       not_196_out, not_197_out, not_198_out, not_199_out, not_200_out, not_201_out, not_202_out,
       not_203_out, not_204_out, not_205_out, not_206_out, not_207_out, not_208_out, not_209_out,
       not_210_out, not_211_out, not_212_out, not_213_out, not_214_out, not_215_out, not_216_out,
       not_217_out, not_218_out, not_219_out, not_220_out, not_221_out, not_222_out, not_223_out,
       not_224_out, not_225_out, not_226_out, not_227_out, not_228_out, not_229_out, not_230_out,
       not_231_out, not_232_out, not_233_out, not_234_out, not_235_out, not_236_out, not_237_out,
       not_238_out, not_239_out, not_240_out, not_241_out, not_242_out, not_243_out, not_244_out,
       not_245_out, not_246_out, not_247_out, not_248_out, not_249_out, not_250_out, not_251_out,
       not_252_out, not_253_out, not_254_out, not_255_out, not_256_out, not_257_out, not_258_out,
       not_259_out, not_260_out, not_261_out, not_262_out, not_263_out, not_264_out, not_265_out,
       not_266_out, not_267_out, not_268_out;

  not not_1 (not_1_out, OP5);
  not not_2 (not_2_out, OP4);
  not not_3 (not_3_out, OP3);
  not not_4 (not_4_out, OP2);
  not not_5 (not_5_out, OP1);
  not not_6 (not_6_out, OP0);
  not not_7 (not_7_out, F5);
  not not_8 (not_8_out, F4);
  not not_9 (not_9_out, F3);
  not not_10 (not_10_out, F2);
  not not_11 (not_11_out, OP5);
  not not_12 (not_12_out, OP4);
  not not_13 (not_13_out, OP3);
  not not_14 (not_14_out, OP2);
  not not_15 (not_15_out, OP1);
  not not_16 (not_16_out, OP0);
  not not_17 (not_17_out, F4);
  not not_18 (not_18_out, F3);
  not not_19 (not_19_out, F2);
  not not_20 (not_20_out, F1);
  not not_21 (not_21_out, F0);
  not not_22 (not_22_out, OP5);
  not not_23 (not_23_out, OP4);
  not not_24 (not_24_out, OP3);
  not not_25 (not_25_out, OP2);
  not not_26 (not_26_out, OP1);
  not not_27 (not_27_out, OP0);
  not not_28 (not_28_out, F4);
  not not_29 (not_29_out, F3);
  not not_30 (not_30_out, F2);
  not not_31 (not_31_out, F1);
  not not_32 (not_32_out, OP5);
  not not_33 (not_33_out, OP4);
  not not_34 (not_34_out, OP3);
  not not_35 (not_35_out, OP2);
  not not_36 (not_36_out, OP1);
  not not_37 (not_37_out, OP0);
  not not_38 (not_38_out, F4);
  not not_39 (not_39_out, F3);
  not not_40 (not_40_out, F1);
  not not_41 (not_41_out, F0);
  not not_42 (not_42_out, OP5);
  not not_43 (not_43_out, OP4);
  not not_44 (not_44_out, OP3);
  not not_45 (not_45_out, OP2);
  not not_46 (not_46_out, OP1);
  not not_47 (not_47_out, OP0);
  not not_48 (not_48_out, F4);
  not not_49 (not_49_out, F2);
  not not_50 (not_50_out, F0);
  not not_51 (not_51_out, OP5);
  not not_52 (not_52_out, OP4);
  not not_53 (not_53_out, OP2);
  not not_54 (not_54_out, OP1);
  not not_55 (not_55_out, OP0);
  not not_56 (not_56_out, OP5);
  not not_57 (not_57_out, OP4);
  not not_58 (not_58_out, OP1);
  not not_59 (not_59_out, OP0);
  not not_60 (not_60_out, OP5);
  not not_61 (not_61_out, OP4);
  not not_62 (not_62_out, OP2);
  not not_63 (not_63_out, OP1);
  not not_64 (not_64_out, OP5);
  not not_65 (not_65_out, OP4);
  not not_66 (not_66_out, OP2);
  not not_67 (not_67_out, OP0);
  not not_68 (not_68_out, OP4);
  not not_69 (not_69_out, OP3);
  not not_70 (not_70_out, OP2);
  not not_71 (not_71_out, OP4);
  not not_72 (not_72_out, OP2);
  not not_73 (not_73_out, OP5);
  not not_74 (not_74_out, OP4);
  not not_75 (not_75_out, OP3);
  not not_76 (not_76_out, OP2);
  not not_77 (not_77_out, OP1);
  not not_78 (not_78_out, OP0);
  not not_79 (not_79_out, F5);
  not not_80 (not_80_out, F4);
  not not_81 (not_81_out, F3);
  not not_82 (not_82_out, OP5);
  not not_83 (not_83_out, OP4);
  not not_84 (not_84_out, OP3);
  not not_85 (not_85_out, OP4);
  not not_86 (not_86_out, OP2);
  not not_87 (not_87_out, OP1);
  not not_88 (not_88_out, OP0);
  not not_89 (not_89_out, OP5);
  not not_90 (not_90_out, OP4);
  not not_91 (not_91_out, OP3);
  not not_92 (not_92_out, OP2);
  not not_93 (not_93_out, OP1);
  not not_94 (not_94_out, OP0);
  not not_95 (not_95_out, F5);
  not not_96 (not_96_out, F4);
  not not_97 (not_97_out, F3);
  not not_98 (not_98_out, F2);
  not not_99 (not_99_out, F0);
  not not_100 (not_100_out, OP5);
  not not_101 (not_101_out, OP4);
  not not_102 (not_102_out, OP3);
  not not_103 (not_103_out, OP2);
  not not_104 (not_104_out, OP1);
  not not_105 (not_105_out, OP0);
  not not_106 (not_106_out, F4);
  not not_107 (not_107_out, F3);
  not not_108 (not_108_out, F2);
  not not_109 (not_109_out, F0);
  not not_110 (not_110_out, OP5);
  not not_111 (not_111_out, OP4);
  not not_112 (not_112_out, OP3);
  not not_113 (not_113_out, OP2);
  not not_114 (not_114_out, OP1);
  not not_115 (not_115_out, OP0);
  not not_116 (not_116_out, F4);
  not not_117 (not_117_out, F3);
  not not_118 (not_118_out, F1);
  not not_119 (not_119_out, F0);
  not not_120 (not_120_out, OP5);
  not not_121 (not_121_out, OP4);
  not not_122 (not_122_out, OP3);
  not not_123 (not_123_out, OP2);
  not not_124 (not_124_out, OP1);
  not not_125 (not_125_out, OP0);
  not not_126 (not_126_out, F4);
  not not_127 (not_127_out, F3);
  not not_128 (not_128_out, OP5);
  not not_129 (not_129_out, OP4);
  not not_130 (not_130_out, OP3);
  not not_131 (not_131_out, OP2);
  not not_132 (not_132_out, OP1);
  not not_133 (not_133_out, OP0);
  not not_134 (not_134_out, F4);
  not not_135 (not_135_out, F2);
  not not_136 (not_136_out, F0);
  not not_137 (not_137_out, OP5);
  not not_138 (not_138_out, OP4);
  not not_139 (not_139_out, OP1);
  not not_140 (not_140_out, OP0);
  not not_141 (not_141_out, OP5);
  not not_142 (not_142_out, OP4);
  not not_143 (not_143_out, OP2);
  not not_144 (not_144_out, OP0);
  not not_145 (not_145_out, OP5);
  not not_146 (not_146_out, OP4);
  not not_147 (not_147_out, OP3);
  not not_148 (not_148_out, OP5);
  not not_149 (not_149_out, OP4);
  not not_150 (not_150_out, OP3);
  not not_151 (not_151_out, OP2);
  not not_152 (not_152_out, OP1);
  not not_153 (not_153_out, OP0);
  not not_154 (not_154_out, F4);
  not not_155 (not_155_out, F3);
  not not_156 (not_156_out, F2);
  not not_157 (not_157_out, F1);
  not not_158 (not_158_out, F0);
  not not_159 (not_159_out, OP5);
  not not_160 (not_160_out, OP4);
  not not_161 (not_161_out, OP3);
  not not_162 (not_162_out, OP2);
  not not_163 (not_163_out, OP1);
  not not_164 (not_164_out, OP0);
  not not_165 (not_165_out, F4);
  not not_166 (not_166_out, F3);
  not not_167 (not_167_out, F2);
  not not_168 (not_168_out, F1);
  not not_169 (not_169_out, OP5);
  not not_170 (not_170_out, OP4);
  not not_171 (not_171_out, OP3);
  not not_172 (not_172_out, OP2);
  not not_173 (not_173_out, OP1);
  not not_174 (not_174_out, OP0);
  not not_175 (not_175_out, F4);
  not not_176 (not_176_out, F3);
  not not_177 (not_177_out, F2);
  not not_178 (not_178_out, F0);
  not not_179 (not_179_out, OP5);
  not not_180 (not_180_out, OP4);
  not not_181 (not_181_out, OP3);
  not not_182 (not_182_out, OP2);
  not not_183 (not_183_out, OP1);
  not not_184 (not_184_out, OP0);
  not not_185 (not_185_out, F4);
  not not_186 (not_186_out, F3);
  not not_187 (not_187_out, F1);
  not not_188 (not_188_out, F0);
  not not_189 (not_189_out, OP5);
  not not_190 (not_190_out, OP4);
  not not_191 (not_191_out, OP3);
  not not_192 (not_192_out, OP2);
  not not_193 (not_193_out, OP1);
  not not_194 (not_194_out, OP0);
  not not_195 (not_195_out, F4);
  not not_196 (not_196_out, F2);
  not not_197 (not_197_out, OP5);
  not not_198 (not_198_out, OP4);
  not not_199 (not_199_out, OP2);
  not not_200 (not_200_out, OP1);
  not not_201 (not_201_out, OP0);
  not not_202 (not_202_out, OP5);
  not not_203 (not_203_out, OP4);
  not not_204 (not_204_out, OP1);
  not not_205 (not_205_out, OP0);
  not not_206 (not_206_out, OP5);
  not not_207 (not_207_out, OP4);
  not not_208 (not_208_out, OP2);
  not not_209 (not_209_out, OP1);
  not not_210 (not_210_out, OP4);
  not not_211 (not_211_out, OP3);
  not not_212 (not_212_out, OP2);
  not not_213 (not_213_out, OP4);
  not not_214 (not_214_out, OP2);
  not not_215 (not_215_out, OP5);
  not not_216 (not_216_out, OP4);
  not not_217 (not_217_out, OP2);
  not not_218 (not_218_out, OP4);
  not not_219 (not_219_out, OP2);
  not not_220 (not_220_out, OP1);
  not not_221 (not_221_out, OP0);
  not not_222 (not_222_out, OP5);
  not not_223 (not_223_out, OP4);
  not not_224 (not_224_out, OP3);
  not not_225 (not_225_out, OP2);
  not not_226 (not_226_out, OP1);
  not not_227 (not_227_out, OP0);
  not not_228 (not_228_out, F4);
  not not_229 (not_229_out, F3);
  not not_230 (not_230_out, F1);
  not not_231 (not_231_out, OP5);
  not not_232 (not_232_out, OP4);
  not not_233 (not_233_out, OP3);
  not not_234 (not_234_out, OP2);
  not not_235 (not_235_out, OP1);
  not not_236 (not_236_out, OP0);
  not not_237 (not_237_out, F4);
  not not_238 (not_238_out, F3);
  not not_239 (not_239_out, OP5);
  not not_240 (not_240_out, OP4);
  not not_241 (not_241_out, OP3);
  not not_242 (not_242_out, OP2);
  not not_243 (not_243_out, OP1);
  not not_244 (not_244_out, OP0);
  not not_245 (not_245_out, F4);
  not not_246 (not_246_out, F2);
  not not_247 (not_247_out, F0);
  not not_248 (not_248_out, OP5);
  not not_249 (not_249_out, OP4);
  not not_250 (not_250_out, OP3);
  not not_251 (not_251_out, OP2);
  not not_252 (not_252_out, OP1);
  not not_253 (not_253_out, OP0);
  not not_254 (not_254_out, F4);
  not not_255 (not_255_out, F2);
  not not_256 (not_256_out, OP5);
  not not_257 (not_257_out, OP4);
  not not_258 (not_258_out, OP2);
  not not_259 (not_259_out, OP0);
  not not_260 (not_260_out, OP5);
  not not_261 (not_261_out, OP4);
  not not_262 (not_262_out, OP1);
  not not_263 (not_263_out, OP5);
  not not_264 (not_264_out, OP4);
  not not_265 (not_265_out, OP2);
  not not_266 (not_266_out, OP5);
  not not_267 (not_267_out, OP4);
  not not_268 (not_268_out, OP3);
  and and_1 (and_1_out, not_1_out, not_2_out, not_3_out, not_4_out, not_5_out, not_6_out, not_7_out, not_8_out, not_9_out, not_10_out, F1, F0);
  and and_2 (and_2_out, not_11_out, not_12_out, not_13_out, not_14_out, not_15_out, not_16_out, F5, not_17_out, not_18_out, not_19_out, not_20_out, not_21_out);
  and and_3 (and_3_out, not_22_out, not_23_out, not_24_out, not_25_out, not_26_out, not_27_out, F5, not_28_out, not_29_out, not_30_out, not_31_out, F0);
  and and_4 (and_4_out, not_32_out, not_33_out, not_34_out, not_35_out, not_36_out, not_37_out, F5, not_38_out, not_39_out, F2, not_40_out, not_41_out);
  and and_5 (and_5_out, not_42_out, not_43_out, not_44_out, not_45_out, not_46_out, not_47_out, F5, not_48_out, F3, not_49_out, F1, not_50_out);
  and and_6 (and_6_out, not_51_out, not_52_out, OP3, not_53_out, not_54_out, not_55_out);
  and and_7 (and_7_out, not_56_out, not_57_out, OP3, OP2, not_58_out, not_59_out);
  and and_8 (and_8_out, not_60_out, not_61_out, OP3, not_62_out, not_63_out, OP0);
  and and_9 (and_9_out, not_64_out, not_65_out, OP3, not_66_out, OP1, not_67_out);
  and and_10 (and_10_out, OP5, not_68_out, not_69_out, not_70_out, OP1, OP0);
  and and_11 (and_11_out, OP5, not_71_out, OP3, not_72_out, OP1, OP0);
  and and_12 (and_12_out, not_73_out, not_74_out, not_75_out, not_76_out, not_77_out, not_78_out, not_79_out, not_80_out, not_81_out, F2, F1, F0);
  and and_13 (and_13_out, not_82_out, not_83_out, not_84_out, OP2, OP1, OP0);
  and and_14 (and_14_out, OP5, not_85_out, OP3, not_86_out, not_87_out, not_88_out);
  and and_15 (and_15_out, not_89_out, not_90_out, not_91_out, not_92_out, not_93_out, not_94_out, not_95_out, not_96_out, not_97_out, not_98_out, F1, not_99_out);
  and and_16 (and_16_out, not_100_out, not_101_out, not_102_out, not_103_out, not_104_out, not_105_out, F5, not_106_out, not_107_out, not_108_out, F1, not_109_out);
  and and_17 (and_17_out, not_110_out, not_111_out, not_112_out, not_113_out, not_114_out, not_115_out, F5, not_116_out, not_117_out, F2, not_118_out, not_119_out);
  and and_18 (and_18_out, not_120_out, not_121_out, not_122_out, not_123_out, not_124_out, not_125_out, F5, not_126_out, not_127_out, F2, F1, F0);
  and and_19 (and_19_out, not_128_out, not_129_out, not_130_out, not_131_out, not_132_out, not_133_out, F5, not_134_out, F3, not_135_out, F1, not_136_out);
  and and_20 (and_20_out, not_137_out, not_138_out, OP3, OP2, not_139_out, not_140_out);
  and and_21 (and_21_out, not_141_out, not_142_out, OP3, not_143_out, OP1, not_144_out);
  and and_22 (and_22_out, not_145_out, not_146_out, not_147_out, OP2, OP1, OP0);
  and and_23 (and_23_out, not_148_out, not_149_out, not_150_out, not_151_out, not_152_out, not_153_out, F5, not_154_out, not_155_out, not_156_out, not_157_out, not_158_out);
  and and_24 (and_24_out, not_159_out, not_160_out, not_161_out, not_162_out, not_163_out, not_164_out, F5, not_165_out, not_166_out, not_167_out, not_168_out, F0);
  and and_25 (and_25_out, not_169_out, not_170_out, not_171_out, not_172_out, not_173_out, not_174_out, F5, not_175_out, not_176_out, not_177_out, F1, not_178_out);
  and and_26 (and_26_out, not_179_out, not_180_out, not_181_out, not_182_out, not_183_out, not_184_out, F5, not_185_out, not_186_out, F2, not_187_out, not_188_out);
  and and_27 (and_27_out, not_189_out, not_190_out, not_191_out, not_192_out, not_193_out, not_194_out, F5, not_195_out, F3, not_196_out, F1, F0);
  and and_28 (and_28_out, not_197_out, not_198_out, OP3, not_199_out, not_200_out, not_201_out);
  and and_29 (and_29_out, not_202_out, not_203_out, OP3, OP2, not_204_out, not_205_out);
  and and_30 (and_30_out, not_206_out, not_207_out, OP3, not_208_out, not_209_out, OP0);
  and and_31 (and_31_out, OP5, not_210_out, not_211_out, not_212_out, OP1, OP0);
  and and_32 (and_32_out, OP5, not_213_out, OP3, not_214_out, OP1, OP0);
  and and_33 (and_33_out, not_215_out, not_216_out, OP3, not_217_out, OP1, OP0);
  and and_34 (and_34_out, OP5, not_218_out, OP3, not_219_out, not_220_out, not_221_out);
  and and_35 (and_35_out, not_222_out, not_223_out, not_224_out, not_225_out, not_226_out, not_227_out, F5, not_228_out, not_229_out, F2, not_230_out, F0);
  and and_36 (and_36_out, not_231_out, not_232_out, not_233_out, not_234_out, not_235_out, not_236_out, F5, not_237_out, not_238_out, F2, F1, F0);
  and and_37 (and_37_out, not_239_out, not_240_out, not_241_out, not_242_out, not_243_out, not_244_out, F5, not_245_out, F3, not_246_out, F1, not_247_out);
  and and_38 (and_38_out, not_248_out, not_249_out, not_250_out, not_251_out, not_252_out, not_253_out, F5, not_254_out, F3, not_255_out, F1, F0);
  and and_39 (and_39_out, not_256_out, not_257_out, OP3, not_258_out, OP1, not_259_out);
  and and_40 (and_40_out, not_260_out, not_261_out, OP3, OP2, not_262_out, OP0);
  and and_41 (and_41_out, not_263_out, not_264_out, OP3, not_265_out, OP1, OP0);
  and and_42 (and_42_out, not_266_out, not_267_out, not_268_out, OP2, OP1, OP0);
  or or_1 (S1, and_15_out, and_16_out, and_17_out, and_18_out, and_19_out, and_20_out, and_21_out, and_22_out);
  or or_2 (S3, and_35_out, and_36_out, and_37_out, and_38_out, and_39_out, and_40_out, and_41_out, and_42_out);
  or or_3 (S0, and_1_out, and_2_out, and_3_out, and_4_out, and_5_out, and_6_out, and_7_out, and_8_out, and_9_out, and_10_out, and_11_out, and_12_out, and_13_out, and_14_out);
  or or_4 (S2, and_23_out, and_24_out, and_25_out, and_26_out, and_27_out, and_28_out, and_29_out, and_30_out, and_31_out, and_32_out, and_33_out, and_34_out);
endmodule

// 控制信号生成
module \控制信号自动生成  (
  input  OP0,
  input  OP1,
  input  OP2,
  input  OP3,
  input  OP4,
  input  OP5,
  input  F0,
  input  F1,
  input  F2,
  input  F3,
  input  F4,
  input  F5,
  output MemToReg,
  output MemWrite,
  output ALU_SRC,
  output RegWrite,
  output SysCALL,
  output SignedExt,
  output RegDst,
  output BEQ,
  output BNE,
  output JR,
  output JUMP,
  output JAL,
  output BGTZ,
  output SRAV,
  output SB
);

  wire and_2_out, and_3_out, and_4_out, and_5_out, and_6_out, and_7_out, and_8_out, and_9_out, and_10_out,
       and_11_out, and_12_out, and_13_out, and_14_out, and_15_out, and_17_out, and_18_out, and_19_out,
       and_20_out, and_21_out, and_22_out, and_23_out, and_27_out, and_28_out, not_1_out, not_2_out,
       not_3_out, not_4_out, not_5_out, not_6_out, not_7_out, not_8_out, not_9_out, not_10_out, not_11_out,
       not_12_out, not_13_out, not_14_out, not_15_out, not_16_out, not_17_out, not_18_out, not_19_out,
       not_20_out, not_21_out, not_22_out, not_23_out, not_24_out, not_25_out, not_26_out, not_27_out,
       not_28_out, not_29_out, not_30_out, not_31_out, not_32_out, not_33_out, not_34_out, not_35_out,
       not_36_out, not_37_out, not_38_out, not_39_out, not_40_out, not_41_out, not_42_out, not_43_out,
       not_44_out, not_45_out, not_46_out, not_47_out, not_48_out, not_49_out, not_50_out, not_51_out,
       not_52_out, not_53_out, not_54_out, not_55_out, not_56_out, not_57_out, not_58_out, not_59_out,
       not_60_out, not_61_out, not_62_out, not_63_out, not_64_out, not_65_out, not_66_out, not_67_out,
       not_68_out, not_69_out, not_70_out, not_71_out, not_72_out, not_73_out, not_74_out, not_75_out,
       not_76_out, not_77_out, not_78_out, not_79_out, not_80_out, not_81_out, not_82_out, not_83_out,
       not_84_out, not_85_out, not_86_out, not_87_out, not_88_out, not_89_out, not_90_out, not_91_out,
       not_92_out, not_93_out, not_94_out, not_95_out, not_96_out, not_97_out, not_98_out, not_99_out,
       not_100_out, not_101_out, not_102_out, not_103_out, not_104_out, not_105_out, not_106_out,
       not_107_out, not_108_out, not_109_out, not_110_out, not_111_out, not_112_out, not_113_out,
       not_114_out, not_115_out, not_116_out, not_117_out, not_118_out, not_119_out, not_120_out,
       not_121_out, not_122_out, not_123_out, not_124_out, not_125_out, not_126_out, not_127_out,
       not_128_out, not_129_out, not_130_out, not_131_out, not_132_out, not_133_out, not_134_out,
       not_135_out, not_136_out, not_137_out, not_138_out, not_139_out, not_140_out, not_141_out,
       not_142_out, not_143_out, not_144_out, not_145_out, not_146_out, not_147_out, not_148_out,
       not_149_out, not_150_out, not_151_out, not_152_out, not_153_out, not_154_out, not_155_out,
       not_156_out, not_157_out, not_158_out, not_159_out, not_160_out, not_161_out, not_162_out,
       not_163_out, not_164_out, not_165_out, not_166_out, not_167_out, not_168_out, not_169_out,
       not_170_out, not_171_out, not_172_out, not_173_out, not_174_out, not_175_out, not_176_out,
       not_177_out, not_178_out, not_179_out, not_180_out, not_181_out, not_182_out, not_183_out,
       not_184_out, not_185_out;

  not not_1 (not_1_out, OP2);
  not not_2 (not_2_out, OP3);
  not not_3 (not_3_out, OP4);
  not not_4 (not_4_out, OP0);
  not not_5 (not_5_out, OP1);
  not not_6 (not_6_out, OP2);
  not not_7 (not_7_out, OP4);
  not not_8 (not_8_out, OP2);
  not not_9 (not_9_out, OP4);
  not not_10 (not_10_out, OP0);
  not not_11 (not_11_out, OP1);
  not not_12 (not_12_out, OP2);
  not not_13 (not_13_out, OP4);
  not not_14 (not_14_out, OP1);
  not not_15 (not_15_out, OP4);
  not not_16 (not_16_out, OP5);
  not not_17 (not_17_out, OP2);
  not not_18 (not_18_out, OP4);
  not not_19 (not_19_out, OP5);
  not not_20 (not_20_out, OP2);
  not not_21 (not_21_out, OP4);
  not not_22 (not_22_out, OP0);
  not not_23 (not_23_out, OP1);
  not not_24 (not_24_out, OP2);
  not not_25 (not_25_out, OP4);
  not not_26 (not_26_out, OP5);
  not not_27 (not_27_out, F0);
  not not_28 (not_28_out, F2);
  not not_29 (not_29_out, F3);
  not not_30 (not_30_out, F4);
  not not_31 (not_31_out, OP0);
  not not_32 (not_32_out, OP1);
  not not_33 (not_33_out, OP2);
  not not_34 (not_34_out, OP4);
  not not_35 (not_35_out, OP5);
  not not_36 (not_36_out, F1);
  not not_37 (not_37_out, F3);
  not not_38 (not_38_out, F4);
  not not_39 (not_39_out, OP0);
  not not_40 (not_40_out, OP1);
  not not_41 (not_41_out, OP2);
  not not_42 (not_42_out, OP4);
  not not_43 (not_43_out, OP5);
  not not_44 (not_44_out, F2);
  not not_45 (not_45_out, F4);
  not not_46 (not_46_out, OP0);
  not not_47 (not_47_out, OP1);
  not not_48 (not_48_out, OP2);
  not not_49 (not_49_out, OP4);
  not not_50 (not_50_out, OP5);
  not not_51 (not_51_out, F3);
  not not_52 (not_52_out, F4);
  not not_53 (not_53_out, F5);
  not not_54 (not_54_out, OP0);
  not not_55 (not_55_out, OP1);
  not not_56 (not_56_out, OP2);
  not not_57 (not_57_out, OP4);
  not not_58 (not_58_out, OP5);
  not not_59 (not_59_out, F3);
  not not_60 (not_60_out, F4);
  not not_61 (not_61_out, OP1);
  not not_62 (not_62_out, OP4);
  not not_63 (not_63_out, OP5);
  not not_64 (not_64_out, OP2);
  not not_65 (not_65_out, OP4);
  not not_66 (not_66_out, OP5);
  not not_67 (not_67_out, OP2);
  not not_68 (not_68_out, OP3);
  not not_69 (not_69_out, OP4);
  not not_70 (not_70_out, OP0);
  not not_71 (not_71_out, OP1);
  not not_72 (not_72_out, OP2);
  not not_73 (not_73_out, OP3);
  not not_74 (not_74_out, OP4);
  not not_75 (not_75_out, OP5);
  not not_76 (not_76_out, F0);
  not not_77 (not_77_out, F1);
  not not_78 (not_78_out, F4);
  not not_79 (not_79_out, F5);
  not not_80 (not_80_out, OP0);
  not not_81 (not_81_out, OP2);
  not not_82 (not_82_out, OP4);
  not not_83 (not_83_out, OP5);
  not not_84 (not_84_out, OP1);
  not not_85 (not_85_out, OP2);
  not not_86 (not_86_out, OP4);
  not not_87 (not_87_out, OP5);
  not not_88 (not_88_out, OP0);
  not not_89 (not_89_out, OP1);
  not not_90 (not_90_out, OP2);
  not not_91 (not_91_out, OP3);
  not not_92 (not_92_out, OP4);
  not not_93 (not_93_out, OP5);
  not not_94 (not_94_out, F0);
  not not_95 (not_95_out, F2);
  not not_96 (not_96_out, F3);
  not not_97 (not_97_out, F4);
  not not_98 (not_98_out, OP0);
  not not_99 (not_99_out, OP1);
  not not_100 (not_100_out, OP2);
  not not_101 (not_101_out, OP3);
  not not_102 (not_102_out, OP4);
  not not_103 (not_103_out, OP5);
  not not_104 (not_104_out, F1);
  not not_105 (not_105_out, F3);
  not not_106 (not_106_out, F4);
  not not_107 (not_107_out, OP0);
  not not_108 (not_108_out, OP1);
  not not_109 (not_109_out, OP2);
  not not_110 (not_110_out, OP3);
  not not_111 (not_111_out, OP4);
  not not_112 (not_112_out, OP5);
  not not_113 (not_113_out, F2);
  not not_114 (not_114_out, F4);
  not not_115 (not_115_out, OP0);
  not not_116 (not_116_out, OP1);
  not not_117 (not_117_out, OP2);
  not not_118 (not_118_out, OP3);
  not not_119 (not_119_out, OP4);
  not not_120 (not_120_out, OP5);
  not not_121 (not_121_out, F3);
  not not_122 (not_122_out, F4);
  not not_123 (not_123_out, F5);
  not not_124 (not_124_out, OP0);
  not not_125 (not_125_out, OP1);
  not not_126 (not_126_out, OP2);
  not not_127 (not_127_out, OP3);
  not not_128 (not_128_out, OP4);
  not not_129 (not_129_out, OP5);
  not not_130 (not_130_out, F3);
  not not_131 (not_131_out, F4);
  not not_132 (not_132_out, OP0);
  not not_133 (not_133_out, OP1);
  not not_134 (not_134_out, OP3);
  not not_135 (not_135_out, OP4);
  not not_136 (not_136_out, OP5);
  not not_137 (not_137_out, OP1);
  not not_138 (not_138_out, OP3);
  not not_139 (not_139_out, OP4);
  not not_140 (not_140_out, OP5);
  not not_141 (not_141_out, OP0);
  not not_142 (not_142_out, OP1);
  not not_143 (not_143_out, OP2);
  not not_144 (not_144_out, OP3);
  not not_145 (not_145_out, OP4);
  not not_146 (not_146_out, OP5);
  not not_147 (not_147_out, F0);
  not not_148 (not_148_out, F1);
  not not_149 (not_149_out, F2);
  not not_150 (not_150_out, F4);
  not not_151 (not_151_out, F5);
  not not_152 (not_152_out, OP0);
  not not_153 (not_153_out, OP2);
  not not_154 (not_154_out, OP3);
  not not_155 (not_155_out, OP4);
  not not_156 (not_156_out, OP5);
  not not_157 (not_157_out, F0);
  not not_158 (not_158_out, F1);
  not not_159 (not_159_out, F2);
  not not_160 (not_160_out, F4);
  not not_161 (not_161_out, F5);
  not not_162 (not_162_out, OP2);
  not not_163 (not_163_out, OP3);
  not not_164 (not_164_out, OP4);
  not not_165 (not_165_out, OP5);
  not not_166 (not_166_out, OP2);
  not not_167 (not_167_out, OP3);
  not not_168 (not_168_out, OP4);
  not not_169 (not_169_out, OP5);
  not not_170 (not_170_out, OP3);
  not not_171 (not_171_out, OP4);
  not not_172 (not_172_out, OP5);
  not not_173 (not_173_out, OP0);
  not not_174 (not_174_out, OP1);
  not not_175 (not_175_out, OP2);
  not not_176 (not_176_out, OP3);
  not not_177 (not_177_out, OP4);
  not not_178 (not_178_out, OP5);
  not not_179 (not_179_out, F3);
  not not_180 (not_180_out, F4);
  not not_181 (not_181_out, F5);
  not not_182 (not_182_out, OP4);
  not not_183 (not_183_out, OP2);
  not not_184 (not_184_out, OP1);
  not not_185 (not_185_out, OP0);
  and and_1 (MemToReg, OP0, OP1, not_1_out, not_2_out, not_3_out, OP5);
  and and_2 (and_2_out, not_4_out, not_5_out, not_6_out, OP3, not_7_out, OP5);
  and and_3 (and_3_out, OP0, OP1, not_8_out, OP3, not_9_out, OP5);
  and and_4 (and_4_out, not_10_out, not_11_out, not_12_out, OP3, not_13_out);
  and and_5 (and_5_out, not_14_out, OP3, not_15_out, not_16_out);
  and and_6 (and_6_out, not_17_out, OP3, not_18_out, not_19_out);
  and and_7 (and_7_out, OP0, OP1, not_20_out, not_21_out, OP5);
  and and_8 (and_8_out, not_22_out, not_23_out, not_24_out, not_25_out, not_26_out, not_27_out, not_28_out, not_29_out, not_30_out);
  and and_9 (and_9_out, not_31_out, not_32_out, not_33_out, not_34_out, not_35_out, not_36_out, not_37_out, not_38_out, F5);
  and and_10 (and_10_out, not_39_out, not_40_out, not_41_out, not_42_out, not_43_out, F1, not_44_out, F3, not_45_out, F5);
  and and_11 (and_11_out, not_46_out, not_47_out, not_48_out, not_49_out, not_50_out, F0, F1, not_51_out, not_52_out, not_53_out);
  and and_12 (and_12_out, not_54_out, not_55_out, not_56_out, not_57_out, not_58_out, F0, F1, F2, not_59_out, not_60_out);
  and and_13 (and_13_out, not_61_out, OP3, not_62_out, not_63_out);
  and and_14 (and_14_out, not_64_out, OP3, not_65_out, not_66_out);
  and and_15 (and_15_out, OP0, OP1, not_67_out, not_68_out, not_69_out);
  and and_16 (SysCALL, not_70_out, not_71_out, not_72_out, not_73_out, not_74_out, not_75_out, not_76_out, not_77_out, F2, F3, not_78_out, not_79_out);
  and and_17 (and_17_out, not_80_out, not_81_out, OP3, not_82_out, not_83_out);
  or or_1 (SignedExt, and_17_out, and_18_out);
  and and_18 (and_18_out, not_84_out, not_85_out, OP3, not_86_out, not_87_out);
  and and_19 (and_19_out, not_88_out, not_89_out, not_90_out, not_91_out, not_92_out, not_93_out, not_94_out, not_95_out, not_96_out, not_97_out);
  and and_20 (and_20_out, not_98_out, not_99_out, not_100_out, not_101_out, not_102_out, not_103_out, not_104_out, not_105_out, not_106_out, F5);
  and and_21 (and_21_out, not_107_out, not_108_out, not_109_out, not_110_out, not_111_out, not_112_out, F1, not_113_out, F3, not_114_out, F5);
  and and_22 (and_22_out, not_115_out, not_116_out, not_117_out, not_118_out, not_119_out, not_120_out, F0, F1, not_121_out, not_122_out, not_123_out);
  and and_23 (and_23_out, not_124_out, not_125_out, not_126_out, not_127_out, not_128_out, not_129_out, F0, F1, F2, not_130_out, not_131_out);
  and and_24 (BEQ, not_132_out, not_133_out, OP2, not_134_out, not_135_out, not_136_out);
  and and_25 (BNE, OP0, not_137_out, OP2, not_138_out, not_139_out, not_140_out);
  and and_26 (JR, not_141_out, not_142_out, not_143_out, not_144_out, not_145_out, not_146_out, not_147_out, not_148_out, not_149_out, F3, not_150_out, not_151_out);
  and and_27 (and_27_out, not_152_out, not_153_out, not_154_out, not_155_out, not_156_out, not_157_out, not_158_out, not_159_out, F3, not_160_out, not_161_out);
  and and_28 (and_28_out, OP1, not_162_out, not_163_out, not_164_out, not_165_out);
  and and_29 (JAL, OP0, OP1, not_166_out, not_167_out, not_168_out, not_169_out);
  and and_30 (BGTZ, OP0, OP1, OP2, not_170_out, not_171_out, not_172_out);
  and and_31 (SRAV, not_173_out, not_174_out, not_175_out, not_176_out, not_177_out, not_178_out, F0, F1, F2, not_179_out, not_180_out, not_181_out);
  and and_32 (SB, OP5, not_182_out, OP3, not_183_out, not_184_out, not_185_out);
  or or_2 (MemWrite, and_2_out, and_3_out);
  or or_3 (ALU_SRC, and_4_out, and_5_out, and_6_out, and_7_out);
  or or_4 (RegWrite, and_8_out, and_9_out, and_10_out, and_11_out, and_12_out, and_13_out, and_14_out, and_15_out);
  or or_5 (RegDst, and_19_out, and_20_out, and_21_out, and_22_out, and_23_out);
  or or_6 (JUMP, and_27_out, and_28_out);
endmodule

// ALU
module MIPS_ALU (
  input  [4:0] shamt,
  input  [31:0] X,
  input  [31:0] Y,
  input  [3:0] AluOP,
  output Equal,
  output [31:0] Result,
  output [31:0] Result_2
);

  wire [0:0] comparator_1_lt, comparator_2_lt;
  wire [31:0] adder_1_out, AND_out, divider_1_out, divider_1_rem, multiplier_1_cout, multiplier_1_out,
       NOR_out, OR_out, shifter_1_out, shifter_2_out, shifter_3_out, subtractor_1_out, XOR_out;

  assign AND_out = X & Y;  // AND_Gate AND, 32 bits wide
  assign OR_out = X | Y;  // OR_Gate OR, 32 bits wide
  Shifter #(.width(32), .shift("ll")) shifter_1 (.in(Y), .\dist (shamt), .out(shifter_1_out));
  Shifter #(.width(32), .shift("ar")) shifter_2 (.in(Y), .\dist (shamt), .out(shifter_2_out));
  Shifter #(.width(32), .shift("lr")) shifter_3 (.in(Y), .\dist (shamt), .out(shifter_3_out));
  Multiplier #(.width(32)) multiplier_1 (.a(X), .b(Y), .out(multiplier_1_out), .cout(multiplier_1_cout));  // open: cin
  Divider #(.width(32)) divider_1 (.a(X), .b(Y), .out(divider_1_out), .rem(divider_1_rem));  // open: upper
  Adder #(.width(32)) adder_1 (.a(X), .b(Y), .out(adder_1_out));  // open: cin, cout
  Subtractor #(.width(32)) subtractor_1 (.a(X), .b(Y), .out(subtractor_1_out));  // open: bin, bout
  assign XOR_out = X ^ Y;  // XOR_Gate XOR, 32 bits wide
  assign NOR_out = ~(X | Y);  // NOR_Gate NOR, 32 bits wide
  Comparator #(.width(32), .mode("twosComplement")) comparator_1 (
    .a(X), .b(Y), .eq(Equal), .lt(comparator_1_lt[0]));  // open: gt
  Comparator #(.width(32), .mode("unsigned")) comparator_2 (.a(X), .b(Y), .lt(comparator_2_lt[0]));  // open: gt, eq
  Multiplexer #(.select(4), .width(32), .disabled("Z"), .enable("false")) multiplexer_1 (
    .in0(shifter_1_out), .in1(shifter_2_out), .in2(shifter_3_out), .in3(multiplier_1_out),
    .in4(divider_1_out), .in5(adder_1_out), .in6(subtractor_1_out), .in7(AND_out), .in8(OR_out),
    .in9(XOR_out), .in10(NOR_out), .in11({{31{1'b0}}, comparator_1_lt[0]}),
    .in12({{31{1'b0}}, comparator_2_lt[0]}), .in13({32{1'b0}}), .in14({32{1'b0}}), .in15({32{1'b0}}),
    .out(Result), .sel(AluOP));
  Multiplexer #(.select(4), .width(32), .disabled("Z"), .enable("false")) multiplexer_2 (
    .in0({32{1'b0}}), .in1({32{1'b0}}), .in2({32{1'b0}}), .in3(multiplier_1_cout), .in4(divider_1_rem),
    .in5({32{1'b0}}), .in6({32{1'b0}}), .in7({32{1'b0}}), .in8({32{1'b0}}), .in9({32{1'b0}}),
    .in10({32{1'b0}}), .in11({32{1'b0}}), .in12({32{1'b0}}), .in13({32{1'b0}}), .in14({32{1'b0}}),
    .in15({32{1'b0}}), .out(Result_2), .sel(AluOP));

  // Other names for the same wires on the sheet: Result2[31:0] = Result_2; S[3:0] = AluOP

  // Notes on the sheet:
  //   不要改变此引脚区域内容，也不要改变ALU封装形式
  //   输入引脚
  //   输出引脚
endmodule

module MIPS_Regifile (
  input  [31:0] Din,
  input  Clk,
  input  WE,
  input  [4:0] R1_num,
  input  [4:0] W_num,
  input  [4:0] R2_num,
  output [31:0] R1,
  output [31:0] R2
);

  // RegisterFile registerfile_1: pin names not known; wires that end beside it: Din, Clk, WE, W_num, R1_num, R2_num, R1, R2
endmodule

module \理想流水线  (
  output RegWrite,
  output MemWrite,
  output [31:0] IF_PC,
  output [31:0] ID_PC,
  output [31:0] EX_PC,
  output [31:0] M_PC,
  output [31:0] WB_PC,
  output [31:0] RDin,
  output [31:0] MDin,
  output [31:0] LedData
);

  wire and_2_out, and_3_out, CLK, clock_1_out, clock_2_out, comparator_1_eq, comparator_1_lt, d_ff_1_q,
       ex_mem_1_jal_2, ex_mem_1_jmp_2, ex_mem_1_jr_2, ex_mem_1_memtoreg_2, ex_mem_1_regwrite_2,
       ex_mem_1_syscall_2, Go, id_ex_1_alu_src_2, id_ex_1_beq_2, id_ex_1_bne_2, id_ex_1_jal_2, id_ex_1_jmp_2,
       id_ex_1_jr_2, id_ex_1_memtoreg_2, id_ex_1_memwrite_2, id_ex_1_regwrite_2, id_ex_1_syscall_2, IR1, IR2,
       IR3, mem_wb_1_memtoreg_2, mips_alu_1_equal, nand_1_out, or_1_out, or_2_out, RST, SB, SignedExt, SRAV,
       syscall, W1, W2, W3, \单周期硬布线控制器_1_alu_src , \单周期硬布线控制器_1_beq , \单周期硬布线控制器_1_bne , \单周期硬布线控制器_1_jal ,
       \单周期硬布线控制器_1_jmp , \单周期硬布线控制器_1_jr , \单周期硬布线控制器_1_memtoreg , \单周期硬布线控制器_1_memwrite ,
       \单周期硬布线控制器_1_regdst , \单周期硬布线控制器_1_regwrite , \单周期硬布线控制器_1_syscall ;
  wire [3:0] id_ex_1_alu_op_2, \单周期硬布线控制器_1_alu_op ;
  wire [4:0] ex_mem_1_writereg_num_2, id_ex_1_writereg_num_2, mem_wb_1_writereg_num_2, multiplexer_2_out,
       multiplexer_4_out, multiplexer_7_out;
  wire [12:0] CNT_num;
  wire [15:0] \LoadUse次数 , \总周期数 , \插入气泡数 , \无条件分支数 , \条件分支成功数 ;
  wire [31:0] adder_1_out, adder_2_out, Address, and_1_out, bit_extender_1_out, bit_extender_2_out, EX_IR,
       ex_mem_1_ir_ex, id_ex_1_ir_ex, id_ex_1_rt_2, id_ex_1_unsignimm_2, id_ex_1_zeroimm_2, ID_IR,
       if_id_1_ir_id, IF_IR, IR, MDinByte, MDout, MEM_IR, mem_wb_1_rd_2, mem_wb_1_result_2,
       mips_alu_1_result, mips_regifile_1_r1, mips_regifile_1_r2, multiplexer_1_out, multiplexer_3_out,
       multiplexer_5_out, multiplexer_6_out, multiplexer_8_out, R_rs, shifter_1_out, shifter_2_out, WB_IR;

  Button \u_总复位  (.out(RST));
  Button _1 (.out(IR1));
  Button _2 (.out(IR2));
  Button _3 (.out(IR3));
  // Probe on \总周期数 
  // Probe on \总周期数 
  Button \u_继续运行  (.out(Go));
  LED #(.active("true")) led_1 (.in(W1));
  LED #(.active("true")) led_2 (.in(W2));
  LED #(.active("true")) led_3 (.in(W3));
  Hex_Digit_Display hex_digit_display_1 (.value(LedData[31:28]));  // open: dp
  // Probe on IF_PC[19:0]
  // Mips_Probe mips_probe_1: pin names not known; wires that end beside it: IF_IR
  Hex_Digit_Display hex_digit_display_2 (.value(LedData[27:24]));  // open: dp
  Hex_Digit_Display hex_digit_display_3 (.value(LedData[23:20]));  // open: dp
  // Probe on ID_PC[19:0]
  // Mips_Probe mips_probe_2: pin names not known; wires that end beside it: ID_IR
  Multiplexer #(.select(1), .width(32), .disabled("Z"), .enable("false")) multiplexer_1 (
    .in0(adder_1_out), .in1(adder_2_out), .out(multiplexer_1_out), .sel(or_2_out));
  Hex_Digit_Display hex_digit_display_4 (.value(LedData[15:12]));  // open: dp
  Hex_Digit_Display hex_digit_display_5 (.value(LedData[19:16]));  // open: dp
  Register #(.width(32), .trigger("rising"), .Select("low")) register_1 (
    .D(multiplexer_1_out), .en(or_1_out), .Q(IF_PC), .clk(CLK));  // open: clr
  or or_1 (or_1_out, ~syscall, Go);  // OR_Gate
  Hex_Digit_Display hex_digit_display_6 (.value(LedData[11:8]));  // open: dp
  Hex_Digit_Display hex_digit_display_7 (.value(LedData[7:4]));  // open: dp
  Clock #(.highDuration(1), .lowDuration(1)) clock_1 (.out(clock_1_out));
  // Probe on EX_PC[19:0]
  // Mips_Probe mips_probe_3: pin names not known; wires that end beside it: clock_1_out, EX_IR, CLK
  Adder #(.width(32)) adder_1 (.a(IF_PC), .b(32'h4), .out(adder_1_out));  // open: cin, cout
  Hex_Digit_Display hex_digit_display_8 (.value(LedData[3:0]));  // open: dp
  // Probe on \总周期数 
  // Probe on M_PC[19:0]
  // Mips_Probe mips_probe_4: pin names not known; wires that end beside it: MEM_IR
  Counter #(.width(16), .max('hffff), .ongoal("wrap"), .trigger("rising"), .behavior("new")) counter_1 (
    .count(or_1_out), .Q(\总周期数 ), .clk(CLK));  // open: load, D, carry, clr, preset, down
  // Probe on \总周期数 
  // Probe on \无条件分支数 
  // Probe on \条件分支成功数 
  // Probe on \插入气泡数 
  // Probe on \LoadUse次数 
  // Mips_Probe mips_probe_5: pin names not known; wires that end beside it: IR
  ROM #(.addrWidth(10), .dataWidth(32), .Select("high")) rom_1 (.addr(IF_PC[11:2]), .data(IR));
  // Probe on IF_PC[11:0]
  // Probe on WB_PC[19:0]
  // Mips_Probe mips_probe_6: pin names not known; wires that end beside it: WB_IR
  IF_ID if_id_1 (
    .IR_IF(IR), .PC_IF(IF_PC), .IR_ID(if_id_1_ir_id), .PC_ID(ID_PC), .EN(or_1_out), .CLK(CLK));  // open: RST
  // Probe on EX_PC[11:0]
  // Probe on ID_PC[11:0]
  // Probe on M_PC[11:0]
  D_Flip_Flop #(.trigger("high"), .Pre_Clr_Positions("LEGACY"), .NegatePresetClear("false"), .enable("true"), .NewFFLayout("false")) d_ff_1 (.Q(d_ff_1_q));  // open: clk, D, Qn, preset, en, reset
  // Probe on 13'hc
  \单周期硬布线控制器  \u_单周期硬布线控制器_1  (
    .Func(if_id_1_ir_id[5:0]), .OP(if_id_1_ir_id[31:26]), .ALU_OP(\单周期硬布线控制器_1_alu_op ),
    .MemToReg(\单周期硬布线控制器_1_memtoreg ), .MemWrite(\单周期硬布线控制器_1_memwrite ), .ALU_SRC(\单周期硬布线控制器_1_alu_src ),
    .RegWrite(\单周期硬布线控制器_1_regwrite ), .SysCALL(\单周期硬布线控制器_1_syscall ), .SignedExt(SignedExt),
    .RegDst(\单周期硬布线控制器_1_regdst ), .JR(\单周期硬布线控制器_1_jr ), .JMP(\单周期硬布线控制器_1_jmp ), .Beq(\单周期硬布线控制器_1_beq ),
    .JAL(\单周期硬布线控制器_1_jal ), .Bne(\单周期硬布线控制器_1_bne ), .SRAV(SRAV), .SB(SB));  // open: BGTZ
  Multiplexer #(.select(1), .width(5), .disabled("Z"), .enable("false")) multiplexer_2 (
    .in0(if_id_1_ir_id[20:16]), .in1(if_id_1_ir_id[15:11]), .out(multiplexer_2_out),
    .sel(\单周期硬布线控制器_1_regdst ));
  assign bit_extender_1_out = {{16{1'b0}}, if_id_1_ir_id[15:0]};  // Bit_Extender bit_extender_1
  assign bit_extender_2_out = {{16{if_id_1_ir_id[15]}}, if_id_1_ir_id[15:0]};  // Bit_Extender bit_extender_2
  // Probe on WB_PC[11:0]
  Comparator #(.width(13), .mode("twosComplement")) comparator_1 (
    .a(CNT_num), .b(13'hc), .eq(comparator_1_eq), .lt(comparator_1_lt));  // open: gt
  Clock #(.highDuration(1), .lowDuration(1)) clock_2 (.out(clock_2_out));
  Multiplexer #(.select(1), .width(32), .disabled("Z"), .enable("false")) multiplexer_3 (
    .in0(bit_extender_1_out), .in1(bit_extender_2_out), .out(multiplexer_3_out), .sel(SignedExt));
  nand nand_1 (nand_1_out, d_ff_1_q, comparator_1_eq);
  Counter #(.width(13), .max('h1fff), .ongoal("stay"), .trigger("rising"), .behavior("old")) counter_2 (
    .count(comparator_1_lt), .Q(CNT_num), .clk(clock_2_out));  // open: load, D, carry, clr, preset
  assign CLK = nand_1_out ? clock_2_out : 1'bz;  // Controlled_Buffer controlled_buffer_1
  Pull_Resistor #(.pull(1)) pull_resistor_1 (.node(CLK));
  MIPS_Regifile mips_regifile_1 (
    .Din(RDin), .Clk(CLK), .R1(mips_regifile_1_r1), .R2(mips_regifile_1_r2), .WE(RegWrite),
    .W_num(mem_wb_1_writereg_num_2), .R1_num(if_id_1_ir_id[25:21]), .R2_num(if_id_1_ir_id[20:16]));
  ID_EX id_ex_1 (
    .JR(\单周期硬布线控制器_1_jr ), .JMP(\单周期硬布线控制器_1_jmp ), .Beq(\单周期硬布线控制器_1_beq ), .Bne(\单周期硬布线控制器_1_bne ),
    .MemToReg(\单周期硬布线控制器_1_memtoreg ), .MemWrite(\单周期硬布线控制器_1_memwrite ), .ALU_OP(\单周期硬布线控制器_1_alu_op ),
    .ALU_SRC(\单周期硬布线控制器_1_alu_src ), .RegWrite(\单周期硬布线控制器_1_regwrite ), .JAL(\单周期硬布线控制器_1_jal ),
    .SysCALL(\单周期硬布线控制器_1_syscall ), .RS(mips_regifile_1_r1), .RT(mips_regifile_1_r2),
    .WriteReg_num(multiplexer_2_out), .ZeroImm(multiplexer_3_out), .IR_ID(if_id_1_ir_id), .PC_ID(ID_PC),
    .JR_2(id_ex_1_jr_2), .JMP_2(id_ex_1_jmp_2), .Beq_2(id_ex_1_beq_2), .Bne_2(id_ex_1_bne_2),
    .MemToReg_2(id_ex_1_memtoreg_2), .MemWrite_2(id_ex_1_memwrite_2), .ALU_OP_2(id_ex_1_alu_op_2),
    .ALU_SRC_2(id_ex_1_alu_src_2), .RegWrite_2(id_ex_1_regwrite_2), .JAL_2(id_ex_1_jal_2),
    .SysCALL_2(id_ex_1_syscall_2), .RS_2(R_rs), .RT_2(id_ex_1_rt_2), .WriteReg_num_2(id_ex_1_writereg_num_2),
    .ZeroImm_2(id_ex_1_zeroimm_2), .IR_EX(id_ex_1_ir_ex), .PC_EX(EX_PC), .EN(or_1_out), .CLK(CLK),
    .UnSignImm(bit_extender_2_out), .UnSignImm_2(id_ex_1_unsignimm_2));  // open: RST, FwdA, FwdB, FwdA_2, FwdB_2
  Multiplexer #(.select(2), .width(5), .disabled("Z"), .enable("false")) multiplexer_4 (
    .in0({5{1'b0}}), .in1(5'b01000), .in2(5'b10000), .in3(5'b11000), .out(multiplexer_4_out),
    .sel(Address[1:0]));
  Multiplexer #(.select(2), .width(32), .disabled("Z"), .enable("false")) multiplexer_5 (
    .in0(32'hff), .in1(32'hff00), .in2(32'hff0000), .in3(32'hff000000), .out(multiplexer_5_out),
    .sel(Address[1:0]));
  or or_2 (or_2_out, and_2_out, and_3_out);
  Multiplexer #(.select(1), .width(32), .disabled("Z"), .enable("false")) multiplexer_6 (
    .in0(id_ex_1_rt_2), .in1(id_ex_1_zeroimm_2), .out(multiplexer_6_out), .sel(id_ex_1_alu_src_2));
  Shifter #(.width(32), .shift("ll")) shifter_1 (.in(id_ex_1_unsignimm_2), .\dist (5'b00010), .out(shifter_1_out));
  Shifter #(.width(32), .shift("ll")) shifter_2 (.in(MDin), .\dist (multiplexer_4_out), .out(shifter_2_out));
  assign and_1_out = MDout & ~multiplexer_5_out;  // AND_Gate and_1, 32 bits wide
  assign MDinByte = shifter_2_out | and_1_out;  // OR_Gate or_3, 32 bits wide
  and and_2 (and_2_out, ~mips_alu_1_equal, id_ex_1_bne_2);  // AND_Gate
  and and_3 (and_3_out, id_ex_1_beq_2, mips_alu_1_equal);
  MIPS_ALU mips_alu_1 (
    .X(R_rs), .Y(multiplexer_6_out), .AluOP(id_ex_1_alu_op_2), .Equal(mips_alu_1_equal),
    .Result(mips_alu_1_result), .shamt(multiplexer_7_out));  // open: Result_2
  Multiplexer #(.select(1), .width(5), .disabled("Z"), .enable("false")) multiplexer_7 (
    .in0(id_ex_1_ir_ex[10:6]), .in1(R_rs[4:0]), .out(multiplexer_7_out), .sel(SRAV));
  Adder #(.width(32)) adder_2 (.a(shifter_1_out), .b(EX_PC), .out(adder_2_out));  // open: cin, cout
  EX_MEM ex_mem_1 (
    .JR(id_ex_1_jr_2), .JMP(id_ex_1_jmp_2), .MemToReg(id_ex_1_memtoreg_2), .MemWrite(id_ex_1_memwrite_2),
    .RegWrite(id_ex_1_regwrite_2), .JAL(id_ex_1_jal_2), .SysCALL(id_ex_1_syscall_2),
    .RESULT(mips_alu_1_result), .WriteData(id_ex_1_rt_2), .WriteReg_num(id_ex_1_writereg_num_2),
    .IR_ID(id_ex_1_ir_ex), .PC_ID(EX_PC), .JR_2(ex_mem_1_jr_2), .JMP_2(ex_mem_1_jmp_2),
    .MemToReg_2(ex_mem_1_memtoreg_2), .MemWrite_2(MemWrite), .RegWrite_2(ex_mem_1_regwrite_2),
    .JAL_2(ex_mem_1_jal_2), .SysCALL_2(ex_mem_1_syscall_2), .RESULT_2(Address), .WriteData_2(MDin),
    .WriteReg_num_2(ex_mem_1_writereg_num_2), .IR_EX(ex_mem_1_ir_ex), .PC_EX(M_PC), .EN(or_1_out), .CLK(CLK));  // open: RST, r_v0, r_v0_2
  Register #(.width(32), .trigger("rising"), .Select("low")) register_2 (
    .D(MDin), .Q(LedData), .clk(CLK));  // open: en, clr
  Multiplexer #(.select(1), .width(32), .disabled("Z"), .enable("false")) multiplexer_8 (
    .in0(MDin), .in1(MDinByte), .out(multiplexer_8_out), .sel(SB));
  RAM #(.addrWidth(10), .dataWidth(32), .bus("separate"), .Select("high")) ram_1 (
    .addr(Address[11:2]), .din(multiplexer_8_out), .data(MDout), .str(MemWrite), .clk(CLK));  // open: sel, ld, clr
  MEM_WB mem_wb_1 (
    .JR(ex_mem_1_jr_2), .JMP(ex_mem_1_jmp_2), .MemToReg(ex_mem_1_memtoreg_2), .RegWrite(ex_mem_1_regwrite_2),
    .JAL(ex_mem_1_jal_2), .SysCALL(ex_mem_1_syscall_2), .RESULT(Address), .RD(MDout),
    .WriteReg_num(ex_mem_1_writereg_num_2), .IR_ID(ex_mem_1_ir_ex), .PC_ID(M_PC),
    .MemToReg_2(mem_wb_1_memtoreg_2), .RegWrite_2(RegWrite), .SysCALL_2(syscall),
    .RESULT_2(mem_wb_1_result_2), .RD_2(mem_wb_1_rd_2), .WriteReg_num_2(mem_wb_1_writereg_num_2),
    .PC_EX(WB_PC), .EN(or_1_out), .CLK(CLK));  // open: JR_2, JMP_2, JAL_2, IR_EX, RST, r_v0, r_v0_2
  Multiplexer #(.select(1), .width(32), .disabled("Z"), .enable("false")) multiplexer_9 (
    .in0(mem_wb_1_result_2), .in1(mem_wb_1_rd_2), .out(RDin), .sel(mem_wb_1_memtoreg_2));

  // Other names for the same wires on the sheet: MEM_PC[31:0] = M_PC

  // Notes on the sheet:
  //   中断源
  //   时空图监测，可删除
  //   中断等待指示
  //   数码管输出
  //   指令存储器
  //   contents of rom_1 (hex, n*v repeats v):
  //   20090000 200b0020 20110000 20120001 a1310000 112020 20020022 c 2328820 21290001 216bffff 1560fff8
  //   200b0008 20090000 8d310000 112020 20020022 c 21290004 216bffff 1560fff9 2002000a c
  //   控制位
  //   OP
  //   Func
  //   rs
  //   rt
  //   rd
  //   流水调试日志用
  //   暂停节拍，不能为0
  //   Beq
  //   JMP
  //   JR
  //   Bne
  //   OP
  //   JAL
  //   Func
  //   Syscall
  //   戳工具置1进入计数暂停模式，ctrl+k时钟自动运行到对应节拍暂停
  //   ctrl+k关闭时钟连续运行，将控制位置零，进入单步调试模式调试
  //   用这个时钟源需要去掉电路中的其他时钟源
  //   MemToReg
  //   MemWrite
  //   AluOP
  //   AluSrcB
  //   RegWrite
  //   RegDst
  //   可计数暂停的时钟源
  //   为方便自动评测，需要输出流水线各段保存的PC值，注意是PC不是PC+4，另外ID段寄存器写入信息，Mem段内存写入信息也要输出
endmodule

module \气泡流水线  (
  output RegWrite,
  output MemWrite,
  output [31:0] IF_PC,
  output [31:0] ID_PC,
  output [31:0] EX_PC,
  output [31:0] M_PC,
  output [31:0] WB_PC,
  output [31:0] RDin,
  output [31:0] MDin,
  output [31:0] LedData
);

  wire and_1_out, and_4_out, and_5_out, branch, CLK, clock_1_out, clock_2_out, comparator_1_eq,
       comparator_1_lt, comparator_2_eq, d_ff_1_q, ex_mem_1_jal_2, ex_mem_1_jmp_2, ex_mem_1_jr_2,
       ex_mem_1_memtoreg_2, ex_mem_1_regwrite_2, ex_mem_1_syscall_2, Go, halt, ID_BGTZ, id_ex_1_alu_src_2,
       id_ex_1_beq_2, id_ex_1_bne_2, id_ex_1_jal_2, id_ex_1_memtoreg_2, id_ex_1_memwrite_2,
       id_ex_1_regwrite_2, id_ex_1_syscall_2, IR1, IR2, IR3, jmp, jr, led_en, mem_wb_1_jal_2,
       mem_wb_1_memtoreg_2, mips_alu_1_equal, nand_1_out, not_1_out, not_2_out, not_3_out, or_1_out,
       or_2_out, or_3_out, or_5_out, RST, SB, SignedExt, stall, syscall, W1, W2, W3, \单周期硬布线控制器_1_alu_src ,
       \单周期硬布线控制器_1_beq , \单周期硬布线控制器_1_bne , \单周期硬布线控制器_1_jal , \单周期硬布线控制器_1_jmp , \单周期硬布线控制器_1_jr ,
       \单周期硬布线控制器_1_memtoreg , \单周期硬布线控制器_1_memwrite , \单周期硬布线控制器_1_regdst , \单周期硬布线控制器_1_regwrite ,
       \单周期硬布线控制器_1_syscall , \气泡流水线控制逻辑_1_flushid_ex , \气泡流水线控制逻辑_1_flushif_id ;
  wire [3:0] id_ex_1_alu_op_2, \单周期硬布线控制器_1_alu_op ;
  wire [4:0] ex_mem_1_writereg_num_2, id_ex_1_writereg_num_2, if_id_1_ir_id_3, mem_wb_1_writereg_num_2,
       multiplexer_4_out, multiplexer_5_out, multiplexer_7_out, multiplexer_8_out;
  wire [5:0] if_id_1_ir_id, if_id_1_ir_id_5;
  wire [10:6] if_id_1_ir_id_2;
  wire [12:0] CNT_num;
  wire [15:0] \LoadUse次数 , \总周期数 , \插入气泡数 , \无条件分支数 , \条件分支成功数 ;
  wire [25:16] if_id_1_ir_id_4;
  wire [31:0] adder_4_out, \beq跳转 , bit_extender_1_out, bit_extender_2_out, EX_IR, ex_mem_1_ir_ex,
       ex_mem_1_r_v0_2, ex_mem_1_result_2, EX_PC_4, id_ex_1_rt_2, id_ex_1_unsignimm_2, id_ex_1_zeroimm_2,
       ID_IR, IF_IR, IR, MEM_IR, mem_wb_1_ir_ex, mem_wb_1_rd_2, mem_wb_1_result_2, mips_alu_1_result,
       mips_regifile_1_r1, mips_regifile_1_r2, multiplexer_1_out, multiplexer_2_out, multiplexer_3_out,
       multiplexer_6_out, multiplexer_9_out, multiplexer_10_out, PC_4, r_v0, ram_1_data, rs, shifter_1_out,
       WB_IR, \指令字 ;

  Button \u_总复位  (.out(RST));
  Button _1 (.out(IR1));
  Button _2 (.out(IR2));
  Button _3 (.out(IR3));
  // Probe on \总周期数 
  // Probe on \总周期数 
  Button \u_继续运行  (.out(Go));
  LED #(.active("true")) led_1 (.in(W1));
  LED #(.active("true")) led_2 (.in(W2));
  LED #(.active("true")) led_3 (.in(W3));
  Hex_Digit_Display hex_digit_display_1 (.value(LedData[31:28]));  // open: dp
  // Probe on IF_PC[19:0]
  // Mips_Probe mips_probe_1: pin names not known; wires that end beside it: IF_IR
  Hex_Digit_Display hex_digit_display_2 (.value(LedData[23:20]));  // open: dp
  Hex_Digit_Display hex_digit_display_3 (.value(LedData[27:24]));  // open: dp
  // Probe on ID_PC[19:0]
  // Mips_Probe mips_probe_2: pin names not known; wires that end beside it: ID_IR
  Multiplexer #(.select(1), .width(32), .disabled("Z"), .enable("false")) multiplexer_1 (
    .in0(PC_4), .in1(\beq跳转 ), .out(multiplexer_1_out), .sel(branch));
  Hex_Digit_Display hex_digit_display_4 (.value(LedData[19:16]));  // open: dp
  Hex_Digit_Display hex_digit_display_5 (.value(LedData[15:12]));  // open: dp
  Hex_Digit_Display hex_digit_display_6 (.value(LedData[11:8]));  // open: dp
  Hex_Digit_Display hex_digit_display_7 (.value(LedData[7:4]));  // open: dp
  Clock #(.highDuration(1), .lowDuration(1)) clock_1 (.out(clock_1_out));
  // Probe on EX_PC[19:0]
  // Mips_Probe mips_probe_3: pin names not known; wires that end beside it: EX_IR, clock_1_out, CLK
  Multiplexer #(.select(1), .width(32), .disabled("Z"), .enable("false")) multiplexer_2 (
    .in0(multiplexer_1_out), .in1({EX_PC_4[31:28], \指令字 [25:0], 2'b00}), .out(multiplexer_2_out), .sel(jmp));
  not not_1 (not_1_out, stall);
  Hex_Digit_Display hex_digit_display_8 (.value(LedData[3:0]));  // open: dp
  Multiplexer #(.select(1), .width(32), .disabled("Z"), .enable("false")) multiplexer_3 (
    .in0(multiplexer_2_out), .in1(rs), .out(multiplexer_3_out), .sel(jr));
  and and_1 (and_1_out, not_1_out, or_1_out);
  or or_1 (or_1_out, ~halt, Go);  // OR_Gate
  // Probe on \总周期数 
  // Probe on M_PC[19:0]
  // Mips_Probe mips_probe_4: pin names not known; wires that end beside it: MEM_IR
  Register #(.width(32), .trigger("rising"), .Select("low")) register_1 (
    .D(multiplexer_3_out), .en(and_1_out), .Q(IF_PC), .clk(CLK));  // open: clr
  // Probe on \总周期数 
  // Probe on \无条件分支数 
  // Probe on \条件分支成功数 
  // Probe on \插入气泡数 
  // Probe on \LoadUse次数 
  Adder #(.width(32)) adder_1 (.a(IF_PC), .b(32'h4), .out(PC_4));  // open: cin, cout
  // Probe on IF_PC[11:0]
  // Probe on WB_PC[19:0]
  // Mips_Probe mips_probe_5: pin names not known; wires that end beside it: WB_IR
  Counter #(.width(8), .max('hff), .ongoal("wrap"), .trigger("rising"), .behavior("new")) counter_1 (.clk(\气泡流水线控制逻辑_1_flushif_id ));  // open: load, D, count, Q, carry, clr, preset, down
  // Probe on ID_PC[11:0]
  // Probe on EX_PC[11:0]
  ROM #(.addrWidth(10), .dataWidth(32), .Select("high")) rom_1 (.addr(IF_PC[11:2]), .data(IR));
  // Probe on IF_PC
  // Probe on M_PC[11:0]
  D_Flip_Flop #(.trigger("high"), .Pre_Clr_Positions("LEGACY"), .NegatePresetClear("false"), .enable("true"), .NewFFLayout("false")) d_ff_1 (.Q(d_ff_1_q));  // open: clk, D, Qn, preset, en, reset
  // Probe on 13'h5b7
  // Mips_Probe mips_probe_6: pin names not known; wires that end beside it: IR
  // Probe on WB_PC[11:0]
  Comparator #(.width(13), .mode("twosComplement")) comparator_1 (
    .a(CNT_num), .b(13'h5b7), .eq(comparator_1_eq), .lt(comparator_1_lt));  // open: gt
  Clock #(.highDuration(1), .lowDuration(1)) clock_2 (.out(clock_2_out));
  IF_ID if_id_1 (
    .IR_IF(IR), .PC_IF(IF_PC),
    .IR_ID({if_id_1_ir_id_5, if_id_1_ir_id_4, if_id_1_ir_id_3, if_id_1_ir_id_2, if_id_1_ir_id}),
    .PC_ID(ID_PC), .EN(and_1_out), .CLK(CLK), .RST(\气泡流水线控制逻辑_1_flushif_id ));
  nand nand_1 (nand_1_out, d_ff_1_q, comparator_1_eq);
  Counter #(.width(13), .max('h1fff), .ongoal("stay"), .trigger("rising"), .behavior("old")) counter_2 (
    .count(comparator_1_lt), .Q(CNT_num), .clk(clock_2_out));  // open: load, D, carry, clr, preset
  // Mips_Probe mips_probe_7: pin names not known; wires that end beside it: {if_id_1_ir_id_5, if_id_1_ir_id_4, if_id_1_ir_id_3, if_id_1_ir_id_2, if_id_1_ir_id}
  Multiplexer #(.select(1), .width(5), .disabled("Z"), .enable("false")) multiplexer_4 (
    .in0(if_id_1_ir_id_4[20:16]), .in1(if_id_1_ir_id_3), .out(multiplexer_4_out), .sel(\单周期硬布线控制器_1_regdst ));
  or or_2 (or_2_out, ~halt, Go);  // OR_Gate
  assign CLK = nand_1_out ? clock_2_out : 1'bz;  // Controlled_Buffer controlled_buffer_1
  \单周期硬布线控制器  \u_单周期硬布线控制器_1  (
    .Func(if_id_1_ir_id), .OP(if_id_1_ir_id_5), .ALU_OP(\单周期硬布线控制器_1_alu_op ),
    .MemToReg(\单周期硬布线控制器_1_memtoreg ), .MemWrite(\单周期硬布线控制器_1_memwrite ), .ALU_SRC(\单周期硬布线控制器_1_alu_src ),
    .RegWrite(\单周期硬布线控制器_1_regwrite ), .SysCALL(\单周期硬布线控制器_1_syscall ), .SignedExt(SignedExt),
    .RegDst(\单周期硬布线控制器_1_regdst ), .JR(\单周期硬布线控制器_1_jr ), .JMP(\单周期硬布线控制器_1_jmp ), .Beq(\单周期硬布线控制器_1_beq ),
    .JAL(\单周期硬布线控制器_1_jal ), .Bne(\单周期硬布线控制器_1_bne ), .BGTZ(ID_BGTZ), .SB(SB));  // open: SRAV
  assign bit_extender_1_out = {{16{1'b0}}, {if_id_1_ir_id_3, if_id_1_ir_id_2, if_id_1_ir_id}};  // Bit_Extender bit_extender_1
  assign bit_extender_2_out = {{16{if_id_1_ir_id_3[4]}}, {if_id_1_ir_id_3, if_id_1_ir_id_2, if_id_1_ir_id}};  // Bit_Extender bit_extender_2
  Pull_Resistor #(.pull(1)) pull_resistor_1 (.node(CLK));
  Multiplexer #(.select(1), .width(5), .disabled("Z"), .enable("false")) multiplexer_5 (
    .in0(multiplexer_4_out), .in1({5{1'b1}}), .out(multiplexer_5_out), .sel(\单周期硬布线控制器_1_jal ));
  Multiplexer #(.select(1), .width(32), .disabled("Z"), .enable("false")) multiplexer_6 (
    .in0(bit_extender_1_out), .in1(bit_extender_2_out), .out(multiplexer_6_out), .sel(SignedExt));
  Multiplexer #(.select(1), .width(5), .disabled("Z"), .enable("false")) multiplexer_7 (
    .in0(if_id_1_ir_id_4[25:21]), .in1(5'b00010), .out(multiplexer_7_out), .sel(\单周期硬布线控制器_1_syscall ));
  Multiplexer #(.select(1), .width(5), .disabled("Z"), .enable("false")) multiplexer_8 (
    .in0(if_id_1_ir_id_4[20:16]), .in1(5'b00100), .out(multiplexer_8_out), .sel(\单周期硬布线控制器_1_syscall ));
  \气泡流水线控制逻辑  \u_气泡流水线控制逻辑_1  (
    .MEM_WriteReg_num(ex_mem_1_writereg_num_2), .EX_WriteReg_num(id_ex_1_writereg_num_2), .Stall(stall),
    .FlushID_EX(\气泡流水线控制逻辑_1_flushid_ex ), .FlushIF_ID(\气泡流水线控制逻辑_1_flushif_id ),
    .IR({if_id_1_ir_id_5, if_id_1_ir_id_4, if_id_1_ir_id_3, if_id_1_ir_id_2, if_id_1_ir_id}),
    .MEM_RegWrite(ex_mem_1_regwrite_2), .EX_RegWrite(id_ex_1_regwrite_2), .branch(or_3_out),
    .rs(multiplexer_7_out), .rt(multiplexer_8_out));
  not not_2 (not_2_out, halt);
  MIPS_Regifile mips_regifile_1 (
    .Din(RDin), .Clk(not_3_out), .R1(mips_regifile_1_r1), .R2(mips_regifile_1_r2), .WE(RegWrite),
    .W_num(mem_wb_1_writereg_num_2), .R1_num(multiplexer_7_out), .R2_num(multiplexer_8_out));
  not not_3 (not_3_out, CLK);
  Comparator #(.width(32), .mode("twosComplement")) comparator_2 (
    .a(r_v0), .b(32'h22), .eq(comparator_2_eq));  // open: gt, lt
  Counter #(.width(16), .max('hffff), .ongoal("wrap"), .trigger("rising"), .behavior("new")) counter_3 (
    .count(not_2_out), .Q(\总周期数 ), .clk(CLK));  // open: load, D, carry, clr, preset, down
  ID_EX id_ex_1 (
    .JR(\单周期硬布线控制器_1_jr ), .JMP(\单周期硬布线控制器_1_jmp ), .Beq(\单周期硬布线控制器_1_beq ), .Bne(\单周期硬布线控制器_1_bne ),
    .MemToReg(\单周期硬布线控制器_1_memtoreg ), .MemWrite(\单周期硬布线控制器_1_memwrite ), .ALU_OP(\单周期硬布线控制器_1_alu_op ),
    .ALU_SRC(\单周期硬布线控制器_1_alu_src ), .RegWrite(\单周期硬布线控制器_1_regwrite ), .JAL(\单周期硬布线控制器_1_jal ),
    .SysCALL(\单周期硬布线控制器_1_syscall ), .RS(mips_regifile_1_r1), .RT(mips_regifile_1_r2),
    .WriteReg_num(multiplexer_5_out), .ZeroImm(multiplexer_6_out),
    .IR_ID({if_id_1_ir_id_5, if_id_1_ir_id_4, if_id_1_ir_id_3, if_id_1_ir_id_2, if_id_1_ir_id}),
    .PC_ID(ID_PC), .JR_2(jr), .JMP_2(jmp), .Beq_2(id_ex_1_beq_2), .Bne_2(id_ex_1_bne_2),
    .MemToReg_2(id_ex_1_memtoreg_2), .MemWrite_2(id_ex_1_memwrite_2), .ALU_OP_2(id_ex_1_alu_op_2),
    .ALU_SRC_2(id_ex_1_alu_src_2), .RegWrite_2(id_ex_1_regwrite_2), .JAL_2(id_ex_1_jal_2),
    .SysCALL_2(id_ex_1_syscall_2), .RS_2(rs), .RT_2(id_ex_1_rt_2), .WriteReg_num_2(id_ex_1_writereg_num_2),
    .ZeroImm_2(id_ex_1_zeroimm_2), .IR_EX(\指令字 ), .PC_EX(EX_PC), .EN(or_2_out), .CLK(CLK),
    .RST(\气泡流水线控制逻辑_1_flushid_ex ), .UnSignImm(bit_extender_2_out), .UnSignImm_2(id_ex_1_unsignimm_2));  // open: FwdA, FwdB, FwdA_2, FwdB_2
  and and_2 (led_en, syscall, comparator_2_eq);
  and and_3 (halt, syscall, ~comparator_2_eq);  // AND_Gate
  or or_3 (or_3_out, branch, or_5_out);
  Multiplexer #(.select(1), .width(32), .disabled("Z"), .enable("false")) multiplexer_9 (
    .in0(id_ex_1_rt_2), .in1(id_ex_1_zeroimm_2), .out(multiplexer_9_out), .sel(id_ex_1_alu_src_2));
  Adder #(.width(32)) adder_2 (.a(32'h4), .b(EX_PC), .out(EX_PC_4));  // open: cin, cout
  or or_4 (branch, and_5_out, and_4_out);
  or or_5 (or_5_out, jmp, jr, id_ex_1_jal_2);
  // Mips_Probe mips_probe_8: pin names not known; wires that end beside it: \气泡流水线控制逻辑_1_flushid_ex , \指令字 
  Shifter #(.width(32), .shift("ll")) shifter_1 (.in(id_ex_1_unsignimm_2), .\dist (5'b00010), .out(shifter_1_out));
  and and_4 (and_4_out, id_ex_1_beq_2, mips_alu_1_equal);
  Register #(.width(32), .trigger("rising"), .Select("low")) register_2 (
    .D(MDin), .en(led_en), .Q(LedData), .clk(CLK));  // open: clr
  and and_5 (and_5_out, ~mips_alu_1_equal, id_ex_1_bne_2);  // AND_Gate
  MIPS_ALU mips_alu_1 (
    .X(rs), .Y(multiplexer_9_out), .AluOP(id_ex_1_alu_op_2), .Equal(mips_alu_1_equal),
    .Result(mips_alu_1_result), .shamt(\指令字 [10:6]));  // open: Result_2
  Adder #(.width(32)) adder_3 (.a(shifter_1_out), .b(EX_PC_4), .out(\beq跳转 ));  // open: cin, cout
  EX_MEM ex_mem_1 (
    .JR(jr), .JMP(jmp), .MemToReg(id_ex_1_memtoreg_2), .MemWrite(id_ex_1_memwrite_2),
    .RegWrite(id_ex_1_regwrite_2), .JAL(id_ex_1_jal_2), .SysCALL(id_ex_1_syscall_2),
    .RESULT(mips_alu_1_result), .WriteData(id_ex_1_rt_2), .WriteReg_num(id_ex_1_writereg_num_2),
    .IR_ID(\指令字 ), .PC_ID(EX_PC), .JR_2(ex_mem_1_jr_2), .JMP_2(ex_mem_1_jmp_2),
    .MemToReg_2(ex_mem_1_memtoreg_2), .MemWrite_2(MemWrite), .RegWrite_2(ex_mem_1_regwrite_2),
    .JAL_2(ex_mem_1_jal_2), .SysCALL_2(ex_mem_1_syscall_2), .RESULT_2(ex_mem_1_result_2), .WriteData_2(MDin),
    .WriteReg_num_2(ex_mem_1_writereg_num_2), .IR_EX(ex_mem_1_ir_ex), .PC_EX(M_PC), .EN(or_2_out), .CLK(CLK),
    .r_v0(rs), .r_v0_2(ex_mem_1_r_v0_2));  // open: RST
  // Mips_Probe mips_probe_9: pin names not known; wires that end beside it: ex_mem_1_ir_ex
  RAM #(.addrWidth(10), .dataWidth(32), .bus("separate"), .Select("high")) ram_1 (
    .addr(ex_mem_1_result_2[11:2]), .din(MDin), .data(ram_1_data), .str(MemWrite), .clk(CLK));  // open: sel, ld, clr
  MEM_WB mem_wb_1 (
    .JR(ex_mem_1_jr_2), .JMP(ex_mem_1_jmp_2), .MemToReg(ex_mem_1_memtoreg_2), .RegWrite(ex_mem_1_regwrite_2),
    .JAL(ex_mem_1_jal_2), .SysCALL(ex_mem_1_syscall_2), .RESULT(ex_mem_1_result_2), .RD(ram_1_data),
    .WriteReg_num(ex_mem_1_writereg_num_2), .IR_ID(ex_mem_1_ir_ex), .PC_ID(M_PC),
    .MemToReg_2(mem_wb_1_memtoreg_2), .RegWrite_2(RegWrite), .JAL_2(mem_wb_1_jal_2), .SysCALL_2(syscall),
    .RESULT_2(mem_wb_1_result_2), .RD_2(mem_wb_1_rd_2), .WriteReg_num_2(mem_wb_1_writereg_num_2),
    .IR_EX(mem_wb_1_ir_ex), .PC_EX(WB_PC), .EN(or_2_out), .CLK(CLK), .r_v0(ex_mem_1_r_v0_2), .r_v0_2(r_v0));  // open: JR_2, JMP_2, RST
  Multiplexer #(.select(1), .width(32), .disabled("Z"), .enable("false")) multiplexer_10 (
    .in0(mem_wb_1_result_2), .in1(mem_wb_1_rd_2), .out(multiplexer_10_out), .sel(mem_wb_1_memtoreg_2));
  // Mips_Probe mips_probe_10: pin names not known; wires that end beside it: mem_wb_1_ir_ex
  Adder #(.width(32)) adder_4 (.a(WB_PC), .b(32'h4), .out(adder_4_out));  // open: cin, cout
  Multiplexer #(.select(1), .width(32), .disabled("Z"), .enable("false")) multiplexer_11 (
    .in0(multiplexer_10_out), .in1(adder_4_out), .out(RDin), .sel(mem_wb_1_jal_2));

  // Other names for the same wires on the sheet: MEM_PC[31:0] = M_PC

  // Notes on the sheet:
  //   中断源
  //   时空图监测，可删除
  //   中断等待指示
  //   数码管输出
  //   指令存储器
  //   控制位
  //   contents of rom_1 (hex, n*v repeats v):
  //   20110001 8000c05 20110001 20120002 20130003 8000c09 20110001 20120002 20130003 8000c0d 20110001
  //   20120002 20130003 8000c11 20110001 20120002 20130003 c000cb8 20100001 20110001 118fc0 112020
  //   20020022 c 118882 12200001 8000c15 112020 20020022 c 20110001 118880 112020 20020022 c 12200001
  //   8000c1f 20110001 118fc0 112020 20020022 c 1188c3 112020 20020022 c 118903 112020 20020022 c 118903
  //   112020 20020022 c 118903 112020 20020022 c 118903 112020 20020022 c 118903 112020 20020022 c 118903
  //   112020 20020022 c 118903 112020 20020022 c 20100001 109fc0 139fc3 8021 2012000c 24160003 26100001
  //   3210000f 20080008 20090001 139900 2709825 132020 20020022 c 1094022 1500fff9 22100001 2018000f
  //   2188024 108700 20080008 20090001 139902 2709825 132021 20020022 c 1094022 1500fff9 108702 2c9b022
  //   12c00001 8000c50 4020 1084027 84400 3508ffff 82021 20020022 c 2010ffff 20110000 ae300000 22100001
  //   22310004 ae300000 22100001 22310004 ae300000 22100001 22310004 ae300000 22100001 22310004 ae300000
  //   22100001 22310004 ae300000 22100001 22310004 ae300000 22100001 22310004 ae300000 22100001 22310004
  //   ae300000 22100001 22310004 ae300000 22100001 22310004 ae300000 22100001 22310004 ae300000 22100001
  //   22310004 ae300000 22100001 22310004 ae300000 22100001 22310004 ae300000 22100001 22310004 ae300000
  //   22100001 22310004 22100001 8020 2011003c 8e130000 8e340000 274402a 11000002 ae330000 ae140000
  //   2231fffc 1611fff8 102020 20020022 c 22100004 2011003c 1611fff2 20020032 c 20100000 22100001 102020
  //   20020022 c 22100002 102020 20020022 c 22100003 102020 20020022 c 22100004 102020 20020022 c 22100005
  //   102020 20020022 c 22100006 102020 20020022 c 22100007 102020 20020022 c 22100008 102020 20020022
  //   20020022 c 3e00008
  //   流水调试日志用
  //   暂停节拍，不能为0
  //   戳工具置1进入计数暂停模式，ctrl+k时钟自动运行到对应节拍暂停
  //   ctrl+k关闭时钟连续运行，将控制位置零，进入单步调试模式调试
  //   OP
  //   rs
  //   rt
  //   rd
  //   JMP
  //   JR
  //   OP
  //   Func
  //   Func
  //   可计数暂停的时钟源
  //   Beq
  //   Bne
  //   MemToReg
  //   MemWrite
  //   AluOP
  //   AluSrcB
  //   RegWrite
  //   JAL
  //   RegDst
  //   Syscall
  //   为方便自动评测，需要输出流水线各段保存的PC值，注意是PC不是PC+4，另外ID段寄存器写入信息，Mem段内存写入信息也要输出
endmodule

module \重定向流水线  (
  output RegWrite,
  output MemWrite,
  output [31:0] IF_PC,
  output [31:0] ID_PC,
  output [31:0] EX_PC,
  output [31:0] M_PC,
  output [31:0] WB_PC,
  output [31:0] RDin,
  output [31:0] MDin,
  output [31:0] LedData
);

  wire and_1_out, and_5_out, and_6_out, beq, bne, branch, CLK, clock_1_out, clock_2_out, comparator_1_eq,
       comparator_1_lt, comparator_2_eq, comparator_3_eq, d_ff_1_q, ex_mem_1_jal_2, ex_mem_1_jmp_2,
       ex_mem_1_jr_2, ex_mem_1_memtoreg_2, ex_mem_1_regwrite_2, ex_mem_1_syscall_2, Go, halt, ID_BGTZ,
       id_ex_1_alu_src_2, id_ex_1_jal_2, id_ex_1_jmp_2, id_ex_1_jr_2, id_ex_1_memtoreg_2, id_ex_1_memwrite_2,
       id_ex_1_regwrite_2, id_ex_1_syscall_2, ID_SB, \id重定向控制逻辑_1_flushid_ex , \id重定向控制逻辑_1_flushif_id , IR1,
       IR2, IR3, jmp, jr, led_en, mem_wb_1_jal_2, mem_wb_1_memtoreg_2, nand_1_out, not_1_out, not_2_out,
       not_3_out, or_1_out, or_2_out, RST, SignedExt, stall, syscall, W1, W2, W3, \单周期硬布线控制器_1_alu_src ,
       \单周期硬布线控制器_1_jal , \单周期硬布线控制器_1_memtoreg , \单周期硬布线控制器_1_memwrite , \单周期硬布线控制器_1_regdst ,
       \单周期硬布线控制器_1_regwrite , \单周期硬布线控制器_1_syscall , \跳转 ;
  wire [1:0] Address, FwdA, FwdB, id_ex_1_fwda_2, id_ex_1_fwdb_2;
  wire [3:0] id_ex_1_alu_op_2, \单周期硬布线控制器_1_alu_op ;
  wire [4:0] ex_mem_1_writereg_num_2, id_ex_1_writereg_num_2, mem_wb_1_writereg_num_2, multiplexer_4_out,
       multiplexer_5_out, multiplexer_7_out, multiplexer_8_out, multiplexer_14_out;
  wire [12:0] CNT_num;
  wire [15:0] \LoadUse次数 , \总周期数 , \插入气泡数 , \无条件分支数 , \条件分支成功数 ;
  wire [31:0] adder_4_out, and_4_out, \beq跳转 , bit_extender_1_out, bit_extender_2_out, EX_IR,
       ex_mem_1_r_v0_2, ex_mem_1_result_2, id_ex_1_rs_2, id_ex_1_rt_2, id_ex_1_zeroimm_2, ID_IR, ID_PC_4,
       IF_IR, MDinByte, MDout, MEM_IR, mem_wb_1_rd_2, mem_wb_1_result_2, mips_alu_1_result,
       mips_regifile_1_r1, mips_regifile_1_r2, multiplexer_1_out, multiplexer_2_out, multiplexer_3_out,
       multiplexer_6_out, multiplexer_11_out, multiplexer_12_out, multiplexer_13_out, multiplexer_15_out,
       multiplexer_16_out, PC_4, r_v0, ram_1_data, RS, RT, shifter_1_out, shifter_2_out, WB_IR;

  Button \u_总复位  (.out(RST));
  Button _1 (.out(IR1));
  Button _2 (.out(IR2));
  Button _3 (.out(IR3));
  // Probe on \总周期数 
  // Probe on \总周期数 
  Button \u_继续运行  (.out(Go));
  LED #(.active("true")) led_1 (.in(W1));
  LED #(.active("true")) led_2 (.in(W2));
  LED #(.active("true")) led_3 (.in(W3));
  Hex_Digit_Display hex_digit_display_1 (.value(LedData[31:28]));  // open: dp
  // Probe on IF_PC[19:0]
  // Mips_Probe mips_probe_1: pin names not known; wires that end beside it: IF_IR
  Hex_Digit_Display hex_digit_display_2 (.value(LedData[23:20]));  // open: dp
  Hex_Digit_Display hex_digit_display_3 (.value(LedData[27:24]));  // open: dp
  // Probe on ID_PC[19:0]
  // Mips_Probe mips_probe_2: pin names not known; wires that end beside it: ID_IR
  Multiplexer #(.select(1), .width(32), .disabled("Z"), .enable("false")) multiplexer_1 (
    .in0(PC_4), .in1(\beq跳转 ), .out(multiplexer_1_out), .sel(branch));
  Hex_Digit_Display hex_digit_display_4 (.value(LedData[15:12]));  // open: dp
  Hex_Digit_Display hex_digit_display_5 (.value(LedData[19:16]));  // open: dp
  Hex_Digit_Display hex_digit_display_6 (.value(LedData[7:4]));  // open: dp
  Hex_Digit_Display hex_digit_display_7 (.value(LedData[11:8]));  // open: dp
  Clock #(.highDuration(1), .lowDuration(1)) clock_1 (.out(clock_1_out));
  // Probe on EX_PC[19:0]
  // Mips_Probe mips_probe_3: pin names not known; wires that end beside it: EX_IR, clock_1_out, CLK
  Multiplexer #(.select(1), .width(32), .disabled("Z"), .enable("false")) multiplexer_2 (
    .in0(multiplexer_1_out), .in1({ID_PC_4[31:28], ID_IR[25:0], 2'b00}), .out(multiplexer_2_out), .sel(jmp));
  not not_1 (not_1_out, stall);
  Hex_Digit_Display hex_digit_display_8 (.value(LedData[3:0]));  // open: dp
  Multiplexer #(.select(1), .width(32), .disabled("Z"), .enable("false")) multiplexer_3 (
    .in0(multiplexer_2_out), .in1(RS), .out(multiplexer_3_out), .sel(jr));
  and and_1 (and_1_out, not_1_out, or_1_out);
  or or_1 (or_1_out, ~halt, Go);  // OR_Gate
  // Probe on \总周期数 
  // Probe on M_PC[19:0]
  // Mips_Probe mips_probe_4: pin names not known; wires that end beside it: MEM_IR
  Register #(.width(32), .trigger("rising"), .Select("low")) register_1 (
    .D(multiplexer_3_out), .en(and_1_out), .Q(IF_PC), .clk(CLK));  // open: clr
  // Probe on \总周期数 
  // Probe on \无条件分支数 
  // Probe on \条件分支成功数 
  // Probe on \插入气泡数 
  // Probe on \LoadUse次数 
  Adder #(.width(32)) adder_1 (.a(IF_PC), .b(32'h4), .out(PC_4));  // open: cin, cout
  // Probe on IF_PC[11:0]
  // Probe on WB_PC[19:0]
  // Mips_Probe mips_probe_5: pin names not known; wires that end beside it: WB_IR
  // Probe on ID_PC[11:0]
  // Probe on EX_PC[11:0]
  Counter #(.width(8), .max('hff), .ongoal("wrap"), .trigger("rising"), .behavior("new")) counter_1 (.clk(stall));  // open: load, D, count, Q, carry, clr, preset, down
  ROM #(.addrWidth(10), .dataWidth(32), .Select("high")) rom_1 (.addr(IF_PC[11:2]), .data(IF_IR));
  // Probe on IF_PC
  // Probe on M_PC[11:0]
  D_Flip_Flop #(.trigger("high"), .Pre_Clr_Positions("LEGACY"), .NegatePresetClear("false"), .enable("true"), .NewFFLayout("false")) d_ff_1 (.Q(d_ff_1_q));  // open: clk, D, Qn, preset, en, reset
  // Probe on 13'h322
  // Mips_Probe mips_probe_6: pin names not known; wires that end beside it: IF_IR
  // Probe on WB_PC[11:0]
  Comparator #(.width(13), .mode("twosComplement")) comparator_1 (
    .a(CNT_num), .b(13'h322), .eq(comparator_1_eq), .lt(comparator_1_lt));  // open: gt
  Clock #(.highDuration(1), .lowDuration(1)) clock_2 (.out(clock_2_out));
  IF_ID if_id_1 (
    .IR_IF(IF_IR), .PC_IF(IF_PC), .IR_ID(ID_IR), .PC_ID(ID_PC), .EN(and_1_out), .CLK(CLK),
    .RST(\id重定向控制逻辑_1_flushif_id ));
  nand nand_1 (nand_1_out, d_ff_1_q, comparator_1_eq);
  Counter #(.width(13), .max('h1fff), .ongoal("stay"), .trigger("rising"), .behavior("old")) counter_2 (
    .count(comparator_1_lt), .Q(CNT_num), .clk(clock_2_out));  // open: load, D, carry, clr, preset
  Multiplexer #(.select(1), .width(5), .disabled("Z"), .enable("false")) multiplexer_4 (
    .in0(ID_IR[20:16]), .in1(ID_IR[15:11]), .out(multiplexer_4_out), .sel(\单周期硬布线控制器_1_regdst ));
  or or_2 (or_2_out, ~halt, Go);  // OR_Gate
  assign CLK = nand_1_out ? clock_2_out : 1'bz;  // Controlled_Buffer controlled_buffer_1
  \单周期硬布线控制器  \u_单周期硬布线控制器_1  (
    .Func(ID_IR[5:0]), .OP(ID_IR[31:26]), .ALU_OP(\单周期硬布线控制器_1_alu_op ), .MemToReg(\单周期硬布线控制器_1_memtoreg ),
    .MemWrite(\单周期硬布线控制器_1_memwrite ), .ALU_SRC(\单周期硬布线控制器_1_alu_src ), .RegWrite(\单周期硬布线控制器_1_regwrite ),
    .SysCALL(\单周期硬布线控制器_1_syscall ), .SignedExt(SignedExt), .RegDst(\单周期硬布线控制器_1_regdst ), .JR(jr),
    .JMP(jmp), .Beq(beq), .JAL(\单周期硬布线控制器_1_jal ), .Bne(bne), .BGTZ(ID_BGTZ), .SB(ID_SB));  // open: SRAV
  assign bit_extender_1_out = {{16{1'b0}}, ID_IR[15:0]};  // Bit_Extender bit_extender_1
  assign bit_extender_2_out = {{16{ID_IR[15]}}, ID_IR[15:0]};  // Bit_Extender bit_extender_2
  Pull_Resistor #(.pull(1)) pull_resistor_1 (.node(CLK));
  Multiplexer #(.select(1), .width(5), .disabled("Z"), .enable("false")) multiplexer_5 (
    .in0(multiplexer_4_out), .in1({5{1'b1}}), .out(multiplexer_5_out), .sel(\单周期硬布线控制器_1_jal ));
  Multiplexer #(.select(1), .width(32), .disabled("Z"), .enable("false")) multiplexer_6 (
    .in0(bit_extender_1_out), .in1(bit_extender_2_out), .out(multiplexer_6_out), .sel(SignedExt));
  Multiplexer #(.select(1), .width(5), .disabled("Z"), .enable("false")) multiplexer_7 (
    .in0(ID_IR[25:21]), .in1(5'b00010), .out(multiplexer_7_out), .sel(\单周期硬布线控制器_1_syscall ));
  Multiplexer #(.select(1), .width(5), .disabled("Z"), .enable("false")) multiplexer_8 (
    .in0(ID_IR[20:16]), .in1(5'b00100), .out(multiplexer_8_out), .sel(\单周期硬布线控制器_1_syscall ));
  not not_2 (not_2_out, halt);
  \ID重定向控制逻辑  \id重定向控制逻辑_1  (
    .MEM_WriteReg_num(ex_mem_1_writereg_num_2), .EX_WriteReg_num(id_ex_1_writereg_num_2), .FwdA(FwdA),
    .FwdB(FwdB), .Stall(stall), .FlushID_EX(\id重定向控制逻辑_1_flushid_ex ), .FlushIF_ID(\id重定向控制逻辑_1_flushif_id ),
    .rs(multiplexer_7_out), .IR(ID_IR), .rt(multiplexer_8_out), .MEM_RegWrite(ex_mem_1_regwrite_2),
    .EX_RegWrite(id_ex_1_regwrite_2), .EX_MemRead(id_ex_1_memtoreg_2), .\跳转 (\跳转 ));
  MIPS_Regifile mips_regifile_1 (
    .Din(RDin), .Clk(not_3_out), .R1(mips_regifile_1_r1), .R2(mips_regifile_1_r2), .WE(RegWrite),
    .W_num(mem_wb_1_writereg_num_2), .R1_num(multiplexer_7_out), .R2_num(multiplexer_8_out));
  not not_3 (not_3_out, CLK);
  Comparator #(.width(32), .mode("twosComplement")) comparator_2 (
    .a(r_v0), .b(32'h22), .eq(comparator_2_eq));  // open: gt, lt
  Multiplexer #(.select(2), .width(32), .disabled("Z"), .enable("false")) multiplexer_9 (
    .in0(mips_regifile_1_r1), .in1(ex_mem_1_result_2), .in2(mips_alu_1_result), .out(RS), .sel(FwdA));  // open: in3
  Multiplexer #(.select(2), .width(32), .disabled("Z"), .enable("false")) multiplexer_10 (
    .in0(mips_regifile_1_r2), .in1(ex_mem_1_result_2), .in2(mips_alu_1_result), .out(RT), .sel(FwdB));  // open: in3
  Counter #(.width(16), .max('hffff), .ongoal("wrap"), .trigger("rising"), .behavior("new")) counter_3 (
    .count(not_2_out), .Q(\总周期数 ), .clk(CLK));  // open: load, D, carry, clr, preset, down
  ID_EX id_ex_1 (
    .JR(jr), .JMP(jmp), .Beq(beq), .Bne(bne), .MemToReg(\单周期硬布线控制器_1_memtoreg ),
    .MemWrite(\单周期硬布线控制器_1_memwrite ), .ALU_OP(\单周期硬布线控制器_1_alu_op ), .ALU_SRC(\单周期硬布线控制器_1_alu_src ),
    .RegWrite(\单周期硬布线控制器_1_regwrite ), .JAL(\单周期硬布线控制器_1_jal ), .SysCALL(\单周期硬布线控制器_1_syscall ), .RS(RS),
    .RT(RT), .WriteReg_num(multiplexer_5_out), .ZeroImm(multiplexer_6_out), .IR_ID(ID_IR), .PC_ID(ID_PC),
    .JR_2(id_ex_1_jr_2), .JMP_2(id_ex_1_jmp_2), .MemToReg_2(id_ex_1_memtoreg_2),
    .MemWrite_2(id_ex_1_memwrite_2), .ALU_OP_2(id_ex_1_alu_op_2), .ALU_SRC_2(id_ex_1_alu_src_2),
    .RegWrite_2(id_ex_1_regwrite_2), .JAL_2(id_ex_1_jal_2), .SysCALL_2(id_ex_1_syscall_2),
    .RS_2(id_ex_1_rs_2), .RT_2(id_ex_1_rt_2), .WriteReg_num_2(id_ex_1_writereg_num_2),
    .ZeroImm_2(id_ex_1_zeroimm_2), .IR_EX(EX_IR), .PC_EX(EX_PC), .EN(or_2_out), .CLK(CLK),
    .RST(\id重定向控制逻辑_1_flushid_ex ), .UnSignImm(bit_extender_2_out), .FwdA(FwdA), .FwdB(FwdB),
    .FwdA_2(id_ex_1_fwda_2), .FwdB_2(id_ex_1_fwdb_2));  // open: Beq_2, Bne_2, UnSignImm_2
  and and_2 (led_en, syscall, comparator_2_eq);
  and and_3 (halt, syscall, ~comparator_2_eq);  // AND_Gate
  Adder #(.width(32)) adder_2 (.a(32'h4), .b(ID_PC), .out(ID_PC_4));  // open: cin, cout
  Multiplexer #(.select(2), .width(32), .disabled("Z"), .enable("false")) multiplexer_11 (
    .in0(id_ex_1_rs_2), .in1(RDin), .in2(ex_mem_1_result_2), .out(multiplexer_11_out), .sel(id_ex_1_fwda_2));  // open: in3
  Multiplexer #(.select(2), .width(32), .disabled("Z"), .enable("false")) multiplexer_12 (
    .in0(id_ex_1_rt_2), .in1(RDin), .in2(ex_mem_1_result_2), .out(multiplexer_12_out), .sel(id_ex_1_fwdb_2));  // open: in3
  Shifter #(.width(32), .shift("ll")) shifter_1 (.in(bit_extender_2_out), .\dist (5'b00010), .out(shifter_1_out));
  Multiplexer #(.select(1), .width(32), .disabled("Z"), .enable("false")) multiplexer_13 (
    .in0(multiplexer_12_out), .in1(id_ex_1_zeroimm_2), .out(multiplexer_13_out), .sel(id_ex_1_alu_src_2));
  Register #(.width(32), .trigger("rising"), .Select("low")) register_2 (
    .D(MDin), .en(led_en), .Q(LedData), .clk(CLK));  // open: clr
  MIPS_ALU mips_alu_1 (
    .X(multiplexer_11_out), .Y(multiplexer_13_out), .AluOP(id_ex_1_alu_op_2), .Result(mips_alu_1_result),
    .shamt(EX_IR[10:6]));  // open: Equal, Result_2
  Adder #(.width(32)) adder_3 (.a(shifter_1_out), .b(ID_PC_4), .out(\beq跳转 ));  // open: cin, cout
  EX_MEM ex_mem_1 (
    .JR(id_ex_1_jr_2), .JMP(id_ex_1_jmp_2), .MemToReg(id_ex_1_memtoreg_2), .MemWrite(id_ex_1_memwrite_2),
    .RegWrite(id_ex_1_regwrite_2), .JAL(id_ex_1_jal_2), .SysCALL(id_ex_1_syscall_2),
    .RESULT(mips_alu_1_result), .WriteData(multiplexer_12_out), .WriteReg_num(id_ex_1_writereg_num_2),
    .IR_ID(EX_IR), .PC_ID(EX_PC), .JR_2(ex_mem_1_jr_2), .JMP_2(ex_mem_1_jmp_2),
    .MemToReg_2(ex_mem_1_memtoreg_2), .MemWrite_2(MemWrite), .RegWrite_2(ex_mem_1_regwrite_2),
    .JAL_2(ex_mem_1_jal_2), .SysCALL_2(ex_mem_1_syscall_2), .RESULT_2(ex_mem_1_result_2), .WriteData_2(MDin),
    .WriteReg_num_2(ex_mem_1_writereg_num_2), .IR_EX(MEM_IR), .PC_EX(M_PC), .EN(or_2_out), .CLK(CLK),
    .r_v0(multiplexer_11_out), .r_v0_2(ex_mem_1_r_v0_2));  // open: RST
  RAM #(.addrWidth(10), .dataWidth(32), .bus("separate"), .Select("high")) ram_1 (
    .addr(ex_mem_1_result_2[11:2]), .din(MDin), .data(ram_1_data), .str(MemWrite), .clk(CLK));  // open: sel, ld, clr
  Multiplexer #(.select(2), .width(5), .disabled("Z"), .enable("false")) multiplexer_14 (
    .in0({5{1'b0}}), .in1(5'b01000), .in2(5'b10000), .in3(5'b11000), .out(multiplexer_14_out), .sel(Address));
  Multiplexer #(.select(2), .width(32), .disabled("Z"), .enable("false")) multiplexer_15 (
    .in0(32'hff), .in1(32'hff00), .in2(32'hff0000), .in3(32'hff000000), .out(multiplexer_15_out),
    .sel(Address));
  MEM_WB mem_wb_1 (
    .JR(ex_mem_1_jr_2), .JMP(ex_mem_1_jmp_2), .MemToReg(ex_mem_1_memtoreg_2), .RegWrite(ex_mem_1_regwrite_2),
    .JAL(ex_mem_1_jal_2), .SysCALL(ex_mem_1_syscall_2), .RESULT(ex_mem_1_result_2), .RD(ram_1_data),
    .WriteReg_num(ex_mem_1_writereg_num_2), .IR_ID(MEM_IR), .PC_ID(M_PC), .MemToReg_2(mem_wb_1_memtoreg_2),
    .RegWrite_2(RegWrite), .JAL_2(mem_wb_1_jal_2), .SysCALL_2(syscall), .RESULT_2(mem_wb_1_result_2),
    .RD_2(mem_wb_1_rd_2), .WriteReg_num_2(mem_wb_1_writereg_num_2), .IR_EX(WB_IR), .PC_EX(WB_PC),
    .EN(or_2_out), .CLK(CLK), .r_v0(ex_mem_1_r_v0_2), .r_v0_2(r_v0));  // open: JR_2, JMP_2, RST
  Shifter #(.width(32), .shift("ll")) shifter_2 (.in(MDin), .\dist (multiplexer_14_out), .out(shifter_2_out));
  assign and_4_out = MDout & ~multiplexer_15_out;  // AND_Gate and_4, 32 bits wide
  Multiplexer #(.select(1), .width(32), .disabled("Z"), .enable("false")) multiplexer_16 (
    .in0(mem_wb_1_result_2), .in1(mem_wb_1_rd_2), .out(multiplexer_16_out), .sel(mem_wb_1_memtoreg_2));
  assign MDinByte = shifter_2_out | and_4_out;  // OR_Gate or_3, 32 bits wide
  or or_4 (\跳转 , branch, jmp);
  Adder #(.width(32)) adder_4 (.a(WB_PC), .b(32'h4), .out(adder_4_out));  // open: cin, cout
  or or_5 (branch, and_6_out, and_5_out);
  Multiplexer #(.select(1), .width(32), .disabled("Z"), .enable("false")) multiplexer_17 (
    .in0(multiplexer_16_out), .in1(adder_4_out), .out(RDin), .sel(mem_wb_1_jal_2));
  and and_5 (and_5_out, beq, comparator_3_eq);
  Comparator #(.width(32), .mode("twosComplement")) comparator_3 (
    .a(RS), .b(RT), .eq(comparator_3_eq));  // open: gt, lt
  and and_6 (and_6_out, ~comparator_3_eq, bne);  // AND_Gate

  // Other names for the same wires on the sheet: MEM_PC[31:0] = M_PC

  // Notes on the sheet:
  //   中断源
  //   时空图监测，可删除
  //   中断等待指示
  //   数码管输出
  //   指令存储器
  //   控制位
  //   contents of rom_1 (hex, n*v repeats v):
  //   20110001 8000c05 20110001 20120002 20130003 8000c09 20110001 20120002 20130003 8000c0d 20110001
  //   20120002 20130003 8000c11 20110001 20120002 20130003 c000cb8 20100001 20110001 118fc0 112020
  //   20020022 c 118882 12200001 8000c15 112020 20020022 c 20110001 118880 112020 20020022 c 12200001
  //   8000c1f 20110001 118fc0 112020 20020022 c 1188c3 112020 20020022 c 118903 112020 20020022 c 118903
  //   112020 20020022 c 118903 112020 20020022 c 118903 112020 20020022 c 118903 112020 20020022 c 118903
  //   112020 20020022 c 118903 112020 20020022 c 20100001 109fc0 139fc3 8021 2012000c 24160003 26100001
  //   3210000f 20080008 20090001 139900 2709825 132020 20020022 c 1094022 1500fff9 22100001 2018000f
  //   2188024 108700 20080008 20090001 139902 2709825 132021 20020022 c 1094022 1500fff9 108702 2c9b022
  //   12c00001 8000c50 4020 1084027 84400 3508ffff 82021 20020022 c 2010ffff 20110000 ae300000 22100001
  //   22310004 ae300000 22100001 22310004 ae300000 22100001 22310004 ae300000 22100001 22310004 ae300000
  //   22100001 22310004 ae300000 22100001 22310004 ae300000 22100001 22310004 ae300000 22100001 22310004
  //   ae300000 22100001 22310004 ae300000 22100001 22310004 ae300000 22100001 22310004 ae300000 22100001
  //   22310004 ae300000 22100001 22310004 ae300000 22100001 22310004 ae300000 22100001 22310004 ae300000
  //   22100001 22310004 22100001 8020 2011003c 8e130000 8e340000 274402a 11000002 ae330000 ae140000
  //   2231fffc 1611fff8 102020 20020022 c 22100004 2011003c 1611fff2 20020032 c 20100000 22100001 102020
  //   20020022 c 22100002 102020 20020022 c 22100003 102020 20020022 c 22100004 102020 20020022 c 22100005
  //   102020 20020022 c 22100006 102020 20020022 c 22100007 102020 20020022 c 22100008 102020 20020022
  //   20020022 c 3e00008
  //   流水调试日志用
  //   暂停节拍，不能为0
  //   戳工具置1进入计数暂停模式，ctrl+k时钟自动运行到对应节拍暂停
  //   ctrl+k关闭时钟连续运行，将控制位置零，进入单步调试模式调试
  //   OP
  //   rs
  //   rt
  //   rd
  //   JMP
  //   JR
  //   OP
  //   Func
  //   Func
  //   可计数暂停的时钟源
  //   Beq
  //   Bne
  //   MemToReg
  //   MemWrite
  //   AluOP
  //   AluSrcB
  //   RegWrite
  //   JAL
  //   RegDst
  //   Syscall
  //   为方便自动评测，需要输出流水线各段保存的PC值，注意是PC不是PC+4，另外ID段寄存器写入信息，Mem段内存写入信息也要输出
endmodule
module \EX重定向  (
  output RegWrite,
  output MemWrite,
  output [31:0] IF_PC,
  output [31:0] ID_PC,
  output [31:0] EX_PC,
  output [31:0] M_PC,
  output [31:0] WB_PC,
  output [31:0] RDin,
  output [31:0] MDin,
  output [31:0] LedData
);

  wire and_1_out, and_4_out, and_5_out, BGTZ, branch, CLK, clock_1_out, clock_2_out, comparator_1_eq,
       comparator_1_lt, comparator_2_eq, d_ff_1_q, EX_BGTZ, ex_mem_1_jal_2, ex_mem_1_jmp_2, ex_mem_1_jr_2,
       ex_mem_1_memtoreg_2, ex_mem_1_regwrite_2, ex_mem_1_syscall_2, EX_MEM_EN, EX_MEM_RST, EX_SB, EX_SRAV,
       \ex重定向控制逻辑_1_flushif_id , Go, halt, ID_BGTZ, id_ex_1_alu_src_2, id_ex_1_beq_2, id_ex_1_bne_2,
       id_ex_1_jal_2, id_ex_1_memtoreg_2, id_ex_1_memwrite_2, id_ex_1_regwrite_2, id_ex_1_syscall_2,
       ID_EX_RST, ID_SB, ID_SRAV, IR1, IR2, IR3, jmp, jr, led_en, MEM_SB, mem_wb_1_jal_2,
       mem_wb_1_memtoreg_2, mips_alu_1_equal, multiplexer_9_out, multiplexer_10_out, multiplexer_11_out,
       multiplexer_17_out, nand_1_out, not_1_out, not_2_out, not_3_out, or_1_out, or_2_out, or_4_out,
       or_6_out, RST, SignedExt, stall, syscall, W1, W2, W3, \单周期硬布线控制器_1_alu_src , \单周期硬布线控制器_1_beq ,
       \单周期硬布线控制器_1_bne , \单周期硬布线控制器_1_jal , \单周期硬布线控制器_1_jmp , \单周期硬布线控制器_1_jr , \单周期硬布线控制器_1_memtoreg ,
       \单周期硬布线控制器_1_memwrite , \单周期硬布线控制器_1_regdst , \单周期硬布线控制器_1_regwrite , \单周期硬布线控制器_1_syscall ;
  wire [1:0] FwdA, FwdB, id_ex_1_fwda_2, id_ex_1_fwdb_2;
  wire [3:0] id_ex_1_alu_op_2, \单周期硬布线控制器_1_alu_op ;
  wire [4:0] ex_mem_1_writereg_num_2, id_ex_1_writereg_num_2, mem_wb_1_writereg_num_2, multiplexer_4_out,
       multiplexer_5_out, multiplexer_7_out, multiplexer_8_out, multiplexer_18_out, shamt;
  wire [12:0] CNT_num;
  wire [15:0] \LoadUse次数 , \总周期数 , \插入气泡数 , \无条件分支数 , \条件分支成功数 ;
  wire [31:0] adder_4_out, Address, aluresult, and_6_out, \beq跳转 , bit_extender_1_out, bit_extender_2_out,
       EX_IR, ex_mem_1_r_v0_2, EX_PC_4, id_ex_1_rs_2, id_ex_1_rt_2, id_ex_1_unsignimm_2, id_ex_1_zeroimm_2,
       ID_IR, IF_IR, MDinByte, MDout, MEM_IR, mem_wb_1_rd_2, mem_wb_1_result_2, mips_regifile_1_r1,
       mips_regifile_1_r2, multiplexer_1_out, multiplexer_2_out, multiplexer_3_out, multiplexer_6_out,
       multiplexer_13_out, multiplexer_15_out, multiplexer_19_out, multiplexer_20_out, PC_4, r_v0, Real_MDin,
       register_2_q, rs, shifter_1_out, shifter_2_out, WB_IR;

  Button \u_总复位  (.out(RST));
  Button _1 (.out(IR1));
  Button _2 (.out(IR2));
  Button _3 (.out(IR3));
  // Probe on \总周期数 
  // Probe on \总周期数 
  Button \u_继续运行  (.out(Go));
  LED #(.active("true")) led_1 (.in(W1));
  LED #(.active("true")) led_2 (.in(W2));
  LED #(.active("true")) led_3 (.in(W3));
  Hex_Digit_Display hex_digit_display_1 (.value(LedData[31:28]));  // open: dp
  // Probe on nothing
  // Mips_Probe mips_probe_1: pin names not known; wires that end beside it: IF_IR
  Hex_Digit_Display hex_digit_display_2 (.value(LedData[27:24]));  // open: dp
  Hex_Digit_Display hex_digit_display_3 (.value(LedData[23:20]));  // open: dp
  // Probe on nothing
  // Mips_Probe mips_probe_2: pin names not known; wires that end beside it: ID_IR
  or or_1 (or_1_out, branch, BGTZ);
  Multiplexer #(.select(1), .width(32), .disabled("Z"), .enable("false")) multiplexer_1 (
    .in0(PC_4), .in1(\beq跳转 ), .out(multiplexer_1_out), .sel(or_1_out));
  Hex_Digit_Display hex_digit_display_4 (.value(LedData[19:16]));  // open: dp
  Hex_Digit_Display hex_digit_display_5 (.value(LedData[15:12]));  // open: dp
  Hex_Digit_Display hex_digit_display_6 (.value(LedData[7:4]));  // open: dp
  Hex_Digit_Display hex_digit_display_7 (.value(LedData[11:8]));  // open: dp
  Clock #(.highDuration(1), .lowDuration(1)) clock_1 (.out(clock_1_out));
  // Probe on nothing
  // Mips_Probe mips_probe_3: pin names not known; wires that end beside it: EX_IR, clock_1_out, CLK
  Multiplexer #(.select(1), .width(32), .disabled("Z"), .enable("false")) multiplexer_2 (
    .in0(multiplexer_1_out), .in1({EX_PC_4[31:28], EX_IR[25:0], 2'b00}), .out(multiplexer_2_out), .sel(jmp));
  not not_1 (not_1_out, stall);
  Hex_Digit_Display hex_digit_display_8 (.value(LedData[3:0]));  // open: dp
  Multiplexer #(.select(1), .width(32), .disabled("Z"), .enable("false")) multiplexer_3 (
    .in0(multiplexer_2_out), .in1(rs), .out(multiplexer_3_out), .sel(jr));
  and and_1 (and_1_out, not_1_out, or_2_out);
  or or_2 (or_2_out, ~halt, Go);  // OR_Gate
  // Probe on \总周期数 
  // Probe on nothing
  // Mips_Probe mips_probe_4: pin names not known; wires that end beside it: MEM_IR
  Register #(.width(32), .trigger("rising"), .Select("low")) register_1 (
    .D(multiplexer_3_out), .en(and_1_out), .Q(IF_PC), .clk(CLK));  // open: clr
  // Probe on \总周期数 
  // Probe on \无条件分支数 
  // Probe on \条件分支成功数 
  // Probe on \插入气泡数 
  // Probe on \LoadUse次数 
  Adder #(.width(32)) adder_1 (.a(IF_PC), .b(32'h4), .out(PC_4));  // open: cin, cout
  // Probe on IF_PC[11:0]
  // Probe on nothing
  // Mips_Probe mips_probe_5: pin names not known; wires that end beside it: WB_IR
  Counter #(.width(8), .max('hff), .ongoal("wrap"), .trigger("rising"), .behavior("new")) counter_1 (.clk(\ex重定向控制逻辑_1_flushif_id ));  // open: load, D, count, Q, carry, clr, preset, down
  // Probe on ID_PC[11:0]
  // Probe on EX_PC[11:0]
  ROM #(.addrWidth(10), .dataWidth(32), .Select("high")) rom_1 (.addr(IF_PC[11:2]), .data(IF_IR));
  // Probe on IF_PC
  // Probe on M_PC[11:0]
  D_Flip_Flop #(.trigger("high"), .Pre_Clr_Positions("LEGACY"), .NegatePresetClear("false"), .enable("true"), .NewFFLayout("false")) d_ff_1 (.Q(d_ff_1_q));  // open: clk, D, Qn, preset, en, reset
  // Probe on 13'h372
  // Mips_Probe mips_probe_6: pin names not known; wires that end beside it: IF_IR
  // Probe on WB_PC[11:0]
  Comparator #(.width(13), .mode("twosComplement")) comparator_1 (
    .a(CNT_num), .b(13'h372), .eq(comparator_1_eq), .lt(comparator_1_lt));  // open: gt
  Clock #(.highDuration(1), .lowDuration(1)) clock_2 (.out(clock_2_out));
  IF_ID if_id_1 (
    .IR_IF(IF_IR), .PC_IF(IF_PC), .IR_ID(ID_IR), .PC_ID(ID_PC), .EN(and_1_out), .CLK(CLK),
    .RST(\ex重定向控制逻辑_1_flushif_id ));
  nand nand_1 (nand_1_out, d_ff_1_q, comparator_1_eq);
  Counter #(.width(13), .max('h1fff), .ongoal("stay"), .trigger("rising"), .behavior("old")) counter_2 (
    .count(comparator_1_lt), .Q(CNT_num), .clk(clock_2_out));  // open: load, D, carry, clr, preset
  Multiplexer #(.select(1), .width(5), .disabled("Z"), .enable("false")) multiplexer_4 (
    .in0(ID_IR[20:16]), .in1(ID_IR[15:11]), .out(multiplexer_4_out), .sel(\单周期硬布线控制器_1_regdst ));
  or or_3 (EX_MEM_EN, ~halt, Go);  // OR_Gate
  assign CLK = nand_1_out ? clock_2_out : 1'bz;  // Controlled_Buffer controlled_buffer_1
  \单周期硬布线控制器  \u_单周期硬布线控制器_1  (
    .Func(ID_IR[5:0]), .OP(ID_IR[31:26]), .ALU_OP(\单周期硬布线控制器_1_alu_op ), .MemToReg(\单周期硬布线控制器_1_memtoreg ),
    .MemWrite(\单周期硬布线控制器_1_memwrite ), .ALU_SRC(\单周期硬布线控制器_1_alu_src ), .RegWrite(\单周期硬布线控制器_1_regwrite ),
    .SysCALL(\单周期硬布线控制器_1_syscall ), .SignedExt(SignedExt), .RegDst(\单周期硬布线控制器_1_regdst ),
    .JR(\单周期硬布线控制器_1_jr ), .JMP(\单周期硬布线控制器_1_jmp ), .Beq(\单周期硬布线控制器_1_beq ), .JAL(\单周期硬布线控制器_1_jal ),
    .Bne(\单周期硬布线控制器_1_bne ), .BGTZ(ID_BGTZ), .SRAV(ID_SRAV), .SB(ID_SB));
  assign bit_extender_1_out = {{16{1'b0}}, ID_IR[15:0]};  // Bit_Extender bit_extender_1
  assign bit_extender_2_out = {{16{ID_IR[15]}}, ID_IR[15:0]};  // Bit_Extender bit_extender_2
  Pull_Resistor #(.pull(1)) pull_resistor_1 (.node(CLK));
  Multiplexer #(.select(1), .width(5), .disabled("Z"), .enable("false")) multiplexer_5 (
    .in0(multiplexer_4_out), .in1({5{1'b1}}), .out(multiplexer_5_out), .sel(\单周期硬布线控制器_1_jal ));
  Multiplexer #(.select(1), .width(32), .disabled("Z"), .enable("false")) multiplexer_6 (
    .in0(bit_extender_1_out), .in1(bit_extender_2_out), .out(multiplexer_6_out), .sel(SignedExt));
  Multiplexer #(.select(1), .width(5), .disabled("Z"), .enable("false")) multiplexer_7 (
    .in0(ID_IR[25:21]), .in1(5'b00010), .out(multiplexer_7_out), .sel(\单周期硬布线控制器_1_syscall ));
  Multiplexer #(.select(1), .width(5), .disabled("Z"), .enable("false")) multiplexer_8 (
    .in0(ID_IR[20:16]), .in1(5'b00100), .out(multiplexer_8_out), .sel(\单周期硬布线控制器_1_syscall ));
  not not_2 (not_2_out, halt);
  \EX重定向控制逻辑  \ex重定向控制逻辑_1  (
    .MEM_WriteReg_num(ex_mem_1_writereg_num_2), .EX_WriteReg_num(id_ex_1_writereg_num_2), .FwdA(FwdA),
    .FwdB(FwdB), .Stall(stall), .FlushID_EX(ID_EX_RST), .FlushIF_ID(\ex重定向控制逻辑_1_flushif_id ),
    .rs(multiplexer_7_out), .IR(ID_IR), .rt(multiplexer_8_out), .MEM_RegWrite(ex_mem_1_regwrite_2),
    .EX_RegWrite(id_ex_1_regwrite_2), .EX_MemRead(id_ex_1_memtoreg_2), .branch(or_4_out));
  MIPS_Regifile mips_regifile_1 (
    .Din(RDin), .Clk(not_3_out), .R1(mips_regifile_1_r1), .R2(mips_regifile_1_r2), .WE(RegWrite),
    .W_num(mem_wb_1_writereg_num_2), .R1_num(multiplexer_7_out), .R2_num(multiplexer_8_out));
  not not_3 (not_3_out, CLK);
  Comparator #(.width(32), .mode("twosComplement")) comparator_2 (
    .a(r_v0), .b(32'h22), .eq(comparator_2_eq));  // open: gt, lt
  Counter #(.width(16), .max('hffff), .ongoal("wrap"), .trigger("rising"), .behavior("new")) counter_3 (
    .count(not_2_out), .Q(\总周期数 ), .clk(CLK));  // open: load, D, carry, clr, preset, down
  ID_EX id_ex_1 (
    .JR(\单周期硬布线控制器_1_jr ), .JMP(\单周期硬布线控制器_1_jmp ), .Beq(\单周期硬布线控制器_1_beq ), .Bne(\单周期硬布线控制器_1_bne ),
    .MemToReg(\单周期硬布线控制器_1_memtoreg ), .MemWrite(\单周期硬布线控制器_1_memwrite ), .ALU_OP(\单周期硬布线控制器_1_alu_op ),
    .ALU_SRC(\单周期硬布线控制器_1_alu_src ), .RegWrite(\单周期硬布线控制器_1_regwrite ), .JAL(\单周期硬布线控制器_1_jal ),
    .SysCALL(\单周期硬布线控制器_1_syscall ), .RS(mips_regifile_1_r1), .RT(mips_regifile_1_r2),
    .WriteReg_num(multiplexer_5_out), .ZeroImm(multiplexer_6_out), .IR_ID(ID_IR), .PC_ID(ID_PC), .JR_2(jr),
    .JMP_2(jmp), .Beq_2(id_ex_1_beq_2), .Bne_2(id_ex_1_bne_2), .MemToReg_2(id_ex_1_memtoreg_2),
    .MemWrite_2(id_ex_1_memwrite_2), .ALU_OP_2(id_ex_1_alu_op_2), .ALU_SRC_2(id_ex_1_alu_src_2),
    .RegWrite_2(id_ex_1_regwrite_2), .JAL_2(id_ex_1_jal_2), .SysCALL_2(id_ex_1_syscall_2),
    .RS_2(id_ex_1_rs_2), .RT_2(id_ex_1_rt_2), .WriteReg_num_2(id_ex_1_writereg_num_2),
    .ZeroImm_2(id_ex_1_zeroimm_2), .IR_EX(EX_IR), .PC_EX(EX_PC), .EN(EX_MEM_EN), .CLK(CLK), .RST(ID_EX_RST),
    .UnSignImm(bit_extender_2_out), .UnSignImm_2(id_ex_1_unsignimm_2), .FwdA(FwdA), .FwdB(FwdB),
    .FwdA_2(id_ex_1_fwda_2), .FwdB_2(id_ex_1_fwdb_2));
  and and_2 (led_en, syscall, comparator_2_eq);
  and and_3 (halt, syscall, ~comparator_2_eq);  // AND_Gate
  Pull_Resistor #(.pull(0)) pull_resistor_2 (.node(ID_EX_RST));
  or or_4 (or_4_out, branch, BGTZ, or_6_out);
  Adder #(.width(32)) adder_2 (.a(32'h4), .b(EX_PC), .out(EX_PC_4));  // open: cin, cout
  Multiplexer #(.select(1), .width(1), .disabled("Z"), .enable("false")) multiplexer_9 (
    .in0(ID_BGTZ), .in1(1'b0), .out(multiplexer_9_out), .sel(ID_EX_RST));
  Multiplexer #(.select(1), .width(1), .disabled("Z"), .enable("false")) multiplexer_10 (
    .in0(ID_SB), .in1(1'b0), .out(multiplexer_10_out), .sel(ID_EX_RST));
  Multiplexer #(.select(1), .width(1), .disabled("Z"), .enable("false")) multiplexer_11 (
    .in0(ID_SRAV), .in1(1'b0), .out(multiplexer_11_out), .sel(ID_EX_RST));
  or or_5 (branch, and_5_out, and_4_out);
  or or_6 (or_6_out, jmp, jr, id_ex_1_jal_2);
  Multiplexer #(.select(2), .width(32), .disabled("Z"), .enable("false")) multiplexer_12 (
    .in0(id_ex_1_rs_2), .in1(RDin), .in2(Address), .out(rs), .sel(id_ex_1_fwda_2));  // open: in3
  Multiplexer #(.select(2), .width(32), .disabled("Z"), .enable("false")) multiplexer_13 (
    .in0(id_ex_1_rt_2), .in1(RDin), .in2(Address), .out(multiplexer_13_out), .sel(id_ex_1_fwdb_2));  // open: in3
  Shifter #(.width(32), .shift("ll")) shifter_1 (.in(id_ex_1_unsignimm_2), .\dist (5'b00010), .out(shifter_1_out));
  Multiplexer #(.select(1), .width(5), .disabled("Z"), .enable("false")) multiplexer_14 (
    .in0(EX_IR[10:6]), .in1(rs[4:0]), .out(shamt), .sel(EX_SRAV));
  and and_4 (and_4_out, id_ex_1_beq_2, mips_alu_1_equal);
  Multiplexer #(.select(1), .width(32), .disabled("Z"), .enable("false")) multiplexer_15 (
    .in0(multiplexer_13_out), .in1(id_ex_1_zeroimm_2), .out(multiplexer_15_out), .sel(id_ex_1_alu_src_2));
  Register #(.width(32), .trigger("rising"), .Select("low")) register_2 (
    .D(MDin), .Q(register_2_q), .clk(CLK));  // open: en, clr
  Register #(.width(32), .trigger("rising"), .Select("low")) register_3 (
    .D(register_2_q), .en(led_en), .Q(LedData), .clk(CLK));  // open: clr
  Register #(.width(1), .trigger("rising"), .Select("low")) register_4 (
    .D(multiplexer_9_out), .en(EX_MEM_EN), .Q(EX_BGTZ), .clk(CLK));  // open: clr
  Register #(.width(1), .trigger("rising"), .Select("low")) register_5 (
    .D(multiplexer_10_out), .en(EX_MEM_EN), .Q(EX_SB), .clk(CLK));  // open: clr
  Register #(.width(1), .trigger("rising"), .Select("low")) register_6 (
    .D(multiplexer_11_out), .en(EX_MEM_EN), .Q(EX_SRAV), .clk(CLK));  // open: clr
  and and_5 (and_5_out, ~mips_alu_1_equal, id_ex_1_bne_2);  // AND_Gate
  MIPS_ALU mips_alu_1 (
    .X(rs), .Y(multiplexer_15_out), .AluOP(id_ex_1_alu_op_2), .Equal(mips_alu_1_equal), .Result(aluresult),
    .shamt(shamt));  // open: Result_2
  Adder #(.width(32)) adder_3 (.a(shifter_1_out), .b(EX_PC_4), .out(\beq跳转 ));  // open: cin, cout
  Multiplexer #(.select(1), .width(32), .disabled("Z"), .enable("false")) multiplexer_16 (
    .in0(MDin), .in1(MDinByte), .out(Real_MDin), .sel(MEM_SB));
  EX_MEM ex_mem_1 (
    .JR(jr), .JMP(jmp), .MemToReg(id_ex_1_memtoreg_2), .MemWrite(id_ex_1_memwrite_2),
    .RegWrite(id_ex_1_regwrite_2), .JAL(id_ex_1_jal_2), .SysCALL(id_ex_1_syscall_2), .RESULT(aluresult),
    .WriteData(multiplexer_13_out), .WriteReg_num(id_ex_1_writereg_num_2), .IR_ID(EX_IR), .PC_ID(EX_PC),
    .JR_2(ex_mem_1_jr_2), .JMP_2(ex_mem_1_jmp_2), .MemToReg_2(ex_mem_1_memtoreg_2), .MemWrite_2(MemWrite),
    .RegWrite_2(ex_mem_1_regwrite_2), .JAL_2(ex_mem_1_jal_2), .SysCALL_2(ex_mem_1_syscall_2),
    .RESULT_2(Address), .WriteData_2(MDin), .WriteReg_num_2(ex_mem_1_writereg_num_2), .IR_EX(MEM_IR),
    .PC_EX(M_PC), .EN(EX_MEM_EN), .CLK(CLK), .r_v0(rs), .r_v0_2(ex_mem_1_r_v0_2));  // open: RST
  Multiplexer #(.select(1), .width(1), .disabled("Z"), .enable("false")) multiplexer_17 (
    .in0(EX_SB), .in1(1'b0), .out(multiplexer_17_out), .sel(EX_MEM_RST));
  Pull_Resistor #(.pull(0)) pull_resistor_3 (.node(EX_MEM_RST));
  RAM #(.addrWidth(10), .dataWidth(32), .bus("separate"), .Select("high")) ram_1 (
    .addr(Address[11:2]), .din(Real_MDin), .data(MDout), .str(MemWrite), .clk(CLK));  // open: sel, ld, clr
  Multiplexer #(.select(2), .width(5), .disabled("Z"), .enable("false")) multiplexer_18 (
    .in0({5{1'b0}}), .in1(5'b01000), .in2(5'b10000), .in3(5'b11000), .out(multiplexer_18_out),
    .sel(Address[1:0]));
  Multiplexer #(.select(2), .width(32), .disabled("Z"), .enable("false")) multiplexer_19 (
    .in0(32'hff), .in1(32'hff00), .in2(32'hff0000), .in3(32'hff000000), .out(multiplexer_19_out),
    .sel(Address[1:0]));
  Register #(.width(1), .trigger("rising"), .Select("low")) register_7 (
    .D(multiplexer_17_out), .en(EX_MEM_EN), .Q(MEM_SB), .clk(CLK));  // open: clr
  Shifter #(.width(32), .shift("ll")) shifter_2 (.in(MDin), .\dist (multiplexer_18_out), .out(shifter_2_out));
  MEM_WB mem_wb_1 (
    .JR(ex_mem_1_jr_2), .JMP(ex_mem_1_jmp_2), .MemToReg(ex_mem_1_memtoreg_2), .RegWrite(ex_mem_1_regwrite_2),
    .JAL(ex_mem_1_jal_2), .SysCALL(ex_mem_1_syscall_2), .RESULT(Address), .RD(MDout),
    .WriteReg_num(ex_mem_1_writereg_num_2), .IR_ID(MEM_IR), .PC_ID(M_PC), .MemToReg_2(mem_wb_1_memtoreg_2),
    .RegWrite_2(RegWrite), .JAL_2(mem_wb_1_jal_2), .SysCALL_2(syscall), .RESULT_2(mem_wb_1_result_2),
    .RD_2(mem_wb_1_rd_2), .WriteReg_num_2(mem_wb_1_writereg_num_2), .IR_EX(WB_IR), .PC_EX(WB_PC),
    .EN(EX_MEM_EN), .CLK(CLK), .r_v0(ex_mem_1_r_v0_2), .r_v0_2(r_v0));  // open: JR_2, JMP_2, RST
  assign MDinByte = shifter_2_out | and_6_out;  // OR_Gate or_7, 32 bits wide
  assign and_6_out = MDout & ~multiplexer_19_out;  // AND_Gate and_6, 32 bits wide
  and and_7 (BGTZ, ~aluresult[0], EX_BGTZ);  // AND_Gate
  Multiplexer #(.select(1), .width(32), .disabled("Z"), .enable("false")) multiplexer_20 (
    .in0(mem_wb_1_result_2), .in1(mem_wb_1_rd_2), .out(multiplexer_20_out), .sel(mem_wb_1_memtoreg_2));
  Adder #(.width(32)) adder_4 (.a(WB_PC), .b(32'h4), .out(adder_4_out));  // open: cin, cout
  Multiplexer #(.select(1), .width(32), .disabled("Z"), .enable("false")) multiplexer_21 (
    .in0(multiplexer_20_out), .in1(adder_4_out), .out(RDin), .sel(mem_wb_1_jal_2));

  // Other names for the same wires on the sheet: ID_EX_EN = EX_MEM_EN; MEM_PC[31:0] = M_PC

  // Notes on the sheet:
  //   中断源
  //   时空图监测，可删除
  //   中断等待指示
  //   数码管输出
  //   指令存储器
  //   控制位
  //   contents of rom_1 (hex, n*v repeats v):
  //   20110001 8000c05 20110001 20120002 20130003 8000c09 20110001 20120002 20130003 8000c0d 20110001
  //   20120002 20130003 8000c11 20110001 20120002 20130003 c000cf3 20100001 20110001 118fc0 112020
  //   20020022 c 118882 12200001 8000c15 112020 20020022 c 20110001 118880 112020 20020022 c 12200001
  //   8000c1f 20110001 118fc0 112020 20020022 c 1188c3 112020 20020022 c 118903 112020 20020022 c 118903
  //   112020 20020022 c 118903 112020 20020022 c 118903 112020 20020022 c 118903 112020 20020022 c 118903
  //   112020 20020022 c 118903 112020 20020022 c 20100001 109fc0 139fc3 8021 2012000c 24160003 26100001
  //   3210000f 20080008 20090001 139900 2709825 132020 20020022 c 1094022 1500fff9 22100001 2018000f
  //   2188024 108700 20080008 20090001 139902 2709825 132021 20020022 c 1094022 1500fff9 108702 2c9b022
  //   12c00001 8000c50 4020 1084027 84400 3508ffff 82021 20020022 c 2010ffff 20110000 ae300000 22100001
  //   22310004 ae300000 22100001 22310004 ae300000 22100001 22310004 ae300000 22100001 22310004 ae300000
  //   22100001 22310004 ae300000 22100001 22310004 ae300000 22100001 22310004 ae300000 22100001 22310004
  //   ae300000 22100001 22310004 ae300000 22100001 22310004 ae300000 22100001 22310004 ae300000 22100001
  //   22310004 ae300000 22100001 22310004 ae300000 22100001 22310004 ae300000 22100001 22310004 ae300000
  //   22100001 22310004 22100001 8020 2011003c 8e130000 8e340000 274402a 11000002 ae330000 ae140000
  //   2231fffc 1611fff8 102020 20020022 c 22100004 2011003c 1611fff2 20020032 c 20080001 20090003 20110876
  //   118d00 112020 20020022 c 200b0008 1118807 1318807 112020 20020022 c 216bffff 1560fff9 2002000a c
  //   2008ffff 20090000 20111997 112020 20020022 c 2288820 2e291949 1120fffa 2002000a c 20090000 200b0020
  //   20110000 20120001 a1310000 112020 20020022 c 2328820 21290001 216bffff 1560fff8 200b0008 20090000
  //   8d310000 112020 20020022 c 21290004 216bffff 1560fff9 2002000a c 2011000f 112020 20020022 c 2231ffff
  //   1e20fffb 2002000a c 20100000 22100001 102020 20020022 c 22100002 102020 20020022 c 22100003 102020
  //   20020022 c 22100004 102020 20020022 c 22100005 102020 20020022 c 22100006 102020 20020022 c 22100007
  //   102020 20020022 c 22100008 102020 20020022 20020022 c 3e00008
  //   流水调试日志用
  //   暂停节拍，不能为0
  //   戳工具置1进入计数暂停模式，ctrl+k时钟自动运行到对应节拍暂停
  //   ctrl+k关闭时钟连续运行，将控制位置零，进入单步调试模式调试
  //   OP
  //   rs
  //   rt
  //   rd
  //   JMP
  //   JR
  //   OP
  //   Func
  //   Func
  //   可计数暂停的时钟源
  //   Beq
  //   Bne
  //   MemToReg
  //   MemWrite
  //   AluOP
  //   AluSrcB
  //   RegWrite
  //   JAL
  //   RegDst
  //   Syscall
  //   为方便自动评测，需要输出流水线各段保存的PC值，注意是PC不是PC+4，另外ID段寄存器写入信息，Mem段内存写入信息也要输出
endmodule

module \中断按键参考电路  (
  input  \同步清零信号 ,
  output \与中断屏蔽位与 
);

  wire \_1号中断_out , and_1_out, clock_1_out, d_ff_1_q, or_1_out, or_2_out;

  Clock #(.highDuration(1), .lowDuration(1)) clock_1 (.out(clock_1_out));
  Button \_1号中断  (.out(\_1号中断_out ));
  LED #(.active("true")) \_1号中断等待指示灯  (.in(or_1_out));
  or or_1 (or_1_out, \与中断屏蔽位与 , d_ff_1_q);
  D_Flip_Flop #(.trigger("rising"), .Pre_Clr_Positions("LEGACY"), .NegatePresetClear("false"), .enable("true"), .NewFFLayout("false")) d_ff_1 (
    .clk(\_1号中断_out ), .D(1'b1), .Q(d_ff_1_q), .reset(\与中断屏蔽位与 ));  // open: Qn, preset, en
  or or_2 (or_2_out, d_ff_1_q, \与中断屏蔽位与 );
  and and_1 (and_1_out, or_2_out, ~\同步清零信号 );  // AND_Gate
  D_Flip_Flop #(.trigger("rising"), .Pre_Clr_Positions("LEGACY"), .NegatePresetClear("false"), .enable("true"), .NewFFLayout("false")) IR1 (
    .clk(clock_1_out), .D(and_1_out), .Q(\与中断屏蔽位与 ));  // open: Qn, preset, en, reset

  // Notes on the sheet:
  //   中断信号采样参考电路
  //   Reset 
endmodule

module \单周期MIPS_单级中断  (
  input  in_1,
  input  in_2,
  input  in_3,
  input  in_4,
  input  in_5,
  input  in_6,
  input  in_7,
  input  in_8,
  input  in_9,
  input  in_10,
  output out_11,
  output out_12,
  output [6:0] out_13,
  output [6:0] out_14,
  output [15:0] out_15,
  output [31:0] out_16
);

  wire and_1_out, and_6_out, and_7_out, and_8_out, and_9_out, and_10_out, and_11_out, and_12_out, and_13_out,
       and_14_out, and_15_out, and_16_out, and_17_out, CLR1, CLR2, CLR3, comparator_1_eq, comparator_2_eq,
       comparator_3_eq, comparator_4_eq, comparator_5_eq, comparator_6_eq, controlled_inverter_1_out,
       controlled_inverter_2_out, controlled_inverter_3_out, d_ff_1_q, d_ff_2_q, d_ff_3_q, d_ff_4_q,
       d_ff_5_q, d_ff_6_q, d_ff_7_q, d_ff_8_q, d_ff_9_q, d_ff_10_q, d_ff_11_q, d_ff_12_q, d_ff_13_q,
       d_ff_14_q, d_ff_15_q, d_ff_16_q, d_ff_17_q, d_ff_18_q, d_ff_19_q, eret, Go, halt, IE, INT, INT1,
       INT_Req, IR1, IRA, MemWrite, mips_alu_1_equal, not_1_out, not_2_out, not_3_out, not_4_out, or_1_out,
       or_3_out, or_4_out, or_6_out, or_8_out, RegWrite, SignedExt, syscall, W1, zi_en,
       \单周期硬布线控制器_1_alu_src , \单周期硬布线控制器_1_beq , \单周期硬布线控制器_1_bne , \单周期硬布线控制器_1_jal , \单周期硬布线控制器_1_jmp ,
       \单周期硬布线控制器_1_jr , \单周期硬布线控制器_1_memtoreg , \单周期硬布线控制器_1_regdst ;
  wire [1:0] InprogressInt, register_1_q;
  wire [3:0] priority_encoder_2_out, \单周期硬布线控制器_1_alu_op ;
  wire [4:0] multiplexer_7_out, multiplexer_9_out, multiplexer_10_out, multiplexer_11_out;
  wire [9:0] MAin, multiplexer_17_out;
  wire [15:0] \总周期数 ;
  wire [31:0] adder_2_out, bit_extender_1_out, bit_extender_2_out, INTADDR, IR, LedData, MDOUT,
       mips_alu_1_result, multiplexer_1_out, multiplexer_2_out, multiplexer_4_out, multiplexer_5_out,
       multiplexer_8_out, multiplexer_12_out, multiplexer_13_out, multiplexer_15_out, multiplexer_16_out, PC,
       PC_4, R_rs, RDin, shifter_1_out, \断点 , \返回地址 ;
  wire [31:7] MDin;

  Clock #(.highDuration(1), .lowDuration(1)) clock_1 (.out(out_12));
  Button \u_继续运行  (.out(Go));
  Hex_Digit_Display hex_digit_display_1 (.value(LedData[31:28]));  // open: dp
  Comparator #(.width(16), .mode("twosComplement")) comparator_1 (
    .a(16'h23b), .b(\总周期数 ), .eq(comparator_1_eq));  // open: gt, lt
  Comparator #(.width(16), .mode("twosComplement")) comparator_2 (
    .a(\总周期数 ), .b(16'h1), .eq(comparator_2_eq));  // open: gt, lt
  Comparator #(.width(16), .mode("twosComplement")) comparator_3 (
    .a(\总周期数 ), .b(16'h4), .eq(comparator_3_eq));  // open: gt, lt
  Comparator #(.width(16), .mode("twosComplement")) comparator_4 (
    .a(\总周期数 ), .b(16'h7), .eq(comparator_4_eq));  // open: gt, lt
  Hex_Digit_Display hex_digit_display_2 (.value(LedData[27:24]));  // open: dp
  Hex_Digit_Display hex_digit_display_3 (.value(LedData[23:20]));  // open: dp
  or or_1 (or_1_out, comparator_1_eq, comparator_2_eq);
  assign controlled_inverter_1_out = or_1_out ? ~out_12 : 1'bz;  // Controlled_Inverter controlled_inverter_1
  assign controlled_inverter_2_out = comparator_3_eq ? ~out_12 : 1'bz;  // Controlled_Inverter controlled_inverter_2
  assign controlled_inverter_3_out = comparator_4_eq ? ~out_12 : 1'bz;  // Controlled_Inverter controlled_inverter_3
  Hex_Digit_Display hex_digit_display_4 (.value(LedData[15:12]));  // open: dp
  Hex_Digit_Display hex_digit_display_5 (.value(LedData[19:16]));  // open: dp
  Pull_Resistor #(.pull(0)) pull_resistor_1 (.node(controlled_inverter_1_out));
  Pull_Resistor #(.pull(0)) pull_resistor_2 (.node(controlled_inverter_2_out));
  Pull_Resistor #(.pull(0)) pull_resistor_3 (.node(controlled_inverter_3_out));
  Hex_Digit_Display hex_digit_display_6 (.value(LedData[7:4]));  // open: dp
  Hex_Digit_Display hex_digit_display_7 (.value(LedData[11:8]));  // open: dp
  // Probe on \总周期数 
  Multiplexer #(.select(1), .width(32), .disabled("Z"), .enable("false")) multiplexer_1 (
    .in0(PC_4), .in1(adder_2_out), .out(multiplexer_1_out), .sel(or_4_out));
  Hex_Digit_Display hex_digit_display_8 (.value(LedData[3:0]));  // open: dp
  Multiplexer #(.select(1), .width(32), .disabled("Z"), .enable("false")) multiplexer_2 (
    .in0(multiplexer_1_out), .in1({PC_4[31:28], IR[25:0], 2'b00}), .out(multiplexer_2_out),
    .sel(\单周期硬布线控制器_1_jmp ));
  or or_2 (IR1, 1'b0, IRA);
  Multiplexer #(.select(1), .width(32), .disabled("Z"), .enable("false")) multiplexer_3 (
    .in0(multiplexer_2_out), .in1(R_rs), .out(\断点 ), .sel(\单周期硬布线控制器_1_jr ));
  Multiplexer #(.select(1), .width(32), .disabled("Z"), .enable("false")) multiplexer_4 (
    .in0(multiplexer_5_out), .in1(\返回地址 ), .out(multiplexer_4_out), .sel(eret));
  Multiplexer #(.select(1), .width(32), .disabled("Z"), .enable("false")) multiplexer_5 (
    .in0(\断点 ), .in1(INTADDR), .out(multiplexer_5_out), .sel(INT));
  or or_3 (or_3_out, ~halt, Go);  // OR_Gate
  Register #(.width(32), .trigger("rising"), .Select("low")) u_PC (
    .D(multiplexer_4_out), .en(or_3_out), .Q(PC), .clk(out_12), .clr(in_1));
  Priority_Encoder #(.select(2), .disabled("Z")) priority_encoder_1 (
    .in1(INT1), .in2(1'b0), .in3(1'b0), .out(InprogressInt), .gs(INT_Req));  // open: in0, en_out, en_in
  not not_1 (not_1_out, eret);
  not not_2 (not_2_out, halt);
  Adder #(.width(32)) adder_1 (.a(PC), .b(32'h4), .out(PC_4));  // open: cin, cout
  and and_1 (and_1_out, INT_Req, not_1_out);
  Counter #(.width(16), .max('hffff), .ongoal("wrap"), .trigger("rising"), .behavior("new")) counter_1 (
    .count(not_2_out), .Q(\总周期数 ), .clk(out_12));  // open: load, D, carry, clr, preset, down
  // Mips_Probe mips_probe_1: pin names not known; wires that end beside it: IR
  ROM #(.addrWidth(10), .dataWidth(32), .Select("high")) rom_1 (.addr(PC[11:2]), .data(IR));
  Comparator #(.width(32), .mode("twosComplement")) comparator_5 (
    .a(R_rs), .b(32'h22), .eq(comparator_5_eq));  // open: gt, lt
  Comparator #(.width(32), .mode("twosComplement")) comparator_6 (
    .a(R_rs), .b(32'h23), .eq(comparator_6_eq));  // open: gt, lt
  Register #(.width(1), .trigger("rising"), .Select("low")) u_IE (
    .D(and_1_out), .Q(IE), .clk(out_12), .clr(in_1));  // open: en
  Pull_Resistor #(.pull(0)) pull_resistor_4 (.node(InprogressInt));
  Multiplexer #(.select(2), .width(32), .disabled("Z"), .enable("false")) multiplexer_6 (
    .in1(32'h3014), .in2(32'h3150), .in3(32'h31f4), .out(INTADDR), .sel(InprogressInt));  // open: in0
  and and_2 (out_11, syscall, comparator_5_eq);
  and and_3 (halt, syscall, ~comparator_6_eq, ~comparator_5_eq);  // AND_Gate
  and and_4 (zi_en, syscall, comparator_6_eq);
  Register #(.width(2), .trigger("rising"), .Select("low")) register_1 (
    .D(InprogressInt), .en(INT), .Q(register_1_q), .clk(out_12));  // open: clr
  not not_3 (not_3_out, IE);
  and and_5 (INT, not_3_out, INT_Req);
  Register #(.width(32), .trigger("rising"), .Select("low")) register_2 (
    .D({MDin[31:15], out_13, MDin[7], out_14}), .en(zi_en), .Q(out_16), .clk(out_12), .clr(in_1));
  \单周期硬布线控制器  \u_单周期硬布线控制器_1  (
    .Func(IR[5:0]), .OP(IR[31:26]), .ALU_OP(\单周期硬布线控制器_1_alu_op ), .MemToReg(\单周期硬布线控制器_1_memtoreg ),
    .MemWrite(MemWrite), .ALU_SRC(\单周期硬布线控制器_1_alu_src ), .RegWrite(RegWrite), .SysCALL(syscall),
    .SignedExt(SignedExt), .RegDst(\单周期硬布线控制器_1_regdst ), .JR(\单周期硬布线控制器_1_jr ), .JMP(\单周期硬布线控制器_1_jmp ),
    .Beq(\单周期硬布线控制器_1_beq ), .JAL(\单周期硬布线控制器_1_jal ), .Bne(\单周期硬布线控制器_1_bne ));  // open: BGTZ, SRAV, SB
  assign bit_extender_1_out = {{16{1'b0}}, IR[15:0]};  // Bit_Extender bit_extender_1
  assign bit_extender_2_out = {{16{IR[15]}}, IR[15:0]};  // Bit_Extender bit_extender_2
  Demultiplexer #(.select(2), .width(1), .tristate("false"), .disabled("Z"), .enable("false")) demultiplexer_1 (
    .out1(CLR1), .out2(CLR2), .out3(CLR3), .in(eret), .sel(register_1_q));  // open: out0
  Multiplexer #(.select(1), .width(5), .disabled("Z"), .enable("false")) multiplexer_7 (
    .in0(IR[20:16]), .in1(IR[15:11]), .out(multiplexer_7_out), .sel(\单周期硬布线控制器_1_regdst ));
  Multiplexer #(.select(1), .width(32), .disabled("Z"), .enable("false")) multiplexer_8 (
    .in0(bit_extender_1_out), .in1(bit_extender_2_out), .out(multiplexer_8_out), .sel(SignedExt));
  Register #(.width(32), .trigger("rising"), .Select("low")) register_3 (
    .D({MDin[31:15], out_13, MDin[7], out_14}), .en(out_11), .Q(LedData), .clk(out_12));  // open: clr
  // Probe on \断点 
  Multiplexer #(.select(1), .width(5), .disabled("Z"), .enable("false")) multiplexer_9 (
    .in0(multiplexer_7_out), .in1({5{1'b1}}), .out(multiplexer_9_out), .sel(\单周期硬布线控制器_1_jal ));
  Register #(.width(32), .trigger("rising"), .Select("low")) EPC (
    .D(\断点 ), .en(INT), .Q(\返回地址 ), .clk(out_12), .clr(in_1));
  Multiplexer #(.select(1), .width(5), .disabled("Z"), .enable("false")) multiplexer_10 (
    .in0(IR[25:21]), .in1(5'b00010), .out(multiplexer_10_out), .sel(syscall));
  Multiplexer #(.select(1), .width(5), .disabled("Z"), .enable("false")) multiplexer_11 (
    .in0(IR[20:16]), .in1(5'b00100), .out(multiplexer_11_out), .sel(syscall));
  // Probe on \返回地址 
  MIPS_Regifile mips_regifile_1 (
    .Din(RDin), .Clk(out_12), .R1(R_rs), .R2({MDin[31:15], out_13, MDin[7], out_14}), .WE(RegWrite),
    .W_num(multiplexer_9_out), .R1_num(multiplexer_10_out), .R2_num(multiplexer_11_out));
  \ERET判别  \eret判别_1  (.fun(IR[5:0]), .op(IR[31:26]), .co(IR[25]), .eret(eret));
  Multiplexer #(.select(1), .width(32), .disabled("Z"), .enable("false")) multiplexer_12 (
    .in0({MDin[31:15], out_13, MDin[7], out_14}), .in1(multiplexer_8_out), .out(multiplexer_12_out),
    .sel(\单周期硬布线控制器_1_alu_src ));
  // Probe on \总周期数 
  Shifter #(.width(32), .shift("ll")) shifter_1 (.in(bit_extender_2_out), .\dist (5'b00010), .out(shifter_1_out));
  not not_4 (not_4_out, mips_alu_1_equal);
  MIPS_ALU mips_alu_1 (
    .X(R_rs), .Y(multiplexer_12_out), .AluOP(\单周期硬布线控制器_1_alu_op ), .Equal(mips_alu_1_equal),
    .Result({mips_alu_1_result[31:12], MAin, mips_alu_1_result[1:0]}), .shamt(IR[10:6]));  // open: Result_2
  Adder #(.width(32)) adder_2 (.a(shifter_1_out), .b(PC_4), .out(adder_2_out));  // open: cin, cout
  or or_4 (or_4_out, and_6_out, and_7_out);
  and and_6 (and_6_out, \单周期硬布线控制器_1_bne , not_4_out);
  and and_7 (and_7_out, \单周期硬布线控制器_1_beq , mips_alu_1_equal);
  or or_5 (W1, INT1, d_ff_1_q);
  D_Flip_Flop #(.trigger("rising"), .Pre_Clr_Positions("LEGACY"), .NegatePresetClear("false"), .enable("true"), .NewFFLayout("false")) d_ff_1 (
    .clk(IR1), .D(1'b1), .Q(d_ff_1_q), .reset(INT1));  // open: Qn, preset, en
  or or_6 (or_6_out, d_ff_1_q, INT1);
  Multiplexer #(.select(1), .width(32), .disabled("Z"), .enable("false")) multiplexer_13 (
    .in0({mips_alu_1_result[31:12], MAin, mips_alu_1_result[1:0]}), .in1(MDOUT), .out(multiplexer_13_out),
    .sel(\单周期硬布线控制器_1_memtoreg ));
  Multiplexer #(.select(1), .width(32), .disabled("Z"), .enable("false")) multiplexer_14 (
    .in0(multiplexer_13_out), .in1(PC_4), .out(RDin), .sel(\单周期硬布线控制器_1_jal ));
  and and_8 (and_8_out, or_6_out, ~CLR1);  // AND_Gate
  D_Flip_Flop #(.trigger("rising"), .Pre_Clr_Positions("LEGACY"), .NegatePresetClear("false"), .enable("true"), .NewFFLayout("false")) u_IR1 (
    .clk(out_12), .D(and_8_out), .Q(INT1));  // open: Qn, preset, en, reset
  and and_9 (and_9_out, 1'b1, ~INT1);  // AND_Gate
  and and_10 (and_10_out, 1'b1, ~INT1);  // AND_Gate
  and and_11 (and_11_out, 1'b1, ~INT1);  // AND_Gate
  and and_12 (and_12_out, 1'b1, ~INT1);  // AND_Gate
  and and_13 (and_13_out, 1'b1, ~INT1);  // AND_Gate
  and and_14 (and_14_out, 1'b1, ~INT1);  // AND_Gate
  and and_15 (and_15_out, 1'b1, ~INT1);  // AND_Gate
  and and_16 (and_16_out, 1'b1, ~INT1);  // AND_Gate
  and and_17 (and_17_out, 1'b1, ~INT1);  // AND_Gate
  D_Flip_Flop #(.trigger("rising"), .Pre_Clr_Positions("LEGACY"), .NegatePresetClear("false"), .enable("true"), .NewFFLayout("false")) d_ff_2 (
    .clk(in_2), .D(and_9_out), .Q(d_ff_2_q), .reset(d_ff_11_q));  // open: Qn, preset, en
  D_Flip_Flop #(.trigger("rising"), .Pre_Clr_Positions("LEGACY"), .NegatePresetClear("false"), .enable("true"), .NewFFLayout("false")) d_ff_3 (
    .clk(in_3), .D(and_10_out), .Q(d_ff_3_q), .reset(d_ff_12_q));  // open: Qn, preset, en
  D_Flip_Flop #(.trigger("rising"), .Pre_Clr_Positions("LEGACY"), .NegatePresetClear("false"), .enable("true"), .NewFFLayout("false")) d_ff_4 (
    .clk(in_4), .D(and_11_out), .Q(d_ff_4_q), .reset(d_ff_13_q));  // open: Qn, preset, en
  D_Flip_Flop #(.trigger("rising"), .Pre_Clr_Positions("LEGACY"), .NegatePresetClear("false"), .enable("true"), .NewFFLayout("false")) d_ff_5 (
    .clk(in_5), .D(and_12_out), .Q(d_ff_5_q), .reset(d_ff_14_q));  // open: Qn, preset, en
  D_Flip_Flop #(.trigger("rising"), .Pre_Clr_Positions("LEGACY"), .NegatePresetClear("false"), .enable("true"), .NewFFLayout("false")) d_ff_6 (
    .clk(in_6), .D(and_13_out), .Q(d_ff_6_q), .reset(d_ff_15_q));  // open: Qn, preset, en
  D_Flip_Flop #(.trigger("rising"), .Pre_Clr_Positions("LEGACY"), .NegatePresetClear("false"), .enable("true"), .NewFFLayout("false")) d_ff_7 (
    .clk(in_7), .D(and_14_out), .Q(d_ff_7_q), .reset(d_ff_16_q));  // open: Qn, preset, en
  D_Flip_Flop #(.trigger("rising"), .Pre_Clr_Positions("LEGACY"), .NegatePresetClear("false"), .enable("true"), .NewFFLayout("false")) d_ff_8 (
    .clk(in_8), .D(and_15_out), .Q(d_ff_8_q), .reset(d_ff_17_q));  // open: Qn, preset, en
  D_Flip_Flop #(.trigger("rising"), .Pre_Clr_Positions("LEGACY"), .NegatePresetClear("false"), .enable("true"), .NewFFLayout("false")) d_ff_9 (
    .clk(in_9), .D(and_16_out), .Q(d_ff_9_q), .reset(d_ff_18_q));  // open: Qn, preset, en
  D_Flip_Flop #(.trigger("rising"), .Pre_Clr_Positions("LEGACY"), .NegatePresetClear("false"), .enable("true"), .NewFFLayout("false")) d_ff_10 (
    .clk(in_10), .D(and_17_out), .Q(d_ff_10_q), .reset(d_ff_19_q));  // open: Qn, preset, en
  D_Flip_Flop #(.trigger("rising"), .Pre_Clr_Positions("LEGACY"), .NegatePresetClear("false"), .enable("true"), .NewFFLayout("false")) d_ff_11 (
    .clk(out_12), .D(d_ff_2_q), .Q(d_ff_11_q));  // open: Qn, preset, en, reset
  D_Flip_Flop #(.trigger("rising"), .Pre_Clr_Positions("LEGACY"), .NegatePresetClear("false"), .enable("true"), .NewFFLayout("false")) d_ff_12 (
    .clk(out_12), .D(d_ff_3_q), .Q(d_ff_12_q));  // open: Qn, preset, en, reset
  D_Flip_Flop #(.trigger("rising"), .Pre_Clr_Positions("LEGACY"), .NegatePresetClear("false"), .enable("true"), .NewFFLayout("false")) d_ff_13 (
    .clk(out_12), .D(d_ff_4_q), .Q(d_ff_13_q));  // open: Qn, preset, en, reset
  D_Flip_Flop #(.trigger("rising"), .Pre_Clr_Positions("LEGACY"), .NegatePresetClear("false"), .enable("true"), .NewFFLayout("false")) d_ff_14 (
    .clk(out_12), .D(d_ff_5_q), .Q(d_ff_14_q));  // open: Qn, preset, en, reset
  D_Flip_Flop #(.trigger("rising"), .Pre_Clr_Positions("LEGACY"), .NegatePresetClear("false"), .enable("true"), .NewFFLayout("false")) d_ff_15 (
    .clk(out_12), .D(d_ff_6_q), .Q(d_ff_15_q));  // open: Qn, preset, en, reset
  D_Flip_Flop #(.trigger("rising"), .Pre_Clr_Positions("LEGACY"), .NegatePresetClear("false"), .enable("true"), .NewFFLayout("false")) d_ff_16 (
    .clk(out_12), .D(d_ff_7_q), .Q(d_ff_16_q));  // open: Qn, preset, en, reset
  D_Flip_Flop #(.trigger("rising"), .Pre_Clr_Positions("LEGACY"), .NegatePresetClear("false"), .enable("true"), .NewFFLayout("false")) d_ff_17 (
    .clk(out_12), .D(d_ff_8_q), .Q(d_ff_17_q));  // open: Qn, preset, en, reset
  D_Flip_Flop #(.trigger("rising"), .Pre_Clr_Positions("LEGACY"), .NegatePresetClear("false"), .enable("true"), .NewFFLayout("false")) d_ff_18 (
    .clk(out_12), .D(d_ff_9_q), .Q(d_ff_18_q));  // open: Qn, preset, en, reset
  D_Flip_Flop #(.trigger("rising"), .Pre_Clr_Positions("LEGACY"), .NegatePresetClear("false"), .enable("true"), .NewFFLayout("false")) d_ff_19 (
    .clk(out_12), .D(d_ff_10_q), .Q(d_ff_19_q));  // open: Qn, preset, en, reset
  or or_7 (IRA, in_10, in_9, in_8, in_7, in_6, in_5, in_4, in_3, in_2);
  Priority_Encoder #(.select(4), .disabled("Z")) priority_encoder_2 (
    .in1(d_ff_11_q), .in2(d_ff_12_q), .in3(d_ff_13_q), .in4(d_ff_14_q), .in5(d_ff_15_q), .in6(d_ff_16_q),
    .in7(d_ff_17_q), .in8(d_ff_18_q), .in9(d_ff_19_q), .out(priority_encoder_2_out));  // open: in0, in10, in11, in12, in13, in14, in15, gs, en_out, en_in
  Pull_Resistor #(.pull(0)) pull_resistor_5 (.node(priority_encoder_2_out));
  Multiplexer #(.select(4), .width(32), .disabled("Z"), .enable("false")) multiplexer_15 (
    .in0({32{1'b0}}), .in1(32'h4), .in2(32'h8), .in3(32'hc), .in4(32'h10), .in5(32'h14), .in6(32'h18),
    .in7(32'h1c), .in8(32'h20), .in9(32'h24), .out(multiplexer_15_out), .sel(priority_encoder_2_out));  // open: in10, in11, in12, in13, in14, in15
  Multiplexer #(.select(1), .width(32), .disabled("Z"), .enable("false")) multiplexer_16 (
    .in0({MDin[31:15], out_13, MDin[7], out_14}), .in1(multiplexer_15_out), .out(multiplexer_16_out),
    .sel(INT));
  Multiplexer #(.select(1), .width(10), .disabled("Z"), .enable("false")) multiplexer_17 (
    .in0(MAin), .in1({10{1'b0}}), .out(multiplexer_17_out), .sel(INT));
  or or_8 (or_8_out, INT, MemWrite);
  RAM #(.addrWidth(10), .dataWidth(32), .bus("separate"), .Select("high")) ram_1 (
    .addr(multiplexer_17_out), .din(multiplexer_16_out), .data(MDOUT), .str(or_8_out), .clk(out_12));  // open: sel, ld, clr

  // Other names for the same wires on the sheet: 指令字[31:0] = IR; CLK = out_12; color[15:0] = out_15; led_en = out_11;
  //   MDin (some bits) = {out_13, out_14}; y[6:0] = out_14; x[6:0] = out_13; R_v0[31:0] = R_rs; RST = in_1;
  //   zi_data[31:0] = out_16

  // Notes on the sheet:
  //   中断源
  //   中断等待指示
  //   总复位信号应将除ROM以外所有存储组件全部清零
  //   单级中断测试信号模拟器
  //   数码管输出
  //   数码管输出应该用寄存器锁存，否则显示数据只能一闪而过
  //   指令存储器
  //   为方便自动评测，需要输出PC，IR，寄存器堆写如数据RDin
  //   OP
  //   rs
  //   指令字
  //   contents of rom_1 (hex, n*v repeats v):
  //   20050002 0 0 0 8000c01 8c030000 8c680000 150000fc 15e000fb 20010004 10230010 20010008 10230018
  //   2001000c 10230020 20010010 10230028 20010014 10230030 20010018 10230038 2001001c 10230040 20010020
  //   10230048 20010024 10230050 20090000 200a0000 20010001 10250002 20010002 10250002 37180001 8000c75
  //   37390001 8000c75 2009002a 200a0000 20010001 10250002 20010002 10250002 37180002 8000c75 37390002
  //   8000c75 20090054 200a0000 20010001 10250002 20010002 10250002 37180004 8000c75 37390004 8000c75
  //   20090000 200a002a 20010001 10250002 20010002 10250002 37180008 8000c75 37390008 8000c75 2009002a
  //   200a002a 20010001 10250002 20010002 10250002 37180010 8000c75 37390010 8000c75 20090054 200a002a
  //   20010001 10250002 20010002 10250002 37180020 8000c75 37390020 8000c75 20090000 200a0054 20010001
  //   10250002 20010002 10250002 37180040 8000c75 37390040 8000c75 2009002a 200a0054 20010001 10250002
  //   20010002 10250002 37180080 8000c75 37390080 8000c75 20090054 200a0054 20010001 10250002 20010002
  //   10250002 37180100 8000c75 37390100 8000c75 20010002 1025003f 8000c78 20100024 20110005 102020 892020
  //   42200 902020 8a2020 20020022 c 2210ffff 1611fff7 20120024 20100024 102020 892020 42200 912020 8a2020
  //   20020022 c 2210ffff 22310001 1632fff6 ac650000 33100007 20010007 10300017 33100038 20010038 10300014
  //   331001c0 200101c0 10300011 33100049 20010049 1030000e 33100092 20010092 1030000b 33100124 20010124
  //   10300008 33100111 20010111 10300005 33100054 20010054 10300002 20050002 8000d04 200f0001 200400a3
  //   42200 208400b2 42200 208400ca 42200 208400a4 20020023 c 20050002 8000d04 20100006 20110014 2012000d
  //   102020 892020 42200 912020 8a2020 20020022 c 22100001 22310001 2252ffff 1640fff5 20120013 102020
  //   892020 42200 912020 8a2020 20020022 c 22100001 2231ffff 2252ffff 1640fff5 ac650000 3197025 200101ff
  //   102e001a 33300007 20010007 10300021 33300038 20010038 1030001e 333001c0 200101c0 1030001b 33300049
  //   20010049 10300018 33300092 20010092 10300015 33300124 20010124 10300012 33300111 20010111 1030000f
  //   33300054 20010054 1030000c 20050001 8000d04 200400c6 42200 208400bd 42200 208400be 42200 208400d6
  //   20020023 c 8000d04 200f0001 200400a3 42200 208400b1 42200 208400ca 42200 208400a4 20020023 c
  //   20050001 8000d04 42000018
  //   rt
  //   rd
  //   RAM写使能MemWrite、RAM写入数据MDin等信号
  //   Func
  //   JMP
  //   JR
  //   OP
  //   Func
  //   Beq
  //   Bne
  //   MemToReg
  //   MemWrite
  //   AluOP
  //   AluSrcB
  //   RegWrite
  //   JAL
  //   RegDst
  //   Syscall
  //   OP
  //   Func
  //   Reset 
endmodule

module \单周期MIPS_多级中断  (
  input  IR1,
  input  IR2,
  input  IR3,
  output RegWrite,
  output MemWrite,
  output [31:0] PC,
  output [31:0] IR,
  output [31:0] RDin,
  output [31:0] MDin,
  output [31:0] LedData
);

  wire and_1_out, and_2_out, and_3_out, and_7_out, and_8_out, CLK, CLR1, CLR2, CLR3, comparator_1_eq,
       comparator_2_eq, comparator_3_eq, comparator_4_eq, comparator_5_eq, comparator_6_eq, comparator_9_gt,
       controlled_inverter_1_out, controlled_inverter_2_out, controlled_inverter_3_out, d_ff_1_q, d_ff_2_q,
       d_ff_3_q, eret, Go, halt, IE, INT, INT1, INT2, INT3, INT_Req, IR1_t, IR2_t, IR3_t, IRA, IRB, IRC,
       led_en, MFC0, mips_alu_1_equal, MTC0, not_1_out, not_2_out, not_3_out, or_1_out, or_2_out, or_6_out,
       or_7_out, or_8_out, or_11_out, or_13_out, or_14_out, or_15_out, or_16_out, or_17_out, SignedExt,
       syscall, W1, W2, W3, \单周期硬布线控制器_1_alu_src , \单周期硬布线控制器_1_beq , \单周期硬布线控制器_1_bne , \单周期硬布线控制器_1_jal ,
       \单周期硬布线控制器_1_jmp , \单周期硬布线控制器_1_jr , \单周期硬布线控制器_1_memtoreg , \单周期硬布线控制器_1_regdst ;
  wire [1:0] multiplexer_14_out, multiplexer_16_out, multiplexer_18_out, register_5_q, register_7_q, \响应号 ,
       \请求号 ;
  wire [3:0] \单周期硬布线控制器_1_alu_op ;
  wire [4:0] multiplexer_7_out, multiplexer_9_out, multiplexer_10_out, multiplexer_11_out;
  wire [15:0] \总周期数 ;
  wire [31:0] adder_2_out, bit_extender_1_out, bit_extender_2_out, INTADDR, mips_alu_1_result,
       multiplexer_1_out, multiplexer_2_out, multiplexer_4_out, multiplexer_5_out, multiplexer_8_out,
       multiplexer_12_out, multiplexer_13_out, multiplexer_15_out, multiplexer_17_out, multiplexer_19_out,
       PC_4, R_rs, ram_1_data, register_4_q, register_6_q, shifter_1_out, \断点 , \返回地址 ;

  Clock #(.highDuration(1), .lowDuration(1)) clock_1 (.out(CLK));
  Button _1 (.out(IRA));
  Button _2 (.out(IRB));
  Button _3 (.out(IRC));
  Button \u_继续运行  (.out(Go));
  LED #(.active("true")) led_1 (.in(W1));
  LED #(.active("true")) led_2 (.in(W2));
  LED #(.active("true")) led_3 (.in(W3));
  Hex_Digit_Display hex_digit_display_1 (.value(LedData[31:28]));  // open: dp
  Comparator #(.width(16), .mode("twosComplement")) comparator_1 (
    .a(16'h258), .b(\总周期数 ), .eq(comparator_1_eq));  // open: gt, lt
  Comparator #(.width(16), .mode("twosComplement")) comparator_2 (
    .a(\总周期数 ), .b(16'h1), .eq(comparator_2_eq));  // open: gt, lt
  Comparator #(.width(16), .mode("twosComplement")) comparator_3 (
    .a(\总周期数 ), .b(16'h4), .eq(comparator_3_eq));  // open: gt, lt
  Comparator #(.width(16), .mode("twosComplement")) comparator_4 (
    .a(\总周期数 ), .b(16'h7), .eq(comparator_4_eq));  // open: gt, lt
  Comparator #(.width(16), .mode("twosComplement")) comparator_5 (
    .a(\总周期数 ), .b(16'h241), .eq(comparator_5_eq));  // open: gt, lt
  Hex_Digit_Display hex_digit_display_2 (.value(LedData[27:24]));  // open: dp
  Hex_Digit_Display hex_digit_display_3 (.value(LedData[23:20]));  // open: dp
  or or_1 (or_1_out, comparator_1_eq, comparator_2_eq);
  assign controlled_inverter_1_out = or_1_out ? ~CLK : 1'bz;  // Controlled_Inverter controlled_inverter_1
  assign controlled_inverter_2_out = comparator_3_eq ? ~CLK : 1'bz;  // Controlled_Inverter controlled_inverter_2
  or or_2 (or_2_out, comparator_4_eq, comparator_5_eq);
  assign controlled_inverter_3_out = or_2_out ? ~CLK : 1'bz;  // Controlled_Inverter controlled_inverter_3
  Hex_Digit_Display hex_digit_display_4 (.value(LedData[15:12]));  // open: dp
  Hex_Digit_Display hex_digit_display_5 (.value(LedData[19:16]));  // open: dp
  Pull_Resistor #(.pull(0)) pull_resistor_1 (.node(controlled_inverter_1_out));
  Pull_Resistor #(.pull(0)) pull_resistor_2 (.node(controlled_inverter_2_out));
  Pull_Resistor #(.pull(0)) pull_resistor_3 (.node(controlled_inverter_3_out));
  or or_3 (W1, INT1, d_ff_1_q);
  or or_4 (W2, INT2, d_ff_2_q);
  or or_5 (W3, INT3, d_ff_3_q);
  Hex_Digit_Display hex_digit_display_6 (.value(LedData[11:8]));  // open: dp
  Hex_Digit_Display hex_digit_display_7 (.value(LedData[7:4]));  // open: dp
  // Probe on \总周期数 
  Multiplexer #(.select(1), .width(32), .disabled("Z"), .enable("false")) multiplexer_1 (
    .in0(PC_4), .in1(adder_2_out), .out(multiplexer_1_out), .sel(or_17_out));
  D_Flip_Flop #(.trigger("rising"), .Pre_Clr_Positions("LEGACY"), .NegatePresetClear("false"), .enable("true"), .NewFFLayout("false")) d_ff_1 (
    .clk(IR1_t), .D(1'b1), .Q(d_ff_1_q), .reset(INT1));  // open: Qn, preset, en
  D_Flip_Flop #(.trigger("rising"), .Pre_Clr_Positions("LEGACY"), .NegatePresetClear("false"), .enable("true"), .NewFFLayout("false")) d_ff_2 (
    .clk(IR2_t), .D(1'b1), .Q(d_ff_2_q), .reset(INT2));  // open: Qn, preset, en
  D_Flip_Flop #(.trigger("rising"), .Pre_Clr_Positions("LEGACY"), .NegatePresetClear("false"), .enable("true"), .NewFFLayout("false")) d_ff_3 (
    .clk(IR3_t), .D(1'b1), .Q(d_ff_3_q), .reset(INT3));  // open: Qn, preset, en
  Hex_Digit_Display hex_digit_display_8 (.value(LedData[3:0]));  // open: dp
  Multiplexer #(.select(1), .width(32), .disabled("Z"), .enable("false")) multiplexer_2 (
    .in0(multiplexer_1_out), .in1({PC_4[31:28], IR[25:0], 2'b00}), .out(multiplexer_2_out),
    .sel(\单周期硬布线控制器_1_jmp ));
  or or_6 (or_6_out, d_ff_1_q, INT1);
  or or_7 (or_7_out, d_ff_2_q, INT2);
  or or_8 (or_8_out, d_ff_3_q, INT3);
  Priority_Encoder #(.select(2), .disabled("Z")) priority_encoder_1 (
    .in1(INT1), .in2(INT2), .in3(INT3), .out(\请求号 ), .gs(INT_Req));  // open: in0, en_out, en_in
  and and_1 (and_1_out, or_6_out, ~CLR1);  // AND_Gate
  and and_2 (and_2_out, or_7_out, ~CLR2);  // AND_Gate
  and and_3 (and_3_out, or_8_out, ~CLR3);  // AND_Gate
  or or_9 (IR1_t, IR1, IRA);
  Multiplexer #(.select(1), .width(32), .disabled("Z"), .enable("false")) multiplexer_3 (
    .in0(multiplexer_2_out), .in1(R_rs), .out(\断点 ), .sel(\单周期硬布线控制器_1_jr ));
  D_Flip_Flop #(.trigger("rising"), .Pre_Clr_Positions("LEGACY"), .NegatePresetClear("false"), .enable("true"), .NewFFLayout("false")) u_IR1 (
    .clk(CLK), .D(and_1_out), .Q(INT1));  // open: Qn, preset, en, reset
  D_Flip_Flop #(.trigger("rising"), .Pre_Clr_Positions("LEGACY"), .NegatePresetClear("false"), .enable("true"), .NewFFLayout("false")) IR1_2 (
    .clk(CLK), .D(and_2_out), .Q(INT2));  // open: Qn, preset, en, reset
  D_Flip_Flop #(.trigger("rising"), .Pre_Clr_Positions("LEGACY"), .NegatePresetClear("false"), .enable("true"), .NewFFLayout("false")) IR1_3 (
    .clk(CLK), .D(and_3_out), .Q(INT3));  // open: Qn, preset, en, reset
  or or_10 (IR2_t, IR2, IRB);
  Multiplexer #(.select(1), .width(32), .disabled("Z"), .enable("false")) multiplexer_4 (
    .in0(multiplexer_5_out), .in1(\返回地址 ), .out(multiplexer_4_out), .sel(eret));
  Multiplexer #(.select(1), .width(32), .disabled("Z"), .enable("false")) multiplexer_5 (
    .in0(\断点 ), .in1(INTADDR), .out(multiplexer_5_out), .sel(INT));
  or or_11 (or_11_out, ~halt, Go);  // OR_Gate
  Pull_Resistor #(.pull(0)) pull_resistor_4 (.node(\请求号 ));
  Multiplexer #(.select(2), .width(32), .disabled("Z"), .enable("false")) multiplexer_6 (
    .in1(32'h30ac), .in2(32'h3158), .in3(32'h3204), .out(INTADDR), .sel(\请求号 ));  // open: in0
  or or_12 (IR3_t, IR3, IRC);
  Register #(.width(32), .trigger("rising"), .Select("low")) u_PC (
    .D(multiplexer_4_out), .en(or_11_out), .Q(PC), .clk(CLK));  // open: clr
  Demultiplexer #(.select(2), .width(1), .tristate("false"), .disabled("Z"), .enable("false")) demultiplexer_1 (
    .out1(CLR1), .out2(CLR2), .out3(CLR3), .in(eret), .sel(\请求号 ));  // open: out0
  Adder #(.width(32)) adder_1 (.a(PC), .b(32'h4), .out(PC_4));  // open: cin, cout
  not not_1 (not_1_out, halt);
  // Mips_Probe mips_probe_1: pin names not known; wires that end beside it: IR
  ROM #(.addrWidth(10), .dataWidth(32), .Select("high")) rom_1 (.addr(PC[11:2]), .data(IR));
  Comparator #(.width(32), .mode("twosComplement")) comparator_6 (
    .a(R_rs), .b(32'h22), .eq(comparator_6_eq));  // open: gt, lt
  Counter #(.width(16), .max('hffff), .ongoal("wrap"), .trigger("rising"), .behavior("new")) counter_1 (
    .count(not_1_out), .Q(\总周期数 ), .clk(CLK));  // open: load, D, carry, clr, preset, down
  and and_4 (led_en, syscall, comparator_6_eq);
  and and_5 (halt, syscall, ~comparator_6_eq);  // AND_Gate
  \单周期硬布线控制器  \u_单周期硬布线控制器_1  (
    .Func(IR[5:0]), .OP(IR[31:26]), .ALU_OP(\单周期硬布线控制器_1_alu_op ), .MemToReg(\单周期硬布线控制器_1_memtoreg ),
    .MemWrite(MemWrite), .ALU_SRC(\单周期硬布线控制器_1_alu_src ), .RegWrite(RegWrite), .SysCALL(syscall),
    .SignedExt(SignedExt), .RegDst(\单周期硬布线控制器_1_regdst ), .JR(\单周期硬布线控制器_1_jr ), .JMP(\单周期硬布线控制器_1_jmp ),
    .Beq(\单周期硬布线控制器_1_beq ), .JAL(\单周期硬布线控制器_1_jal ), .Bne(\单周期硬布线控制器_1_bne ));  // open: BGTZ, SRAV, SB
  assign bit_extender_1_out = {{16{1'b0}}, IR[15:0]};  // Bit_Extender bit_extender_1
  assign bit_extender_2_out = {{16{IR[15]}}, IR[15:0]};  // Bit_Extender bit_extender_2
  Comparator #(.width(32), .mode("twosComplement")) comparator_7 (.a(IR), .b(32'h40000000), .eq(MFC0));  // open: gt, lt
  Comparator #(.width(32), .mode("twosComplement")) comparator_8 (.a(IR), .b(32'h40800000), .eq(MTC0));  // open: gt, lt
  Multiplexer #(.select(1), .width(5), .disabled("Z"), .enable("false")) multiplexer_7 (
    .in0(IR[20:16]), .in1(IR[15:11]), .out(multiplexer_7_out), .sel(\单周期硬布线控制器_1_regdst ));
  Multiplexer #(.select(1), .width(32), .disabled("Z"), .enable("false")) multiplexer_8 (
    .in0(bit_extender_1_out), .in1(bit_extender_2_out), .out(multiplexer_8_out), .sel(SignedExt));
  Register #(.width(32), .trigger("rising"), .Select("low")) register_1 (
    .D(MDin), .en(led_en), .Q(LedData), .clk(CLK));  // open: clr
  Multiplexer #(.select(1), .width(5), .disabled("Z"), .enable("false")) multiplexer_9 (
    .in0(multiplexer_7_out), .in1({5{1'b1}}), .out(multiplexer_9_out), .sel(\单周期硬布线控制器_1_jal ));
  Multiplexer #(.select(1), .width(5), .disabled("Z"), .enable("false")) multiplexer_10 (
    .in0(IR[25:21]), .in1(5'b00010), .out(multiplexer_10_out), .sel(syscall));
  Multiplexer #(.select(1), .width(5), .disabled("Z"), .enable("false")) multiplexer_11 (
    .in0(IR[20:16]), .in1(5'b00100), .out(multiplexer_11_out), .sel(syscall));
  not not_2 (not_2_out, IE);
  Comparator #(.width(2), .mode("unsigned")) comparator_9 (.a(\请求号 ), .b(\响应号 ), .gt(comparator_9_gt));  // open: eq, lt
  MIPS_Regifile mips_regifile_1 (
    .Din(RDin), .Clk(CLK), .R1(R_rs), .R2(MDin), .WE(RegWrite), .W_num(multiplexer_9_out),
    .R1_num(multiplexer_10_out), .R2_num(multiplexer_11_out));
  \ERET判别  \eret判别_1  (.fun(IR[5:0]), .op(IR[31:26]), .co(IR[25]), .eret(eret));
  and and_6 (INT, not_2_out, comparator_9_gt);
  Multiplexer #(.select(1), .width(32), .disabled("Z"), .enable("false")) multiplexer_12 (
    .in0(MDin), .in1(multiplexer_8_out), .out(multiplexer_12_out), .sel(\单周期硬布线控制器_1_alu_src ));
  Shifter #(.width(32), .shift("ll")) shifter_1 (.in(bit_extender_2_out), .\dist (5'b00010), .out(shifter_1_out));
  not not_3 (not_3_out, mips_alu_1_equal);
  MIPS_ALU mips_alu_1 (
    .X(R_rs), .Y(multiplexer_12_out), .AluOP(\单周期硬布线控制器_1_alu_op ), .Equal(mips_alu_1_equal),
    .Result(mips_alu_1_result), .shamt(IR[10:6]));  // open: Result_2
  Adder #(.width(32)) adder_2 (.a(shifter_1_out), .b(PC_4), .out(adder_2_out));  // open: cin, cout
  or or_13 (or_13_out, INT, MTC0);
  or or_14 (or_14_out, INT, MTC0, MFC0, eret);
  Multiplexer #(.select(1), .width(32), .disabled("Z"), .enable("false")) multiplexer_13 (
    .in0(\断点 ), .in1(register_4_q), .out(multiplexer_13_out), .sel(eret));
  or or_15 (or_15_out, INT, eret);
  Multiplexer #(.select(1), .width(2), .disabled("Z"), .enable("false")) multiplexer_14 (
    .in0(\请求号 ), .in1(register_5_q), .out(multiplexer_14_out), .sel(eret));
  or or_16 (or_16_out, INT, eret);
  or or_17 (or_17_out, and_7_out, and_8_out);
  and and_7 (and_7_out, \单周期硬布线控制器_1_bne , not_3_out);
  and and_8 (and_8_out, \单周期硬布线控制器_1_beq , mips_alu_1_equal);
  Register #(.width(1), .trigger("rising"), .Select("low")) u_IE (
    .D(or_13_out), .en(or_14_out), .Q(IE), .clk(CLK));  // open: clr
  Register #(.width(32), .trigger("rising"), .Select("low")) register_2 (
    .D(multiplexer_13_out), .en(or_15_out), .Q(\返回地址 ), .clk(CLK));  // open: clr
  Register #(.width(2), .trigger("rising"), .Select("low")) register_3 (
    .D(multiplexer_14_out), .en(or_16_out), .Q(\响应号 ), .clk(CLK));  // open: clr
  Multiplexer #(.select(1), .width(32), .disabled("Z"), .enable("false")) multiplexer_15 (
    .in0(\返回地址 ), .in1(register_6_q), .out(multiplexer_15_out), .sel(eret));
  Multiplexer #(.select(1), .width(2), .disabled("Z"), .enable("false")) multiplexer_16 (
    .in0(\响应号 ), .in1(register_7_q), .out(multiplexer_16_out), .sel(eret));
  RAM #(.addrWidth(10), .dataWidth(32), .bus("separate"), .Select("high")) ram_1 (
    .addr(mips_alu_1_result[11:2]), .din(MDin), .data(ram_1_data), .str(MemWrite), .clk(CLK));  // open: sel, ld, clr
  Register #(.width(32), .trigger("rising"), .Select("low")) register_4 (
    .D(multiplexer_15_out), .en(or_15_out), .Q(register_4_q), .clk(CLK));  // open: clr
  Register #(.width(2), .trigger("rising"), .Select("low")) register_5 (
    .D(multiplexer_16_out), .en(or_16_out), .Q(register_5_q), .clk(CLK));  // open: clr
  Multiplexer #(.select(1), .width(32), .disabled("Z"), .enable("false")) multiplexer_17 (
    .in0(register_4_q), .in1({32{1'b0}}), .out(multiplexer_17_out), .sel(eret));
  Multiplexer #(.select(1), .width(2), .disabled("Z"), .enable("false")) multiplexer_18 (
    .in0(register_5_q), .in1(2'b00), .out(multiplexer_18_out), .sel(eret));
  Multiplexer #(.select(1), .width(32), .disabled("Z"), .enable("false")) multiplexer_19 (
    .in0(mips_alu_1_result), .in1(ram_1_data), .out(multiplexer_19_out), .sel(\单周期硬布线控制器_1_memtoreg ));
  Multiplexer #(.select(1), .width(32), .disabled("Z"), .enable("false")) multiplexer_20 (
    .in0(multiplexer_19_out), .in1(PC_4), .out(RDin), .sel(\单周期硬布线控制器_1_jal ));
  Register #(.width(32), .trigger("rising"), .Select("low")) register_6 (
    .D(multiplexer_17_out), .en(or_15_out), .Q(register_6_q), .clk(CLK));  // open: clr
  Register #(.width(2), .trigger("rising"), .Select("low")) register_7 (
    .D(multiplexer_18_out), .en(or_16_out), .Q(register_7_q), .clk(CLK));  // open: clr

  // Other names for the same wires on the sheet: 指令字[31:0] = IR; R_v0[31:0] = R_rs

  // Notes on the sheet:
  //   中断源
  //   中断等待指示
  //   总复位信号应将除ROM以外所有存储组件全部清零
  //   数码管输出
  //   数码管输出应该用寄存器锁存，否则显示数据只能一闪而过
  //   Reset 
  //   Reset 
  //   Reset 
  //   指令存储器
  //   为方便自动评测，需要输出PC，IR，寄存器堆写如数据RDin
  //   OP
  //   rs
  //   指令字
  //   contents of rom_1 (hex, n*v repeats v):
  //   201d07d0 20100001 109fc0 139fc3 8021 2012000c 24160008 26100001 3210000f 20080008 20090001 139900
  //   2709825 132020 20020022 c 1094022 1500fff9 22100001 2018000f 2188024 108700 20080008 20090001 139902
  //   2709825 132021 20020022 c 1094022 1500fff9 108702 2c9b022 12c00001 8000c07 4020 1084027 84400
  //   3508ffff 82021 20020022 c 8000c01 afa20000 23bd0004 afa40000 23bd0004 afb00000 23bd0004 afb30000
  //   23bd0004 afb40000 23bd0004 afb50000 23bd0004 afb60000 23bd0004 40000000 20160001 20140003 20150001
  //   168020 108100 2149825 132020 20020022 c 1600fffa 295a022 1680fff7 40800000 23bdfffc 8fb60000
  //   23bdfffc 8fb50000 23bdfffc 8fb40000 23bdfffc 8fb30000 23bdfffc 8fb00000 23bdfffc 8fa40000 23bdfffc
  //   8fa20000 42000018 afa20000 23bd0004 afa40000 23bd0004 afb00000 23bd0004 afb30000 23bd0004 afb40000
  //   23bd0004 afb50000 23bd0004 afb60000 23bd0004 40000000 20160002 20140003 20150001 168020 108100
  //   2149825 132020 20020022 c 1600fffa 295a022 1680fff7 40800000 23bdfffc 8fb60000 23bdfffc 8fb50000
  //   23bdfffc 8fb40000 23bdfffc 8fb30000 23bdfffc 8fb00000 23bdfffc 8fa40000 23bdfffc 8fa20000 42000018
  //   afa20000 23bd0004 afa40000 23bd0004 afb00000 23bd0004 afb30000 23bd0004 afb40000 23bd0004 afb50000
  //   23bd0004 afb60000 23bd0004 40000000 20160003 20140003 20150001 168020 108100 2149825 132020 20020022
  //   c 1600fffa 295a022 1680fff7 40800000 23bdfffc 8fb60000 23bdfffc 8fb50000 23bdfffc 8fb40000 23bdfffc
  //   8fb30000 23bdfffc 8fb00000 23bdfffc 8fa40000 23bdfffc 8fa20000 42000018
  //   rt
  //   rd
  //   RAM写使能MemWrite、RAM写入数据MDin等信号
  //   Func
  //   JMP
  //   JR
  //   OP
  //   Func
  //   Beq
  //   Bne
  //   MemToReg
  //   MemWrite
  //   AluOP
  //   AluSrcB
  //   RegWrite
  //   JAL
  //   RegDst
  //   Syscall
  //   OP
  //   Func
endmodule

module \封装正确性测试  (
);

  wire IR1, IR2, IR3, MemW, RegW;
  wire [31:0] EX_PC, ID_PC, IF_PC, IR, LED, MDin, MDinr, MEM_PC, PC, RDin, RDinr, WB_PC;

  \单周期MIPS  \u_单周期mips_1  (
    .RegWrite(RegW), .MemWrite(MemW), .PC(PC), .IR(IR), .RDin(RDin), .MDin(MDin), .LedData(LED));  // open: IR1, IR2, IR3
  \气泡流水线  \u_气泡流水线_1  (
    .RegWrite(RegW), .MemWrite(MemW), .IF_PC(IF_PC), .ID_PC(ID_PC), .EX_PC(EX_PC), .M_PC(MEM_PC),
    .WB_PC(WB_PC), .RDin(RDinr), .MDin(MDinr), .LedData(LED));
  // 单周期MIPS_单级中断 单周期mips_单级中断_1: pin names not known; wires that end beside it: IR1, IR2, IR3, RegW, MemW, PC, RDin, MDin, LED, IR, IR, IR
  \理想流水线  \u_理想流水线_1  (
    .RegWrite(RegW), .MemWrite(MemW), .IF_PC(IF_PC), .ID_PC(ID_PC), .EX_PC(EX_PC), .M_PC(MEM_PC),
    .WB_PC(WB_PC), .RDin(RDinr), .MDin(MDinr), .LedData(LED));
  \重定向流水线  \u_重定向流水线_1  (
    .RegWrite(RegW), .MemWrite(MemW), .IF_PC(IF_PC), .ID_PC(ID_PC), .EX_PC(EX_PC), .M_PC(MEM_PC),
    .WB_PC(WB_PC), .RDin(RDinr), .MDin(MDinr), .LedData(LED));
  \单周期MIPS_多级中断  \u_单周期mips_多级中断_1  (
    .IR1(IR1), .IR2(IR2), .IR3(IR3), .RegWrite(RegW), .MemWrite(MemW), .PC(PC), .IR(IR), .RDin(RDin),
    .MDin(MDin), .LedData(LED));

  // Notes on the sheet:
  //   单周期封装测试
  //   气泡流水封装测试
  //   单周期+单级中断封装测试
  //   请检查上面封装有无位宽不匹配，引脚标签是否和连接的标签相对应，否则无法在educoder平台上正确测试
  //   理想流水封装测试
  //   重定向流水封装测试
  //   单周期+多级中断封装测试
endmodule

module IF_ID (
  input  [31:0] IR_IF,
  input  [31:0] PC_IF,
  input  EN,
  input  CLK,
  input  RST,
  output [31:0] IR_ID,
  output [31:0] PC_ID
);

  wire [31:0] multiplexer_1_out, multiplexer_2_out;

  Multiplexer #(.select(1), .width(32), .disabled("Z"), .enable("false")) multiplexer_1 (
    .in0(IR_IF), .in1({32{1'b0}}), .out(multiplexer_1_out), .sel(RST));
  Multiplexer #(.select(1), .width(32), .disabled("Z"), .enable("false")) multiplexer_2 (
    .in0(PC_IF), .in1({32{1'b0}}), .out(multiplexer_2_out), .sel(RST));
  Register #(.width(32), .trigger("rising"), .Select("low")) register_1 (
    .D(multiplexer_1_out), .en(EN), .Q(IR_ID), .clk(CLK));  // open: clr
  Register #(.width(32), .trigger("rising"), .Select("low")) register_2 (
    .D(multiplexer_2_out), .en(EN), .Q(PC_ID), .clk(CLK));  // open: clr
  Pull_Resistor #(.pull(0)) pull_resistor_1 (.node(RST));
endmodule

module ID_EX (
  input  [1:0] FwdA,
  input  [1:0] FwdB,
  input  JR,
  input  JMP,
  input  Beq,
  input  Bne,
  input  MemToReg,
  input  MemWrite,
  input  [3:0] ALU_OP,
  input  ALU_SRC,
  input  RegWrite,
  input  JAL,
  input  SysCALL,
  input  [31:0] RS,
  input  [31:0] RT,
  input  [4:0] WriteReg_num,
  input  [31:0] ZeroImm,
  input  [31:0] UnSignImm,
  input  [31:0] IR_ID,
  input  [31:0] PC_ID,
  input  EN,
  input  CLK,
  input  RST,
  output [1:0] FwdA_2,
  output [1:0] FwdB_2,
  output JR_2,
  output JMP_2,
  output Beq_2,
  output Bne_2,
  output MemToReg_2,
  output MemWrite_2,
  output [3:0] ALU_OP_2,
  output ALU_SRC_2,
  output RegWrite_2,
  output JAL_2,
  output SysCALL_2,
  output [31:0] RS_2,
  output [31:0] RT_2,
  output [4:0] WriteReg_num_2,
  output [31:0] ZeroImm_2,
  output [31:0] UnSignImm_2,
  output [31:0] IR_EX,
  output [31:0] PC_EX
);

  wire multiplexer_3_out, multiplexer_4_out, multiplexer_5_out, multiplexer_6_out, multiplexer_7_out,
       multiplexer_8_out, multiplexer_10_out, multiplexer_11_out, multiplexer_12_out, multiplexer_13_out;
  wire [1:0] multiplexer_1_out, multiplexer_2_out;
  wire [3:0] multiplexer_9_out;
  wire [4:0] multiplexer_16_out;
  wire [31:0] multiplexer_14_out, multiplexer_15_out, multiplexer_17_out, multiplexer_18_out,
       multiplexer_19_out, multiplexer_20_out;

  Multiplexer #(.select(1), .width(2), .disabled("Z"), .enable("false")) multiplexer_1 (
    .in0(FwdA), .in1(2'b00), .out(multiplexer_1_out), .sel(RST));
  Multiplexer #(.select(1), .width(2), .disabled("Z"), .enable("false")) multiplexer_2 (
    .in0(FwdB), .in1(2'b00), .out(multiplexer_2_out), .sel(RST));
  Multiplexer #(.select(1), .width(1), .disabled("Z"), .enable("false")) multiplexer_3 (
    .in0(JR), .in1(1'b0), .out(multiplexer_3_out), .sel(RST));
  Multiplexer #(.select(1), .width(1), .disabled("Z"), .enable("false")) multiplexer_4 (
    .in0(JMP), .in1(1'b0), .out(multiplexer_4_out), .sel(RST));
  Multiplexer #(.select(1), .width(1), .disabled("Z"), .enable("false")) multiplexer_5 (
    .in0(Beq), .in1(1'b0), .out(multiplexer_5_out), .sel(RST));
  Multiplexer #(.select(1), .width(1), .disabled("Z"), .enable("false")) multiplexer_6 (
    .in0(Bne), .in1(1'b0), .out(multiplexer_6_out), .sel(RST));
  Multiplexer #(.select(1), .width(1), .disabled("Z"), .enable("false")) multiplexer_7 (
    .in0(MemToReg), .in1(1'b0), .out(multiplexer_7_out), .sel(RST));
  Multiplexer #(.select(1), .width(1), .disabled("Z"), .enable("false")) multiplexer_8 (
    .in0(MemWrite), .in1(1'b0), .out(multiplexer_8_out), .sel(RST));
  Multiplexer #(.select(1), .width(4), .disabled("Z"), .enable("false")) multiplexer_9 (
    .in0(ALU_OP), .in1(4'b0000), .out(multiplexer_9_out), .sel(RST));
  Multiplexer #(.select(1), .width(1), .disabled("Z"), .enable("false")) multiplexer_10 (
    .in0(ALU_SRC), .in1(1'b0), .out(multiplexer_10_out), .sel(RST));
  Multiplexer #(.select(1), .width(1), .disabled("Z"), .enable("false")) multiplexer_11 (
    .in0(RegWrite), .in1(1'b0), .out(multiplexer_11_out), .sel(RST));
  Multiplexer #(.select(1), .width(1), .disabled("Z"), .enable("false")) multiplexer_12 (
    .in0(JAL), .in1(1'b0), .out(multiplexer_12_out), .sel(RST));
  Multiplexer #(.select(1), .width(1), .disabled("Z"), .enable("false")) multiplexer_13 (
    .in0(SysCALL), .in1(1'b0), .out(multiplexer_13_out), .sel(RST));
  Multiplexer #(.select(1), .width(32), .disabled("Z"), .enable("false")) multiplexer_14 (
    .in0(RS), .in1({32{1'b0}}), .out(multiplexer_14_out), .sel(RST));
  Multiplexer #(.select(1), .width(32), .disabled("Z"), .enable("false")) multiplexer_15 (
    .in0(RT), .in1({32{1'b0}}), .out(multiplexer_15_out), .sel(RST));
  Multiplexer #(.select(1), .width(5), .disabled("Z"), .enable("false")) multiplexer_16 (
    .in0(WriteReg_num), .in1({5{1'b0}}), .out(multiplexer_16_out), .sel(RST));
  Multiplexer #(.select(1), .width(32), .disabled("Z"), .enable("false")) multiplexer_17 (
    .in0(ZeroImm), .in1({32{1'b0}}), .out(multiplexer_17_out), .sel(RST));
  Multiplexer #(.select(1), .width(32), .disabled("Z"), .enable("false")) multiplexer_18 (
    .in0(UnSignImm), .in1({32{1'b0}}), .out(multiplexer_18_out), .sel(RST));
  Multiplexer #(.select(1), .width(32), .disabled("Z"), .enable("false")) multiplexer_19 (
    .in0(IR_ID), .in1({32{1'b0}}), .out(multiplexer_19_out), .sel(RST));
  Multiplexer #(.select(1), .width(32), .disabled("Z"), .enable("false")) multiplexer_20 (
    .in0(PC_ID), .in1({32{1'b0}}), .out(multiplexer_20_out), .sel(RST));
  Register #(.width(2), .trigger("rising"), .Select("low")) register_1 (
    .D(multiplexer_1_out), .en(EN), .Q(FwdA_2), .clk(CLK));  // open: clr
  Register #(.width(2), .trigger("rising"), .Select("low")) register_2 (
    .D(multiplexer_2_out), .en(EN), .Q(FwdB_2), .clk(CLK));  // open: clr
  Register #(.width(1), .trigger("rising"), .Select("low")) register_3 (
    .D(multiplexer_3_out), .en(EN), .Q(JR_2), .clk(CLK));  // open: clr
  Register #(.width(1), .trigger("rising"), .Select("low")) register_4 (
    .D(multiplexer_4_out), .en(EN), .Q(JMP_2), .clk(CLK));  // open: clr
  Register #(.width(1), .trigger("rising"), .Select("low")) register_5 (
    .D(multiplexer_5_out), .en(EN), .Q(Beq_2), .clk(CLK));  // open: clr
  Register #(.width(1), .trigger("rising"), .Select("low")) register_6 (
    .D(multiplexer_6_out), .en(EN), .Q(Bne_2), .clk(CLK));  // open: clr
  Register #(.width(1), .trigger("rising"), .Select("low")) register_7 (
    .D(multiplexer_7_out), .en(EN), .Q(MemToReg_2), .clk(CLK));  // open: clr
  Register #(.width(1), .trigger("rising"), .Select("low")) register_8 (
    .D(multiplexer_8_out), .en(EN), .Q(MemWrite_2), .clk(CLK));  // open: clr
  Register #(.width(4), .trigger("rising"), .Select("low")) register_9 (
    .D(multiplexer_9_out), .en(EN), .Q(ALU_OP_2), .clk(CLK));  // open: clr
  Register #(.width(1), .trigger("rising"), .Select("low")) register_10 (
    .D(multiplexer_10_out), .en(EN), .Q(ALU_SRC_2), .clk(CLK));  // open: clr
  Register #(.width(1), .trigger("rising"), .Select("low")) register_11 (
    .D(multiplexer_11_out), .en(EN), .Q(RegWrite_2), .clk(CLK));  // open: clr
  Register #(.width(1), .trigger("rising"), .Select("low")) register_12 (
    .D(multiplexer_12_out), .en(EN), .Q(JAL_2), .clk(CLK));  // open: clr
  Register #(.width(1), .trigger("rising"), .Select("low")) register_13 (
    .D(multiplexer_13_out), .en(EN), .Q(SysCALL_2), .clk(CLK));  // open: clr
  Register #(.width(32), .trigger("rising"), .Select("low")) register_14 (
    .D(multiplexer_14_out), .en(EN), .Q(RS_2), .clk(CLK));  // open: clr
  Register #(.width(32), .trigger("rising"), .Select("low")) register_15 (
    .D(multiplexer_15_out), .en(EN), .Q(RT_2), .clk(CLK));  // open: clr
  Register #(.width(5), .trigger("rising"), .Select("low")) register_16 (
    .D(multiplexer_16_out), .en(EN), .Q(WriteReg_num_2), .clk(CLK));  // open: clr
  Register #(.width(32), .trigger("rising"), .Select("low")) register_17 (
    .D(multiplexer_17_out), .en(EN), .Q(ZeroImm_2), .clk(CLK));  // open: clr
  Register #(.width(32), .trigger("rising"), .Select("low")) register_18 (
    .D(multiplexer_18_out), .en(EN), .Q(UnSignImm_2), .clk(CLK));  // open: clr
  Register #(.width(32), .trigger("rising"), .Select("low")) register_19 (
    .D(multiplexer_19_out), .en(EN), .Q(IR_EX), .clk(CLK));  // open: clr
  Register #(.width(32), .trigger("rising"), .Select("low")) register_20 (
    .D(multiplexer_20_out), .en(EN), .Q(PC_EX), .clk(CLK));  // open: clr
  Pull_Resistor #(.pull(0)) pull_resistor_1 (.node(RST));
endmodule

module EX_MEM (
  input  [31:0] r_v0,
  input  JR,
  input  JMP,
  input  MemToReg,
  input  MemWrite,
  input  RegWrite,
  input  JAL,
  input  SysCALL,
  input  [31:0] RESULT,
  input  [31:0] WriteData,
  input  [4:0] WriteReg_num,
  input  [31:0] IR_ID,
  input  [31:0] PC_ID,
  input  EN,
  input  CLK,
  input  RST,
  output [31:0] r_v0_2,
  output JR_2,
  output JMP_2,
  output MemToReg_2,
  output MemWrite_2,
  output RegWrite_2,
  output JAL_2,
  output SysCALL_2,
  output [31:0] RESULT_2,
  output [31:0] WriteData_2,
  output [4:0] WriteReg_num_2,
  output [31:0] IR_EX,
  output [31:0] PC_EX
);

  wire multiplexer_2_out, multiplexer_3_out, multiplexer_4_out, multiplexer_5_out, multiplexer_6_out,
       multiplexer_7_out, multiplexer_8_out;
  wire [4:0] multiplexer_11_out;
  wire [31:0] multiplexer_1_out, multiplexer_9_out, multiplexer_10_out, multiplexer_12_out,
       multiplexer_13_out;

  Multiplexer #(.select(1), .width(32), .disabled("Z"), .enable("false")) multiplexer_1 (
    .in0(r_v0), .in1({32{1'b0}}), .out(multiplexer_1_out), .sel(RST));
  Multiplexer #(.select(1), .width(1), .disabled("Z"), .enable("false")) multiplexer_2 (
    .in0(JR), .in1(1'b0), .out(multiplexer_2_out), .sel(RST));
  Multiplexer #(.select(1), .width(1), .disabled("Z"), .enable("false")) multiplexer_3 (
    .in0(JMP), .out(multiplexer_3_out), .sel(RST));  // open: in1
  Multiplexer #(.select(1), .width(1), .disabled("Z"), .enable("false")) multiplexer_4 (
    .in0(MemToReg), .in1(1'b0), .out(multiplexer_4_out), .sel(RST));
  Multiplexer #(.select(1), .width(1), .disabled("Z"), .enable("false")) multiplexer_5 (
    .in0(MemWrite), .in1(1'b0), .out(multiplexer_5_out), .sel(RST));
  Multiplexer #(.select(1), .width(1), .disabled("Z"), .enable("false")) multiplexer_6 (
    .in0(RegWrite), .in1(1'b0), .out(multiplexer_6_out), .sel(RST));
  Multiplexer #(.select(1), .width(1), .disabled("Z"), .enable("false")) multiplexer_7 (
    .in0(JAL), .in1(1'b0), .out(multiplexer_7_out), .sel(RST));
  Multiplexer #(.select(1), .width(1), .disabled("Z"), .enable("false")) multiplexer_8 (
    .in0(SysCALL), .in1(1'b0), .out(multiplexer_8_out), .sel(RST));
  Multiplexer #(.select(1), .width(32), .disabled("Z"), .enable("false")) multiplexer_9 (
    .in0(RESULT), .in1({32{1'b0}}), .out(multiplexer_9_out), .sel(RST));
  Multiplexer #(.select(1), .width(32), .disabled("Z"), .enable("false")) multiplexer_10 (
    .in0(WriteData), .in1({32{1'b0}}), .out(multiplexer_10_out), .sel(RST));
  Multiplexer #(.select(1), .width(5), .disabled("Z"), .enable("false")) multiplexer_11 (
    .in0(WriteReg_num), .in1({5{1'b0}}), .out(multiplexer_11_out), .sel(RST));
  Multiplexer #(.select(1), .width(32), .disabled("Z"), .enable("false")) multiplexer_12 (
    .in0(IR_ID), .in1({32{1'b0}}), .out(multiplexer_12_out), .sel(RST));
  Multiplexer #(.select(1), .width(32), .disabled("Z"), .enable("false")) multiplexer_13 (
    .in0(PC_ID), .in1({32{1'b0}}), .out(multiplexer_13_out), .sel(RST));
  Register #(.width(32), .trigger("rising"), .Select("low")) register_1 (
    .D(multiplexer_1_out), .en(EN), .Q(r_v0_2), .clk(CLK));  // open: clr
  Register #(.width(1), .trigger("rising"), .Select("low")) register_2 (
    .D(multiplexer_2_out), .en(EN), .Q(JR_2), .clk(CLK));  // open: clr
  Register #(.width(1), .trigger("rising"), .Select("low")) register_3 (
    .D(multiplexer_3_out), .en(EN), .Q(JMP_2), .clk(CLK));  // open: clr
  Register #(.width(1), .trigger("rising"), .Select("low")) register_4 (
    .D(multiplexer_4_out), .en(EN), .Q(MemToReg_2), .clk(CLK));  // open: clr
  Register #(.width(1), .trigger("rising"), .Select("low")) register_5 (
    .D(multiplexer_5_out), .en(EN), .Q(MemWrite_2), .clk(CLK));  // open: clr
  Register #(.width(1), .trigger("rising"), .Select("low")) register_6 (
    .D(multiplexer_6_out), .en(EN), .Q(RegWrite_2), .clk(CLK));  // open: clr
  Register #(.width(1), .trigger("rising"), .Select("low")) register_7 (
    .D(multiplexer_7_out), .en(EN), .Q(JAL_2), .clk(CLK));  // open: clr
  Register #(.width(1), .trigger("rising"), .Select("low")) register_8 (
    .D(multiplexer_8_out), .en(EN), .Q(SysCALL_2), .clk(CLK));  // open: clr
  Register #(.width(32), .trigger("rising"), .Select("low")) register_9 (
    .D(multiplexer_9_out), .en(EN), .Q(RESULT_2), .clk(CLK));  // open: clr
  Register #(.width(32), .trigger("rising"), .Select("low")) register_10 (
    .D(multiplexer_10_out), .en(EN), .Q(WriteData_2), .clk(CLK));  // open: clr
  Register #(.width(5), .trigger("rising"), .Select("low")) register_11 (
    .D(multiplexer_11_out), .en(EN), .Q(WriteReg_num_2), .clk(CLK));  // open: clr
  Register #(.width(32), .trigger("rising"), .Select("low")) register_12 (
    .D(multiplexer_12_out), .en(EN), .Q(IR_EX), .clk(CLK));  // open: clr
  Register #(.width(32), .trigger("rising"), .Select("low")) register_13 (
    .D(multiplexer_13_out), .en(EN), .Q(PC_EX), .clk(CLK));  // open: clr
  Pull_Resistor #(.pull(0)) pull_resistor_1 (.node(RST));
endmodule

module MEM_WB (
  input  [31:0] r_v0,
  input  JR,
  input  JMP,
  input  MemToReg,
  input  RegWrite,
  input  JAL,
  input  SysCALL,
  input  [31:0] RESULT,
  input  [31:0] RD,
  input  [4:0] WriteReg_num,
  input  [31:0] IR_ID,
  input  [31:0] PC_ID,
  input  EN,
  input  CLK,
  input  RST,
  output [31:0] r_v0_2,
  output JR_2,
  output JMP_2,
  output MemToReg_2,
  output RegWrite_2,
  output JAL_2,
  output SysCALL_2,
  output [31:0] RESULT_2,
  output [31:0] RD_2,
  output [4:0] WriteReg_num_2,
  output [31:0] IR_EX,
  output [31:0] PC_EX
);

  wire multiplexer_2_out, multiplexer_3_out, multiplexer_4_out, multiplexer_5_out, multiplexer_6_out,
       multiplexer_7_out;
  wire [4:0] multiplexer_10_out;
  wire [31:0] multiplexer_1_out, multiplexer_8_out, multiplexer_9_out, multiplexer_11_out, multiplexer_12_out;

  Multiplexer #(.select(1), .width(32), .disabled("Z"), .enable("false")) multiplexer_1 (
    .in0(r_v0), .in1({32{1'b0}}), .out(multiplexer_1_out), .sel(RST));
  Multiplexer #(.select(1), .width(1), .disabled("Z"), .enable("false")) multiplexer_2 (
    .in0(JR), .in1(1'b0), .out(multiplexer_2_out), .sel(RST));
  Multiplexer #(.select(1), .width(1), .disabled("Z"), .enable("false")) multiplexer_3 (
    .in0(JMP), .in1(1'b0), .out(multiplexer_3_out), .sel(RST));
  Multiplexer #(.select(1), .width(1), .disabled("Z"), .enable("false")) multiplexer_4 (
    .in0(MemToReg), .in1(1'b0), .out(multiplexer_4_out), .sel(RST));
  Multiplexer #(.select(1), .width(1), .disabled("Z"), .enable("false")) multiplexer_5 (
    .in0(RegWrite), .in1(1'b0), .out(multiplexer_5_out), .sel(RST));
  Multiplexer #(.select(1), .width(1), .disabled("Z"), .enable("false")) multiplexer_6 (
    .in0(JAL), .in1(1'b0), .out(multiplexer_6_out), .sel(RST));
  Multiplexer #(.select(1), .width(1), .disabled("Z"), .enable("false")) multiplexer_7 (
    .in0(SysCALL), .in1(1'b0), .out(multiplexer_7_out), .sel(RST));
  Multiplexer #(.select(1), .width(32), .disabled("Z"), .enable("false")) multiplexer_8 (
    .in0(RESULT), .in1({32{1'b0}}), .out(multiplexer_8_out), .sel(RST));
  Multiplexer #(.select(1), .width(32), .disabled("Z"), .enable("false")) multiplexer_9 (
    .in0(RD), .in1({32{1'b0}}), .out(multiplexer_9_out), .sel(RST));
  Multiplexer #(.select(1), .width(5), .disabled("Z"), .enable("false")) multiplexer_10 (
    .in0(WriteReg_num), .in1({5{1'b0}}), .out(multiplexer_10_out), .sel(RST));
  Multiplexer #(.select(1), .width(32), .disabled("Z"), .enable("false")) multiplexer_11 (
    .in0(IR_ID), .in1({32{1'b0}}), .out(multiplexer_11_out), .sel(RST));
  Multiplexer #(.select(1), .width(32), .disabled("Z"), .enable("false")) multiplexer_12 (
    .in0(PC_ID), .in1({32{1'b0}}), .out(multiplexer_12_out), .sel(RST));
  Register #(.width(32), .trigger("rising"), .Select("low")) register_1 (
    .D(multiplexer_1_out), .en(EN), .Q(r_v0_2), .clk(CLK));  // open: clr
  Register #(.width(1), .trigger("rising"), .Select("low")) register_2 (
    .D(multiplexer_2_out), .en(EN), .Q(JR_2), .clk(CLK));  // open: clr
  Register #(.width(1), .trigger("rising"), .Select("low")) register_3 (
    .D(multiplexer_3_out), .en(EN), .Q(JMP_2), .clk(CLK));  // open: clr
  Register #(.width(1), .trigger("rising"), .Select("low")) register_4 (
    .D(multiplexer_4_out), .en(EN), .Q(MemToReg_2), .clk(CLK));  // open: clr
  Register #(.width(1), .trigger("rising"), .Select("low")) register_5 (
    .D(multiplexer_5_out), .en(EN), .Q(RegWrite_2), .clk(CLK));  // open: clr
  Register #(.width(1), .trigger("rising"), .Select("low")) register_6 (
    .D(multiplexer_6_out), .en(EN), .Q(JAL_2), .clk(CLK));  // open: clr
  Register #(.width(1), .trigger("rising"), .Select("low")) register_7 (
    .D(multiplexer_7_out), .en(EN), .Q(SysCALL_2), .clk(CLK));  // open: clr
  Register #(.width(32), .trigger("rising"), .Select("low")) register_8 (
    .D(multiplexer_8_out), .en(EN), .Q(RESULT_2), .clk(CLK));  // open: clr
  Register #(.width(32), .trigger("rising"), .Select("low")) register_9 (
    .D(multiplexer_9_out), .en(EN), .Q(RD_2), .clk(CLK));  // open: clr
  Register #(.width(5), .trigger("rising"), .Select("low")) register_10 (
    .D(multiplexer_10_out), .en(EN), .Q(WriteReg_num_2), .clk(CLK));  // open: clr
  Register #(.width(32), .trigger("rising"), .Select("low")) register_11 (
    .D(multiplexer_11_out), .en(EN), .Q(IR_EX), .clk(CLK));  // open: clr
  Register #(.width(32), .trigger("rising"), .Select("low")) register_12 (
    .D(multiplexer_12_out), .en(EN), .Q(PC_EX), .clk(CLK));  // open: clr
  Pull_Resistor #(.pull(0)) pull_resistor_1 (.node(RST));
endmodule

module \中断  (
  input  F0,
  input  OP0,
  input  F1,
  input  OP1,
  input  F2,
  input  OP2,
  input  F3,
  input  OP3,
  input  F4,
  input  OP4,
  input  F5,
  input  OP5,
  input  CO,
  output ERET
);

  wire not_1_out, not_2_out, not_3_out, not_4_out, not_5_out, not_6_out, not_7_out, not_8_out, not_9_out;

  not not_1 (not_1_out, F0);
  not not_2 (not_2_out, F1);
  not not_3 (not_3_out, F2);
  not not_4 (not_4_out, F5);
  not not_5 (not_5_out, OP0);
  not not_6 (not_6_out, OP1);
  not not_7 (not_7_out, OP2);
  not not_8 (not_8_out, OP3);
  not not_9 (not_9_out, OP5);
  and and_1 (ERET, not_1_out, not_2_out, not_3_out, F3, F4, not_4_out, not_5_out, not_6_out, not_7_out, not_8_out, OP4, not_9_out, CO);
endmodule

module \ERET判别  (
  input  [5:0] fun,
  input  [5:0] op,
  input  co,
  output eret
);

  \中断  \u_中断_1  (
    .F0(fun[0]), .OP0(op[0]), .F1(fun[1]), .OP1(op[1]), .F2(fun[2]), .OP2(op[2]), .F3(fun[3]), .OP3(op[3]),
    .F4(fun[4]), .OP4(op[4]), .F5(fun[5]), .OP5(op[5]), .CO(co), .ERET(eret));
endmodule

module test (
  input  \关中断 ,
  input  \同步清零信号 ,
  input  \开中断 ,
  output \与中断屏蔽位与 ,
  output out_5,
  output \中断请求 ,
  output [9:0] out_7,
  output out_8
);

  wire \_1号中断_out , and_2_out, and_4_out, button_1_out, clk, d_ff_3_q, IE, not_1_out, not_2_out, or_1_out,
       or_2_out;
  wire [9:0] PC_q, undriven;
  wire [31:0] rom_1_data;

  Button button_1 (.out(button_1_out));
  Counter #(.width(10), .max('h3ff), .ongoal("wrap"), .trigger("rising"), .behavior("new")) PC (
    .D(undriven), .Q(PC_q), .clk(button_1_out));  // open: load, count, carry, clr, preset, down
  ROM #(.addrWidth(10), .dataWidth(32), .Select("high")) rom_1 (.addr(PC_q), .data(rom_1_data));
  D_Flip_Flop #(.trigger("rising"), .Pre_Clr_Positions("LEGACY"), .NegatePresetClear("false"), .enable("true"), .NewFFLayout("false")) d_ff_1 (
    .Qn(out_5), .preset(\关中断 ), .reset(\开中断 ));  // open: clk, D, Q, en
  and and_1 (\中断请求 , out_5, \与中断屏蔽位与 );
  \ERET判别  \eret判别_1  (.fun(rom_1_data[5:0]), .op(rom_1_data[31:26]), .co(rom_1_data[25]));  // open: eret
  Register #(.width(1), .trigger("rising"), .Select("low")) u_IE ();  // open: D, en, Q, clk, clr
  and and_2 (and_2_out, \中断请求 , not_1_out);
  not not_1 (not_1_out, 1'b0);
  not not_2 (not_2_out, IE);
  Clock #(.highDuration(1), .lowDuration(1)) clock_1 (.out(clk));
  Button \_1号中断  (.out(\_1号中断_out ));
  LED #(.active("true")) \_1号中断等待指示灯  (.in(or_1_out));
  D_Flip_Flop #(.trigger("rising"), .Pre_Clr_Positions("LEGACY"), .NegatePresetClear("false"), .enable("true"), .NewFFLayout("false")) d_ff_2 (
    .clk(clk), .D(and_2_out), .Q(IE));  // open: Qn, preset, en, reset
  and and_3 (out_8, \中断请求 , not_2_out);
  or or_1 (or_1_out, \与中断屏蔽位与 , d_ff_3_q);
  Register #(.width(10), .trigger("rising"), .Select("low")) register_1 (
    .D(PC_q), .en(out_8), .Q(out_7), .clk(clk));  // open: clr
  D_Flip_Flop #(.trigger("rising"), .Pre_Clr_Positions("LEGACY"), .NegatePresetClear("false"), .enable("true"), .NewFFLayout("false")) d_ff_3 (
    .clk(\_1号中断_out ), .D(1'b1), .Q(d_ff_3_q), .reset(\与中断屏蔽位与 ));  // open: Qn, preset, en
  or or_2 (or_2_out, d_ff_3_q, \与中断屏蔽位与 );
  and and_4 (and_4_out, or_2_out, ~\同步清零信号 );  // AND_Gate
  D_Flip_Flop #(.trigger("rising"), .Pre_Clr_Positions("LEGACY"), .NegatePresetClear("false"), .enable("true"), .NewFFLayout("false")) IR1 (
    .clk(clk), .D(and_4_out), .Q(\与中断屏蔽位与 ));  // open: Qn, preset, en, reset

  // Notes on the sheet:
  //   contents of rom_1 (hex, n*v repeats v):
  //   42000018 8000c05 20110001 20120002 20130003 8000c09 20110001 20120002 20130003 8000c0d 20110001
  //   20120002 20130003 8000c11 20110001 20120002 20130003 c000cb8 20100001 20110001 118fc0 112020
  //   20020022 c 118882 12200001 8000c15 112020 20020022 c 20110001 118880 112020 20020022 c 12200001
  //   8000c1f 20110001 118fc0 112020 20020022 c 1188c3 112020 20020022 c 118903 112020 20020022 c 118903
  //   112020 20020022 c 118903 112020 20020022 c 118903 112020 20020022 c 118903 112020 20020022 c 118903
  //   112020 20020022 c 118903 112020 20020022 c 20100001 109fc0 139fc3 8021 2012000c 24160003 26100001
  //   3210000f 20080008 20090001 139900 2709825 132020 20020022 c 1094022 1500fff9 22100001 2018000f
  //   2188024 108700 20080008 20090001 139902 2709825 132021 20020022 c 1094022 1500fff9 108702 2c9b022
  //   12c00001 8000c50 4020 1084027 84400 3508ffff 82021 20020022 c 2010ffff 20110000 ae300000 22100001
  //   22310004 ae300000 22100001 22310004 ae300000 22100001 22310004 ae300000 22100001 22310004 ae300000
  //   22100001 22310004 ae300000 22100001 22310004 ae300000 22100001 22310004 ae300000 22100001 22310004
  //   ae300000 22100001 22310004 ae300000 22100001 22310004 ae300000 22100001 22310004 ae300000 22100001
  //   22310004 ae300000 22100001 22310004 ae300000 22100001 22310004 ae300000 22100001 22310004 ae300000
  //   22100001 22310004 22100001 8020 2011003c 8e130000 8e340000 274402a 11000002 ae330000 ae140000
  //   2231fffc 1611fff8 102020 20020022 c 22100004 2011003c 1611fff2 20020032 c 20100000 22100001 102020
  //   20020022 c 22100002 102020 20020022 c 22100003 102020 20020022 c 22100004 102020 20020022 c 22100005
  //   102020 20020022 c 22100006 102020 20020022 c 22100007 102020 20020022 c 22100008 102020 20020022
  //   20020022 c 3e00008
  //   OP
  //   Func
  //   中断信号采样参考电路
  //   Reset 
endmodule
module rsrtused (
  input  OP0,
  input  OP1,
  input  OP2,
  input  OP3,
  input  OP4,
  input  OP5,
  input  F0,
  input  F1,
  input  F2,
  input  F3,
  input  F4,
  input  F5,
  output RsUsed,
  output RtUsed
);

  wire and_1_out, and_2_out, and_3_out, and_4_out, and_5_out, and_6_out, and_7_out, and_8_out, and_9_out,
       and_10_out, and_11_out, and_12_out, and_13_out, and_14_out, and_15_out, and_16_out, and_17_out,
       and_18_out, and_19_out, and_20_out, and_21_out, and_22_out, and_23_out, and_24_out, and_25_out,
       and_26_out, and_27_out, and_28_out, and_29_out, and_30_out, and_31_out, and_32_out, and_33_out,
       and_34_out, and_35_out, and_36_out, and_37_out, and_38_out, and_39_out, and_40_out, and_41_out,
       not_1_out, not_2_out, not_3_out, not_4_out, not_5_out, not_6_out, not_7_out, not_8_out, not_9_out,
       not_10_out, not_11_out, not_12_out, not_13_out, not_14_out, not_15_out, not_16_out, not_17_out,
       not_18_out, not_19_out, not_20_out, not_21_out, not_22_out, not_23_out, not_24_out, not_25_out,
       not_26_out, not_27_out, not_28_out, not_29_out, not_30_out, not_31_out, not_32_out, not_33_out,
       not_34_out, not_35_out, not_36_out, not_37_out, not_38_out, not_39_out, not_40_out, not_41_out,
       not_42_out, not_43_out, not_44_out, not_45_out, not_46_out, not_47_out, not_48_out, not_49_out,
       not_50_out, not_51_out, not_52_out, not_53_out, not_54_out, not_55_out, not_56_out, not_57_out,
       not_58_out, not_59_out, not_60_out, not_61_out, not_62_out, not_63_out, not_64_out, not_65_out,
       not_66_out, not_67_out, not_68_out, not_69_out, not_70_out, not_71_out, not_72_out, not_73_out,
       not_74_out, not_75_out, not_76_out, not_77_out, not_78_out, not_79_out, not_80_out, not_81_out,
       not_82_out, not_83_out, not_84_out, not_85_out, not_86_out, not_87_out, not_88_out, not_89_out,
       not_90_out, not_91_out, not_92_out, not_93_out, not_94_out, not_95_out, not_96_out, not_97_out,
       not_98_out, not_99_out, not_100_out, not_101_out, not_102_out, not_103_out, not_104_out, not_105_out,
       not_106_out, not_107_out, not_108_out, not_109_out, not_110_out, not_111_out, not_112_out,
       not_113_out, not_114_out, not_115_out, not_116_out, not_117_out, not_118_out, not_119_out,
       not_120_out, not_121_out, not_122_out, not_123_out, not_124_out, not_125_out, not_126_out,
       not_127_out, not_128_out, not_129_out, not_130_out, not_131_out, not_132_out, not_133_out,
       not_134_out, not_135_out, not_136_out, not_137_out, not_138_out, not_139_out, not_140_out,
       not_141_out, not_142_out, not_143_out, not_144_out, not_145_out, not_146_out, not_147_out,
       not_148_out, not_149_out, not_150_out, not_151_out, not_152_out, not_153_out, not_154_out,
       not_155_out, not_156_out, not_157_out, not_158_out, not_159_out, not_160_out, not_161_out,
       not_162_out, not_163_out, not_164_out, not_165_out, not_166_out, not_167_out, not_168_out,
       not_169_out, not_170_out, not_171_out, not_172_out, not_173_out, not_174_out, not_175_out,
       not_176_out, not_177_out, not_178_out, not_179_out, not_180_out, not_181_out, not_182_out,
       not_183_out, not_184_out, not_185_out, not_186_out, not_187_out, not_188_out, not_189_out,
       not_190_out, not_191_out, not_192_out, not_193_out, not_194_out, not_195_out, not_196_out,
       not_197_out, not_198_out, not_199_out, not_200_out, not_201_out, not_202_out, not_203_out,
       not_204_out, not_205_out, not_206_out, not_207_out, not_208_out, not_209_out, not_210_out,
       not_211_out, not_212_out, not_213_out, not_214_out, not_215_out, not_216_out, not_217_out,
       not_218_out, not_219_out, not_220_out, not_221_out, not_222_out, not_223_out, not_224_out,
       not_225_out, not_226_out, not_227_out, not_228_out, not_229_out, not_230_out, not_231_out,
       not_232_out, not_233_out, not_234_out, not_235_out, not_236_out, not_237_out, not_238_out,
       not_239_out, not_240_out, not_241_out, not_242_out, not_243_out, not_244_out, not_245_out,
       not_246_out, not_247_out, not_248_out, not_249_out, not_250_out, not_251_out, not_252_out,
       not_253_out, not_254_out, not_255_out, not_256_out, not_257_out, not_258_out, not_259_out,
       not_260_out, not_261_out, not_262_out, not_263_out, not_264_out, not_265_out, not_266_out,
       not_267_out, not_268_out, not_269_out, not_270_out, not_271_out, not_272_out, not_273_out,
       not_274_out, not_275_out, not_276_out, not_277_out, not_278_out, not_279_out, not_280_out,
       not_281_out, not_282_out, not_283_out, not_284_out, not_285_out, not_286_out, not_287_out,
       not_288_out, not_289_out, not_290_out, not_291_out, not_292_out, not_293_out, not_294_out;

  not not_1 (not_1_out, OP5);
  not not_2 (not_2_out, OP4);
  not not_3 (not_3_out, OP3);
  not not_4 (not_4_out, OP2);
  not not_5 (not_5_out, OP1);
  not not_6 (not_6_out, OP0);
  not not_7 (not_7_out, F4);
  not not_8 (not_8_out, F3);
  not not_9 (not_9_out, F2);
  not not_10 (not_10_out, F1);
  not not_11 (not_11_out, F0);
  not not_12 (not_12_out, OP5);
  not not_13 (not_13_out, OP4);
  not not_14 (not_14_out, OP3);
  not not_15 (not_15_out, OP2);
  not not_16 (not_16_out, OP1);
  not not_17 (not_17_out, OP0);
  not not_18 (not_18_out, F4);
  not not_19 (not_19_out, F3);
  not not_20 (not_20_out, F2);
  not not_21 (not_21_out, F1);
  not not_22 (not_22_out, OP5);
  not not_23 (not_23_out, OP4);
  not not_24 (not_24_out, OP3);
  not not_25 (not_25_out, OP2);
  not not_26 (not_26_out, OP1);
  not not_27 (not_27_out, OP0);
  not not_28 (not_28_out, F4);
  not not_29 (not_29_out, F3);
  not not_30 (not_30_out, F2);
  not not_31 (not_31_out, F0);
  not not_32 (not_32_out, OP5);
  not not_33 (not_33_out, OP4);
  not not_34 (not_34_out, OP3);
  not not_35 (not_35_out, OP2);
  not not_36 (not_36_out, OP1);
  not not_37 (not_37_out, OP0);
  not not_38 (not_38_out, F4);
  not not_39 (not_39_out, F3);
  not not_40 (not_40_out, F1);
  not not_41 (not_41_out, F0);
  not not_42 (not_42_out, OP5);
  not not_43 (not_43_out, OP4);
  not not_44 (not_44_out, OP3);
  not not_45 (not_45_out, OP2);
  not not_46 (not_46_out, OP1);
  not not_47 (not_47_out, OP0);
  not not_48 (not_48_out, F4);
  not not_49 (not_49_out, F3);
  not not_50 (not_50_out, F1);
  not not_51 (not_51_out, OP5);
  not not_52 (not_52_out, OP4);
  not not_53 (not_53_out, OP3);
  not not_54 (not_54_out, OP2);
  not not_55 (not_55_out, OP1);
  not not_56 (not_56_out, OP0);
  not not_57 (not_57_out, F4);
  not not_58 (not_58_out, F3);
  not not_59 (not_59_out, OP5);
  not not_60 (not_60_out, OP4);
  not not_61 (not_61_out, OP3);
  not not_62 (not_62_out, OP2);
  not not_63 (not_63_out, OP1);
  not not_64 (not_64_out, OP0);
  not not_65 (not_65_out, F4);
  not not_66 (not_66_out, F2);
  not not_67 (not_67_out, F0);
  not not_68 (not_68_out, OP5);
  not not_69 (not_69_out, OP4);
  not not_70 (not_70_out, OP3);
  not not_71 (not_71_out, OP2);
  not not_72 (not_72_out, OP1);
  not not_73 (not_73_out, OP0);
  not not_74 (not_74_out, F4);
  not not_75 (not_75_out, F2);
  not not_76 (not_76_out, OP5);
  not not_77 (not_77_out, OP4);
  not not_78 (not_78_out, OP3);
  not not_79 (not_79_out, OP2);
  not not_80 (not_80_out, OP1);
  not not_81 (not_81_out, OP0);
  not not_82 (not_82_out, F5);
  not not_83 (not_83_out, F4);
  not not_84 (not_84_out, F2);
  not not_85 (not_85_out, F1);
  not not_86 (not_86_out, F0);
  not not_87 (not_87_out, OP5);
  not not_88 (not_88_out, OP4);
  not not_89 (not_89_out, OP3);
  not not_90 (not_90_out, OP2);
  not not_91 (not_91_out, OP1);
  not not_92 (not_92_out, OP0);
  not not_93 (not_93_out, F5);
  not not_94 (not_94_out, F4);
  not not_95 (not_95_out, F1);
  not not_96 (not_96_out, F0);
  not not_97 (not_97_out, OP5);
  not not_98 (not_98_out, OP4);
  not not_99 (not_99_out, OP3);
  not not_100 (not_100_out, OP1);
  not not_101 (not_101_out, OP0);
  not not_102 (not_102_out, OP5);
  not not_103 (not_103_out, OP4);
  not not_104 (not_104_out, OP3);
  not not_105 (not_105_out, OP1);
  not not_106 (not_106_out, OP5);
  not not_107 (not_107_out, OP4);
  not not_108 (not_108_out, OP2);
  not not_109 (not_109_out, OP1);
  not not_110 (not_110_out, OP0);
  not not_111 (not_111_out, OP5);
  not not_112 (not_112_out, OP4);
  not not_113 (not_113_out, OP1);
  not not_114 (not_114_out, OP0);
  not not_115 (not_115_out, OP5);
  not not_116 (not_116_out, OP4);
  not not_117 (not_117_out, OP2);
  not not_118 (not_118_out, OP1);
  not not_119 (not_119_out, OP5);
  not not_120 (not_120_out, OP4);
  not not_121 (not_121_out, OP2);
  not not_122 (not_122_out, OP0);
  not not_123 (not_123_out, OP5);
  not not_124 (not_124_out, OP4);
  not not_125 (not_125_out, OP1);
  not not_126 (not_126_out, OP4);
  not not_127 (not_127_out, OP3);
  not not_128 (not_128_out, OP2);
  not not_129 (not_129_out, OP4);
  not not_130 (not_130_out, OP2);
  not not_131 (not_131_out, OP5);
  not not_132 (not_132_out, OP4);
  not not_133 (not_133_out, OP3);
  not not_134 (not_134_out, OP2);
  not not_135 (not_135_out, OP1);
  not not_136 (not_136_out, OP0);
  not not_137 (not_137_out, F5);
  not not_138 (not_138_out, F4);
  not not_139 (not_139_out, F3);
  not not_140 (not_140_out, OP5);
  not not_141 (not_141_out, OP4);
  not not_142 (not_142_out, OP2);
  not not_143 (not_143_out, OP5);
  not not_144 (not_144_out, OP4);
  not not_145 (not_145_out, OP3);
  not not_146 (not_146_out, OP4);
  not not_147 (not_147_out, OP2);
  not not_148 (not_148_out, OP1);
  not not_149 (not_149_out, OP0);
  not not_150 (not_150_out, OP5);
  not not_151 (not_151_out, OP4);
  not not_152 (not_152_out, OP3);
  not not_153 (not_153_out, OP2);
  not not_154 (not_154_out, OP1);
  not not_155 (not_155_out, OP0);
  not not_156 (not_156_out, F5);
  not not_157 (not_157_out, F4);
  not not_158 (not_158_out, F3);
  not not_159 (not_159_out, F2);
  not not_160 (not_160_out, F1);
  not not_161 (not_161_out, F0);
  not not_162 (not_162_out, OP5);
  not not_163 (not_163_out, OP4);
  not not_164 (not_164_out, OP3);
  not not_165 (not_165_out, OP2);
  not not_166 (not_166_out, OP1);
  not not_167 (not_167_out, OP0);
  not not_168 (not_168_out, F5);
  not not_169 (not_169_out, F4);
  not not_170 (not_170_out, F3);
  not not_171 (not_171_out, F2);
  not not_172 (not_172_out, OP5);
  not not_173 (not_173_out, OP4);
  not not_174 (not_174_out, OP3);
  not not_175 (not_175_out, OP2);
  not not_176 (not_176_out, OP1);
  not not_177 (not_177_out, OP0);
  not not_178 (not_178_out, F5);
  not not_179 (not_179_out, F4);
  not not_180 (not_180_out, F3);
  not not_181 (not_181_out, F2);
  not not_182 (not_182_out, F0);
  not not_183 (not_183_out, OP5);
  not not_184 (not_184_out, OP4);
  not not_185 (not_185_out, OP3);
  not not_186 (not_186_out, OP2);
  not not_187 (not_187_out, OP1);
  not not_188 (not_188_out, OP0);
  not not_189 (not_189_out, F4);
  not not_190 (not_190_out, F3);
  not not_191 (not_191_out, F2);
  not not_192 (not_192_out, F1);
  not not_193 (not_193_out, F0);
  not not_194 (not_194_out, OP5);
  not not_195 (not_195_out, OP4);
  not not_196 (not_196_out, OP3);
  not not_197 (not_197_out, OP2);
  not not_198 (not_198_out, OP1);
  not not_199 (not_199_out, OP0);
  not not_200 (not_200_out, F4);
  not not_201 (not_201_out, F3);
  not not_202 (not_202_out, F2);
  not not_203 (not_203_out, F1);
  not not_204 (not_204_out, OP5);
  not not_205 (not_205_out, OP4);
  not not_206 (not_206_out, OP3);
  not not_207 (not_207_out, OP2);
  not not_208 (not_208_out, OP1);
  not not_209 (not_209_out, OP0);
  not not_210 (not_210_out, F4);
  not not_211 (not_211_out, F3);
  not not_212 (not_212_out, F2);
  not not_213 (not_213_out, F0);
  not not_214 (not_214_out, OP5);
  not not_215 (not_215_out, OP4);
  not not_216 (not_216_out, OP3);
  not not_217 (not_217_out, OP2);
  not not_218 (not_218_out, OP1);
  not not_219 (not_219_out, OP0);
  not not_220 (not_220_out, F4);
  not not_221 (not_221_out, F3);
  not not_222 (not_222_out, F1);
  not not_223 (not_223_out, F0);
  not not_224 (not_224_out, OP5);
  not not_225 (not_225_out, OP4);
  not not_226 (not_226_out, OP3);
  not not_227 (not_227_out, OP2);
  not not_228 (not_228_out, OP1);
  not not_229 (not_229_out, OP0);
  not not_230 (not_230_out, F4);
  not not_231 (not_231_out, F3);
  not not_232 (not_232_out, F1);
  not not_233 (not_233_out, OP5);
  not not_234 (not_234_out, OP4);
  not not_235 (not_235_out, OP3);
  not not_236 (not_236_out, OP2);
  not not_237 (not_237_out, OP1);
  not not_238 (not_238_out, OP0);
  not not_239 (not_239_out, F4);
  not not_240 (not_240_out, F3);
  not not_241 (not_241_out, OP5);
  not not_242 (not_242_out, OP4);
  not not_243 (not_243_out, OP3);
  not not_244 (not_244_out, OP2);
  not not_245 (not_245_out, OP1);
  not not_246 (not_246_out, OP0);
  not not_247 (not_247_out, F4);
  not not_248 (not_248_out, F2);
  not not_249 (not_249_out, F0);
  not not_250 (not_250_out, OP5);
  not not_251 (not_251_out, OP4);
  not not_252 (not_252_out, OP3);
  not not_253 (not_253_out, OP2);
  not not_254 (not_254_out, OP1);
  not not_255 (not_255_out, OP0);
  not not_256 (not_256_out, F4);
  not not_257 (not_257_out, F2);
  not not_258 (not_258_out, OP5);
  not not_259 (not_259_out, OP4);
  not not_260 (not_260_out, OP3);
  not not_261 (not_261_out, OP2);
  not not_262 (not_262_out, OP1);
  not not_263 (not_263_out, OP0);
  not not_264 (not_264_out, F5);
  not not_265 (not_265_out, F4);
  not not_266 (not_266_out, F1);
  not not_267 (not_267_out, F0);
  not not_268 (not_268_out, OP5);
  not not_269 (not_269_out, OP4);
  not not_270 (not_270_out, OP3);
  not not_271 (not_271_out, OP1);
  not not_272 (not_272_out, OP0);
  not not_273 (not_273_out, OP5);
  not not_274 (not_274_out, OP4);
  not not_275 (not_275_out, OP3);
  not not_276 (not_276_out, OP1);
  not not_277 (not_277_out, OP4);
  not not_278 (not_278_out, OP2);
  not not_279 (not_279_out, OP5);
  not not_280 (not_280_out, OP4);
  not not_281 (not_281_out, OP3);
  not not_282 (not_282_out, OP2);
  not not_283 (not_283_out, OP1);
  not not_284 (not_284_out, OP0);
  not not_285 (not_285_out, F5);
  not not_286 (not_286_out, F4);
  not not_287 (not_287_out, F3);
  not not_288 (not_288_out, OP5);
  not not_289 (not_289_out, OP4);
  not not_290 (not_290_out, OP3);
  not not_291 (not_291_out, OP4);
  not not_292 (not_292_out, OP2);
  not not_293 (not_293_out, OP1);
  not not_294 (not_294_out, OP0);
  and and_1 (and_1_out, not_1_out, not_2_out, not_3_out, not_4_out, not_5_out, not_6_out, F5, not_7_out, not_8_out, not_9_out, not_10_out, not_11_out);
  and and_2 (and_2_out, not_12_out, not_13_out, not_14_out, not_15_out, not_16_out, not_17_out, F5, not_18_out, not_19_out, not_20_out, not_21_out, F0);
  and and_3 (and_3_out, not_22_out, not_23_out, not_24_out, not_25_out, not_26_out, not_27_out, F5, not_28_out, not_29_out, not_30_out, F1, not_31_out);
  and and_4 (and_4_out, not_32_out, not_33_out, not_34_out, not_35_out, not_36_out, not_37_out, F5, not_38_out, not_39_out, F2, not_40_out, not_41_out);
  and and_5 (and_5_out, not_42_out, not_43_out, not_44_out, not_45_out, not_46_out, not_47_out, F5, not_48_out, not_49_out, F2, not_50_out, F0);
  and and_6 (and_6_out, not_51_out, not_52_out, not_53_out, not_54_out, not_55_out, not_56_out, F5, not_57_out, not_58_out, F2, F1, F0);
  and and_7 (and_7_out, not_59_out, not_60_out, not_61_out, not_62_out, not_63_out, not_64_out, F5, not_65_out, F3, not_66_out, F1, not_67_out);
  and and_8 (and_8_out, not_68_out, not_69_out, not_70_out, not_71_out, not_72_out, not_73_out, F5, not_74_out, F3, not_75_out, F1, F0);
  and and_9 (and_9_out, not_76_out, not_77_out, not_78_out, not_79_out, not_80_out, not_81_out, not_82_out, not_83_out, F3, not_84_out, not_85_out, not_86_out);
  and and_10 (and_10_out, not_87_out, not_88_out, not_89_out, not_90_out, not_91_out, not_92_out, not_93_out, not_94_out, F3, F2, not_95_out, not_96_out);
  and and_11 (and_11_out, not_97_out, not_98_out, not_99_out, OP2, not_100_out, not_101_out);
  and and_12 (and_12_out, not_102_out, not_103_out, not_104_out, OP2, not_105_out, OP0);
  and and_13 (and_13_out, not_106_out, not_107_out, OP3, not_108_out, not_109_out, not_110_out);
  and and_14 (and_14_out, not_111_out, not_112_out, OP3, OP2, not_113_out, not_114_out);
  and and_15 (and_15_out, not_115_out, not_116_out, OP3, not_117_out, not_118_out, OP0);
  and and_16 (and_16_out, not_119_out, not_120_out, OP3, not_121_out, OP1, not_122_out);
  and and_17 (and_17_out, not_123_out, not_124_out, OP3, OP2, not_125_out, OP0);
  and and_18 (and_18_out, OP5, not_126_out, not_127_out, not_128_out, OP1, OP0);
  and and_19 (and_19_out, OP5, not_129_out, OP3, not_130_out, OP1, OP0);
  and and_20 (and_20_out, not_131_out, not_132_out, not_133_out, not_134_out, not_135_out, not_136_out, not_137_out, not_138_out, not_139_out, F2, F1, F0);
  and and_21 (and_21_out, not_140_out, not_141_out, OP3, not_142_out, OP1, OP0);
  and and_22 (and_22_out, not_143_out, not_144_out, not_145_out, OP2, OP1, OP0);
  and and_23 (and_23_out, OP5, not_146_out, OP3, not_147_out, not_148_out, not_149_out);
  and and_24 (and_24_out, not_150_out, not_151_out, not_152_out, not_153_out, not_154_out, not_155_out, not_156_out, not_157_out, not_158_out, not_159_out, not_160_out, not_161_out);
  and and_25 (and_25_out, not_162_out, not_163_out, not_164_out, not_165_out, not_166_out, not_167_out, not_168_out, not_169_out, not_170_out, not_171_out, F1, F0);
  and and_26 (and_26_out, not_172_out, not_173_out, not_174_out, not_175_out, not_176_out, not_177_out, not_178_out, not_179_out, not_180_out, not_181_out, F1, not_182_out);
  and and_27 (and_27_out, not_183_out, not_184_out, not_185_out, not_186_out, not_187_out, not_188_out, F5, not_189_out, not_190_out, not_191_out, not_192_out, not_193_out);
  and and_28 (and_28_out, not_194_out, not_195_out, not_196_out, not_197_out, not_198_out, not_199_out, F5, not_200_out, not_201_out, not_202_out, not_203_out, F0);
  and and_29 (and_29_out, not_204_out, not_205_out, not_206_out, not_207_out, not_208_out, not_209_out, F5, not_210_out, not_211_out, not_212_out, F1, not_213_out);
  and and_30 (and_30_out, not_214_out, not_215_out, not_216_out, not_217_out, not_218_out, not_219_out, F5, not_220_out, not_221_out, F2, not_222_out, not_223_out);
  and and_31 (and_31_out, not_224_out, not_225_out, not_226_out, not_227_out, not_228_out, not_229_out, F5, not_230_out, not_231_out, F2, not_232_out, F0);
  and and_32 (and_32_out, not_233_out, not_234_out, not_235_out, not_236_out, not_237_out, not_238_out, F5, not_239_out, not_240_out, F2, F1, F0);
  and and_33 (and_33_out, not_241_out, not_242_out, not_243_out, not_244_out, not_245_out, not_246_out, F5, not_247_out, F3, not_248_out, F1, not_249_out);
  and and_34 (and_34_out, not_250_out, not_251_out, not_252_out, not_253_out, not_254_out, not_255_out, F5, not_256_out, F3, not_257_out, F1, F0);
  and and_35 (and_35_out, not_258_out, not_259_out, not_260_out, not_261_out, not_262_out, not_263_out, not_264_out, not_265_out, F3, F2, not_266_out, not_267_out);
  and and_36 (and_36_out, not_268_out, not_269_out, not_270_out, OP2, not_271_out, not_272_out);
  and and_37 (and_37_out, not_273_out, not_274_out, not_275_out, OP2, not_276_out, OP0);
  and and_38 (and_38_out, OP5, not_277_out, OP3, not_278_out, OP1, OP0);
  and and_39 (and_39_out, not_279_out, not_280_out, not_281_out, not_282_out, not_283_out, not_284_out, not_285_out, not_286_out, not_287_out, F2, F1, F0);
  and and_40 (and_40_out, not_288_out, not_289_out, not_290_out, OP2, OP1, OP0);
  and and_41 (and_41_out, OP5, not_291_out, OP3, not_292_out, not_293_out, not_294_out);
  or or_1 (RsUsed, and_1_out, and_2_out, and_3_out, and_4_out, and_5_out, and_6_out, and_7_out, and_8_out, and_9_out, and_10_out, and_11_out, and_12_out, and_13_out, and_14_out, and_15_out, and_16_out, and_17_out, and_18_out, and_19_out, and_20_out, and_21_out, and_22_out, and_23_out);
  or or_2 (RtUsed, and_24_out, and_25_out, and_26_out, and_27_out, and_28_out, and_29_out, and_30_out, and_31_out, and_32_out, and_33_out, and_34_out, and_35_out, and_36_out, and_37_out, and_38_out, and_39_out, and_40_out, and_41_out);
endmodule

module \气泡流水线控制逻辑  (
  input  branch,
  input  [31:0] IR,
  input  [4:0] MEM_WriteReg_num,
  input  [4:0] rs,
  input  [4:0] rt,
  input  [4:0] EX_WriteReg_num,
  input  EX_RegWrite,
  input  MEM_RegWrite,
  output FlushID_EX,
  output FlushIF_ID,
  output Stall
);

  wire and_1_out, and_2_out, and_3_out, and_4_out, comparator_1_gt, comparator_1_lt, comparator_2_gt,
       comparator_2_lt, comparator_3_eq, comparator_4_eq, comparator_5_eq, comparator_6_eq, rs__0, RsUsed,
       rt__0, RtUsed;

  rsrtused rsrtused_1 (
    .OP0(IR[26]), .OP1(IR[27]), .OP2(IR[28]), .OP3(IR[29]), .OP4(IR[30]), .OP5(IR[31]), .F0(IR[0]),
    .F1(IR[1]), .F2(IR[2]), .F3(IR[3]), .F4(IR[4]), .F5(IR[5]), .RsUsed(RsUsed), .RtUsed(RtUsed));
  Comparator #(.width(5), .mode("twosComplement")) comparator_1 (
    .a(rs), .b({5{1'b0}}), .gt(comparator_1_gt), .lt(comparator_1_lt));  // open: eq
  Comparator #(.width(5), .mode("twosComplement")) comparator_2 (
    .a(rt), .b({5{1'b0}}), .gt(comparator_2_gt), .lt(comparator_2_lt));  // open: eq
  or or_1 (rs__0, comparator_1_gt, comparator_1_lt);
  or or_2 (rt__0, comparator_2_gt, comparator_2_lt);
  and and_1 (and_1_out, rs__0, RsUsed, MEM_RegWrite, comparator_3_eq);
  Comparator #(.width(5), .mode("twosComplement")) comparator_3 (
    .a(MEM_WriteReg_num), .b(rs), .eq(comparator_3_eq));  // open: gt, lt
  Comparator #(.width(5), .mode("twosComplement")) comparator_4 (
    .a(MEM_WriteReg_num), .b(rt), .eq(comparator_4_eq));  // open: gt, lt
  Comparator #(.width(5), .mode("twosComplement")) comparator_5 (
    .a(EX_WriteReg_num), .b(rs), .eq(comparator_5_eq));  // open: gt, lt
  Comparator #(.width(5), .mode("twosComplement")) comparator_6 (
    .a(EX_WriteReg_num), .b(rt), .eq(comparator_6_eq));  // open: gt, lt
  or or_3 (Stall, and_1_out, and_2_out, and_3_out, and_4_out);
  and and_2 (and_2_out, rt__0, RtUsed, MEM_RegWrite, comparator_4_eq);
  and and_3 (and_3_out, rs__0, RsUsed, EX_RegWrite, comparator_5_eq);
  and and_4 (and_4_out, rt__0, RtUsed, EX_RegWrite, comparator_6_eq);
  or or_4 (FlushID_EX, Stall, branch);

  assign FlushIF_ID = branch;

  // Notes on the sheet:
  //   op
  //   Func
endmodule

module \EX重定向控制逻辑  (
  input  branch,
  input  [31:0] IR,
  input  [4:0] rs,
  input  [4:0] rt,
  input  [4:0] MEM_WriteReg_num,
  input  EX_MemRead,
  input  [4:0] EX_WriteReg_num,
  input  MEM_RegWrite,
  input  EX_RegWrite,
  output FlushID_EX,
  output FlushIF_ID,
  output Stall,
  output [1:0] FwdA,
  output [1:0] FwdB
);

  wire and_1_out, and_2_out, and_3_out, and_4_out, and_5_out, and_6_out, comparator_1_gt, comparator_1_lt,
       comparator_2_gt, comparator_2_lt, EX_WriteReg__rs, EX_WriteReg__rt, MEM_WriteReg__rs,
       MEM_WriteReg__rt, rs__0, RsUsed, rt__0, RtUsed;
  wire [1:0] multiplexer_1_out, multiplexer_3_out;

  rsrtused rsrtused_1 (
    .OP0(IR[26]), .OP1(IR[27]), .OP2(IR[28]), .OP3(IR[29]), .OP4(IR[30]), .OP5(IR[31]), .F0(IR[0]),
    .F1(IR[1]), .F2(IR[2]), .F3(IR[3]), .F4(IR[4]), .F5(IR[5]), .RsUsed(RsUsed), .RtUsed(RtUsed));
  Comparator #(.width(5), .mode("twosComplement")) comparator_1 (
    .a(rs), .b({5{1'b0}}), .gt(comparator_1_gt), .lt(comparator_1_lt));  // open: eq
  Comparator #(.width(5), .mode("twosComplement")) comparator_2 (
    .a(rt), .b({5{1'b0}}), .gt(comparator_2_gt), .lt(comparator_2_lt));  // open: eq
  or or_1 (rs__0, comparator_1_gt, comparator_1_lt);
  or or_2 (rt__0, comparator_2_gt, comparator_2_lt);
  Multiplexer #(.select(1), .width(2), .disabled("Z"), .enable("false")) multiplexer_1 (
    .in0(2'b00), .in1(2'b01), .out(multiplexer_1_out), .sel(and_1_out));
  and and_1 (and_1_out, RsUsed, MEM_RegWrite, rs__0, MEM_WriteReg__rs);
  Comparator #(.width(5), .mode("twosComplement")) comparator_3 (
    .a(MEM_WriteReg_num), .b(rs), .eq(MEM_WriteReg__rs));  // open: gt, lt
  Comparator #(.width(5), .mode("twosComplement")) comparator_4 (
    .a(MEM_WriteReg_num), .b(rt), .eq(MEM_WriteReg__rt));  // open: gt, lt
  Comparator #(.width(5), .mode("twosComplement")) comparator_5 (
    .a(EX_WriteReg_num), .b(rs), .eq(EX_WriteReg__rs));  // open: gt, lt
  Comparator #(.width(5), .mode("twosComplement")) comparator_6 (
    .a(EX_WriteReg_num), .b(rt), .eq(EX_WriteReg__rt));  // open: gt, lt
  Multiplexer #(.select(1), .width(2), .disabled("Z"), .enable("false")) multiplexer_2 (
    .in0(multiplexer_1_out), .in1(2'b10), .out(FwdA), .sel(and_2_out));
  and and_2 (and_2_out, RsUsed, EX_RegWrite, rs__0, EX_WriteReg__rs);
  and and_3 (and_3_out, EX_WriteReg__rs, RsUsed, EX_MemRead, rs__0);
  or or_3 (Stall, and_3_out, and_4_out);
  and and_4 (and_4_out, EX_WriteReg__rt, RtUsed, EX_MemRead, rt__0);
  Multiplexer #(.select(1), .width(2), .disabled("Z"), .enable("false")) multiplexer_3 (
    .in0(2'b00), .in1(2'b01), .out(multiplexer_3_out), .sel(and_5_out));
  and and_5 (and_5_out, RtUsed, MEM_RegWrite, rt__0, MEM_WriteReg__rt);
  or or_4 (FlushID_EX, Stall, branch);
  Multiplexer #(.select(1), .width(2), .disabled("Z"), .enable("false")) multiplexer_4 (
    .in0(multiplexer_3_out), .in1(2'b10), .out(FwdB), .sel(and_6_out));
  and and_6 (and_6_out, RtUsed, EX_RegWrite, rt__0, EX_WriteReg__rt);

  assign FlushIF_ID = branch;

  // Notes on the sheet:
  //   op
  //   Func
endmodule

module \ID重定向控制逻辑  (
  input  \跳转 ,
  input  [31:0] IR,
  input  [4:0] rs,
  input  [4:0] rt,
  input  [4:0] MEM_WriteReg_num,
  input  EX_MemRead,
  input  [4:0] EX_WriteReg_num,
  input  MEM_RegWrite,
  input  EX_RegWrite,
  output Stall,
  output FlushID_EX,
  output FlushIF_ID,
  output [1:0] FwdA,
  output [1:0] FwdB
);

  wire and_1_out, and_2_out, and_3_out, and_4_out, and_5_out, and_6_out, comparator_1_gt, comparator_1_lt,
       comparator_2_gt, comparator_2_lt, EX_WriteReg__rs, EX_WriteReg__rt, MEM_WriteReg__rs,
       MEM_WriteReg__rt, rs__0, RsUsed, rt__0, RtUsed;
  wire [1:0] multiplexer_1_out, multiplexer_3_out;

  rsrtused rsrtused_1 (
    .OP0(IR[26]), .OP1(IR[27]), .OP2(IR[28]), .OP3(IR[29]), .OP4(IR[30]), .OP5(IR[31]), .F0(IR[0]),
    .F1(IR[1]), .F2(IR[2]), .F3(IR[3]), .F4(IR[4]), .F5(IR[5]), .RsUsed(RsUsed), .RtUsed(RtUsed));
  Comparator #(.width(5), .mode("twosComplement")) comparator_1 (
    .a(rs), .b({5{1'b0}}), .gt(comparator_1_gt), .lt(comparator_1_lt));  // open: eq
  Comparator #(.width(5), .mode("twosComplement")) comparator_2 (
    .a(rt), .b({5{1'b0}}), .gt(comparator_2_gt), .lt(comparator_2_lt));  // open: eq
  or or_1 (rs__0, comparator_1_gt, comparator_1_lt);
  or or_2 (rt__0, comparator_2_gt, comparator_2_lt);
  Multiplexer #(.select(1), .width(2), .disabled("Z"), .enable("false")) multiplexer_1 (
    .in0(2'b00), .in1(2'b01), .out(multiplexer_1_out), .sel(and_1_out));
  and and_1 (and_1_out, RsUsed, MEM_RegWrite, rs__0, MEM_WriteReg__rs);
  Comparator #(.width(5), .mode("twosComplement")) comparator_3 (
    .a(MEM_WriteReg_num), .b(rs), .eq(MEM_WriteReg__rs));  // open: gt, lt
  Comparator #(.width(5), .mode("twosComplement")) comparator_4 (
    .a(MEM_WriteReg_num), .b(rt), .eq(MEM_WriteReg__rt));  // open: gt, lt
  Comparator #(.width(5), .mode("twosComplement")) comparator_5 (
    .a(EX_WriteReg_num), .b(rs), .eq(EX_WriteReg__rs));  // open: gt, lt
  Comparator #(.width(5), .mode("twosComplement")) comparator_6 (
    .a(EX_WriteReg_num), .b(rt), .eq(EX_WriteReg__rt));  // open: gt, lt
  Multiplexer #(.select(1), .width(2), .disabled("Z"), .enable("false")) multiplexer_2 (
    .in0(multiplexer_1_out), .in1(2'b10), .out(FwdA), .sel(and_2_out));
  and and_2 (and_2_out, RsUsed, EX_RegWrite, rs__0, EX_WriteReg__rs);
  and and_3 (and_3_out, EX_WriteReg__rs, RsUsed, EX_MemRead, rs__0);
  or or_3 (FlushID_EX, and_3_out, and_4_out);
  and and_4 (and_4_out, EX_WriteReg__rt, RtUsed, EX_MemRead, rt__0);
  Multiplexer #(.select(1), .width(2), .disabled("Z"), .enable("false")) multiplexer_3 (
    .in0(2'b00), .in1(2'b01), .out(multiplexer_3_out), .sel(and_5_out));
  and and_5 (and_5_out, RtUsed, MEM_RegWrite, rt__0, MEM_WriteReg__rt);
  Multiplexer #(.select(1), .width(2), .disabled("Z"), .enable("false")) multiplexer_4 (
    .in0(multiplexer_3_out), .in1(2'b10), .out(FwdB), .sel(and_6_out));
  and and_6 (and_6_out, RtUsed, EX_RegWrite, rt__0, EX_WriteReg__rt);

  assign FlushIF_ID = \跳转 ;
  assign Stall = FlushID_EX;

  // Notes on the sheet:
  //   op
  //   Func
  //   loaduse
endmodule

module lcdtest (
  input  in_1,
  input  in_2,
  input  [23:0] in_3,
  output [23:0] out_4
);

  wire button_1_out, button_2_out, clock_1_out, clock_2_out, clock_3_out, clock_4_out, clock_5_out,
       clock_6_out, comparator_1_eq, counter_1_carry, d_ff_1_qn, d_ff_2_q, lcd_video_2_p7, not_1_out;
  wire [6:0] counter_1_q, counter_2_q;
  wire [23:0] counter_3_q, counter_4_q;
  wire [31:0] rom_2_data;

  D_Flip_Flop #(.trigger("rising"), .Pre_Clr_Positions("LEGACY"), .NegatePresetClear("false"), .enable("true"), .NewFFLayout("false")) d_ff_1 (
    .D(in_2), .Qn(d_ff_1_qn));  // open: clk, Q, preset, en, reset
  Counter #(.width(7), .max('h7f), .ongoal("wrap"), .trigger("rising"), .behavior("new")) counter_1 (
    .count(d_ff_1_qn), .Q(counter_1_q), .carry(counter_1_carry), .clk(clock_1_out));  // open: load, D, clr, preset, down
  Clock #(.highDuration(1), .lowDuration(1)) clock_1 (.out(clock_1_out));
  Clock #(.highDuration(1), .lowDuration(1)) clock_2 (.out(clock_2_out));
  Button button_1 (.out(button_1_out));
  Clock #(.highDuration(1), .lowDuration(1)) clock_3 (.out(clock_3_out));
  Counter #(.width(7), .max('h7f), .ongoal("wrap"), .trigger("rising"), .behavior("new")) counter_2 (
    .Q(counter_2_q), .clk(counter_1_carry));  // open: load, D, count, carry, clr, preset, down
  Counter #(.width(24), .max('hffffff), .ongoal("wrap"), .trigger("rising"), .behavior("new")) counter_3 (
    .Q(counter_3_q), .clk(clock_2_out));  // open: load, D, count, carry, clr, preset, down
  ROM #(.addrWidth(24), .dataWidth(24), .Select("low")) rom_1 (.addr(counter_3_q), .data(out_4));
  // LCD_Video lcd_video_1: pin names not known; wires that end beside it: button_1_out, clock_3_out, in_1, counter_1_q, counter_2_q, {1'b0, out_4[20:16], out_4[12:8], out_4[4:0]}
  Counter #(.width(24), .max('hffffff), .ongoal("wrap"), .trigger("rising"), .behavior("new")) counter_4 (
    .count(not_1_out), .Q(counter_4_q), .clk(clock_4_out));  // open: load, D, carry, clr, preset, down
  Clock #(.highDuration(1), .lowDuration(1)) clock_4 (.out(clock_4_out));
  Clock #(.highDuration(1), .lowDuration(1)) clock_5 (.out(clock_5_out));
  Button button_2 (.out(button_2_out));
  not not_1 (not_1_out, comparator_1_eq);
  Comparator #(.width(32), .mode("twosComplement")) comparator_1 (
    .a({32{1'b1}}), .b(rom_2_data), .eq(comparator_1_eq));  // open: gt, lt
  ROM #(.addrWidth(24), .dataWidth(32), .Select("low")) rom_2 (.addr(counter_4_q), .data(rom_2_data));
  // LCD_Video lcd_video_2: pin names not known; wires that end beside it: button_2_out, clock_5_out, not_1_out, rom_2_data[13:7], rom_2_data[6:0], {16{1'b1}}, lcd_video_2_p7
  Clock #(.highDuration(1), .lowDuration(1)) clock_6 (.out(clock_6_out));
  D_Flip_Flop #(.trigger("rising"), .Pre_Clr_Positions("LEGACY"), .NegatePresetClear("false"), .enable("true"), .NewFFLayout("false")) d_ff_2 (
    .clk(comparator_1_eq), .D(not_1_out), .Q(d_ff_2_q), .reset(lcd_video_2_p7));  // open: Qn, preset, en
  D_Flip_Flop #(.trigger("rising"), .Pre_Clr_Positions("LEGACY"), .NegatePresetClear("false"), .enable("true"), .NewFFLayout("false")) d_ff_3 (
    .clk(clock_6_out), .D(d_ff_2_q), .Q(lcd_video_2_p7));  // open: Qn, preset, en, reset

  // Notes on the sheet:
  //   contents of rom_1 (hex, n*v repeats v):
  //   22*70f11 71011 4*70f11 60f11 4*70f11 60f11 60f11 60f11 70f11 60f10 70f11 60f10 70f11 60f10 6*60f11
  //   60f10 60f11 60e10 60e10 60f11 60e10 60e10 60e10 60f11 60e10 60e10 60e10 60e11 60e10 60e11 4*60e10
  //   50e10 60e11 50e10 60e10 6*50e10 4*50d10 50e10 12*50d10 5*40d10 40c10 40c10 40c10 40d10 40c10 40c10
  //   40c0f 40c0f 40c10 40c0f 40c10 5*40c0f 30c0f 40c0f 30c0f 40c10 40c0f 40c0f 30b0f 30c0f 6*30b0f
  //   10*70f11 70f10 8*70f11 71011 17*70f11 60f10 60f11 4*70f11 4*60f11 60f10 60f11 60f11 60e10 60f11
  //   60e10 5*60f11 60e11 60e11 60e11 5*60e10 60e11 60e10 60e11 60e10 60e11 60e10 50e10 50d10 60e10 50e10
  //   50e10 50d10 50e10 50e10 14*50d10 40d10 50d10 50d10 40d10 40d10 40d10 50d10 40c10 40c10 40d10 40c10
  //   40c0f 40d10 9*40c0f 30c0f 40c0f 30c0f 40c0f 40c0f 30b0f 30b0f 30b0f 30c0f 30b0f 30b0f 30b0f 4*70f11
  //   71011 71011 70f11 70f11 71011 8*70f11 71011 5*70f11 81011 19*70f11 60f10 70f11 70f11 70f11 60f10
  //   9*60f11 4*60e10 60f11 60e10 60f11 8*60e10 50e10 60e11 60e10 6*50e10 50d10 50d10 50d10 50e10 10*50d10
  //   40d10 50d10 50d10 50d10 40d10 50d10 40d10 40c10 40d10 7*40c10 40c0f 40c0f 40c0f 40c10 5*40c0f 30c0f
  //   30b0f 30b0f 30c0f 4*30b0f 70f11 70f11 70f11 81012 71011 70f11 70f11 70f11 71011 70f11 71012 70f11
  //   71011 81011 70f11 71011 70f11 70f11 70f11 81011 70f11 80f11 81011 10*70f11 71011 11*70f11 60f10
  //   70f11 70f11 60f10 70f11 70f11 60f11 70f11 70f11 60f11 60f11 60f10 60f10 4*60f11 60f10 60e10 60f11
  //   12*60e10 4*50e10 50d10 50e10 50e10 12*50d10 40d10 40d10 40d10 50d10 40d10 40c0f 40d0f 40d10 5*40c10
  //   5*40c0f 40c10 40c10 40c10 30c0f 40c0f 40c0f 40c0f 30c0f 30c0f 30b0f 30c0f 30b0f 30b0f 30b0f 70f11
  //   70f11 71011 71011 71011 70f11 71011 71011 81011 70f11 71011 81011 70f11 71011 71011 81011 81011
  //   81011 70f11 80f11 81011 81011 70f11 81011 81011 71011 70f11 70f11 70f11 71011 20*70f11 60f11 60f10
  //   60f11 70f11 70f11 70f11 60f11 60f10 60f10 60f10 60f11 60f11 60f11 60e11 60e10 60e10 60e11 60e10
  //   60f11 8*60e10 8*50e10 50d10 50e10 13*50d10 40d10 40d10 40d10 40c10 40d10 40c0f 40c10 40c10 40d10
  //   40c10 40c10 40c0f 40c0f 40c10 40c10 40c0f 40c0f 30b0f 40c0f 40c0f 40b0f 40c10 40c0f 30c0f 30c0f
  //   30c0f 30b0f 30b0f 71011 70f11 70f11 71011 71011 81011 81011 71011 4*81011 70f11 5*81011 4*71011
  //   81011 70f11 81011 81011 71011 70f11 70f11 70f11 71011 70f11 71011 19*70f11 60f11 70f11 70f11 70f10
  //   70f11 70f11 70f11 60e10 60f10 70f11 70f11 70f11 60f11 60f11 60e10 60e10 70f11 60e10 60f11 60e11
  //   8*60e10 4*50e10 50d10 50e10 50e10 50d10 50e10 12*50d10 7*40d10 40c10 40c10 40c0f 40c10 40c0f 40c10
  //   40c0f 40c10 4*40c0f 40c10 40c0f 40c0f 40c0f 4*30b0f 71011 71011 71011 14*81011 70f11 81011 81011
  //   71011 71011 81011 81011 70f11 81011 4*71011 70f11 70f11 71011 5*70f11 81011 81011 21*70f11 60f10
  //   60f11 60f11 70f10 60f10 60f11 60e10 60e10 60e11 60f11 10*60e10 60e11 60e10 50e10 60e10 50d10 50e10
  //   14*50d10 40d10 40d10 50d10 40d10 40d10 40d10 40c0f 40c10 40c0f 40c10 40c10 8*40c0f 40b10 40c10 40c0f
  //   40c0f 40c0f 30b0f 30b0f 30c0f 81011 70f11 20*81011 70f11 81011 81011 81011 71011 81011 81011 70f11
  //   70f11 71011 71011 71011 70f11 70f11 71011 70f11 70f11 81011 81011 5*70f11 71011 15*70f11 60f10 70f11
  //   70f11 60f10 60f10 70f11 60e10 60f11 60f10 60f10 60f10 60f11 60e10 60e11 9*60e10 50e10 60e10 60e11
  //   50e10 50d10 50d10 50e10 8*50d10 40d10 50d10 50d10 50d10 7*40d10 40c10 40c10 40c10 40c0f 40c0f 40c10
  //   40c10 40c0f 40c0f 40c0f 40c10 40c10 30c0f 30c0f 30c0f 30b0f 30b0f 5*81011 71011 12*81011 71011 71011
  //   7*81011 71011 81011 70f11 81011 81011 71011 81011 81011 71011 5*81011 70f11 81011 6*70f11 71011
  //   70f11 70f11 81011 80f12 70f11 81012 11*70f11 60e10 70f11 60f10 60f10 70f11 60f11 60e10 60f11
  //   10*60e10 50e10 60e10 50e10 60e11 50d10 4*50e10 8*50d10 40d10 50d10 50d10 50d10 40d10 50d10 40d10
  //   40d10 40d10 40d0f 40d10 40d10 40c0f 40c10 40c0f 40c0f 40c10 40c0f 40c10 40c0f 40c0f 30c0f 40c0f
  //   30c0f 40b0f 30b0f 32*81011 71011 81011 71011 4*81011 70f11 81011 70f11 81011 81011 81011 71011 70f11
  //   71011 71011 81011 71012 14*70f11 60f10 70f11 60f10 70f11 70f11 70f11 60e10 70f11 60e10 60f10 60f10
  //   60f11 60f11 8*60e10 4*50e10 60e10 50e10 50e10 13*50d10 40d10 40d10 50d10 40d10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
  //   contents of rom_2 (hex, n*v repeats v):
  //   285 306 387 408 489 50a 58b 60c 68d 70e 78f 810 891 912 993 a14 a95 b16 b97 c18 c99 d1a d9b e1c e9d
  //   f1e f9f 1020 10a1 1122 11a3 1224 2a4 323 3a2 421 4a0 51f 59e 61d 69c 71b 79a 819 898 917 996 a15 a94
  //   b13 b92 c11 c90 d0f d8e e0d e8c f0b f8a 1009 1088 1107 1186 1205 ffffffff
endmodule

module \逻辑判断  (
  input  in_1,
  input  in_2,
  input  in_3,
  input  in_4,
  input  in_5,
  input  in_6,
  input  in_7,
  input  in_8,
  input  in_9,
  output out_10
);

  wire _1, _2, _3, _4, _5, _6, _7, _8, _9, and_1_out, and_2_out, and_3_out, and_4_out, and_5_out, and_6_out,
       and_7_out, and_8_out;

  Counter #(.width(1), .max('h1), .ongoal("wrap"), .trigger("rising"), .behavior("new")) counter_1 (
    .Q(_1), .clk(in_1));  // open: load, D, count, carry, clr, preset, down
  Counter #(.width(1), .max('h1), .ongoal("wrap"), .trigger("rising"), .behavior("new")) counter_2 (
    .Q(_2), .clk(in_2));  // open: load, D, count, carry, clr, preset, down
  Counter #(.width(1), .max('h1), .ongoal("wrap"), .trigger("rising"), .behavior("new")) counter_3 (
    .Q(_3), .clk(in_3));  // open: load, D, count, carry, clr, preset, down
  Counter #(.width(1), .max('h1), .ongoal("wrap"), .trigger("rising"), .behavior("new")) counter_4 (
    .Q(_4), .clk(in_4));  // open: load, D, count, carry, clr, preset, down
  Counter #(.width(1), .max('h1), .ongoal("wrap"), .trigger("rising"), .behavior("new")) counter_5 (
    .Q(_5), .clk(in_5));  // open: load, D, count, carry, clr, preset, down
  Counter #(.width(1), .max('h1), .ongoal("wrap"), .trigger("rising"), .behavior("new")) counter_6 (
    .Q(_6), .clk(in_6));  // open: load, D, count, carry, clr, preset, down
  Counter #(.width(1), .max('h1), .ongoal("wrap"), .trigger("rising"), .behavior("new")) counter_7 (
    .Q(_7), .clk(in_7));  // open: load, D, count, carry, clr, preset, down
  Counter #(.width(1), .max('h1), .ongoal("wrap"), .trigger("rising"), .behavior("new")) counter_8 (
    .Q(_8), .clk(in_8));  // open: load, D, count, carry, clr, preset, down
  Counter #(.width(1), .max('h1), .ongoal("wrap"), .trigger("rising"), .behavior("new")) counter_9 (
    .Q(_9), .clk(in_9));  // open: load, D, count, carry, clr, preset, down
  and and_1 (and_1_out, _1, _2, _3);
  and and_2 (and_2_out, _4, _5, _6);
  and and_3 (and_3_out, _7, _8, _9);
  and and_4 (and_4_out, _1, _4, _7);
  and and_5 (and_5_out, _2, _5, _8);
  and and_6 (and_6_out, _3, _6, _9);
  and and_7 (and_7_out, _1, _5, _9);
  and and_8 (and_8_out, _3, _5, _7);
  or or_1 (out_10, and_1_out, and_2_out, and_3_out, and_4_out, and_5_out, and_6_out, and_7_out, and_8_out);
endmodule

module \游戏界面  (
);

  wire _1_out, _2_out, _4_out, _5_out, _6_out, _7_out, _8_out, _9_out, lcd_video_1_p5, RST_out;
  wire [6:0] \国标转区位码_1_位号 , \国标转区位码_1_区号 , \国标转区位码_2_位号 , \国标转区位码_2_区号 ;
  wire [31:0] \单周期mips_单级中断_1_out_16 , \字库_1_p3 , \字库_1_p4 , \字库_1_p5 , \字库_1_p6 , \字库_1_p7 , \字库_1_p8 ,
       \字库_1_p9 , \字库_1_p10 , \字库_1_p11 , \字库_1_p12 , \字库_1_p13 , \字库_1_p14 , \字库_1_p15 , \字库_1_p16 ,
       \字库_1_p17 , \字库_1_p18 , \字库_1_p19 , \字库_1_p20 , \字库_2_p3 , \字库_2_p4 , \字库_2_p5 , \字库_2_p6 , \字库_2_p7 ,
       \字库_2_p8 , \字库_2_p9 , \字库_2_p10 , \字库_2_p11 , \字库_2_p12 , \字库_2_p13 , \字库_2_p14 , \字库_2_p15 ,
       \字库_2_p16 , \字库_2_p17 , \字库_2_p18 , \字库_2_p19 , \字库_2_p20 , \字库_2_p21 , \字库_2_p22 , \字库_2_p23 ,
       \字库_2_p24 , \字库_2_p25 , \字库_2_p26 , \字库_2_p27 , \字库_2_p28 , \字库_2_p29 , \字库_2_p30 , \字库_2_p31 ,
       \字库_2_p32 , \字库_2_p33 , \字库_2_p34 , \字库_2_p35 , \字库_2_p36 , \字库_2_p37 , \字库_2_p38 , \字库_2_p39 ,
       \字库_2_p40 , \字库_2_p41 , \字库_2_p42 , \字库_2_p43 , \字库_2_p44 , \字库_2_p45 , \字库_2_p46 , \字库_2_p47 ,
       \字库_2_p48 ;

  Button RST (.out(RST_out));
  \单周期MIPS_单级中断  \u_单周期mips_单级中断_1  (
    .in_2(_1_out), .in_3(_2_out), .in_4(lcd_video_1_p5), .in_5(_4_out), .in_6(_5_out), .in_7(_6_out),
    .in_8(_7_out), .in_9(_8_out), .in_10(_9_out), .in_1(RST_out), .out_16(\单周期mips_单级中断_1_out_16 ));  // open: out_11, out_12, out_13, out_14, out_15
  Button _1 (.out(_1_out));
  Button _4 (.out(_4_out));
  Button _7 (.out(_7_out));
  Button _2 (.out(_2_out));
  Button _5 (.out(_5_out));
  Button _8 (.out(_8_out));
  // LCD_Video lcd_video_1: pin names not known; wires that end beside it: RST_out, _4_out, _2_out, _5_out, lcd_video_1_p5
  Button _3 (.out(lcd_video_1_p5));
  Button _6 (.out(_6_out));
  Button _9 (.out(_9_out));
  \国标转区位码  \u_国标转区位码_1  (.\位号 (\国标转区位码_1_位号 ), .\区号 (\国标转区位码_1_区号 ), .GB2312(\单周期mips_单级中断_1_out_16 [31:16]));
  \国标转区位码  \u_国标转区位码_2  (.\位号 (\国标转区位码_2_位号 ), .\区号 (\国标转区位码_2_区号 ), .GB2312(\单周期mips_单级中断_1_out_16 [15:0]));
  // 字库 字库_1: pin names not known; wires that end beside it: \国标转区位码_1_区号 , \国标转区位码_1_位号 , \字库_1_p3 , \字库_1_p4 , \字库_1_p5 , \字库_1_p6 , \字库_1_p7 , \字库_1_p8 , \字库_1_p9 , \字库_1_p10 , \字库_1_p11 , \字库_1_p12 , \字库_1_p13 , \字库_1_p14 , \字库_1_p15 , \字库_1_p16 , \字库_1_p17 , \字库_1_p18 , \字库_1_p19 , \字库_1_p20 
  // 字库 字库_2: pin names not known; wires that end beside it: \国标转区位码_2_区号 , \国标转区位码_2_位号 , \字库_2_p3 , \字库_2_p4 , \字库_2_p5 , \字库_2_p6 , \字库_2_p7 , \字库_2_p8 , \字库_2_p9 , \字库_2_p10 , \字库_2_p11 , \字库_2_p12 , \字库_2_p13 , \字库_2_p14 , \字库_2_p15 , \字库_2_p16 , \字库_2_p17 , \字库_2_p18 , \字库_2_p19 , \字库_2_p20 , \字库_2_p21 , \字库_2_p22 , \字库_2_p23 , \字库_2_p24 , \字库_2_p25 , \字库_2_p26 , \字库_2_p27 , \字库_2_p28 , \字库_2_p29 , \字库_2_p30 , \字库_2_p31 , \字库_2_p32 , \字库_2_p33 , \字库_2_p34 , \字库_2_p35 , \字库_2_p36 , \字库_2_p37 , \字库_2_p38 , \字库_2_p39 , \字库_2_p40 , \字库_2_p41 , \字库_2_p42 , \字库_2_p43 , \字库_2_p44 , \字库_2_p45 , \字库_2_p46 , \字库_2_p47 , \字库_2_p48 
  DotMatrix #(.inputtype("row"), .matrixcols(32), .matrixrows(32), .persist(0), .dotshape("square")) dotmatrix_1 (
    .row0(\字库_1_p3 ), .row1(\字库_1_p4 ), .row2(\字库_1_p5 ), .row3(\字库_1_p6 ), .row4(\字库_1_p7 ),
    .row5(\字库_1_p8 ), .row6(\字库_1_p9 ), .row7(\字库_1_p10 ), .row8(\字库_1_p11 ), .row9(\字库_1_p12 ),
    .row10(\字库_1_p13 ), .row11(\字库_1_p14 ), .row12(\字库_1_p15 ), .row13(\字库_1_p16 ), .row14(\字库_1_p17 ),
    .row15(\字库_1_p18 ), .row16(\字库_1_p19 ), .row17(\字库_1_p20 ), .row18(\字库_2_p3 ), .row19(\字库_2_p4 ),
    .row20(\字库_2_p5 ), .row21(\字库_2_p6 ), .row22(\字库_2_p7 ), .row23(\字库_2_p8 ), .row24(\字库_2_p9 ),
    .row25(\字库_2_p10 ), .row26(\字库_2_p11 ), .row27(\字库_2_p12 ), .row28(\字库_2_p13 ), .row29(\字库_2_p14 ),
    .row30(\字库_2_p15 ), .row31(\字库_2_p16 ));
  DotMatrix #(.inputtype("row"), .matrixcols(32), .matrixrows(32), .persist(0), .dotshape("square")) dotmatrix_2 (
    .row0(\字库_2_p17 ), .row1(\字库_2_p18 ), .row2(\字库_2_p19 ), .row3(\字库_2_p20 ), .row4(\字库_2_p21 ),
    .row5(\字库_2_p22 ), .row6(\字库_2_p23 ), .row7(\字库_2_p24 ), .row8(\字库_2_p25 ), .row9(\字库_2_p26 ),
    .row10(\字库_2_p27 ), .row11(\字库_2_p28 ), .row12(\字库_2_p29 ), .row13(\字库_2_p30 ), .row14(\字库_2_p31 ),
    .row15(\字库_2_p32 ), .row16(\字库_2_p33 ), .row17(\字库_2_p34 ), .row18(\字库_2_p35 ), .row19(\字库_2_p36 ),
    .row20(\字库_2_p37 ), .row21(\字库_2_p38 ), .row22(\字库_2_p39 ), .row23(\字库_2_p40 ), .row24(\字库_2_p41 ),
    .row25(\字库_2_p42 ), .row26(\字库_2_p43 ), .row27(\字库_2_p44 ), .row28(\字库_2_p45 ), .row29(\字库_2_p46 ),
    .row30(\字库_2_p47 ), .row31(\字库_2_p48 ));
endmodule
